// Logisim project version-C.circ as structural Verilog
module main (
  input  [7:0] in_1,
  input  [7:0] in_2,
  input  subtract_nadd,
  input  or_nand,
  input  logical_naddition,
  output [7:0] out_6,
  output out_7,
  output Not_equal_0
);

  wire clock_1_out;
  wire [7:0] B_output, C_output, D_output, demultiplexer_1_out0, demultiplexer_1_out1, demultiplexer_2_out0,
       demultiplexer_2_out1, demultiplexer_3_out0, demultiplexer_3_out1, demultiplexer_4_out0,
       demultiplexer_4_out1, n8bit_or_1_out, n8bit_or_2_out, n8bit_or_3_out, registers_1_output;

  ALU alu_1 (
    .Input_1(in_1), .Input_2(in_2), .Control(subtract_nadd), .Control_2(or_nand),
    .logical_add(logical_naddition), .Output(out_6), .Carry(out_7), .Equal(Not_equal_0));
  _8bit_OR_Gate u_8bit_or_1 (.In_2(demultiplexer_1_out0), .In_1(demultiplexer_2_out0), .Out(n8bit_or_1_out));
  _8bit_OR_Gate u_8bit_or_2 (.In_2(n8bit_or_1_out), .In_1(demultiplexer_3_out0), .Out(n8bit_or_2_out));
  _8bit_OR_Gate u_8bit_or_3 (.In_2(n8bit_or_2_out), .In_1(demultiplexer_4_out0), .Out(n8bit_or_3_out));
  Demultiplexer #(.width(8), .enable("false")) demultiplexer_1 (
    .out0(demultiplexer_1_out0), .out1(demultiplexer_1_out1), .in(registers_1_output), .sel(1'b0));
  Demultiplexer #(.width(8), .enable("false")) demultiplexer_2 (
    .out0(demultiplexer_2_out0), .out1(demultiplexer_2_out1), .in(B_output), .sel(1'b0));
  Demultiplexer #(.width(8), .enable("false")) demultiplexer_3 (
    .out0(demultiplexer_3_out0), .out1(demultiplexer_3_out1), .in(C_output), .sel(1'b0));
  Demultiplexer #(.width(8), .enable("false")) demultiplexer_4 (
    .out0(demultiplexer_4_out0), .out1(demultiplexer_4_out1), .in(D_output), .sel(1'b0));
  Clock clock_1 (.out(clock_1_out));
  registers registers_1 (.Clock(clock_1_out), .ER(1'b1), .EW(1'b1), .Input({8{1'b1}}), .Output(registers_1_output));
  registers B (.Clock(clock_1_out), .Input({8{1'b1}}), .Output(B_output));  // open: ER, EW
  registers C (.Clock(clock_1_out), .Input({8{1'b1}}), .Output(C_output));  // open: ER, EW
  registers D (.Clock(clock_1_out), .Input({8{1'b1}}), .Output(D_output));  // open: ER, EW
endmodule

module registers (
  input  [7:0] Input,
  input  Clock,
  input  ER,
  input  EW,
  output [7:0] Output
);

  wire [7:0] Mux_output, n8bit_register_1_output;

  _8bit_2_input_multiplexer Mux (.Input_1(Input), .Input_2(n8bit_register_1_output), .Output(Mux_output), .Control(ER));
  _8bit_register u_8bit_register_1 (
    .\input (Mux_output), .clock(Clock), .\output (n8bit_register_1_output));  // open: M, N, CLR, G2, G1
  _8bit_AND_Gate _8_bit_and (.In_2(n8bit_register_1_output), .In_1({8{EW}}), .Out(Output));
endmodule

module ALU (
  input  [7:0] Input_1,
  input  [7:0] Input_2,
  input  Control,
  input  Control_2,
  input  logical_add,
  output [7:0] Output,
  output Carry,
  output Equal
);

  wire quad_or_1__1y, quad_or_1__2y, quad_or_1__3y, quad_or_1__4y, quad_or_2__1y, quad_or_2__2y;
  wire [7:0] adder_2_output, adder_output, demux_2_output_1, demux_2_output_2, demux_output_1,
       demux_output_2, mux_output, n8bit_and_out, n8bit_or_out, or_out, xor_write;

  _8bit_2_output_demuliplexer demux (
    .Output_1(demux_output_1), .Output_2(demux_output_2), .Input(Input_2), .Control(Control_2));
  _8bit_XOR \xor  (.Read_1(Input_2), .Read_2({8{1'b1}}), .Write(xor_write));
  _8bit_AND_Gate u_8bit_and (.In_2(demux_output_2), .In_1(demux_2_output_2), .Out(n8bit_and_out));
  _8bit_OR_Gate u_8bit_or (.In_2(demux_output_1), .In_1(demux_2_output_1), .Out(n8bit_or_out));
  _8bit_adder adder (.Input1(xor_write), .Input_2(8'h1), .Output(adder_output));  // open: Carry
  _8bit_2_output_demuliplexer demux_2 (
    .Output_1(demux_2_output_1), .Output_2(demux_2_output_2), .Input(Input_1), .Control(Control_2));
  _8bit_2_input_multiplexer mux (.Input_1(adder_output), .Input_2(Input_2), .Output(mux_output), .Control(Control));
  _8bit_OR_Gate \or  (.In_2(n8bit_and_out), .In_1(n8bit_or_out), .Out(or_out));
  _8bit_adder adder_2 (.Input1(Input_1), .Input_2(mux_output), .Output(adder_2_output), .Carry(Carry));
  _8bit_2_input_multiplexer Mux_2 (.Input_1(or_out), .Input_2(adder_2_output), .Output(Output), .Control(logical_add));
  Quad_OR_Gate quad_or_1 (
    ._1a(Output[0]), ._1b(Output[1]), ._1y(quad_or_1__1y), ._2a(Output[2]), ._2b(Output[3]),
    ._2y(quad_or_1__2y), ._3a(Output[4]), ._3b(Output[5]), ._3y(quad_or_1__3y), ._4a(Output[6]),
    ._4b(Output[7]), ._4y(quad_or_1__4y));
  Quad_OR_Gate quad_or_2 (
    ._1a(quad_or_1__3y), ._1b(quad_or_1__4y), ._1y(quad_or_2__1y), ._2a(quad_or_1__1y), ._2b(quad_or_1__2y),
    ._2y(quad_or_2__2y), ._4a(quad_or_2__1y), ._4b(quad_or_2__2y), ._4y(Equal));  // open: _3a, _3b, _3y
endmodule

module Input (
  input  Input,
  input  Clock
);

  wire [3:0] multiplexer_1_out, register_1_q, undriven_2;
  wire [3:1] undriven;

  Register #(.width(4)) register_1 (.D(multiplexer_1_out), .Q(register_1_q));  // open: en, clk, clr
  Multiplexer #(.width(4), .enable("false")) multiplexer_1 (
    .in0(undriven_2), .in1({undriven, Input}), .out(multiplexer_1_out));  // open: sel
endmodule

module RAM (
  input  W_TO,
  input  R_FROM,
  input  R_SELECT,
  input  [7:0] Addr,
  input  [7:0] Data,
  input  CLK,
  output [7:0] OUT_1,
  output [7:0] OUT_2
);

  wire hex_inverter_1__1_prime, hex_inverter_1__2_prime, hex_inverter_1__3_prime, hex_inverter_1__4_prime,
       hex_inverter_1__5_prime, hex_inverter_1__6_prime, hex_inverter_2__1_prime, hex_inverter_2__2_prime,
       hex_inverter_2__3_prime, hex_inverter_2__4_prime, hex_inverter_2__5_prime, hex_inverter_2__6_prime,
       hex_inverter_3__1_prime, hex_inverter_3__2_prime, hex_inverter_3__3_prime, hex_inverter_3__4_prime,
       hex_inverter_3__5_prime, hex_inverter_3__6_prime, hex_inverter_4__1_prime, hex_inverter_4__2_prime,
       hex_inverter_4__3_prime, hex_inverter_4__4_prime, hex_inverter_4__5_prime, hex_inverter_4__6_prime,
       hex_inverter_5__1_prime, hex_inverter_5__2_prime, hex_inverter_5__3_prime, hex_inverter_5__4_prime,
       hex_inverter_5__5_prime, hex_inverter_5__6_prime, hex_inverter_6__1_prime, hex_inverter_6__2_prime,
       hex_inverter_6__3_prime, hex_inverter_6__4_prime, hex_inverter_6__5_prime, hex_inverter_6__6_prime,
       hex_inverter_7__1_prime, hex_inverter_7__2_prime, hex_inverter_7__3_prime, hex_inverter_7__4_prime,
       hex_inverter_7__5_prime, hex_inverter_7__6_prime, hex_inverter_8__1_prime, hex_inverter_8__2_prime,
       hex_inverter_8__3_prime, hex_inverter_8__4_prime, hex_inverter_8__5_prime, hex_inverter_8__6_prime,
       hex_inverter_9__1_prime, hex_inverter_9__2_prime, hex_inverter_9__3_prime, hex_inverter_9__4_prime,
       hex_inverter_9__5_prime, hex_inverter_9__6_prime, hex_inverter_10__1_prime, hex_inverter_10__2_prime,
       hex_inverter_10__3_prime, hex_inverter_10__4_prime, hex_inverter_10__5_prime,
       hex_inverter_10__6_prime, hex_inverter_11__1_prime, hex_inverter_11__2_prime,
       hex_inverter_11__4_prime, hex_inverter_11__5_prime, quad_and_1__1y, quad_and_1__2y, quad_and_1__3y,
       quad_and_1__4y, quad_and_2__1y, quad_and_2__2y, quad_and_2__3y, quad_and_2__4y, quad_and_3__1y,
       quad_and_3__2y, quad_and_3__3y, quad_and_3__4y, quad_and_4__1y, quad_and_4__2y, quad_and_4__3y,
       quad_and_4__4y, quad_and_5__1y, quad_and_5__2y, quad_and_5__3y, quad_and_5__4y, quad_and_6__1y,
       quad_and_6__2y, quad_and_6__3y, quad_and_6__4y, quad_and_7__1y, quad_and_7__2y, quad_and_7__3y,
       quad_and_7__4y, quad_and_8__1y, quad_and_8__2y, quad_and_8__3y, quad_and_8__4y, quad_and_9__1y,
       quad_and_9__2y, quad_and_9__3y, quad_and_9__4y, quad_and_10__1y, quad_and_10__2y, quad_and_10__3y,
       quad_and_10__4y, quad_and_11__1y, quad_and_11__2y, quad_and_11__3y, quad_and_11__4y, quad_and_12__1y,
       quad_and_12__2y, quad_and_12__3y, quad_and_12__4y, quad_and_13__1y, quad_and_13__2y, quad_and_13__3y,
       quad_and_13__4y, quad_and_14__1y, quad_and_14__2y, quad_and_14__3y, quad_and_14__4y, quad_and_15__1y,
       quad_and_15__2y, quad_and_15__3y, quad_and_15__4y, quad_and_16__1y, quad_and_16__2y, quad_and_16__3y,
       quad_and_16__4y, quad_and_17__1y, quad_and_17__3y, triple_2_channel_demux_1_ax,
       triple_2_channel_demux_1_ay, triple_2_channel_demux_1_bx, triple_2_channel_demux_1_by,
       triple_2_channel_demux_1_cx, triple_2_channel_demux_1_cy, triple_2_channel_demux_2_ax,
       triple_2_channel_demux_2_ay, triple_2_channel_demux_2_bx, triple_2_channel_demux_2_by,
       triple_2_channel_demux_2_cx, triple_2_channel_demux_2_cy, triple_2_channel_demux_3_ax,
       triple_2_channel_demux_3_ay, triple_2_channel_demux_3_bx, triple_2_channel_demux_3_by,
       triple_2_channel_demux_3_cx, triple_2_channel_demux_3_cy, triple_2_channel_demux_4_ax,
       triple_2_channel_demux_4_ay, triple_2_channel_demux_4_by, triple_2_channel_demux_4_cx,
       triple_2_channel_demux_4_cy, triple_2_channel_demux_5_ax, triple_2_channel_demux_5_ay,
       triple_2_channel_demux_5_bx, triple_2_channel_demux_5_by, triple_2_channel_demux_5_cx,
       triple_2_channel_demux_5_cy, triple_2_channel_demux_6_ax, triple_2_channel_demux_6_ay,
       triple_2_channel_demux_6_bx, triple_2_channel_demux_6_by, triple_2_channel_demux_6_cx,
       triple_2_channel_demux_6_cy, triple_2_channel_demux_7_ax, triple_2_channel_demux_7_ay,
       triple_2_channel_demux_7_bx, triple_2_channel_demux_7_by, triple_2_channel_demux_7_cx,
       triple_2_channel_demux_7_cy, triple_2_channel_demux_8_ax, triple_2_channel_demux_8_ay,
       triple_2_channel_demux_8_bx, triple_2_channel_demux_8_by, triple_2_channel_demux_8_cx,
       triple_2_channel_demux_8_cy, triple_2_channel_demux_9_ax, triple_2_channel_demux_9_ay,
       triple_2_channel_demux_9_bx, triple_2_channel_demux_9_by, triple_2_channel_demux_9_cx,
       triple_2_channel_demux_9_cy, triple_2_channel_demux_10_ax, triple_2_channel_demux_10_ay,
       triple_2_channel_demux_10_bx, triple_2_channel_demux_10_by, triple_2_channel_demux_10_cx,
       triple_2_channel_demux_10_cy, triple_2_channel_demux_11_bx, triple_2_channel_demux_11_by;
  wire [7:0] n8bit_register_1_output;

  triple_2_channel_demux triple_2_channel_demux_1 (
    .bx(triple_2_channel_demux_1_bx), .by(triple_2_channel_demux_1_by), .cy(triple_2_channel_demux_1_cy),
    .c_in(triple_2_channel_demux_2_bx), .cx(triple_2_channel_demux_1_cx), .enable(1'b1),
    .b_in(triple_2_channel_demux_2_cy), .a_in(triple_2_channel_demux_2_cx), .ax(triple_2_channel_demux_1_ax),
    .ay(triple_2_channel_demux_1_ay), .A(Addr[0]), .B(Addr[0]), .C(Addr[0]));
  triple_2_channel_demux triple_2_channel_demux_2 (
    .bx(triple_2_channel_demux_2_bx), .by(triple_2_channel_demux_2_by), .cy(triple_2_channel_demux_2_cy),
    .c_in(triple_2_channel_demux_4_cx), .cx(triple_2_channel_demux_2_cx), .enable(1'b1),
    .b_in(triple_2_channel_demux_4_cy), .a_in(triple_2_channel_demux_4_cy), .ax(triple_2_channel_demux_2_ax),
    .ay(triple_2_channel_demux_2_ay), .A(Addr[1]), .B(Addr[1]), .C(Addr[1]));
  Quad_AND_Gate quad_and_1 (
    ._1a(R_FROM), ._1b(triple_2_channel_demux_1_ax), ._1y(quad_and_1__1y), ._2a(R_FROM),
    ._2b(triple_2_channel_demux_1_ay), ._2y(quad_and_1__2y), ._3a(W_TO), ._3b(triple_2_channel_demux_1_ax),
    ._3y(quad_and_1__3y), ._4a(W_TO), ._4b(triple_2_channel_demux_1_ay), ._4y(quad_and_1__4y));
  Quad_AND_Gate quad_and_2 (
    ._1a(R_FROM), ._1b(triple_2_channel_demux_1_bx), ._1y(quad_and_2__1y), ._2a(R_FROM),
    ._2b(triple_2_channel_demux_1_by), ._2y(quad_and_2__2y), ._3a(W_TO), ._3b(triple_2_channel_demux_1_bx),
    ._3y(quad_and_2__3y), ._4a(W_TO), ._4b(triple_2_channel_demux_1_by), ._4y(quad_and_2__4y));
  Quad_AND_Gate quad_and_3 (
    ._1a(R_FROM), ._1b(triple_2_channel_demux_1_cx), ._1y(quad_and_3__1y), ._2a(R_FROM),
    ._2b(triple_2_channel_demux_1_cy), ._2y(quad_and_3__2y), ._3a(W_TO), ._3b(triple_2_channel_demux_1_cx),
    ._3y(quad_and_3__3y), ._4a(W_TO), ._4b(triple_2_channel_demux_1_cy), ._4y(quad_and_3__4y));
  Hex_Inverter hex_inverter_1 (
    ._1(quad_and_1__1y), ._1_prime(hex_inverter_1__1_prime), ._2(quad_and_1__2y),
    ._2_prime(hex_inverter_1__2_prime), ._3(quad_and_2__1y), ._3_prime(hex_inverter_1__3_prime),
    ._4(quad_and_1__3y), ._4_prime(hex_inverter_1__4_prime), ._5(quad_and_1__4y),
    ._5_prime(hex_inverter_1__5_prime), ._6(quad_and_2__3y), ._6_prime(hex_inverter_1__6_prime));
  Hex_Inverter hex_inverter_2 (
    ._1(quad_and_2__2y), ._1_prime(hex_inverter_2__1_prime), ._2(quad_and_3__1y),
    ._2_prime(hex_inverter_2__2_prime), ._3(quad_and_3__2y), ._3_prime(hex_inverter_2__3_prime),
    ._4(quad_and_2__4y), ._4_prime(hex_inverter_2__4_prime), ._5(quad_and_3__3y),
    ._5_prime(hex_inverter_2__5_prime), ._6(quad_and_3__4y), ._6_prime(hex_inverter_2__6_prime));
  _8bit_register u_8bit_register_1 (
    .M(hex_inverter_1__1_prime), .N(hex_inverter_1__1_prime), .\input (Data), .clock(CLK),
    .CLR(quad_and_17__1y), .\output (n8bit_register_1_output), .G2(hex_inverter_1__4_prime),
    .G1(hex_inverter_1__4_prime));
  _8bit_register u_8bit_register_2 (
    .M(hex_inverter_1__2_prime), .N(hex_inverter_1__2_prime), .\input (Data), .clock(CLK),
    .CLR(quad_and_17__1y), .\output (n8bit_register_1_output), .G2(hex_inverter_1__5_prime),
    .G1(hex_inverter_1__5_prime));
  _8bit_register u_8bit_register_3 (
    .M(hex_inverter_1__3_prime), .N(hex_inverter_1__3_prime), .\input (Data), .clock(CLK),
    .CLR(quad_and_17__1y), .\output (n8bit_register_1_output), .G2(hex_inverter_1__6_prime),
    .G1(hex_inverter_1__6_prime));
  _8bit_register u_8bit_register_4 (
    .M(hex_inverter_2__1_prime), .N(hex_inverter_2__1_prime), .\input (Data), .clock(CLK),
    .CLR(quad_and_17__1y), .\output (n8bit_register_1_output), .G2(hex_inverter_2__4_prime),
    .G1(hex_inverter_2__4_prime));
  _8bit_register u_8bit_register_5 (
    .M(hex_inverter_2__2_prime), .N(hex_inverter_2__2_prime), .\input (Data), .clock(CLK),
    .CLR(quad_and_17__1y), .\output (n8bit_register_1_output), .G2(hex_inverter_2__5_prime),
    .G1(hex_inverter_2__5_prime));
  _8bit_register u_8bit_register_6 (
    .M(hex_inverter_2__3_prime), .N(hex_inverter_2__3_prime), .\input (Data), .clock(CLK),
    .CLR(quad_and_17__1y), .\output (n8bit_register_1_output), .G2(hex_inverter_2__6_prime),
    .G1(hex_inverter_2__6_prime));
  triple_2_channel_demux triple_2_channel_demux_3 (
    .bx(triple_2_channel_demux_3_bx), .by(triple_2_channel_demux_3_by), .cy(triple_2_channel_demux_3_cy),
    .c_in(triple_2_channel_demux_2_ay), .cx(triple_2_channel_demux_3_cx), .enable(1'b1),
    .b_in(triple_2_channel_demux_2_ax), .a_in(triple_2_channel_demux_4_cy), .ax(triple_2_channel_demux_3_ax),
    .ay(triple_2_channel_demux_3_ay), .A(Addr[0]), .B(Addr[0]), .C(Addr[0]));
  Quad_AND_Gate quad_and_4 (
    ._1a(R_FROM), ._1b(triple_2_channel_demux_3_ax), ._1y(quad_and_4__1y), ._2a(R_FROM),
    ._2b(triple_2_channel_demux_3_ay), ._2y(quad_and_4__2y), ._3a(W_TO), ._3b(triple_2_channel_demux_3_ax),
    ._3y(quad_and_4__3y), ._4a(W_TO), ._4b(triple_2_channel_demux_3_ay), ._4y(quad_and_4__4y));
  Quad_AND_Gate quad_and_5 (
    ._1a(R_FROM), ._1b(triple_2_channel_demux_3_bx), ._1y(quad_and_5__1y), ._2a(R_FROM),
    ._2b(triple_2_channel_demux_3_by), ._2y(quad_and_5__2y), ._3a(W_TO), ._3b(triple_2_channel_demux_3_bx),
    ._3y(quad_and_5__3y), ._4a(W_TO), ._4b(triple_2_channel_demux_3_by), ._4y(quad_and_5__4y));
  Quad_AND_Gate quad_and_6 (
    ._1a(R_FROM), ._1b(triple_2_channel_demux_3_cx), ._1y(quad_and_6__1y), ._2a(R_FROM),
    ._2b(triple_2_channel_demux_3_cy), ._2y(quad_and_6__2y), ._3a(W_TO), ._3b(triple_2_channel_demux_3_cx),
    ._3y(quad_and_6__3y), ._4a(W_TO), ._4b(triple_2_channel_demux_3_cy), ._4y(quad_and_6__4y));
  Hex_Inverter hex_inverter_3 (
    ._1(quad_and_4__1y), ._1_prime(hex_inverter_3__1_prime), ._2(quad_and_4__2y),
    ._2_prime(hex_inverter_3__2_prime), ._3(quad_and_5__1y), ._3_prime(hex_inverter_3__3_prime),
    ._4(quad_and_4__3y), ._4_prime(hex_inverter_3__4_prime), ._5(quad_and_4__4y),
    ._5_prime(hex_inverter_3__5_prime), ._6(quad_and_5__3y), ._6_prime(hex_inverter_3__6_prime));
  Hex_Inverter hex_inverter_4 (
    ._1(quad_and_5__2y), ._1_prime(hex_inverter_4__1_prime), ._2(quad_and_6__1y),
    ._2_prime(hex_inverter_4__2_prime), ._3(quad_and_6__2y), ._3_prime(hex_inverter_4__3_prime),
    ._4(quad_and_5__4y), ._4_prime(hex_inverter_4__4_prime), ._5(quad_and_6__3y),
    ._5_prime(hex_inverter_4__5_prime), ._6(quad_and_6__4y), ._6_prime(hex_inverter_4__6_prime));
  _8bit_register u_8bit_register_7 (
    .M(hex_inverter_3__1_prime), .N(hex_inverter_3__1_prime), .\input (Data), .clock(CLK),
    .CLR(quad_and_17__1y), .\output (n8bit_register_1_output), .G2(hex_inverter_3__4_prime),
    .G1(hex_inverter_3__4_prime));
  _8bit_register u_8bit_register_8 (
    .M(hex_inverter_3__2_prime), .N(hex_inverter_3__2_prime), .\input (Data), .clock(CLK),
    .CLR(quad_and_17__1y), .\output (n8bit_register_1_output), .G2(hex_inverter_3__5_prime),
    .G1(hex_inverter_3__5_prime));
  _8bit_register u_8bit_register_9 (
    .M(hex_inverter_3__3_prime), .N(hex_inverter_3__3_prime), .\input (Data), .clock(CLK),
    .CLR(quad_and_17__1y), .\output (n8bit_register_1_output), .G2(hex_inverter_3__6_prime),
    .G1(hex_inverter_3__6_prime));
  _8bit_register u_8bit_register_10 (
    .M(hex_inverter_4__1_prime), .N(hex_inverter_4__1_prime), .\input (Data), .clock(CLK),
    .CLR(quad_and_17__1y), .\output (n8bit_register_1_output), .G2(hex_inverter_4__4_prime),
    .G1(hex_inverter_4__4_prime));
  _8bit_register u_8bit_register_11 (
    .M(hex_inverter_4__2_prime), .N(hex_inverter_4__2_prime), .\input (Data), .clock(CLK),
    .CLR(quad_and_17__1y), .\output (n8bit_register_1_output), .G2(hex_inverter_4__5_prime),
    .G1(hex_inverter_4__5_prime));
  _8bit_register u_8bit_register_12 (
    .M(hex_inverter_4__3_prime), .N(hex_inverter_4__3_prime), .\input (Data), .clock(CLK),
    .CLR(quad_and_17__1y), .\output (n8bit_register_1_output), .G2(hex_inverter_4__6_prime),
    .G1(hex_inverter_4__6_prime));
  triple_2_channel_demux triple_2_channel_demux_4 (
    .bx(triple_2_channel_demux_2_by), .by(triple_2_channel_demux_4_by), .cy(triple_2_channel_demux_4_cy),
    .c_in(triple_2_channel_demux_9_bx), .cx(triple_2_channel_demux_4_cx), .enable(1'b1),
    .b_in(triple_2_channel_demux_9_by), .a_in(triple_2_channel_demux_9_ax), .ax(triple_2_channel_demux_4_ax),
    .ay(triple_2_channel_demux_4_ay), .A(Addr[2]), .B(Addr[2]), .C(Addr[2]));
  triple_2_channel_demux triple_2_channel_demux_5 (
    .bx(triple_2_channel_demux_5_bx), .by(triple_2_channel_demux_5_by), .cy(triple_2_channel_demux_5_cy),
    .c_in(triple_2_channel_demux_6_bx), .cx(triple_2_channel_demux_5_cx), .enable(1'b1),
    .b_in(triple_2_channel_demux_6_cy), .a_in(triple_2_channel_demux_6_cx), .ax(triple_2_channel_demux_5_ax),
    .ay(triple_2_channel_demux_5_ay), .A(Addr[0]), .B(Addr[0]), .C(Addr[0]));
  Quad_AND_Gate quad_and_7 (
    ._1a(R_FROM), ._1b(triple_2_channel_demux_5_ax), ._1y(quad_and_7__1y), ._2a(R_FROM),
    ._2b(triple_2_channel_demux_5_ay), ._2y(quad_and_7__2y), ._3a(W_TO), ._3b(triple_2_channel_demux_5_ax),
    ._3y(quad_and_7__3y), ._4a(W_TO), ._4b(triple_2_channel_demux_5_ay), ._4y(quad_and_7__4y));
  Quad_AND_Gate quad_and_8 (
    ._1a(R_FROM), ._1b(triple_2_channel_demux_5_bx), ._1y(quad_and_8__1y), ._2a(R_FROM),
    ._2b(triple_2_channel_demux_5_by), ._2y(quad_and_8__2y), ._3a(W_TO), ._3b(triple_2_channel_demux_5_bx),
    ._3y(quad_and_8__3y), ._4a(W_TO), ._4b(triple_2_channel_demux_5_by), ._4y(quad_and_8__4y));
  Quad_AND_Gate quad_and_9 (
    ._1a(R_FROM), ._1b(triple_2_channel_demux_5_cx), ._1y(quad_and_9__1y), ._2a(R_FROM),
    ._2b(triple_2_channel_demux_5_cy), ._2y(quad_and_9__2y), ._3a(W_TO), ._3b(triple_2_channel_demux_5_cx),
    ._3y(quad_and_9__3y), ._4a(W_TO), ._4b(triple_2_channel_demux_5_cy), ._4y(quad_and_9__4y));
  Hex_Inverter hex_inverter_5 (
    ._1(quad_and_7__1y), ._1_prime(hex_inverter_5__1_prime), ._2(quad_and_7__2y),
    ._2_prime(hex_inverter_5__2_prime), ._3(quad_and_8__1y), ._3_prime(hex_inverter_5__3_prime),
    ._4(quad_and_7__3y), ._4_prime(hex_inverter_5__4_prime), ._5(quad_and_7__4y),
    ._5_prime(hex_inverter_5__5_prime), ._6(quad_and_8__3y), ._6_prime(hex_inverter_5__6_prime));
  Hex_Inverter hex_inverter_6 (
    ._1(quad_and_8__2y), ._1_prime(hex_inverter_6__1_prime), ._2(quad_and_9__1y),
    ._2_prime(hex_inverter_6__2_prime), ._3(quad_and_9__2y), ._3_prime(hex_inverter_6__3_prime),
    ._4(quad_and_8__4y), ._4_prime(hex_inverter_6__4_prime), ._5(quad_and_9__3y),
    ._5_prime(hex_inverter_6__5_prime), ._6(quad_and_9__4y), ._6_prime(hex_inverter_6__6_prime));
  _8bit_register u_8bit_register_13 (
    .M(hex_inverter_5__1_prime), .N(hex_inverter_5__1_prime), .\input (Data), .clock(CLK),
    .CLR(quad_and_17__1y), .\output (n8bit_register_1_output), .G2(hex_inverter_5__4_prime),
    .G1(hex_inverter_5__4_prime));
  _8bit_register u_8bit_register_14 (
    .M(hex_inverter_5__2_prime), .N(hex_inverter_5__2_prime), .\input (Data), .clock(CLK),
    .CLR(quad_and_17__1y), .\output (n8bit_register_1_output), .G2(hex_inverter_5__5_prime),
    .G1(hex_inverter_5__5_prime));
  _8bit_register u_8bit_register_15 (
    .M(hex_inverter_5__3_prime), .N(hex_inverter_5__3_prime), .\input (Data), .clock(CLK),
    .CLR(quad_and_17__1y), .\output (n8bit_register_1_output), .G2(hex_inverter_5__6_prime),
    .G1(hex_inverter_5__6_prime));
  _8bit_register u_8bit_register_16 (
    .M(hex_inverter_6__1_prime), .N(hex_inverter_6__1_prime), .\input (Data), .clock(CLK),
    .CLR(quad_and_17__1y), .\output (n8bit_register_1_output), .G2(hex_inverter_6__4_prime),
    .G1(hex_inverter_6__4_prime));
  _8bit_register u_8bit_register_17 (
    .M(hex_inverter_6__2_prime), .N(hex_inverter_6__2_prime), .\input (Data), .clock(CLK),
    .CLR(quad_and_17__3y), .\output (n8bit_register_1_output), .G2(hex_inverter_6__5_prime),
    .G1(hex_inverter_6__5_prime));
  _8bit_register u_8bit_register_18 (
    .M(hex_inverter_6__3_prime), .N(hex_inverter_6__3_prime), .\input (Data), .clock(CLK),
    .CLR(quad_and_17__3y), .\output (n8bit_register_1_output), .G2(hex_inverter_6__6_prime),
    .G1(hex_inverter_6__6_prime));
  triple_2_channel_demux triple_2_channel_demux_6 (
    .bx(triple_2_channel_demux_6_bx), .by(triple_2_channel_demux_6_by), .cy(triple_2_channel_demux_6_cy),
    .c_in(triple_2_channel_demux_4_by), .cx(triple_2_channel_demux_6_cx), .enable(1'b1),
    .b_in(triple_2_channel_demux_4_ax), .a_in(triple_2_channel_demux_4_ay), .ax(triple_2_channel_demux_6_ax),
    .ay(triple_2_channel_demux_6_ay), .A(Addr[1]), .B(Addr[1]), .C(Addr[1]));
  triple_2_channel_demux triple_2_channel_demux_7 (
    .bx(triple_2_channel_demux_7_bx), .by(triple_2_channel_demux_7_by), .cy(triple_2_channel_demux_7_cy),
    .c_in(triple_2_channel_demux_6_by), .cx(triple_2_channel_demux_7_cx), .enable(1'b1),
    .b_in(triple_2_channel_demux_6_ax), .a_in(triple_2_channel_demux_6_ay), .ax(triple_2_channel_demux_7_ax),
    .ay(triple_2_channel_demux_7_ay), .A(Addr[0]), .B(Addr[0]), .C(Addr[0]));
  Quad_AND_Gate quad_and_10 (
    ._1a(R_FROM), ._1b(triple_2_channel_demux_7_ax), ._1y(quad_and_10__1y), ._2a(R_FROM),
    ._2b(triple_2_channel_demux_7_ay), ._2y(quad_and_10__2y), ._3a(W_TO), ._3b(triple_2_channel_demux_7_ax),
    ._3y(quad_and_10__3y), ._4a(W_TO), ._4b(triple_2_channel_demux_7_ay), ._4y(quad_and_10__4y));
  Quad_AND_Gate quad_and_11 (
    ._1a(R_FROM), ._1b(triple_2_channel_demux_7_bx), ._1y(quad_and_11__1y), ._2a(R_FROM),
    ._2b(triple_2_channel_demux_7_by), ._2y(quad_and_11__2y), ._3a(W_TO), ._3b(triple_2_channel_demux_7_bx),
    ._3y(quad_and_11__3y), ._4a(W_TO), ._4b(triple_2_channel_demux_7_by), ._4y(quad_and_11__4y));
  Quad_AND_Gate quad_and_12 (
    ._1a(R_FROM), ._1b(triple_2_channel_demux_7_cx), ._1y(quad_and_12__1y), ._2a(R_FROM),
    ._2b(triple_2_channel_demux_7_cy), ._2y(quad_and_12__2y), ._3a(W_TO), ._3b(triple_2_channel_demux_7_cx),
    ._3y(quad_and_12__3y), ._4a(W_TO), ._4b(triple_2_channel_demux_7_cy), ._4y(quad_and_12__4y));
  Hex_Inverter hex_inverter_7 (
    ._1(quad_and_10__1y), ._1_prime(hex_inverter_7__1_prime), ._2(quad_and_10__2y),
    ._2_prime(hex_inverter_7__2_prime), ._3(quad_and_11__1y), ._3_prime(hex_inverter_7__3_prime),
    ._4(quad_and_10__3y), ._4_prime(hex_inverter_7__4_prime), ._5(quad_and_10__4y),
    ._5_prime(hex_inverter_7__5_prime), ._6(quad_and_11__3y), ._6_prime(hex_inverter_7__6_prime));
  Hex_Inverter hex_inverter_8 (
    ._1(quad_and_11__2y), ._1_prime(hex_inverter_8__1_prime), ._2(quad_and_12__1y),
    ._2_prime(hex_inverter_8__2_prime), ._3(quad_and_12__2y), ._3_prime(hex_inverter_8__3_prime),
    ._4(quad_and_11__4y), ._4_prime(hex_inverter_8__4_prime), ._5(quad_and_12__3y),
    ._5_prime(hex_inverter_8__5_prime), ._6(quad_and_12__4y), ._6_prime(hex_inverter_8__6_prime));
  _8bit_register u_8bit_register_19 (
    .M(hex_inverter_7__1_prime), .N(hex_inverter_7__1_prime), .\input (Data), .clock(CLK),
    .CLR(quad_and_17__3y), .\output (n8bit_register_1_output), .G2(hex_inverter_7__4_prime),
    .G1(hex_inverter_7__4_prime));
  _8bit_register u_8bit_register_20 (
    .M(hex_inverter_7__2_prime), .N(hex_inverter_7__2_prime), .\input (Data), .clock(CLK),
    .CLR(quad_and_17__3y), .\output (n8bit_register_1_output), .G2(hex_inverter_7__5_prime),
    .G1(hex_inverter_7__5_prime));
  _8bit_register u_8bit_register_21 (
    .M(hex_inverter_7__3_prime), .N(hex_inverter_7__3_prime), .\input (Data), .clock(CLK),
    .CLR(quad_and_17__3y), .\output (n8bit_register_1_output), .G2(hex_inverter_7__6_prime),
    .G1(hex_inverter_7__6_prime));
  _8bit_register u_8bit_register_22 (
    .M(hex_inverter_8__1_prime), .N(hex_inverter_8__1_prime), .\input (Data), .clock(CLK),
    .CLR(quad_and_17__3y), .\output (n8bit_register_1_output), .G2(hex_inverter_8__4_prime),
    .G1(hex_inverter_8__4_prime));
  _8bit_register u_8bit_register_23 (
    .M(hex_inverter_8__2_prime), .N(hex_inverter_8__2_prime), .\input (Data), .clock(CLK),
    .CLR(quad_and_17__3y), .\output (n8bit_register_1_output), .G2(hex_inverter_8__5_prime),
    .G1(hex_inverter_8__5_prime));
  _8bit_register u_8bit_register_24 (
    .M(hex_inverter_8__3_prime), .N(hex_inverter_8__3_prime), .\input (Data), .clock(CLK),
    .CLR(quad_and_17__3y), .\output (n8bit_register_1_output), .G2(hex_inverter_8__6_prime),
    .G1(hex_inverter_8__6_prime));
  triple_2_channel_demux triple_2_channel_demux_8 (
    .bx(triple_2_channel_demux_8_bx), .by(triple_2_channel_demux_8_by), .cy(triple_2_channel_demux_8_cy),
    .c_in(triple_2_channel_demux_10_bx), .cx(triple_2_channel_demux_8_cx), .enable(1'b1),
    .b_in(triple_2_channel_demux_10_cy), .a_in(triple_2_channel_demux_10_cx),
    .ax(triple_2_channel_demux_8_ax), .ay(triple_2_channel_demux_8_ay), .A(Addr[0]), .B(Addr[0]), .C(Addr[0]));
  triple_2_channel_demux triple_2_channel_demux_9 (
    .bx(triple_2_channel_demux_9_bx), .by(triple_2_channel_demux_9_by), .cy(triple_2_channel_demux_9_cy),
    .c_in(triple_2_channel_demux_9_ay), .cx(triple_2_channel_demux_9_cx), .enable(1'b1),
    .b_in(triple_2_channel_demux_11_bx), .a_in(triple_2_channel_demux_11_by),
    .ax(triple_2_channel_demux_9_ax), .ay(triple_2_channel_demux_9_ay), .A(Addr[3]), .B(Addr[3]), .C(Addr[2]));
  Quad_AND_Gate quad_and_13 (
    ._1a(R_FROM), ._1b(triple_2_channel_demux_8_ax), ._1y(quad_and_13__1y), ._2a(R_FROM),
    ._2b(triple_2_channel_demux_8_ay), ._2y(quad_and_13__2y), ._3a(W_TO), ._3b(triple_2_channel_demux_8_ax),
    ._3y(quad_and_13__3y), ._4a(W_TO), ._4b(triple_2_channel_demux_8_ay), ._4y(quad_and_13__4y));
  Quad_AND_Gate quad_and_14 (
    ._1a(R_FROM), ._1b(triple_2_channel_demux_8_bx), ._1y(quad_and_14__1y), ._2a(R_FROM),
    ._2b(triple_2_channel_demux_8_by), ._2y(quad_and_14__2y), ._3a(W_TO), ._3b(triple_2_channel_demux_8_bx),
    ._3y(quad_and_14__3y), ._4a(W_TO), ._4b(triple_2_channel_demux_8_by), ._4y(quad_and_14__4y));
  Quad_AND_Gate quad_and_15 (
    ._1a(R_FROM), ._1b(triple_2_channel_demux_8_cx), ._1y(quad_and_15__1y), ._2a(R_FROM),
    ._2b(triple_2_channel_demux_8_cy), ._2y(quad_and_15__2y), ._3a(W_TO), ._3b(triple_2_channel_demux_8_cx),
    ._3y(quad_and_15__3y), ._4a(W_TO), ._4b(triple_2_channel_demux_8_cy), ._4y(quad_and_15__4y));
  Hex_Inverter hex_inverter_9 (
    ._1(quad_and_13__1y), ._1_prime(hex_inverter_9__1_prime), ._2(quad_and_13__2y),
    ._2_prime(hex_inverter_9__2_prime), ._3(quad_and_14__1y), ._3_prime(hex_inverter_9__3_prime),
    ._4(quad_and_13__3y), ._4_prime(hex_inverter_9__4_prime), ._5(quad_and_13__4y),
    ._5_prime(hex_inverter_9__5_prime), ._6(quad_and_14__3y), ._6_prime(hex_inverter_9__6_prime));
  Hex_Inverter hex_inverter_10 (
    ._1(quad_and_14__2y), ._1_prime(hex_inverter_10__1_prime), ._2(quad_and_15__1y),
    ._2_prime(hex_inverter_10__2_prime), ._3(quad_and_15__2y), ._3_prime(hex_inverter_10__3_prime),
    ._4(quad_and_14__4y), ._4_prime(hex_inverter_10__4_prime), ._5(quad_and_15__3y),
    ._5_prime(hex_inverter_10__5_prime), ._6(quad_and_15__4y), ._6_prime(hex_inverter_10__6_prime));
  _8bit_register u_8bit_register_25 (
    .M(hex_inverter_9__1_prime), .N(hex_inverter_9__1_prime), .\input (Data), .clock(CLK),
    .CLR(quad_and_17__3y), .\output (n8bit_register_1_output), .G2(hex_inverter_9__4_prime),
    .G1(hex_inverter_9__4_prime));
  _8bit_register u_8bit_register_26 (
    .M(hex_inverter_9__2_prime), .N(hex_inverter_9__2_prime), .\input (Data), .clock(CLK),
    .CLR(quad_and_17__3y), .\output (n8bit_register_1_output), .G2(hex_inverter_9__5_prime),
    .G1(hex_inverter_9__5_prime));
  _8bit_register u_8bit_register_27 (
    .M(hex_inverter_9__3_prime), .N(hex_inverter_9__3_prime), .\input (Data), .clock(CLK),
    .CLR(quad_and_17__3y), .\output (n8bit_register_1_output), .G2(hex_inverter_9__6_prime),
    .G1(hex_inverter_9__6_prime));
  _8bit_register u_8bit_register_28 (
    .M(hex_inverter_10__1_prime), .N(hex_inverter_10__1_prime), .\input (Data), .clock(CLK),
    .CLR(quad_and_17__3y), .\output (n8bit_register_1_output), .G2(hex_inverter_10__4_prime),
    .G1(hex_inverter_10__4_prime));
  _8bit_register u_8bit_register_29 (
    .M(hex_inverter_10__2_prime), .N(hex_inverter_10__2_prime), .\input (Data), .clock(CLK),
    .CLR(quad_and_17__3y), .\output (n8bit_register_1_output), .G2(hex_inverter_10__5_prime),
    .G1(hex_inverter_10__5_prime));
  _8bit_register u_8bit_register_30 (
    .M(hex_inverter_10__3_prime), .N(hex_inverter_10__3_prime), .\input (Data), .clock(CLK),
    .CLR(quad_and_17__3y), .\output (n8bit_register_1_output), .G2(hex_inverter_10__6_prime),
    .G1(hex_inverter_10__6_prime));
  triple_2_channel_demux triple_2_channel_demux_10 (
    .bx(triple_2_channel_demux_10_bx), .by(triple_2_channel_demux_10_by), .cy(triple_2_channel_demux_10_cy),
    .c_in(triple_2_channel_demux_9_cx), .cx(triple_2_channel_demux_10_cx), .enable(1'b1),
    .b_in(triple_2_channel_demux_9_cy), .a_in(triple_2_channel_demux_10_by),
    .ax(triple_2_channel_demux_10_ax), .ay(triple_2_channel_demux_10_ay), .A(Addr[0]), .B(Addr[1]),
    .C(Addr[1]));
  triple_2_channel_demux triple_2_channel_demux_11 (
    .bx(triple_2_channel_demux_11_bx), .by(triple_2_channel_demux_11_by), .enable(1'b1), .b_in(1'b1),
    .B(Addr[4]));  // open: cy, c_in, cx, a_in, ax, ay, A, C
  Quad_AND_Gate quad_and_16 (
    ._1a(R_FROM), ._1b(triple_2_channel_demux_10_ax), ._1y(quad_and_16__1y), ._2a(R_FROM),
    ._2b(triple_2_channel_demux_10_ay), ._2y(quad_and_16__2y), ._3a(W_TO),
    ._3b(triple_2_channel_demux_10_ax), ._3y(quad_and_16__3y), ._4a(W_TO),
    ._4b(triple_2_channel_demux_10_ay), ._4y(quad_and_16__4y));
  Hex_Inverter hex_inverter_11 (
    ._1(quad_and_16__1y), ._1_prime(hex_inverter_11__1_prime), ._2(quad_and_16__2y),
    ._2_prime(hex_inverter_11__2_prime), ._4(quad_and_16__3y), ._4_prime(hex_inverter_11__4_prime),
    ._5(quad_and_16__4y), ._5_prime(hex_inverter_11__5_prime));  // open: _3, _3_prime, _6, _6_prime
  _8bit_register u_8bit_register_31 (
    .M(hex_inverter_11__1_prime), .N(hex_inverter_11__1_prime), .\input (Data), .clock(CLK),
    .CLR(quad_and_17__3y), .\output (n8bit_register_1_output), .G2(hex_inverter_11__4_prime),
    .G1(hex_inverter_11__4_prime));
  _8bit_register u_8bit_register_32 (
    .M(hex_inverter_11__2_prime), .N(hex_inverter_11__2_prime), .\input (Data), .clock(CLK),
    .CLR(quad_and_17__3y), .\output (n8bit_register_1_output), .G2(hex_inverter_11__5_prime),
    .G1(hex_inverter_11__5_prime));
  Quad_AND_Gate quad_and_17 (
    ._1a(Addr[6]), ._1b(W_TO), ._1y(quad_and_17__1y), ._3a(Addr[7]), ._3b(W_TO), ._3y(quad_and_17__3y));  // open: _2a, _2b, _2y, _4a, _4b, _4y
  _8bit_2_output_demuliplexer u_8bit_2_output_demuliplexer_1 (
    .Output_1(OUT_2), .Output_2(OUT_1), .Input(n8bit_register_1_output), .Control(R_SELECT));
endmodule

module _8bit_AND_Gate (
  input  [7:0] In_1,
  input  [7:0] In_2,
  output [7:0] Out
);

  Quad_AND_Gate quad_and_1 (
    ._1a(In_1[0]), ._1b(In_2[0]), ._1y(Out[0]), ._2a(In_1[1]), ._2b(In_2[1]), ._2y(Out[1]), ._3a(In_1[2]),
    ._3b(In_2[2]), ._3y(Out[2]), ._4a(In_1[3]), ._4b(In_2[3]), ._4y(Out[3]));
  Quad_AND_Gate quad_and_2 (
    ._1a(In_1[4]), ._1b(In_2[4]), ._1y(Out[4]), ._2a(In_1[5]), ._2b(In_2[5]), ._2y(Out[5]), ._3a(In_1[6]),
    ._3b(In_2[6]), ._3y(Out[6]), ._4a(In_1[7]), ._4b(In_2[7]), ._4y(Out[7]));
endmodule

module _8bit_OR_Gate (
  input  [7:0] In_1,
  input  [7:0] In_2,
  output [7:0] Out
);

  Quad_OR_Gate quad_or_1 (
    ._1a(In_1[0]), ._1b(In_2[0]), ._1y(Out[0]), ._2a(In_1[1]), ._2b(In_2[1]), ._2y(Out[1]), ._3a(In_1[2]),
    ._3b(In_2[2]), ._3y(Out[2]), ._4a(In_1[3]), ._4b(In_2[3]), ._4y(Out[3]));
  Quad_OR_Gate quad_or_2 (
    ._1a(In_1[4]), ._1b(In_2[4]), ._1y(Out[4]), ._2a(In_1[5]), ._2b(In_2[5]), ._2y(Out[5]), ._3a(In_1[6]),
    ._3b(In_2[6]), ._3y(Out[6]), ._4a(In_1[7]), ._4b(In_2[7]), ._4y(Out[7]));
endmodule

module _8bit_XOR (
  input  [7:0] Read_1,
  input  [7:0] Read_2,
  output [7:0] Write
);

  Quad_XOR_gate quad_xor_gate_1 (
    ._1a(Read_1[2]), ._1b(Read_2[2]), ._1_y(Write[2]), ._2a(Read_2[3]), ._2b(Read_1[3]), ._2_y(Write[3]),
    ._3a(Read_1[0]), ._3b(Read_2[0]), ._3_y(Write[0]), ._4a(Read_2[1]), ._4b(Read_1[1]), ._4_y(Write[1]));
  Quad_XOR_gate quad_xor_gate_2 (
    ._1a(Read_1[6]), ._1b(Read_2[6]), ._1_y(Write[6]), ._2a(Read_1[7]), ._2b(Read_2[7]), ._2_y(Write[7]),
    ._3a(Read_2[4]), ._3b(Read_1[4]), ._3_y(Write[4]), ._4a(Read_2[5]), ._4b(Read_1[5]), ._4_y(Write[5]));
endmodule

module _8bit_2_input_multiplexer (
  input  [7:0] Input_1,
  input  [7:0] Input_2,
  input  Control,
  output [7:0] Output
);

  triple_2_channel_mux triple_2_channel_mux_1 (
    .bx(Input_2[0]), .by(Input_1[0]), .cy(Input_1[1]), .c_out(Output[1]), .cx(Input_2[1]), .enable(1'b1),
    .b_out(Output[0]), .A(Control), .B(Control), .C(Control));  // open: a_out, ax, ay
  triple_2_channel_mux triple_2_channel_mux_2 (
    .bx(Input_2[3]), .by(Input_1[3]), .cy(Input_1[4]), .c_out(Output[4]), .cx(Input_2[4]), .enable(1'b1),
    .b_out(Output[3]), .a_out(Output[2]), .ax(Input_2[2]), .ay(Input_1[2]), .A(Control), .B(Control),
    .C(Control));
  triple_2_channel_mux triple_2_channel_mux_3 (
    .bx(Input_2[6]), .by(Input_1[6]), .cy(Input_1[7]), .c_out(Output[7]), .cx(Input_2[7]), .enable(1'b1),
    .b_out(Output[6]), .a_out(Output[5]), .ax(Input_2[5]), .ay(Input_1[5]), .A(Control), .B(Control),
    .C(Control));
endmodule

module _8bit_2_output_demuliplexer (
  input  [7:0] Input,
  input  Control,
  output [7:0] Output_1,
  output [7:0] Output_2
);

  triple_2_channel_demux triple_2_channel_demux_1 (
    .bx(Output_2[0]), .by(Output_1[0]), .cy(Output_1[1]), .c_in(Input[1]), .cx(Output_2[1]), .enable(1'b1),
    .b_in(Input[0]), .A(Control), .B(Control), .C(Control));  // open: a_in, ax, ay
  triple_2_channel_demux triple_2_channel_demux_2 (
    .bx(Output_2[3]), .by(Output_1[3]), .cy(Output_1[4]), .c_in(Input[4]), .cx(Output_2[4]), .enable(1'b1),
    .b_in(Input[3]), .a_in(Input[2]), .ax(Output_2[2]), .ay(Output_1[2]), .A(Control), .B(Control),
    .C(Control));
  triple_2_channel_demux triple_2_channel_demux_3 (
    .bx(Output_2[6]), .by(Output_1[6]), .cy(Output_1[7]), .c_in(Input[7]), .cx(Output_2[7]), .enable(1'b1),
    .b_in(Input[6]), .a_in(Input[5]), .ax(Output_2[5]), .ay(Output_1[5]), .A(Control), .B(Control),
    .C(Control));
endmodule

module _8bit_register (
  input  M,
  input  CLR,
  input  N,
  input  [7:0] \input ,
  input  clock,
  input  G2,
  input  G1,
  output [7:0] \output 
);

  _4bit_register u_4bit_register_1 (
    .M(M), .N(N), ._1Q(\input [0]), ._2Q(\input [1]), ._3Q(\input [2]), ._4Q(\input [3]), .CLK(clock),
    .CLR(CLR), ._1D(\output [0]), ._2D(\output [1]), ._3D(\output [2]), ._4D(\output [3]), .G2(G2), .G1(G1));
  _4bit_register u_4bit_register_2 (
    .M(M), .N(N), ._1Q(\input [4]), ._2Q(\input [5]), ._3Q(\input [6]), ._4Q(\input [7]), .CLK(clock),
    .CLR(CLR), ._1D(\output [4]), ._2D(\output [5]), ._3D(\output [6]), ._4D(\output [7]), .G2(G2), .G1(G1));
endmodule

module _8bit_adder (
  input  [7:0] Input1,
  input  [7:0] Input_2,
  output [7:0] Output,
  output Carry
);

  wire n4bit_adder_1_c_out;

  _4bit_adder u_4bit_adder_1 (
    .In_1(Input1[3:0]), .In_2(Input_2[3:0]), .C_in(1'b0), .Out(Output[3:0]), .C_out(n4bit_adder_1_c_out));
  _4bit_adder u_4bit_adder_2 (
    .In_1(Input1[7:4]), .In_2(Input_2[7:4]), .C_in(n4bit_adder_1_c_out), .Out(Output[7:4]), .C_out(Carry));
endmodule

module triple_2_channel_mux (
  input  bx,
  input  by,
  input  cy,
  input  ax,
  input  ay,
  input  cx,
  input  A,
  input  enable,
  input  B,
  input  C,
  output b_out,
  output a_out,
  output c_out
);

  Multiplexer multiplexer_1 (.in0(cx), .in1(cy), .out(c_out), .sel(C), .en(enable));
  Multiplexer multiplexer_2 (.in0(bx), .in1(by), .out(b_out), .sel(B), .en(enable));
  Multiplexer multiplexer_3 (.in0(ax), .in1(ay), .out(a_out), .sel(A), .en(enable));

  // Notes on the sheet:
  //   Cd4053B as multiplexer
endmodule

module triple_2_channel_demux (
  input  b_in,
  input  a_in,
  input  c_in,
  input  A,
  input  enable,
  input  B,
  input  C,
  output bx,
  output by,
  output cy,
  output ax,
  output ay,
  output cx
);

  Demultiplexer demultiplexer_1 (.out0(cx), .out1(cy), .in(c_in), .sel(C), .en(enable));
  Demultiplexer demultiplexer_2 (.out0(bx), .out1(by), .in(b_in), .sel(B), .en(enable));
  Demultiplexer demultiplexer_3 (.out0(ax), .out1(ay), .in(a_in), .sel(A), .en(enable));

  // Notes on the sheet:
  //   Cd4053B as demultiplexer
endmodule

module Quad_OR_Gate (
  input  _3a,
  input  _1a,
  input  _3b,
  input  _1b,
  input  _4a,
  input  _2a,
  input  _4b,
  input  _2b,
  output _3y,
  output _1y,
  output _4y,
  output _2y
);

  or or_1 (_1y, _1a, _1b);
  or or_2 (_2y, _2a, _2b);
  or or_3 (_3y, _3a, _3b);
  or or_4 (_4y, _4a, _4b);
endmodule

module Quad_AND_Gate (
  input  _3a,
  input  _1a,
  input  _3b,
  input  _1b,
  input  _4a,
  input  _2a,
  input  _4b,
  input  _2b,
  output _3y,
  output _1y,
  output _4y,
  output _2y
);

  and and_1 (_1y, _1a, _1b);
  and and_2 (_2y, _2a, _2b);
  and and_3 (_3y, _3a, _3b);
  and and_4 (_4y, _4a, _4b);
endmodule

module _4bit_adder (
  input  [3:0] In_1,
  input  [3:0] In_2,
  input  C_in,
  output [3:0] Out,
  output C_out
);

  wire quad_and_1__1y, quad_and_1__2y, quad_and_1__3y, quad_and_1__4y, quad_and_2__1y, quad_and_2__2y,
       quad_and_2__3y, quad_and_2__4y, quad_or_1__1y, quad_or_1__2y, quad_or_1__3y, quad_xor_gate_1__1_y,
       quad_xor_gate_1__3_y, quad_xor_gate_2__1_y, quad_xor_gate_2__3_y;

  Quad_XOR_gate quad_xor_gate_1 (
    ._1a(In_1[0]), ._1b(In_2[0]), ._1_y(quad_xor_gate_1__1_y), ._2a(quad_xor_gate_1__1_y), ._2b(C_in),
    ._2_y(Out[0]), ._3a(In_1[1]), ._3b(In_2[1]), ._3_y(quad_xor_gate_1__3_y), ._4a(quad_xor_gate_1__3_y),
    ._4b(quad_or_1__1y), ._4_y(Out[1]));
  Quad_XOR_gate quad_xor_gate_2 (
    ._1a(In_1[2]), ._1b(In_2[2]), ._1_y(quad_xor_gate_2__1_y), ._2a(quad_xor_gate_2__1_y),
    ._2b(quad_or_1__2y), ._2_y(Out[2]), ._3a(In_1[3]), ._3b(In_2[3]), ._3_y(quad_xor_gate_2__3_y),
    ._4a(quad_xor_gate_2__3_y), ._4b(quad_or_1__3y), ._4_y(Out[3]));
  Quad_AND_Gate quad_and_1 (
    ._1a(quad_xor_gate_1__1_y), ._1b(C_in), ._1y(quad_and_1__1y), ._2a(In_2[0]), ._2b(In_1[0]),
    ._2y(quad_and_1__2y), ._3a(quad_xor_gate_1__3_y), ._3b(quad_or_1__1y), ._3y(quad_and_1__3y),
    ._4a(In_1[1]), ._4b(In_2[1]), ._4y(quad_and_1__4y));
  Quad_AND_Gate quad_and_2 (
    ._1a(quad_xor_gate_2__1_y), ._1b(quad_or_1__2y), ._1y(quad_and_2__1y), ._2a(In_2[2]), ._2b(In_1[2]),
    ._2y(quad_and_2__2y), ._3a(quad_xor_gate_2__3_y), ._3b(quad_or_1__3y), ._3y(quad_and_2__3y),
    ._4a(In_2[3]), ._4b(In_1[3]), ._4y(quad_and_2__4y));
  Quad_OR_Gate quad_or_1 (
    ._1a(quad_and_1__1y), ._1b(quad_and_1__2y), ._1y(quad_or_1__1y), ._2a(quad_and_1__3y),
    ._2b(quad_and_1__4y), ._2y(quad_or_1__2y), ._3a(quad_and_2__1y), ._3b(quad_and_2__2y),
    ._3y(quad_or_1__3y), ._4a(quad_and_2__3y), ._4b(quad_and_2__4y), ._4y(C_out));
endmodule

module _4bit_register (
  input  M,
  input  N,
  input  CLR,
  input  _1Q,
  input  _2Q,
  input  _3Q,
  input  _4Q,
  input  CLK,
  input  G2,
  input  G1,
  output _1D,
  output _2D,
  output _3D,
  output _4D
);

  wire and_1_out, and_2_out, and_3_out, and_4_out, and_5_out, and_6_out, and_7_out, and_8_out, and_9_out,
       and_10_out, d_ff_1_q, d_ff_2_q, d_ff_3_q, d_ff_4_q, not_1_out, not_2_out, not_3_out, not_4_out,
       not_5_out, or_1_out, or_2_out, or_3_out, or_4_out;

  not not_1 (not_1_out, M);
  not not_2 (not_2_out, N);
  and and_1 (and_1_out, not_1_out, not_2_out);
  not not_3 (not_3_out, and_10_out);
  and and_2 (and_2_out, d_ff_1_q, not_3_out);
  and and_3 (and_3_out, _1Q, and_10_out);
  and and_4 (and_4_out, d_ff_2_q, not_3_out);
  and and_5 (and_5_out, _2Q, and_10_out);
  and and_6 (and_6_out, d_ff_3_q, not_3_out);
  and and_7 (and_7_out, _3Q, and_10_out);
  and and_8 (and_8_out, d_ff_4_q, not_3_out);
  and and_9 (and_9_out, _4Q, and_10_out);
  or or_1 (or_1_out, and_2_out, and_3_out);
  or or_2 (or_2_out, and_4_out, and_5_out);
  or or_3 (or_3_out, and_6_out, and_7_out);
  or or_4 (or_4_out, and_8_out, and_9_out);
  D_Flip_Flop d_ff_1 (.clk(CLK), .D(or_1_out), .Q(d_ff_1_q), .en(1'b1), .reset(CLR));  // open: Qn, preset
  D_Flip_Flop d_ff_2 (.clk(CLK), .D(or_2_out), .Q(d_ff_2_q), .en(1'b1), .reset(CLR));  // open: Qn, preset
  D_Flip_Flop d_ff_3 (.clk(CLK), .D(or_3_out), .Q(d_ff_3_q), .en(1'b1), .reset(CLR));  // open: Qn, preset
  D_Flip_Flop d_ff_4 (.clk(CLK), .D(or_4_out), .Q(d_ff_4_q), .en(1'b1), .reset(CLR));  // open: Qn, preset
  and and_10 (and_10_out, not_4_out, not_5_out);
  not not_4 (not_4_out, G2);
  not not_5 (not_5_out, G1);
  assign _1D = and_1_out ? d_ff_1_q : 1'bz;  // Controlled_Buffer controlled_buffer_1
  assign _2D = and_1_out ? d_ff_2_q : 1'bz;  // Controlled_Buffer controlled_buffer_2
  assign _3D = and_1_out ? d_ff_3_q : 1'bz;  // Controlled_Buffer controlled_buffer_3
  assign _4D = and_1_out ? d_ff_4_q : 1'bz;  // Controlled_Buffer controlled_buffer_4
endmodule

module Hex_Inverter (
  input  _1,
  input  _4,
  input  _2,
  input  _5,
  input  _6,
  input  _3,
  output _1_prime,
  output _4_prime,
  output _5_prime,
  output _2_prime,
  output _6_prime,
  output _3_prime
);

  not not_1 (_1_prime, _1);
  not not_2 (_2_prime, _2);
  not not_3 (_3_prime, _3);
  not not_4 (_4_prime, _4);
  not not_5 (_5_prime, _5);
  not not_6 (_6_prime, _6);
endmodule

module Quad_XOR_gate (
  input  _3a,
  input  _1a,
  input  _3b,
  input  _1b,
  input  _4a,
  input  _2a,
  input  _4b,
  input  _2b,
  output _3_y,
  output _1_y,
  output _4_y,
  output _2_y
);

  xor xor_1 (_1_y, _1a, _1b);
  xor xor_2 (_2_y, _2a, _2b);
  xor xor_3 (_3_y, _3a, _3b);
  xor xor_4 (_4_y, _4a, _4b);

  // Notes on the sheet:
  //   XOR Gate Sn74hc86n
endmodule
