// Logisim project version-1.circ as structural Verilog
module main (
);

  wire clock_1_out, control_1_addition_nlogical, control_1_clear_input_reg, control_1_clear_registers,
       control_1_er1, control_1_er2, control_1_er3, control_1_er4, control_1_ew1, control_1_ew2,
       control_1_ew3, control_1_ew4, control_1_load_saved_pc, control_1_logical_naddition,
       control_1_nequal_zero, control_1_nload_lsb, control_1_nload_msb, control_1_or_nand,
       control_1_ram_r_from, control_1_ram_w_to, control_1_read_mux_1_1, control_1_read_mux_1_2,
       control_1_read_mux_1_3, control_1_read_mux_2_1, control_1_read_mux_2_2, control_1_read_mux_2_3,
       control_1_subtract_nadd, control_1_write_mux_1, control_1_write_mux_2, input_1_ninterrupt,
       Input_Button_out, RESET_BUTTON_out, undriven, undriven_2;
  wire [7:0] A_read, B_read, C_read, control_1_const_out, D_read, ram_1_out_1, Read_1_Bus_out_9,
       Read_2_Bus_out_9, undriven_3, Write_Bus_out_6;
  wire [15:0] pc_1_pc_value;
  wire [23:0] rom_1_instruction;

  Button RESET_BUTTON (.out(RESET_BUTTON_out));
  PC pc_1 (
    .write_byte(Read_1_Bus_out_9), .Reset_PC(RESET_BUTTON_out), .nLoad_MSB(control_1_nload_msb),
    .nLoad_LSB(control_1_nload_lsb), .nInterrupt(input_1_ninterrupt),
    .Load_Saved_PC(control_1_load_saved_pc), .Clock(clock_1_out), .PC_value(pc_1_pc_value));
  Button Input_Button (.out(Input_Button_out));
  Control control_1 (
    .Instruction_Input(rom_1_instruction), .carry(undriven), .equals_zero(undriven_2), .EW1(control_1_ew1),
    .ER1(control_1_er1), .EW2(control_1_ew2), .ER2(control_1_er2), .EW3(control_1_ew3), .ER3(control_1_er3),
    .EW4(control_1_ew4), .ER4(control_1_er4), .Clear_registers(control_1_clear_registers),
    .Const_Out(control_1_const_out), .Read_Mux_1_1(control_1_read_mux_1_1),
    .Read_Mux_1_2(control_1_read_mux_1_2), .Read_Mux_1_3(control_1_read_mux_1_3),
    .Read_Mux_2_1(control_1_read_mux_2_1), .Read_Mux_2_2(control_1_read_mux_2_2),
    .Read_Mux_2_3(control_1_read_mux_2_3), .Write_Mux_1(control_1_write_mux_1),
    .Write_Mux_2(control_1_write_mux_2), .nLoad_MSB(control_1_nload_msb), .nLoad_LSB(control_1_nload_lsb),
    .Load_Saved_PC(control_1_load_saved_pc), .RAM_R_From(control_1_ram_r_from),
    .RAM_W_To(control_1_ram_w_to), .nequal_zero(control_1_nequal_zero),
    .subtract_nadd(control_1_subtract_nadd), .or_nand(control_1_or_nand),
    .logical_naddition(control_1_logical_naddition), .addition_nlogical(control_1_addition_nlogical),
    .Clear_Input_reg(control_1_clear_input_reg));
  ROM rom_1 (.PC_Address(pc_1_pc_value), .Instruction(rom_1_instruction));
  Clock clock_1 (.out(clock_1_out));
  Input input_1 (
    .Input(Input_Button_out), .Clear_Reg(control_1_clear_input_reg), .Clock(clock_1_out),
    .nInterrupt(input_1_ninterrupt));  // open: Reg
  registers A (
    .Read(A_read), .Write(Write_Bus_out_6), .Clock(clock_1_out), .ER(control_1_er1), .EW(control_1_ew1),
    .Clear(control_1_clear_registers));
  registers B (
    .Read(B_read), .Write(Write_Bus_out_6), .Clock(clock_1_out), .ER(control_1_er2), .EW(control_1_ew2),
    .Clear(control_1_clear_registers));
  _8bit_3_input_multiplexer Write_Bus (
    .Input_1(ram_1_out_1), .Input_2(undriven_3), .Input_3(Read_1_Bus_out_9),
    .Control_1(control_1_write_mux_1), .Control_2(control_1_write_mux_2), .out_6(Write_Bus_out_6));
  RAM ram_1 (
    .W_TO(control_1_ram_w_to), .R_FROM(control_1_ram_r_from), .R_SELECT(control_1_nequal_zero),
    .Addr(Read_2_Bus_out_9), .Data(Read_1_Bus_out_9), .CLK(clock_1_out), .OUT_1(ram_1_out_1));  // open: OUT_2
  _8bit_5_input_multiplexer Read_1_Bus (
    .Input_1(D_read), .Input_2(C_read), .Input_3(A_read), .Input_4(B_read), .Input_5(control_1_const_out),
    .Control_1(control_1_read_mux_2_1), .Control_2(control_1_read_mux_2_2),
    .Control_3(control_1_read_mux_2_3), .out_9(Read_1_Bus_out_9));
  _8bit_5_input_multiplexer Read_2_Bus (
    .Input_1(D_read), .Input_2(C_read), .Input_3(A_read), .Input_4(B_read), .Input_5(control_1_const_out),
    .Control_1(control_1_read_mux_1_1), .Control_2(control_1_read_mux_1_2),
    .Control_3(control_1_read_mux_1_3), .out_9(Read_2_Bus_out_9));
  registers C (
    .Read(C_read), .Write(Write_Bus_out_6), .Clock(clock_1_out), .ER(control_1_er3), .EW(control_1_ew3),
    .Clear(control_1_clear_registers));
  registers D (
    .Read(D_read), .Write(Write_Bus_out_6), .Clock(clock_1_out), .ER(control_1_er4), .EW(control_1_ew4),
    .Clear(control_1_clear_registers));
endmodule

// Reg
module registers (
  input  Clock,
  input  ER,
  input  [7:0] Write,
  input  EW,
  input  Clear,
  output [7:0] Read
);

  _8bit_register u_8bit_register_1 (
    .M(ER), .N(ER), .\input (Write), .clock(Clock), .CLR(Clear), .\output (Read), .G2(EW), .G1(EW));
endmodule

module ALU (
  input  [7:0] Input_1,
  input  [7:0] Input_2,
  input  nEqual_Zero,
  input  Subtract_nAdd,
  input  Or_nAnd,
  input  in_6,
  input  shift_nother,
  input  addition_nother,
  input  not_nlogical,
  input  regular_nlogical_comparison,
  input  in_11,
  output [7:0] Output,
  output Carry,
  output Equal
);

  wire hex_inverter_1__6_prime, quad_or_1__1y, quad_or_1__2y, quad_or_1__3y, quad_or_1__4y, quad_or_2__1y,
       quad_or_2__2y;
  wire [7:0] adder_2_output, adder_output, And_out, demux_2_output_1, demux_2_output_2, demux_output_1,
       demux_output_2, mux_output, n8bit_2_input_multiplexer_1_output, n8bit_2_input_multiplexer_2_output,
       n8bit_2_output_demuliplexer_1_output_1, n8bit_2_output_demuliplexer_1_output_2,
       n8bit_3_input_multiplexer_1_out_6, n8bit_and_out, n8bit_or_out, or_out, xor_write;

  Hex_Inverter hex_inverter_1 (
    ._6(in_6), ._6_prime(hex_inverter_1__6_prime));  // open: _1, _1_prime, _2, _2_prime, _3, _3_prime, _4, _4_prime, _5, _5_prime
  _8bit_AND_Gate And (.In_2(Input_2), .In_1({8{nEqual_Zero}}), .Out(And_out));
  _8bit_2_output_demuliplexer demux (
    .Output_1(demux_output_1), .Output_2(demux_output_2), .Input(And_out), .Control(Or_nAnd));
  _8bit_2_output_demuliplexer u_8bit_2_output_demuliplexer_1 (
    .Output_1(n8bit_2_output_demuliplexer_1_output_1), .Output_2(n8bit_2_output_demuliplexer_1_output_2),
    .Input(Input_1), .Control(in_6));
  _8bit_XOR \xor  (.Read_1(And_out), .Read_2({8{1'b1}}), .Write(xor_write));
  _8bit_AND_Gate u_8bit_and (.In_2(demux_output_2), .In_1(demux_2_output_2), .Out(n8bit_and_out));
  _8bit_OR_Gate u_8bit_or (.In_2(demux_output_1), .In_1(demux_2_output_1), .Out(n8bit_or_out));
  _8bit_adder adder (.Input1(xor_write), .Input_2(8'h1), .Output(adder_output));  // open: Carry
  _8bit_2_output_demuliplexer demux_2 (
    .Output_1(demux_2_output_1), .Output_2(demux_2_output_2), .Input(Input_1), .Control(Or_nAnd));
  _8bit_2_input_multiplexer mux (
    .Input_1(adder_output), .Input_2(And_out), .Output(mux_output), .Control(Subtract_nAdd));
  _8bit_OR_Gate \or  (.In_2(n8bit_and_out), .In_1(n8bit_or_out), .Out(or_out));
  _8bit_2_input_multiplexer u_8bit_2_input_multiplexer_1 (
    .Input_1({n8bit_2_output_demuliplexer_1_output_2[6:0], 1'b0}),
    .Input_2({1'b0, n8bit_2_output_demuliplexer_1_output_1[7:1]}),
    .Output(n8bit_2_input_multiplexer_1_output), .Control(hex_inverter_1__6_prime));
  _8bit_adder adder_2 (.Input1(Input_1), .Input_2(mux_output), .Output(adder_2_output), .Carry(Carry));
  _8bit_3_input_multiplexer u_8bit_3_input_multiplexer_1 (
    .Input_1(xor_write), .Input_2(or_out), .Input_3(adder_2_output), .Control_1(addition_nother),
    .Control_2(not_nlogical), .out_6(n8bit_3_input_multiplexer_1_out_6));
  _8bit_2_input_multiplexer u_8bit_2_input_multiplexer_2 (
    .Input_1(n8bit_2_input_multiplexer_1_output), .Input_2(n8bit_3_input_multiplexer_1_out_6),
    .Output(n8bit_2_input_multiplexer_2_output), .Control(shift_nother));
  Quad_OR_Gate quad_or_1 (
    ._1a(n8bit_3_input_multiplexer_1_out_6[0]), ._1b(n8bit_3_input_multiplexer_1_out_6[1]),
    ._1y(quad_or_1__1y), ._2a(n8bit_3_input_multiplexer_1_out_6[2]),
    ._2b(n8bit_3_input_multiplexer_1_out_6[3]), ._2y(quad_or_1__2y),
    ._3a(n8bit_3_input_multiplexer_1_out_6[4]), ._3b(n8bit_3_input_multiplexer_1_out_6[5]),
    ._3y(quad_or_1__3y), ._4a(n8bit_3_input_multiplexer_1_out_6[6]),
    ._4b(n8bit_3_input_multiplexer_1_out_6[7]), ._4y(quad_or_1__4y));
  _8bit_3_input_multiplexer u_8bit_3_input_multiplexer_2 (
    .Input_1({{7{1'b0}}, Carry}), .Input_2({{7{1'b0}}, Equal}), .Input_3(n8bit_2_input_multiplexer_2_output),
    .Control_1(regular_nlogical_comparison), .Control_2(in_11), .out_6(Output));
  Quad_OR_Gate quad_or_2 (
    ._1a(quad_or_1__3y), ._1b(quad_or_1__4y), ._1y(quad_or_2__1y), ._2a(quad_or_1__1y), ._2b(quad_or_1__2y),
    ._2y(quad_or_2__2y), ._4a(quad_or_2__1y), ._4b(quad_or_2__2y), ._4y(Equal));  // open: _3a, _3b, _3y
endmodule

module Input (
  input  Input,
  input  Clear_Reg,
  input  Clock,
  output [7:0] Reg,
  output nInterrupt
);

  wire clock_1_out, hex_inverter_1__4_prime, hex_inverter_1__5_prime, hex_inverter_1__6_prime,
       n4bit_register_1__1d, n4bit_register_1__2d, quad_and_1__1y, quad_and_1__2y, quad_and_1__4y;

  Clock clock_1 (.out(clock_1_out));
  Quad_AND_Gate quad_and_1 (
    ._1a(Input), ._1b(quad_and_1__4y), ._1y(quad_and_1__1y), ._2a(quad_and_1__1y),
    ._2b(hex_inverter_1__6_prime), ._2y(quad_and_1__2y), ._4a(hex_inverter_1__4_prime),
    ._4b(n4bit_register_1__1d), ._4y(quad_and_1__4y));  // open: _3a, _3b, _3y
  Hex_Inverter hex_inverter_1 (
    ._1(quad_and_1__2y), ._1_prime(nInterrupt), ._4(n4bit_register_1__2d),
    ._4_prime(hex_inverter_1__4_prime), ._5(quad_and_1__1y), ._5_prime(hex_inverter_1__5_prime), ._6(Reg[0]),
    ._6_prime(hex_inverter_1__6_prime));  // open: _2, _2_prime, _3, _3_prime
  _4bit_register u_4bit_register_1 (
    .M(1'b0), .N(1'b0), ._1Q(Input), ._2Q(n4bit_register_1__1d), .CLK(clock_1_out), .CLR(1'b0),
    ._1D(n4bit_register_1__1d), ._2D(n4bit_register_1__2d), .G2(1'b0), .G1(1'b0));  // open: _3Q, _4Q, _3D, _4D
  _4bit_register u_4bit_register_2 (
    .M(1'b0), .N(1'b0), ._1Q(Input), .CLK(clock_1_out), .CLR(Clear_Reg), ._1D(Reg[0]),
    .G2(hex_inverter_1__5_prime), .G1(hex_inverter_1__5_prime));  // open: _2Q, _3Q, _4Q, _2D, _3D, _4D

  assign Reg[7:1] = {7{1'b0}};
endmodule

module Control (
  input  [23:0] Instruction_Input,
  input  carry,
  input  equals_zero,
  output EW1,
  output ER1,
  output EW2,
  output ER2,
  output EW3,
  output ER3,
  output EW4,
  output ER4,
  output Clear_registers,
  output [7:0] Const_Out,
  output Read_Mux_1_1,
  output Read_Mux_1_2,
  output Read_Mux_1_3,
  output Read_Mux_2_1,
  output Read_Mux_2_2,
  output Read_Mux_2_3,
  output Write_Mux_1,
  output Write_Mux_2,
  output nLoad_MSB,
  output nLoad_LSB,
  output Load_Saved_PC,
  output RAM_R_From,
  output RAM_W_To,
  output nequal_zero,
  output subtract_nadd,
  output or_nand,
  output logical_naddition,
  output addition_nlogical,
  output Clear_Input_reg
);

  // Control_Load control_load_1: pin names not known; wires that end beside it: Instruction_Input[23:18], Instruction_Input[17:0]
  // Control_Addition control_addition_1: pin names not known; wires that end beside it: Instruction_Input[23:18], Instruction_Input[17:0], Instruction_Input[23:18]
  Control_Logical control_logical_1 (.Instruction(Instruction_Input[23:18]), .Data(Instruction_Input[17:0]));
  Control_Logical_Comparison control_logical_comparison_1 (
    .Instruction(Instruction_Input[23:18]), .Data(Instruction_Input[17:0]));
  Control_Load_PC control_load_pc_1 (.Instruction(Instruction_Input[23:18]), .Data(Instruction_Input[17:0]));
  Control_Misc control_misc_1 (.Instruction(Instruction_Input[23:18]), .Data(Instruction_Input[17:0]));

  assign addition_nlogical = 1'b0;
  assign Clear_Input_reg = 1'b1;
  assign Clear_registers = 1'b0;
  assign Const_Out = {8{1'b1}};
  assign ER1 = 1'b0;
  assign ER2 = 1'b0;
  assign ER3 = 1'b0;
  assign ER4 = 1'b0;
  assign EW1 = 1'b0;
  assign EW2 = 1'b0;
  assign EW3 = 1'b0;
  assign EW4 = 1'b0;
  assign Load_Saved_PC = 1'b0;
  assign logical_naddition = 1'b0;
  assign nequal_zero = 1'b1;
  assign nLoad_LSB = 1'b1;
  assign nLoad_MSB = 1'b1;
  assign or_nand = 1'b0;
  assign RAM_R_From = 1'b0;
  assign RAM_W_To = 1'b0;
  assign Read_Mux_1_1 = 1'b0;
  assign Read_Mux_1_2 = 1'b0;
  assign Read_Mux_1_3 = 1'b0;
  assign Read_Mux_2_1 = 1'b0;
  assign Read_Mux_2_2 = 1'b0;
  assign Read_Mux_2_3 = 1'b0;
  assign subtract_nadd = 1'b0;
  assign Write_Mux_1 = 1'b0;
  assign Write_Mux_2 = 1'b0;
endmodule

module ROM (
  input  [15:0] PC_Address,
  output [23:0] Instruction
);

  ROM_part #(.addrWidth(16), .dataWidth(24)) rom_1 (.addr(PC_Address), .data(Instruction), .sel(1'b1));
endmodule

module RAM (
  input  W_TO,
  input  R_FROM,
  input  R_SELECT,
  input  [7:0] Addr,
  input  [7:0] Data,
  input  CLK,
  output [7:0] OUT_1,
  output [7:0] OUT_2
);

  wire hex_inverter_1__1_prime, hex_inverter_1__2_prime, hex_inverter_1__3_prime, hex_inverter_1__4_prime,
       hex_inverter_1__5_prime, hex_inverter_1__6_prime, hex_inverter_2__1_prime, hex_inverter_2__2_prime,
       hex_inverter_2__3_prime, hex_inverter_2__4_prime, hex_inverter_2__5_prime, hex_inverter_2__6_prime,
       hex_inverter_3__1_prime, hex_inverter_3__2_prime, hex_inverter_3__3_prime, hex_inverter_3__4_prime,
       hex_inverter_3__5_prime, hex_inverter_3__6_prime, hex_inverter_4__1_prime, hex_inverter_4__2_prime,
       hex_inverter_4__3_prime, hex_inverter_4__4_prime, hex_inverter_4__5_prime, hex_inverter_4__6_prime,
       hex_inverter_5__1_prime, hex_inverter_5__2_prime, hex_inverter_5__3_prime, hex_inverter_5__4_prime,
       hex_inverter_5__5_prime, hex_inverter_5__6_prime, hex_inverter_6__1_prime, hex_inverter_6__2_prime,
       hex_inverter_6__3_prime, hex_inverter_6__4_prime, hex_inverter_6__5_prime, hex_inverter_6__6_prime,
       hex_inverter_7__1_prime, hex_inverter_7__2_prime, hex_inverter_7__3_prime, hex_inverter_7__4_prime,
       hex_inverter_7__5_prime, hex_inverter_7__6_prime, hex_inverter_8__1_prime, hex_inverter_8__2_prime,
       hex_inverter_8__3_prime, hex_inverter_8__4_prime, hex_inverter_8__5_prime, hex_inverter_8__6_prime,
       hex_inverter_9__1_prime, hex_inverter_9__2_prime, hex_inverter_9__3_prime, hex_inverter_9__4_prime,
       hex_inverter_9__5_prime, hex_inverter_9__6_prime, hex_inverter_10__1_prime, hex_inverter_10__2_prime,
       hex_inverter_10__3_prime, hex_inverter_10__4_prime, hex_inverter_10__5_prime,
       hex_inverter_10__6_prime, hex_inverter_11__1_prime, hex_inverter_11__2_prime,
       hex_inverter_11__4_prime, hex_inverter_11__5_prime, quad_and_1__1y, quad_and_1__2y, quad_and_1__3y,
       quad_and_1__4y, quad_and_2__1y, quad_and_2__2y, quad_and_2__3y, quad_and_2__4y, quad_and_3__1y,
       quad_and_3__2y, quad_and_3__3y, quad_and_3__4y, quad_and_4__1y, quad_and_4__2y, quad_and_4__3y,
       quad_and_4__4y, quad_and_5__1y, quad_and_5__2y, quad_and_5__3y, quad_and_5__4y, quad_and_6__1y,
       quad_and_6__2y, quad_and_6__3y, quad_and_6__4y, quad_and_7__1y, quad_and_7__2y, quad_and_7__3y,
       quad_and_7__4y, quad_and_8__1y, quad_and_8__2y, quad_and_8__3y, quad_and_8__4y, quad_and_9__1y,
       quad_and_9__2y, quad_and_9__3y, quad_and_9__4y, quad_and_10__1y, quad_and_10__2y, quad_and_10__3y,
       quad_and_10__4y, quad_and_11__1y, quad_and_11__2y, quad_and_11__3y, quad_and_11__4y, quad_and_12__1y,
       quad_and_12__2y, quad_and_12__3y, quad_and_12__4y, quad_and_13__1y, quad_and_13__2y, quad_and_13__3y,
       quad_and_13__4y, quad_and_14__1y, quad_and_14__2y, quad_and_14__3y, quad_and_14__4y, quad_and_15__1y,
       quad_and_15__2y, quad_and_15__3y, quad_and_15__4y, quad_and_16__1y, quad_and_16__2y, quad_and_16__3y,
       quad_and_16__4y, quad_and_17__1y, quad_and_17__3y, triple_2_channel_demux_1_ax,
       triple_2_channel_demux_1_ay, triple_2_channel_demux_1_bx, triple_2_channel_demux_1_by,
       triple_2_channel_demux_1_cx, triple_2_channel_demux_1_cy, triple_2_channel_demux_2_ax,
       triple_2_channel_demux_2_ay, triple_2_channel_demux_2_bx, triple_2_channel_demux_2_by,
       triple_2_channel_demux_2_cx, triple_2_channel_demux_2_cy, triple_2_channel_demux_3_ax,
       triple_2_channel_demux_3_ay, triple_2_channel_demux_3_bx, triple_2_channel_demux_3_by,
       triple_2_channel_demux_3_cx, triple_2_channel_demux_3_cy, triple_2_channel_demux_4_ax,
       triple_2_channel_demux_4_ay, triple_2_channel_demux_4_by, triple_2_channel_demux_4_cx,
       triple_2_channel_demux_4_cy, triple_2_channel_demux_5_ax, triple_2_channel_demux_5_ay,
       triple_2_channel_demux_5_bx, triple_2_channel_demux_5_by, triple_2_channel_demux_5_cx,
       triple_2_channel_demux_5_cy, triple_2_channel_demux_6_ax, triple_2_channel_demux_6_ay,
       triple_2_channel_demux_6_bx, triple_2_channel_demux_6_by, triple_2_channel_demux_6_cx,
       triple_2_channel_demux_6_cy, triple_2_channel_demux_7_ax, triple_2_channel_demux_7_ay,
       triple_2_channel_demux_7_bx, triple_2_channel_demux_7_by, triple_2_channel_demux_7_cx,
       triple_2_channel_demux_7_cy, triple_2_channel_demux_8_ax, triple_2_channel_demux_8_ay,
       triple_2_channel_demux_8_bx, triple_2_channel_demux_8_by, triple_2_channel_demux_8_cx,
       triple_2_channel_demux_8_cy, triple_2_channel_demux_9_ax, triple_2_channel_demux_9_ay,
       triple_2_channel_demux_9_bx, triple_2_channel_demux_9_by, triple_2_channel_demux_9_cx,
       triple_2_channel_demux_9_cy, triple_2_channel_demux_10_ax, triple_2_channel_demux_10_ay,
       triple_2_channel_demux_10_bx, triple_2_channel_demux_10_by, triple_2_channel_demux_10_cx,
       triple_2_channel_demux_10_cy, triple_2_channel_demux_11_bx, triple_2_channel_demux_11_by;
  wire [7:0] n8bit_register_1_output;

  triple_2_channel_demux triple_2_channel_demux_1 (
    .bx(triple_2_channel_demux_1_bx), .by(triple_2_channel_demux_1_by), .cy(triple_2_channel_demux_1_cy),
    .c_in(triple_2_channel_demux_2_bx), .cx(triple_2_channel_demux_1_cx), .enable(1'b1),
    .b_in(triple_2_channel_demux_2_cy), .a_in(triple_2_channel_demux_2_cx), .ax(triple_2_channel_demux_1_ax),
    .ay(triple_2_channel_demux_1_ay), .A(Addr[0]), .B(Addr[0]), .C(Addr[0]));
  triple_2_channel_demux triple_2_channel_demux_2 (
    .bx(triple_2_channel_demux_2_bx), .by(triple_2_channel_demux_2_by), .cy(triple_2_channel_demux_2_cy),
    .c_in(triple_2_channel_demux_4_cx), .cx(triple_2_channel_demux_2_cx), .enable(1'b1),
    .b_in(triple_2_channel_demux_4_cy), .a_in(triple_2_channel_demux_4_cy), .ax(triple_2_channel_demux_2_ax),
    .ay(triple_2_channel_demux_2_ay), .A(Addr[1]), .B(Addr[1]), .C(Addr[1]));
  Quad_AND_Gate quad_and_1 (
    ._1a(R_FROM), ._1b(triple_2_channel_demux_1_ax), ._1y(quad_and_1__1y), ._2a(R_FROM),
    ._2b(triple_2_channel_demux_1_ay), ._2y(quad_and_1__2y), ._3a(W_TO), ._3b(triple_2_channel_demux_1_ax),
    ._3y(quad_and_1__3y), ._4a(W_TO), ._4b(triple_2_channel_demux_1_ay), ._4y(quad_and_1__4y));
  Quad_AND_Gate quad_and_2 (
    ._1a(R_FROM), ._1b(triple_2_channel_demux_1_bx), ._1y(quad_and_2__1y), ._2a(R_FROM),
    ._2b(triple_2_channel_demux_1_by), ._2y(quad_and_2__2y), ._3a(W_TO), ._3b(triple_2_channel_demux_1_bx),
    ._3y(quad_and_2__3y), ._4a(W_TO), ._4b(triple_2_channel_demux_1_by), ._4y(quad_and_2__4y));
  Quad_AND_Gate quad_and_3 (
    ._1a(R_FROM), ._1b(triple_2_channel_demux_1_cx), ._1y(quad_and_3__1y), ._2a(R_FROM),
    ._2b(triple_2_channel_demux_1_cy), ._2y(quad_and_3__2y), ._3a(W_TO), ._3b(triple_2_channel_demux_1_cx),
    ._3y(quad_and_3__3y), ._4a(W_TO), ._4b(triple_2_channel_demux_1_cy), ._4y(quad_and_3__4y));
  Hex_Inverter hex_inverter_1 (
    ._1(quad_and_1__1y), ._1_prime(hex_inverter_1__1_prime), ._2(quad_and_1__2y),
    ._2_prime(hex_inverter_1__2_prime), ._3(quad_and_2__1y), ._3_prime(hex_inverter_1__3_prime),
    ._4(quad_and_1__3y), ._4_prime(hex_inverter_1__4_prime), ._5(quad_and_1__4y),
    ._5_prime(hex_inverter_1__5_prime), ._6(quad_and_2__3y), ._6_prime(hex_inverter_1__6_prime));
  Hex_Inverter hex_inverter_2 (
    ._1(quad_and_2__2y), ._1_prime(hex_inverter_2__1_prime), ._2(quad_and_3__1y),
    ._2_prime(hex_inverter_2__2_prime), ._3(quad_and_3__2y), ._3_prime(hex_inverter_2__3_prime),
    ._4(quad_and_2__4y), ._4_prime(hex_inverter_2__4_prime), ._5(quad_and_3__3y),
    ._5_prime(hex_inverter_2__5_prime), ._6(quad_and_3__4y), ._6_prime(hex_inverter_2__6_prime));
  _8bit_register u_8bit_register_1 (
    .M(hex_inverter_1__1_prime), .N(hex_inverter_1__1_prime), .\input (Data), .clock(CLK),
    .CLR(quad_and_17__1y), .\output (n8bit_register_1_output), .G2(hex_inverter_1__4_prime),
    .G1(hex_inverter_1__4_prime));
  _8bit_register u_8bit_register_2 (
    .M(hex_inverter_1__2_prime), .N(hex_inverter_1__2_prime), .\input (Data), .clock(CLK),
    .CLR(quad_and_17__1y), .\output (n8bit_register_1_output), .G2(hex_inverter_1__5_prime),
    .G1(hex_inverter_1__5_prime));
  _8bit_register u_8bit_register_3 (
    .M(hex_inverter_1__3_prime), .N(hex_inverter_1__3_prime), .\input (Data), .clock(CLK),
    .CLR(quad_and_17__1y), .\output (n8bit_register_1_output), .G2(hex_inverter_1__6_prime),
    .G1(hex_inverter_1__6_prime));
  _8bit_register u_8bit_register_4 (
    .M(hex_inverter_2__1_prime), .N(hex_inverter_2__1_prime), .\input (Data), .clock(CLK),
    .CLR(quad_and_17__1y), .\output (n8bit_register_1_output), .G2(hex_inverter_2__4_prime),
    .G1(hex_inverter_2__4_prime));
  _8bit_register u_8bit_register_5 (
    .M(hex_inverter_2__2_prime), .N(hex_inverter_2__2_prime), .\input (Data), .clock(CLK),
    .CLR(quad_and_17__1y), .\output (n8bit_register_1_output), .G2(hex_inverter_2__5_prime),
    .G1(hex_inverter_2__5_prime));
  _8bit_register u_8bit_register_6 (
    .M(hex_inverter_2__3_prime), .N(hex_inverter_2__3_prime), .\input (Data), .clock(CLK),
    .CLR(quad_and_17__1y), .\output (n8bit_register_1_output), .G2(hex_inverter_2__6_prime),
    .G1(hex_inverter_2__6_prime));
  triple_2_channel_demux triple_2_channel_demux_3 (
    .bx(triple_2_channel_demux_3_bx), .by(triple_2_channel_demux_3_by), .cy(triple_2_channel_demux_3_cy),
    .c_in(triple_2_channel_demux_2_ay), .cx(triple_2_channel_demux_3_cx), .enable(1'b1),
    .b_in(triple_2_channel_demux_2_ax), .a_in(triple_2_channel_demux_4_cy), .ax(triple_2_channel_demux_3_ax),
    .ay(triple_2_channel_demux_3_ay), .A(Addr[0]), .B(Addr[0]), .C(Addr[0]));
  Quad_AND_Gate quad_and_4 (
    ._1a(R_FROM), ._1b(triple_2_channel_demux_3_ax), ._1y(quad_and_4__1y), ._2a(R_FROM),
    ._2b(triple_2_channel_demux_3_ay), ._2y(quad_and_4__2y), ._3a(W_TO), ._3b(triple_2_channel_demux_3_ax),
    ._3y(quad_and_4__3y), ._4a(W_TO), ._4b(triple_2_channel_demux_3_ay), ._4y(quad_and_4__4y));
  Quad_AND_Gate quad_and_5 (
    ._1a(R_FROM), ._1b(triple_2_channel_demux_3_bx), ._1y(quad_and_5__1y), ._2a(R_FROM),
    ._2b(triple_2_channel_demux_3_by), ._2y(quad_and_5__2y), ._3a(W_TO), ._3b(triple_2_channel_demux_3_bx),
    ._3y(quad_and_5__3y), ._4a(W_TO), ._4b(triple_2_channel_demux_3_by), ._4y(quad_and_5__4y));
  Quad_AND_Gate quad_and_6 (
    ._1a(R_FROM), ._1b(triple_2_channel_demux_3_cx), ._1y(quad_and_6__1y), ._2a(R_FROM),
    ._2b(triple_2_channel_demux_3_cy), ._2y(quad_and_6__2y), ._3a(W_TO), ._3b(triple_2_channel_demux_3_cx),
    ._3y(quad_and_6__3y), ._4a(W_TO), ._4b(triple_2_channel_demux_3_cy), ._4y(quad_and_6__4y));
  Hex_Inverter hex_inverter_3 (
    ._1(quad_and_4__1y), ._1_prime(hex_inverter_3__1_prime), ._2(quad_and_4__2y),
    ._2_prime(hex_inverter_3__2_prime), ._3(quad_and_5__1y), ._3_prime(hex_inverter_3__3_prime),
    ._4(quad_and_4__3y), ._4_prime(hex_inverter_3__4_prime), ._5(quad_and_4__4y),
    ._5_prime(hex_inverter_3__5_prime), ._6(quad_and_5__3y), ._6_prime(hex_inverter_3__6_prime));
  Hex_Inverter hex_inverter_4 (
    ._1(quad_and_5__2y), ._1_prime(hex_inverter_4__1_prime), ._2(quad_and_6__1y),
    ._2_prime(hex_inverter_4__2_prime), ._3(quad_and_6__2y), ._3_prime(hex_inverter_4__3_prime),
    ._4(quad_and_5__4y), ._4_prime(hex_inverter_4__4_prime), ._5(quad_and_6__3y),
    ._5_prime(hex_inverter_4__5_prime), ._6(quad_and_6__4y), ._6_prime(hex_inverter_4__6_prime));
  _8bit_register u_8bit_register_7 (
    .M(hex_inverter_3__1_prime), .N(hex_inverter_3__1_prime), .\input (Data), .clock(CLK),
    .CLR(quad_and_17__1y), .\output (n8bit_register_1_output), .G2(hex_inverter_3__4_prime),
    .G1(hex_inverter_3__4_prime));
  _8bit_register u_8bit_register_8 (
    .M(hex_inverter_3__2_prime), .N(hex_inverter_3__2_prime), .\input (Data), .clock(CLK),
    .CLR(quad_and_17__1y), .\output (n8bit_register_1_output), .G2(hex_inverter_3__5_prime),
    .G1(hex_inverter_3__5_prime));
  _8bit_register u_8bit_register_9 (
    .M(hex_inverter_3__3_prime), .N(hex_inverter_3__3_prime), .\input (Data), .clock(CLK),
    .CLR(quad_and_17__1y), .\output (n8bit_register_1_output), .G2(hex_inverter_3__6_prime),
    .G1(hex_inverter_3__6_prime));
  _8bit_register u_8bit_register_10 (
    .M(hex_inverter_4__1_prime), .N(hex_inverter_4__1_prime), .\input (Data), .clock(CLK),
    .CLR(quad_and_17__1y), .\output (n8bit_register_1_output), .G2(hex_inverter_4__4_prime),
    .G1(hex_inverter_4__4_prime));
  _8bit_register u_8bit_register_11 (
    .M(hex_inverter_4__2_prime), .N(hex_inverter_4__2_prime), .\input (Data), .clock(CLK),
    .CLR(quad_and_17__1y), .\output (n8bit_register_1_output), .G2(hex_inverter_4__5_prime),
    .G1(hex_inverter_4__5_prime));
  _8bit_register u_8bit_register_12 (
    .M(hex_inverter_4__3_prime), .N(hex_inverter_4__3_prime), .\input (Data), .clock(CLK),
    .CLR(quad_and_17__1y), .\output (n8bit_register_1_output), .G2(hex_inverter_4__6_prime),
    .G1(hex_inverter_4__6_prime));
  triple_2_channel_demux triple_2_channel_demux_4 (
    .bx(triple_2_channel_demux_2_by), .by(triple_2_channel_demux_4_by), .cy(triple_2_channel_demux_4_cy),
    .c_in(triple_2_channel_demux_9_bx), .cx(triple_2_channel_demux_4_cx), .enable(1'b1),
    .b_in(triple_2_channel_demux_9_by), .a_in(triple_2_channel_demux_9_ax), .ax(triple_2_channel_demux_4_ax),
    .ay(triple_2_channel_demux_4_ay), .A(Addr[2]), .B(Addr[2]), .C(Addr[2]));
  triple_2_channel_demux triple_2_channel_demux_5 (
    .bx(triple_2_channel_demux_5_bx), .by(triple_2_channel_demux_5_by), .cy(triple_2_channel_demux_5_cy),
    .c_in(triple_2_channel_demux_6_bx), .cx(triple_2_channel_demux_5_cx), .enable(1'b1),
    .b_in(triple_2_channel_demux_6_cy), .a_in(triple_2_channel_demux_6_cx), .ax(triple_2_channel_demux_5_ax),
    .ay(triple_2_channel_demux_5_ay), .A(Addr[0]), .B(Addr[0]), .C(Addr[0]));
  Quad_AND_Gate quad_and_7 (
    ._1a(R_FROM), ._1b(triple_2_channel_demux_5_ax), ._1y(quad_and_7__1y), ._2a(R_FROM),
    ._2b(triple_2_channel_demux_5_ay), ._2y(quad_and_7__2y), ._3a(W_TO), ._3b(triple_2_channel_demux_5_ax),
    ._3y(quad_and_7__3y), ._4a(W_TO), ._4b(triple_2_channel_demux_5_ay), ._4y(quad_and_7__4y));
  Quad_AND_Gate quad_and_8 (
    ._1a(R_FROM), ._1b(triple_2_channel_demux_5_bx), ._1y(quad_and_8__1y), ._2a(R_FROM),
    ._2b(triple_2_channel_demux_5_by), ._2y(quad_and_8__2y), ._3a(W_TO), ._3b(triple_2_channel_demux_5_bx),
    ._3y(quad_and_8__3y), ._4a(W_TO), ._4b(triple_2_channel_demux_5_by), ._4y(quad_and_8__4y));
  Quad_AND_Gate quad_and_9 (
    ._1a(R_FROM), ._1b(triple_2_channel_demux_5_cx), ._1y(quad_and_9__1y), ._2a(R_FROM),
    ._2b(triple_2_channel_demux_5_cy), ._2y(quad_and_9__2y), ._3a(W_TO), ._3b(triple_2_channel_demux_5_cx),
    ._3y(quad_and_9__3y), ._4a(W_TO), ._4b(triple_2_channel_demux_5_cy), ._4y(quad_and_9__4y));
  Hex_Inverter hex_inverter_5 (
    ._1(quad_and_7__1y), ._1_prime(hex_inverter_5__1_prime), ._2(quad_and_7__2y),
    ._2_prime(hex_inverter_5__2_prime), ._3(quad_and_8__1y), ._3_prime(hex_inverter_5__3_prime),
    ._4(quad_and_7__3y), ._4_prime(hex_inverter_5__4_prime), ._5(quad_and_7__4y),
    ._5_prime(hex_inverter_5__5_prime), ._6(quad_and_8__3y), ._6_prime(hex_inverter_5__6_prime));
  Hex_Inverter hex_inverter_6 (
    ._1(quad_and_8__2y), ._1_prime(hex_inverter_6__1_prime), ._2(quad_and_9__1y),
    ._2_prime(hex_inverter_6__2_prime), ._3(quad_and_9__2y), ._3_prime(hex_inverter_6__3_prime),
    ._4(quad_and_8__4y), ._4_prime(hex_inverter_6__4_prime), ._5(quad_and_9__3y),
    ._5_prime(hex_inverter_6__5_prime), ._6(quad_and_9__4y), ._6_prime(hex_inverter_6__6_prime));
  _8bit_register u_8bit_register_13 (
    .M(hex_inverter_5__1_prime), .N(hex_inverter_5__1_prime), .\input (Data), .clock(CLK),
    .CLR(quad_and_17__1y), .\output (n8bit_register_1_output), .G2(hex_inverter_5__4_prime),
    .G1(hex_inverter_5__4_prime));
  _8bit_register u_8bit_register_14 (
    .M(hex_inverter_5__2_prime), .N(hex_inverter_5__2_prime), .\input (Data), .clock(CLK),
    .CLR(quad_and_17__1y), .\output (n8bit_register_1_output), .G2(hex_inverter_5__5_prime),
    .G1(hex_inverter_5__5_prime));
  _8bit_register u_8bit_register_15 (
    .M(hex_inverter_5__3_prime), .N(hex_inverter_5__3_prime), .\input (Data), .clock(CLK),
    .CLR(quad_and_17__1y), .\output (n8bit_register_1_output), .G2(hex_inverter_5__6_prime),
    .G1(hex_inverter_5__6_prime));
  _8bit_register u_8bit_register_16 (
    .M(hex_inverter_6__1_prime), .N(hex_inverter_6__1_prime), .\input (Data), .clock(CLK),
    .CLR(quad_and_17__1y), .\output (n8bit_register_1_output), .G2(hex_inverter_6__4_prime),
    .G1(hex_inverter_6__4_prime));
  _8bit_register u_8bit_register_17 (
    .M(hex_inverter_6__2_prime), .N(hex_inverter_6__2_prime), .\input (Data), .clock(CLK),
    .CLR(quad_and_17__3y), .\output (n8bit_register_1_output), .G2(hex_inverter_6__5_prime),
    .G1(hex_inverter_6__5_prime));
  _8bit_register u_8bit_register_18 (
    .M(hex_inverter_6__3_prime), .N(hex_inverter_6__3_prime), .\input (Data), .clock(CLK),
    .CLR(quad_and_17__3y), .\output (n8bit_register_1_output), .G2(hex_inverter_6__6_prime),
    .G1(hex_inverter_6__6_prime));
  triple_2_channel_demux triple_2_channel_demux_6 (
    .bx(triple_2_channel_demux_6_bx), .by(triple_2_channel_demux_6_by), .cy(triple_2_channel_demux_6_cy),
    .c_in(triple_2_channel_demux_4_by), .cx(triple_2_channel_demux_6_cx), .enable(1'b1),
    .b_in(triple_2_channel_demux_4_ax), .a_in(triple_2_channel_demux_4_ay), .ax(triple_2_channel_demux_6_ax),
    .ay(triple_2_channel_demux_6_ay), .A(Addr[1]), .B(Addr[1]), .C(Addr[1]));
  triple_2_channel_demux triple_2_channel_demux_7 (
    .bx(triple_2_channel_demux_7_bx), .by(triple_2_channel_demux_7_by), .cy(triple_2_channel_demux_7_cy),
    .c_in(triple_2_channel_demux_6_by), .cx(triple_2_channel_demux_7_cx), .enable(1'b1),
    .b_in(triple_2_channel_demux_6_ax), .a_in(triple_2_channel_demux_6_ay), .ax(triple_2_channel_demux_7_ax),
    .ay(triple_2_channel_demux_7_ay), .A(Addr[0]), .B(Addr[0]), .C(Addr[0]));
  Quad_AND_Gate quad_and_10 (
    ._1a(R_FROM), ._1b(triple_2_channel_demux_7_ax), ._1y(quad_and_10__1y), ._2a(R_FROM),
    ._2b(triple_2_channel_demux_7_ay), ._2y(quad_and_10__2y), ._3a(W_TO), ._3b(triple_2_channel_demux_7_ax),
    ._3y(quad_and_10__3y), ._4a(W_TO), ._4b(triple_2_channel_demux_7_ay), ._4y(quad_and_10__4y));
  Quad_AND_Gate quad_and_11 (
    ._1a(R_FROM), ._1b(triple_2_channel_demux_7_bx), ._1y(quad_and_11__1y), ._2a(R_FROM),
    ._2b(triple_2_channel_demux_7_by), ._2y(quad_and_11__2y), ._3a(W_TO), ._3b(triple_2_channel_demux_7_bx),
    ._3y(quad_and_11__3y), ._4a(W_TO), ._4b(triple_2_channel_demux_7_by), ._4y(quad_and_11__4y));
  Quad_AND_Gate quad_and_12 (
    ._1a(R_FROM), ._1b(triple_2_channel_demux_7_cx), ._1y(quad_and_12__1y), ._2a(R_FROM),
    ._2b(triple_2_channel_demux_7_cy), ._2y(quad_and_12__2y), ._3a(W_TO), ._3b(triple_2_channel_demux_7_cx),
    ._3y(quad_and_12__3y), ._4a(W_TO), ._4b(triple_2_channel_demux_7_cy), ._4y(quad_and_12__4y));
  Hex_Inverter hex_inverter_7 (
    ._1(quad_and_10__1y), ._1_prime(hex_inverter_7__1_prime), ._2(quad_and_10__2y),
    ._2_prime(hex_inverter_7__2_prime), ._3(quad_and_11__1y), ._3_prime(hex_inverter_7__3_prime),
    ._4(quad_and_10__3y), ._4_prime(hex_inverter_7__4_prime), ._5(quad_and_10__4y),
    ._5_prime(hex_inverter_7__5_prime), ._6(quad_and_11__3y), ._6_prime(hex_inverter_7__6_prime));
  Hex_Inverter hex_inverter_8 (
    ._1(quad_and_11__2y), ._1_prime(hex_inverter_8__1_prime), ._2(quad_and_12__1y),
    ._2_prime(hex_inverter_8__2_prime), ._3(quad_and_12__2y), ._3_prime(hex_inverter_8__3_prime),
    ._4(quad_and_11__4y), ._4_prime(hex_inverter_8__4_prime), ._5(quad_and_12__3y),
    ._5_prime(hex_inverter_8__5_prime), ._6(quad_and_12__4y), ._6_prime(hex_inverter_8__6_prime));
  _8bit_register u_8bit_register_19 (
    .M(hex_inverter_7__1_prime), .N(hex_inverter_7__1_prime), .\input (Data), .clock(CLK),
    .CLR(quad_and_17__3y), .\output (n8bit_register_1_output), .G2(hex_inverter_7__4_prime),
    .G1(hex_inverter_7__4_prime));
  _8bit_register u_8bit_register_20 (
    .M(hex_inverter_7__2_prime), .N(hex_inverter_7__2_prime), .\input (Data), .clock(CLK),
    .CLR(quad_and_17__3y), .\output (n8bit_register_1_output), .G2(hex_inverter_7__5_prime),
    .G1(hex_inverter_7__5_prime));
  _8bit_register u_8bit_register_21 (
    .M(hex_inverter_7__3_prime), .N(hex_inverter_7__3_prime), .\input (Data), .clock(CLK),
    .CLR(quad_and_17__3y), .\output (n8bit_register_1_output), .G2(hex_inverter_7__6_prime),
    .G1(hex_inverter_7__6_prime));
  _8bit_register u_8bit_register_22 (
    .M(hex_inverter_8__1_prime), .N(hex_inverter_8__1_prime), .\input (Data), .clock(CLK),
    .CLR(quad_and_17__3y), .\output (n8bit_register_1_output), .G2(hex_inverter_8__4_prime),
    .G1(hex_inverter_8__4_prime));
  _8bit_register u_8bit_register_23 (
    .M(hex_inverter_8__2_prime), .N(hex_inverter_8__2_prime), .\input (Data), .clock(CLK),
    .CLR(quad_and_17__3y), .\output (n8bit_register_1_output), .G2(hex_inverter_8__5_prime),
    .G1(hex_inverter_8__5_prime));
  _8bit_register u_8bit_register_24 (
    .M(hex_inverter_8__3_prime), .N(hex_inverter_8__3_prime), .\input (Data), .clock(CLK),
    .CLR(quad_and_17__3y), .\output (n8bit_register_1_output), .G2(hex_inverter_8__6_prime),
    .G1(hex_inverter_8__6_prime));
  triple_2_channel_demux triple_2_channel_demux_8 (
    .bx(triple_2_channel_demux_8_bx), .by(triple_2_channel_demux_8_by), .cy(triple_2_channel_demux_8_cy),
    .c_in(triple_2_channel_demux_10_bx), .cx(triple_2_channel_demux_8_cx), .enable(1'b1),
    .b_in(triple_2_channel_demux_10_cy), .a_in(triple_2_channel_demux_10_cx),
    .ax(triple_2_channel_demux_8_ax), .ay(triple_2_channel_demux_8_ay), .A(Addr[0]), .B(Addr[0]), .C(Addr[0]));
  triple_2_channel_demux triple_2_channel_demux_9 (
    .bx(triple_2_channel_demux_9_bx), .by(triple_2_channel_demux_9_by), .cy(triple_2_channel_demux_9_cy),
    .c_in(triple_2_channel_demux_9_ay), .cx(triple_2_channel_demux_9_cx), .enable(1'b1),
    .b_in(triple_2_channel_demux_11_bx), .a_in(triple_2_channel_demux_11_by),
    .ax(triple_2_channel_demux_9_ax), .ay(triple_2_channel_demux_9_ay), .A(Addr[3]), .B(Addr[3]), .C(Addr[2]));
  Quad_AND_Gate quad_and_13 (
    ._1a(R_FROM), ._1b(triple_2_channel_demux_8_ax), ._1y(quad_and_13__1y), ._2a(R_FROM),
    ._2b(triple_2_channel_demux_8_ay), ._2y(quad_and_13__2y), ._3a(W_TO), ._3b(triple_2_channel_demux_8_ax),
    ._3y(quad_and_13__3y), ._4a(W_TO), ._4b(triple_2_channel_demux_8_ay), ._4y(quad_and_13__4y));
  Quad_AND_Gate quad_and_14 (
    ._1a(R_FROM), ._1b(triple_2_channel_demux_8_bx), ._1y(quad_and_14__1y), ._2a(R_FROM),
    ._2b(triple_2_channel_demux_8_by), ._2y(quad_and_14__2y), ._3a(W_TO), ._3b(triple_2_channel_demux_8_bx),
    ._3y(quad_and_14__3y), ._4a(W_TO), ._4b(triple_2_channel_demux_8_by), ._4y(quad_and_14__4y));
  Quad_AND_Gate quad_and_15 (
    ._1a(R_FROM), ._1b(triple_2_channel_demux_8_cx), ._1y(quad_and_15__1y), ._2a(R_FROM),
    ._2b(triple_2_channel_demux_8_cy), ._2y(quad_and_15__2y), ._3a(W_TO), ._3b(triple_2_channel_demux_8_cx),
    ._3y(quad_and_15__3y), ._4a(W_TO), ._4b(triple_2_channel_demux_8_cy), ._4y(quad_and_15__4y));
  Hex_Inverter hex_inverter_9 (
    ._1(quad_and_13__1y), ._1_prime(hex_inverter_9__1_prime), ._2(quad_and_13__2y),
    ._2_prime(hex_inverter_9__2_prime), ._3(quad_and_14__1y), ._3_prime(hex_inverter_9__3_prime),
    ._4(quad_and_13__3y), ._4_prime(hex_inverter_9__4_prime), ._5(quad_and_13__4y),
    ._5_prime(hex_inverter_9__5_prime), ._6(quad_and_14__3y), ._6_prime(hex_inverter_9__6_prime));
  Hex_Inverter hex_inverter_10 (
    ._1(quad_and_14__2y), ._1_prime(hex_inverter_10__1_prime), ._2(quad_and_15__1y),
    ._2_prime(hex_inverter_10__2_prime), ._3(quad_and_15__2y), ._3_prime(hex_inverter_10__3_prime),
    ._4(quad_and_14__4y), ._4_prime(hex_inverter_10__4_prime), ._5(quad_and_15__3y),
    ._5_prime(hex_inverter_10__5_prime), ._6(quad_and_15__4y), ._6_prime(hex_inverter_10__6_prime));
  _8bit_register u_8bit_register_25 (
    .M(hex_inverter_9__1_prime), .N(hex_inverter_9__1_prime), .\input (Data), .clock(CLK),
    .CLR(quad_and_17__3y), .\output (n8bit_register_1_output), .G2(hex_inverter_9__4_prime),
    .G1(hex_inverter_9__4_prime));
  _8bit_register u_8bit_register_26 (
    .M(hex_inverter_9__2_prime), .N(hex_inverter_9__2_prime), .\input (Data), .clock(CLK),
    .CLR(quad_and_17__3y), .\output (n8bit_register_1_output), .G2(hex_inverter_9__5_prime),
    .G1(hex_inverter_9__5_prime));
  _8bit_register u_8bit_register_27 (
    .M(hex_inverter_9__3_prime), .N(hex_inverter_9__3_prime), .\input (Data), .clock(CLK),
    .CLR(quad_and_17__3y), .\output (n8bit_register_1_output), .G2(hex_inverter_9__6_prime),
    .G1(hex_inverter_9__6_prime));
  _8bit_register u_8bit_register_28 (
    .M(hex_inverter_10__1_prime), .N(hex_inverter_10__1_prime), .\input (Data), .clock(CLK),
    .CLR(quad_and_17__3y), .\output (n8bit_register_1_output), .G2(hex_inverter_10__4_prime),
    .G1(hex_inverter_10__4_prime));
  _8bit_register u_8bit_register_29 (
    .M(hex_inverter_10__2_prime), .N(hex_inverter_10__2_prime), .\input (Data), .clock(CLK),
    .CLR(quad_and_17__3y), .\output (n8bit_register_1_output), .G2(hex_inverter_10__5_prime),
    .G1(hex_inverter_10__5_prime));
  _8bit_register u_8bit_register_30 (
    .M(hex_inverter_10__3_prime), .N(hex_inverter_10__3_prime), .\input (Data), .clock(CLK),
    .CLR(quad_and_17__3y), .\output (n8bit_register_1_output), .G2(hex_inverter_10__6_prime),
    .G1(hex_inverter_10__6_prime));
  triple_2_channel_demux triple_2_channel_demux_10 (
    .bx(triple_2_channel_demux_10_bx), .by(triple_2_channel_demux_10_by), .cy(triple_2_channel_demux_10_cy),
    .c_in(triple_2_channel_demux_9_cx), .cx(triple_2_channel_demux_10_cx), .enable(1'b1),
    .b_in(triple_2_channel_demux_9_cy), .a_in(triple_2_channel_demux_10_by),
    .ax(triple_2_channel_demux_10_ax), .ay(triple_2_channel_demux_10_ay), .A(Addr[0]), .B(Addr[1]),
    .C(Addr[1]));
  triple_2_channel_demux triple_2_channel_demux_11 (
    .bx(triple_2_channel_demux_11_bx), .by(triple_2_channel_demux_11_by), .enable(1'b1), .b_in(1'b1),
    .B(Addr[4]));  // open: cy, c_in, cx, a_in, ax, ay, A, C
  Quad_AND_Gate quad_and_16 (
    ._1a(R_FROM), ._1b(triple_2_channel_demux_10_ax), ._1y(quad_and_16__1y), ._2a(R_FROM),
    ._2b(triple_2_channel_demux_10_ay), ._2y(quad_and_16__2y), ._3a(W_TO),
    ._3b(triple_2_channel_demux_10_ax), ._3y(quad_and_16__3y), ._4a(W_TO),
    ._4b(triple_2_channel_demux_10_ay), ._4y(quad_and_16__4y));
  Hex_Inverter hex_inverter_11 (
    ._1(quad_and_16__1y), ._1_prime(hex_inverter_11__1_prime), ._2(quad_and_16__2y),
    ._2_prime(hex_inverter_11__2_prime), ._4(quad_and_16__3y), ._4_prime(hex_inverter_11__4_prime),
    ._5(quad_and_16__4y), ._5_prime(hex_inverter_11__5_prime));  // open: _3, _3_prime, _6, _6_prime
  _8bit_register u_8bit_register_31 (
    .M(hex_inverter_11__1_prime), .N(hex_inverter_11__1_prime), .\input (Data), .clock(CLK),
    .CLR(quad_and_17__3y), .\output (n8bit_register_1_output), .G2(hex_inverter_11__4_prime),
    .G1(hex_inverter_11__4_prime));
  _8bit_register u_8bit_register_32 (
    .M(hex_inverter_11__2_prime), .N(hex_inverter_11__2_prime), .\input (Data), .clock(CLK),
    .CLR(quad_and_17__3y), .\output (n8bit_register_1_output), .G2(hex_inverter_11__5_prime),
    .G1(hex_inverter_11__5_prime));
  Quad_AND_Gate quad_and_17 (
    ._1a(Addr[6]), ._1b(W_TO), ._1y(quad_and_17__1y), ._3a(Addr[7]), ._3b(W_TO), ._3y(quad_and_17__3y));  // open: _2a, _2b, _2y, _4a, _4b, _4y
  _8bit_2_output_demuliplexer u_8bit_2_output_demuliplexer_1 (
    .Output_1(OUT_2), .Output_2(OUT_1), .Input(n8bit_register_1_output), .Control(R_SELECT));
endmodule

module PC (
  input  [7:0] write_byte,
  input  Reset_PC,
  input  nLoad_MSB,
  input  nLoad_LSB,
  input  nInterrupt,
  input  Load_Saved_PC,
  input  Clock,
  output [15:0] PC_value
);

  wire [0:0] adder_carry;
  wire [7:0] LSB_reg_output, msb_add_output, MSB_reg_output, mux_2_output, mux_3_output, mux_4_output,
       mux_output, n8bit_2_input_multiplexer_1_output, n8bit_2_input_multiplexer_2_output, Save_LSB_output,
       Save_MSB_output;

  _8bit_register msb_add (
    .M(1'b0), .N(1'b0), .\input (write_byte), .clock(Clock), .CLR(Reset_PC), .\output (msb_add_output),
    .G2(nLoad_MSB), .G1(nLoad_MSB));
  _8bit_2_input_multiplexer mux (
    .Input_1(n8bit_2_input_multiplexer_1_output), .Input_2(write_byte), .Output(mux_output),
    .Control(nLoad_LSB));
  _8bit_2_input_multiplexer mux_2 (.Input_1(mux_output), .Input_2(8'h3), .Output(mux_2_output), .Control(nInterrupt));
  _8bit_2_input_multiplexer u_8bit_2_input_multiplexer_1 (
    .Input_1(Save_LSB_output), .Input_2(PC_value[7:0]), .Output(n8bit_2_input_multiplexer_1_output),
    .Control(Load_Saved_PC));
  _8bit_register LSB_reg (
    .M(1'b0), .N(1'b0), .\input (mux_2_output), .clock(Clock), .CLR(Reset_PC), .\output (LSB_reg_output),
    .G2(1'b0), .G1(1'b0));
  _8bit_register Save_LSB (
    .M(1'b0), .N(1'b0), .\input (PC_value[7:0]), .clock(Clock), .CLR(1'b0), .\output (Save_LSB_output),
    .G2(nInterrupt), .G1(nInterrupt));
  _8bit_adder adder (.Input1(LSB_reg_output), .Input_2(8'h1), .Output(PC_value[7:0]), .Carry(adder_carry[0]));
  _8bit_2_input_multiplexer mux_3 (
    .Input_1(mux_4_output), .Input_2({8{1'b0}}), .Output(mux_3_output), .Control(nInterrupt));
  _8bit_2_input_multiplexer mux_4 (
    .Input_1(n8bit_2_input_multiplexer_2_output), .Input_2(msb_add_output), .Output(mux_4_output),
    .Control(nLoad_LSB));
  _8bit_register Save_MSB (
    .M(1'b0), .N(1'b0), .\input (PC_value[15:8]), .clock(Clock), .CLR(1'b0), .\output (Save_MSB_output),
    .G2(nInterrupt), .G1(nInterrupt));
  _8bit_register MSB_reg (
    .M(1'b0), .N(1'b0), .\input (mux_3_output), .clock(Clock), .CLR(Reset_PC), .\output (MSB_reg_output),
    .G2(1'b0), .G1(1'b0));
  _8bit_2_input_multiplexer u_8bit_2_input_multiplexer_2 (
    .Input_1(Save_MSB_output), .Input_2(PC_value[15:8]), .Output(n8bit_2_input_multiplexer_2_output),
    .Control(Load_Saved_PC));
  _8bit_adder adder_2 (
    .Input1(MSB_reg_output), .Input_2({{7{1'b0}}, adder_carry[0]}), .Output(PC_value[15:8]));  // open: Carry
endmodule

module _8bit_AND_Gate (
  input  [7:0] In_1,
  input  [7:0] In_2,
  output [7:0] Out
);

  Quad_AND_Gate quad_and_1 (
    ._1a(In_1[0]), ._1b(In_2[0]), ._1y(Out[0]), ._2a(In_1[1]), ._2b(In_2[1]), ._2y(Out[1]), ._3a(In_1[2]),
    ._3b(In_2[2]), ._3y(Out[2]), ._4a(In_1[3]), ._4b(In_2[3]), ._4y(Out[3]));
  Quad_AND_Gate quad_and_2 (
    ._1a(In_1[4]), ._1b(In_2[4]), ._1y(Out[4]), ._2a(In_1[5]), ._2b(In_2[5]), ._2y(Out[5]), ._3a(In_1[6]),
    ._3b(In_2[6]), ._3y(Out[6]), ._4a(In_1[7]), ._4b(In_2[7]), ._4y(Out[7]));
endmodule

module _8bit_OR_Gate (
  input  [7:0] In_1,
  input  [7:0] In_2,
  output [7:0] Out
);

  Quad_OR_Gate quad_or_1 (
    ._1a(In_1[0]), ._1b(In_2[0]), ._1y(Out[0]), ._2a(In_1[1]), ._2b(In_2[1]), ._2y(Out[1]), ._3a(In_1[2]),
    ._3b(In_2[2]), ._3y(Out[2]), ._4a(In_1[3]), ._4b(In_2[3]), ._4y(Out[3]));
  Quad_OR_Gate quad_or_2 (
    ._1a(In_1[4]), ._1b(In_2[4]), ._1y(Out[4]), ._2a(In_1[5]), ._2b(In_2[5]), ._2y(Out[5]), ._3a(In_1[6]),
    ._3b(In_2[6]), ._3y(Out[6]), ._4a(In_1[7]), ._4b(In_2[7]), ._4y(Out[7]));
endmodule

module _8bit_XOR (
  input  [7:0] Read_1,
  input  [7:0] Read_2,
  output [7:0] Write
);

  Quad_XOR_gate quad_xor_gate_1 (
    ._1a(Read_1[2]), ._1b(Read_2[2]), ._1_y(Write[2]), ._2a(Read_2[3]), ._2b(Read_1[3]), ._2_y(Write[3]),
    ._3a(Read_1[0]), ._3b(Read_2[0]), ._3_y(Write[0]), ._4a(Read_2[1]), ._4b(Read_1[1]), ._4_y(Write[1]));
  Quad_XOR_gate quad_xor_gate_2 (
    ._1a(Read_1[6]), ._1b(Read_2[6]), ._1_y(Write[6]), ._2a(Read_1[7]), ._2b(Read_2[7]), ._2_y(Write[7]),
    ._3a(Read_2[4]), ._3b(Read_1[4]), ._3_y(Write[4]), ._4a(Read_2[5]), ._4b(Read_1[5]), ._4_y(Write[5]));
endmodule

module _8bit_2_input_multiplexer (
  input  [7:0] Input_1,
  input  [7:0] Input_2,
  input  Control,
  output [7:0] Output
);

  triple_2_channel_mux triple_2_channel_mux_1 (
    .bx(Input_2[0]), .by(Input_1[0]), .cy(Input_1[1]), .c_out(Output[1]), .cx(Input_2[1]), .enable(1'b1),
    .b_out(Output[0]), .A(Control), .B(Control), .C(Control));  // open: a_out, ax, ay
  triple_2_channel_mux triple_2_channel_mux_2 (
    .bx(Input_2[3]), .by(Input_1[3]), .cy(Input_1[4]), .c_out(Output[4]), .cx(Input_2[4]), .enable(1'b1),
    .b_out(Output[3]), .a_out(Output[2]), .ax(Input_2[2]), .ay(Input_1[2]), .A(Control), .B(Control),
    .C(Control));
  triple_2_channel_mux triple_2_channel_mux_3 (
    .bx(Input_2[6]), .by(Input_1[6]), .cy(Input_1[7]), .c_out(Output[7]), .cx(Input_2[7]), .enable(1'b1),
    .b_out(Output[6]), .a_out(Output[5]), .ax(Input_2[5]), .ay(Input_1[5]), .A(Control), .B(Control),
    .C(Control));
endmodule

module _8bit_2_output_demuliplexer (
  input  [7:0] Input,
  input  Control,
  output [7:0] Output_1,
  output [7:0] Output_2
);

  triple_2_channel_demux triple_2_channel_demux_1 (
    .bx(Output_2[0]), .by(Output_1[0]), .cy(Output_1[1]), .c_in(Input[1]), .cx(Output_2[1]), .enable(1'b1),
    .b_in(Input[0]), .A(Control), .B(Control), .C(Control));  // open: a_in, ax, ay
  triple_2_channel_demux triple_2_channel_demux_2 (
    .bx(Output_2[3]), .by(Output_1[3]), .cy(Output_1[4]), .c_in(Input[4]), .cx(Output_2[4]), .enable(1'b1),
    .b_in(Input[3]), .a_in(Input[2]), .ax(Output_2[2]), .ay(Output_1[2]), .A(Control), .B(Control),
    .C(Control));
  triple_2_channel_demux triple_2_channel_demux_3 (
    .bx(Output_2[6]), .by(Output_1[6]), .cy(Output_1[7]), .c_in(Input[7]), .cx(Output_2[7]), .enable(1'b1),
    .b_in(Input[6]), .a_in(Input[5]), .ax(Output_2[5]), .ay(Output_1[5]), .A(Control), .B(Control),
    .C(Control));
endmodule

module _8bit_5_input_multiplexer (
  input  [7:0] Input_1,
  input  [7:0] Input_2,
  input  [7:0] Input_3,
  input  [7:0] Input_4,
  input  [7:0] Input_5,
  input  Control_1,
  input  Control_2,
  input  Control_3,
  output [7:0] out_9
);

  wire hex_inverter_1__3_prime, hex_inverter_1__4_prime, hex_inverter_1__6_prime, quad_and_1__3y;
  wire [7:0] n8bit_and_1_out, n8bit_and_2_out, n8bit_and_3_out, n8bit_and_4_out, n8bit_and_5_out,
       n8bit_or_1_out, n8bit_or_2_out, n8bit_or_3_out;
  wire [7:7] quad_and_1__1y, quad_and_1__2y, quad_and_1__4y, quad_and_2__1y;

  Hex_Inverter hex_inverter_1 (
    ._3(Control_2), ._3_prime(hex_inverter_1__3_prime), ._4(Control_1), ._4_prime(hex_inverter_1__4_prime),
    ._6(Control_3), ._6_prime(hex_inverter_1__6_prime));  // open: _1, _1_prime, _2, _2_prime, _5, _5_prime
  _8bit_AND_Gate u_8bit_and_1 (.In_2(Input_1), .In_1({8{quad_and_2__1y[7]}}), .Out(n8bit_and_1_out));
  _8bit_AND_Gate u_8bit_and_2 (.In_2(Input_2), .In_1({8{quad_and_1__4y[7]}}), .Out(n8bit_and_2_out));
  _8bit_AND_Gate u_8bit_and_3 (.In_2(Input_3), .In_1({8{quad_and_1__2y[7]}}), .Out(n8bit_and_3_out));
  _8bit_AND_Gate u_8bit_and_4 (.In_2(Input_4), .In_1({8{quad_and_1__1y[7]}}), .Out(n8bit_and_4_out));
  _8bit_AND_Gate u_8bit_and_5 (.In_2(Input_5), .In_1({8{Control_1}}), .Out(n8bit_and_5_out));
  Quad_AND_Gate quad_and_1 (
    ._1a(Control_3), ._1b(Control_2), ._1y(quad_and_1__1y[7]), ._2a(hex_inverter_1__3_prime),
    ._2b(Control_3), ._2y(quad_and_1__2y[7]), ._3a(hex_inverter_1__6_prime), ._3b(hex_inverter_1__3_prime),
    ._3y(quad_and_1__3y), ._4a(hex_inverter_1__6_prime), ._4b(Control_2), ._4y(quad_and_1__4y[7]));
  _8bit_OR_Gate u_8bit_or_1 (.In_2(n8bit_and_2_out), .In_1(n8bit_and_1_out), .Out(n8bit_or_1_out));
  _8bit_OR_Gate u_8bit_or_2 (.In_2(n8bit_and_3_out), .In_1(n8bit_or_1_out), .Out(n8bit_or_2_out));
  _8bit_OR_Gate u_8bit_or_3 (.In_2(n8bit_and_5_out), .In_1(n8bit_and_4_out), .Out(n8bit_or_3_out));
  Quad_AND_Gate quad_and_2 (
    ._1a(hex_inverter_1__4_prime), ._1b(quad_and_1__3y), ._1y(quad_and_2__1y[7]));  // open: _2a, _2b, _2y, _3a, _3b, _3y, _4a, _4b, _4y
  _8bit_OR_Gate u_8bit_or_4 (.In_2(n8bit_or_3_out), .In_1(n8bit_or_2_out), .Out(out_9));
endmodule

module _8bit_3_input_multiplexer (
  input  [7:0] Input_1,
  input  [7:0] Input_2,
  input  [7:0] Input_3,
  input  Control_1,
  input  Control_2,
  output [7:0] out_6
);

  wire hex_inverter_1__1_prime, hex_inverter_1__2_prime;
  wire [7:0] n8bit_and_1_out, n8bit_and_2_out, n8bit_and_3_out, n8bit_or_1_out;
  wire [7:7] quad_and_1__1y, quad_and_1__2y, quad_and_1__3y;

  Hex_Inverter hex_inverter_1 (
    ._1(Control_1), ._1_prime(hex_inverter_1__1_prime), ._2(Control_2), ._2_prime(hex_inverter_1__2_prime));  // open: _3, _3_prime, _4, _4_prime, _5, _5_prime, _6, _6_prime
  _8bit_AND_Gate u_8bit_and_1 (.In_2(Input_1), .In_1({8{quad_and_1__1y[7]}}), .Out(n8bit_and_1_out));
  _8bit_AND_Gate u_8bit_and_2 (.In_2(Input_2), .In_1({8{quad_and_1__2y[7]}}), .Out(n8bit_and_2_out));
  _8bit_AND_Gate u_8bit_and_3 (.In_2(Input_3), .In_1({8{quad_and_1__3y[7]}}), .Out(n8bit_and_3_out));
  Quad_AND_Gate quad_and_1 (
    ._1a(hex_inverter_1__2_prime), ._1b(hex_inverter_1__1_prime), ._1y(quad_and_1__1y[7]),
    ._2a(hex_inverter_1__1_prime), ._2b(Control_2), ._2y(quad_and_1__2y[7]), ._3a(Control_1),
    ._3b(hex_inverter_1__2_prime), ._3y(quad_and_1__3y[7]));  // open: _4a, _4b, _4y
  _8bit_OR_Gate u_8bit_or_1 (.In_2(n8bit_and_2_out), .In_1(n8bit_and_1_out), .Out(n8bit_or_1_out));
  _8bit_OR_Gate u_8bit_or_2 (.In_2(n8bit_and_3_out), .In_1(n8bit_or_1_out), .Out(out_6));
endmodule

module _8bit_adder (
  input  [7:0] Input1,
  input  [7:0] Input_2,
  output [7:0] Output,
  output Carry
);

  wire n4bit_adder_1_c_out;

  _4bit_adder u_4bit_adder_1 (
    .In_1(Input1[3:0]), .In_2(Input_2[3:0]), .C_in(1'b0), .Out(Output[3:0]), .C_out(n4bit_adder_1_c_out));
  _4bit_adder u_4bit_adder_2 (
    .In_1(Input1[7:4]), .In_2(Input_2[7:4]), .C_in(n4bit_adder_1_c_out), .Out(Output[7:4]), .C_out(Carry));
endmodule

module _8bit_register (
  input  M,
  input  CLR,
  input  N,
  input  [7:0] \input ,
  input  clock,
  input  G2,
  input  G1,
  output [7:0] \output 
);

  _4bit_register u_4bit_register_1 (
    .M(M), .N(N), ._1Q(\input [0]), ._2Q(\input [1]), ._3Q(\input [2]), ._4Q(\input [3]), .CLK(clock),
    .CLR(CLR), ._1D(\output [0]), ._2D(\output [1]), ._3D(\output [2]), ._4D(\output [3]), .G2(G2), .G1(G1));
  _4bit_register u_4bit_register_2 (
    .M(M), .N(N), ._1Q(\input [4]), ._2Q(\input [5]), ._3Q(\input [6]), ._4Q(\input [7]), .CLK(clock),
    .CLR(CLR), ._1D(\output [4]), ._2D(\output [5]), ._3D(\output [6]), ._4D(\output [7]), .G2(G2), .G1(G1));
endmodule

module triple_2_channel_mux (
  input  bx,
  input  by,
  input  cy,
  input  ax,
  input  ay,
  input  cx,
  input  A,
  input  enable,
  input  B,
  input  C,
  output b_out,
  output a_out,
  output c_out
);

  Multiplexer multiplexer_1 (.in0(cx), .in1(cy), .out(c_out), .sel(C), .en(enable));
  Multiplexer multiplexer_2 (.in0(bx), .in1(by), .out(b_out), .sel(B), .en(enable));
  Multiplexer multiplexer_3 (.in0(ax), .in1(ay), .out(a_out), .sel(A), .en(enable));

  // Notes on the sheet:
  //   Cd4053B as multiplexer
endmodule

module triple_2_channel_demux (
  input  b_in,
  input  a_in,
  input  c_in,
  input  A,
  input  enable,
  input  B,
  input  C,
  output bx,
  output by,
  output cy,
  output ax,
  output ay,
  output cx
);

  Demultiplexer demultiplexer_1 (.out0(cx), .out1(cy), .in(c_in), .sel(C), .en(enable));
  Demultiplexer demultiplexer_2 (.out0(bx), .out1(by), .in(b_in), .sel(B), .en(enable));
  Demultiplexer demultiplexer_3 (.out0(ax), .out1(ay), .in(a_in), .sel(A), .en(enable));

  // Notes on the sheet:
  //   Cd4053B as demultiplexer
endmodule

// Or
module Quad_OR_Gate (
  input  _3a,
  input  _1a,
  input  _3b,
  input  _1b,
  input  _4a,
  input  _2a,
  input  _4b,
  input  _2b,
  output _3y,
  output _1y,
  output _4y,
  output _2y
);

  or or_1 (_1y, _1a, _1b);
  or or_2 (_2y, _2a, _2b);
  or or_3 (_3y, _3a, _3b);
  or or_4 (_4y, _4a, _4b);
endmodule

// And
module Quad_AND_Gate (
  input  _3a,
  input  _1a,
  input  _3b,
  input  _1b,
  input  _4a,
  input  _2a,
  input  _4b,
  input  _2b,
  output _3y,
  output _1y,
  output _4y,
  output _2y
);

  and and_1 (_1y, _1a, _1b);
  and and_2 (_2y, _2a, _2b);
  and and_3 (_3y, _3a, _3b);
  and and_4 (_4y, _4a, _4b);
endmodule

module _4bit_adder (
  input  [3:0] In_1,
  input  [3:0] In_2,
  input  C_in,
  output [3:0] Out,
  output C_out
);

  wire quad_and_1__1y, quad_and_1__2y, quad_and_1__3y, quad_and_1__4y, quad_and_2__1y, quad_and_2__2y,
       quad_and_2__3y, quad_and_2__4y, quad_or_1__1y, quad_or_1__2y, quad_or_1__3y, quad_xor_gate_1__1_y,
       quad_xor_gate_1__3_y, quad_xor_gate_2__1_y, quad_xor_gate_2__3_y;

  Quad_XOR_gate quad_xor_gate_1 (
    ._1a(In_1[0]), ._1b(In_2[0]), ._1_y(quad_xor_gate_1__1_y), ._2a(quad_xor_gate_1__1_y), ._2b(C_in),
    ._2_y(Out[0]), ._3a(In_1[1]), ._3b(In_2[1]), ._3_y(quad_xor_gate_1__3_y), ._4a(quad_xor_gate_1__3_y),
    ._4b(quad_or_1__1y), ._4_y(Out[1]));
  Quad_XOR_gate quad_xor_gate_2 (
    ._1a(In_1[2]), ._1b(In_2[2]), ._1_y(quad_xor_gate_2__1_y), ._2a(quad_xor_gate_2__1_y),
    ._2b(quad_or_1__2y), ._2_y(Out[2]), ._3a(In_1[3]), ._3b(In_2[3]), ._3_y(quad_xor_gate_2__3_y),
    ._4a(quad_xor_gate_2__3_y), ._4b(quad_or_1__3y), ._4_y(Out[3]));
  Quad_AND_Gate quad_and_1 (
    ._1a(quad_xor_gate_1__1_y), ._1b(C_in), ._1y(quad_and_1__1y), ._2a(In_2[0]), ._2b(In_1[0]),
    ._2y(quad_and_1__2y), ._3a(quad_xor_gate_1__3_y), ._3b(quad_or_1__1y), ._3y(quad_and_1__3y),
    ._4a(In_1[1]), ._4b(In_2[1]), ._4y(quad_and_1__4y));
  Quad_AND_Gate quad_and_2 (
    ._1a(quad_xor_gate_2__1_y), ._1b(quad_or_1__2y), ._1y(quad_and_2__1y), ._2a(In_2[2]), ._2b(In_1[2]),
    ._2y(quad_and_2__2y), ._3a(quad_xor_gate_2__3_y), ._3b(quad_or_1__3y), ._3y(quad_and_2__3y),
    ._4a(In_2[3]), ._4b(In_1[3]), ._4y(quad_and_2__4y));
  Quad_OR_Gate quad_or_1 (
    ._1a(quad_and_1__1y), ._1b(quad_and_1__2y), ._1y(quad_or_1__1y), ._2a(quad_and_1__3y),
    ._2b(quad_and_1__4y), ._2y(quad_or_1__2y), ._3a(quad_and_2__1y), ._3b(quad_and_2__2y),
    ._3y(quad_or_1__3y), ._4a(quad_and_2__3y), ._4b(quad_and_2__4y), ._4y(C_out));
endmodule

module _4bit_register (
  input  M,
  input  N,
  input  CLR,
  input  _1Q,
  input  _2Q,
  input  _3Q,
  input  _4Q,
  input  CLK,
  input  G2,
  input  G1,
  output _1D,
  output _2D,
  output _3D,
  output _4D
);

  wire and_1_out, and_2_out, and_3_out, and_4_out, and_5_out, and_6_out, and_7_out, and_8_out, and_9_out,
       and_10_out, d_ff_1_q, d_ff_2_q, d_ff_3_q, d_ff_4_q, not_1_out, not_2_out, not_3_out, not_4_out,
       not_5_out, or_1_out, or_2_out, or_3_out, or_4_out;

  not not_1 (not_1_out, M);
  not not_2 (not_2_out, N);
  and and_1 (and_1_out, not_1_out, not_2_out);
  not not_3 (not_3_out, and_10_out);
  and and_2 (and_2_out, d_ff_1_q, not_3_out);
  and and_3 (and_3_out, _1Q, and_10_out);
  and and_4 (and_4_out, d_ff_2_q, not_3_out);
  and and_5 (and_5_out, _2Q, and_10_out);
  and and_6 (and_6_out, d_ff_3_q, not_3_out);
  and and_7 (and_7_out, _3Q, and_10_out);
  and and_8 (and_8_out, d_ff_4_q, not_3_out);
  and and_9 (and_9_out, _4Q, and_10_out);
  or or_1 (or_1_out, and_2_out, and_3_out);
  or or_2 (or_2_out, and_4_out, and_5_out);
  or or_3 (or_3_out, and_6_out, and_7_out);
  or or_4 (or_4_out, and_8_out, and_9_out);
  D_Flip_Flop d_ff_1 (.clk(CLK), .D(or_1_out), .Q(d_ff_1_q), .en(1'b1), .reset(CLR));  // open: Qn, preset
  D_Flip_Flop d_ff_2 (.clk(CLK), .D(or_2_out), .Q(d_ff_2_q), .en(1'b1), .reset(CLR));  // open: Qn, preset
  D_Flip_Flop d_ff_3 (.clk(CLK), .D(or_3_out), .Q(d_ff_3_q), .en(1'b1), .reset(CLR));  // open: Qn, preset
  D_Flip_Flop d_ff_4 (.clk(CLK), .D(or_4_out), .Q(d_ff_4_q), .en(1'b1), .reset(CLR));  // open: Qn, preset
  and and_10 (and_10_out, not_4_out, not_5_out);
  not not_4 (not_4_out, G2);
  not not_5 (not_5_out, G1);
  assign _1D = and_1_out ? d_ff_1_q : 1'bz;  // Controlled_Buffer controlled_buffer_1
  assign _2D = and_1_out ? d_ff_2_q : 1'bz;  // Controlled_Buffer controlled_buffer_2
  assign _3D = and_1_out ? d_ff_3_q : 1'bz;  // Controlled_Buffer controlled_buffer_3
  assign _4D = and_1_out ? d_ff_4_q : 1'bz;  // Controlled_Buffer controlled_buffer_4
endmodule

// Not
module Hex_Inverter (
  input  _1,
  input  _4,
  input  _2,
  input  _5,
  input  _6,
  input  _3,
  output _1_prime,
  output _4_prime,
  output _5_prime,
  output _2_prime,
  output _6_prime,
  output _3_prime
);

  not not_1 (_1_prime, _1);
  not not_2 (_2_prime, _2);
  not not_3 (_3_prime, _3);
  not not_4 (_4_prime, _4);
  not not_5 (_5_prime, _5);
  not not_6 (_6_prime, _6);
endmodule

module Quad_XOR_gate (
  input  _3a,
  input  _1a,
  input  _3b,
  input  _1b,
  input  _4a,
  input  _2a,
  input  _4b,
  input  _2b,
  output _3_y,
  output _1_y,
  output _4_y,
  output _2_y
);

  xor xor_1 (_1_y, _1a, _1b);
  xor xor_2 (_2_y, _2a, _2b);
  xor xor_3 (_3_y, _3a, _3b);
  xor xor_4 (_4_y, _4a, _4b);

  // Notes on the sheet:
  //   XOR Gate Sn74hc86n
endmodule

module _8bit_5_input_mux_w__zero_output (
  input  [7:0] Input_1,
  input  [7:0] Input_2,
  input  [7:0] Input_3,
  input  [7:0] Input_4,
  input  [7:0] Input_5,
  input  Control_1,
  input  Control_2,
  input  Control_3,
  output [7:0] out_9
);

  wire hex_inverter_1__3_prime, hex_inverter_1__4_prime, hex_inverter_1__6_prime, quad_and_1__3y,
       quad_and_2__2y;
  wire [7:0] n8bit_and_1_out, n8bit_and_2_out, n8bit_and_3_out, n8bit_and_4_out, n8bit_and_5_out,
       n8bit_or_1_out, n8bit_or_2_out, n8bit_or_3_out, n8bit_or_4_out;
  wire [7:7] hex_inverter_1__5_prime, quad_and_1__1y, quad_and_1__2y, quad_and_1__4y, quad_and_2__1y;

  Hex_Inverter hex_inverter_1 (
    ._3(Control_2), ._3_prime(hex_inverter_1__3_prime), ._4(Control_1), ._4_prime(hex_inverter_1__4_prime),
    ._5(quad_and_2__2y), ._5_prime(hex_inverter_1__5_prime[7]), ._6(Control_3),
    ._6_prime(hex_inverter_1__6_prime));  // open: _1, _1_prime, _2, _2_prime
  _8bit_AND_Gate u_8bit_and_1 (.In_2(Input_1), .In_1({8{quad_and_2__1y[7]}}), .Out(n8bit_and_1_out));
  _8bit_AND_Gate u_8bit_and_2 (.In_2(Input_2), .In_1({8{quad_and_1__4y[7]}}), .Out(n8bit_and_2_out));
  _8bit_AND_Gate u_8bit_and_3 (.In_2(Input_3), .In_1({8{quad_and_1__2y[7]}}), .Out(n8bit_and_3_out));
  _8bit_AND_Gate u_8bit_and_4 (.In_2(Input_4), .In_1({8{quad_and_1__1y[7]}}), .Out(n8bit_and_4_out));
  _8bit_AND_Gate u_8bit_and_5 (.In_2(Input_5), .In_1({8{Control_1}}), .Out(n8bit_and_5_out));
  Quad_AND_Gate quad_and_1 (
    ._1a(Control_3), ._1b(Control_2), ._1y(quad_and_1__1y[7]), ._2a(hex_inverter_1__3_prime),
    ._2b(Control_3), ._2y(quad_and_1__2y[7]), ._3a(hex_inverter_1__6_prime), ._3b(hex_inverter_1__3_prime),
    ._3y(quad_and_1__3y), ._4a(hex_inverter_1__6_prime), ._4b(Control_2), ._4y(quad_and_1__4y[7]));
  _8bit_OR_Gate u_8bit_or_1 (.In_2(n8bit_and_2_out), .In_1(n8bit_and_1_out), .Out(n8bit_or_1_out));
  _8bit_OR_Gate u_8bit_or_2 (.In_2(n8bit_and_3_out), .In_1(n8bit_or_1_out), .Out(n8bit_or_2_out));
  _8bit_OR_Gate u_8bit_or_3 (.In_2(n8bit_and_5_out), .In_1(n8bit_and_4_out), .Out(n8bit_or_3_out));
  Quad_AND_Gate quad_and_2 (
    ._1a(hex_inverter_1__4_prime), ._1b(quad_and_1__3y), ._1y(quad_and_2__1y[7]), ._2a(Control_1),
    ._2b(quad_and_1__2y[7]), ._2y(quad_and_2__2y));  // open: _3a, _3b, _3y, _4a, _4b, _4y
  _8bit_OR_Gate u_8bit_or_4 (.In_2(n8bit_or_3_out), .In_1(n8bit_or_2_out), .Out(n8bit_or_4_out));
  _8bit_AND_Gate u_8bit_and_6 (.In_2(n8bit_or_4_out), .In_1({8{hex_inverter_1__5_prime[7]}}), .Out(out_9));
endmodule

module Control_Load (
  input  [5:0] Instruction,
  input  [17:0] Data,
  output Clear,
  output A_EW,
  output B_EW,
  output C_EW,
  output D_EW,
  output [7:0] Write_Value,
  output Mux_1_1,
  output Mux_1_2,
  output Mux_1_3,
  output Mux_3_1,
  output Ram_EW_TO,
  output Ram_ER_FROM
);

  wire hex_inverter_1__1_prime, hex_inverter_1__2_prime, hex_inverter_1__3_prime, hex_inverter_1__4_prime,
       hex_inverter_1__5_prime, hex_inverter_1__6_prime, quad_and_1__2y, quad_and_1__3y, quad_and_2__1y,
       quad_and_2__2y, quad_and_2__3y, quad_and_2__4y, quad_and_3__1y, quad_and_3__2y, quad_and_3__3y,
       quad_and_3__4y, quad_and_4__1y, quad_and_4__2y, quad_and_4__3y, quad_and_4__4y, quad_or_1__2y;
  wire [7:7] quad_or_1__4y;

  Hex_Inverter hex_inverter_1 (
    ._1(Instruction[5]), ._1_prime(hex_inverter_1__1_prime), ._2(Instruction[4]),
    ._2_prime(hex_inverter_1__2_prime), ._3(Instruction[3]), ._3_prime(hex_inverter_1__3_prime),
    ._4(Instruction[2]), ._4_prime(hex_inverter_1__4_prime), ._5(Instruction[1]),
    ._5_prime(hex_inverter_1__5_prime), ._6(Instruction[0]), ._6_prime(hex_inverter_1__6_prime));
  Quad_AND_Gate quad_and_1 (
    ._2a(Instruction[0]), ._2b(hex_inverter_1__5_prime), ._2y(quad_and_1__2y), ._3a(quad_and_1__2y),
    ._3b(hex_inverter_1__4_prime), ._3y(quad_and_1__3y), ._4a(hex_inverter_1__4_prime), ._4b(quad_and_2__3y));  // open: _1a, _1b, _1y, _4y
  Quad_AND_Gate quad_and_2 (
    ._1a(hex_inverter_1__3_prime), ._1b(hex_inverter_1__2_prime), ._1y(quad_and_2__1y),
    ._2a(hex_inverter_1__1_prime), ._2b(quad_and_2__1y), ._2y(quad_and_2__2y), ._3a(Instruction[1]),
    ._3b(hex_inverter_1__6_prime), ._3y(quad_and_2__3y), ._4a(quad_and_3__4y), ._4b(hex_inverter_1__6_prime),
    ._4y(quad_and_2__4y));
  Quad_AND_Gate quad_and_3 (
    ._1a(hex_inverter_1__6_prime), ._1b(hex_inverter_1__5_prime), ._1y(quad_and_3__1y), ._2a(quad_and_3__1y),
    ._2b(hex_inverter_1__4_prime), ._2y(quad_and_3__2y), ._3a(quad_and_3__1y), ._3b(Instruction[2]),
    ._3y(quad_and_3__3y), ._4a(Instruction[2]), ._4b(Instruction[1]), ._4y(quad_and_3__4y));
  Quad_AND_Gate quad_and_4 (
    ._1a(Instruction[0]), ._1b(hex_inverter_1__5_prime), ._1y(quad_and_4__1y), ._2a(quad_and_4__1y),
    ._2b(Instruction[2]), ._2y(quad_and_4__2y), ._3a(quad_and_2__2y), ._3b(quad_and_3__2y),
    ._3y(quad_and_4__3y), ._4a(quad_and_2__2y), ._4b(quad_and_4__2y), ._4y(quad_and_4__4y));
  Quad_OR_Gate quad_or_1 (
    ._1a(quad_and_4__4y), ._1b(quad_and_4__3y), ._1y(Mux_3_1), ._2a(quad_and_4__3y), ._2b(Ram_EW_TO),
    ._2y(quad_or_1__2y), ._4a(Ram_ER_FROM), ._4b(Mux_3_1), ._4y(quad_or_1__4y[7]));  // open: _3a, _3b, _3y
  Quad_AND_Gate quad_and_5 (
    ._1a(quad_or_1__4y[7]), ._1b(Data[17]), ._1y(A_EW), ._2a(quad_or_1__4y[7]), ._2b(Data[16]), ._2y(B_EW),
    ._3a(quad_or_1__4y[7]), ._3b(Data[15]), ._3y(C_EW), ._4a(quad_or_1__4y[7]), ._4b(Data[14]), ._4y(D_EW));
  Quad_AND_Gate quad_and_6 (
    ._1a(quad_or_1__2y), ._1b(Data[13]), ._1y(Mux_1_1), ._2a(quad_or_1__2y), ._2b(Data[12]), ._2y(Mux_1_2),
    ._3a(quad_or_1__2y), ._4a(quad_or_1__2y), ._4b(Data[11]), ._4y(Mux_1_3));  // open: _3b, _3y
  Quad_AND_Gate quad_and_7 (
    ._1a(quad_and_2__2y), ._1b(quad_and_2__4y), ._1y(Ram_EW_TO), ._2a(quad_and_2__2y), ._2b(quad_and_3__3y),
    ._2y(Ram_ER_FROM), ._4a(quad_and_2__2y), ._4b(quad_and_1__3y), ._4y(Clear));  // open: _3a, _3b, _3y
  _8bit_AND_Gate u_8bit_and_1 (.In_2(Data[7:0]), .In_1({8{quad_or_1__4y[7]}}), .Out(Write_Value));
endmodule

module Control_Addition (
  input  [5:0] Instruction,
  input  [17:0] Data,
  output Write_Mux_2,
  output Read_Mux_1_1,
  output Read_Mux_1_2,
  output Read_Mux_1_3,
  output Read_Mux_2_1,
  output Read_Mux_2_2,
  output Read_Mux_2_3,
  output Subtract_nAdd,
  output out_11,
  output shift_nother,
  output [7:0] Write_Value,
  output A_EW,
  output B_EW,
  output C_EW,
  output D_EW
);

  wire hex_inverter_1__1_prime, hex_inverter_1__2_prime, hex_inverter_1__4_prime, hex_inverter_1__5_prime,
       hex_inverter_1__6_prime, quad_and_1__1y, quad_and_1__2y, quad_and_1__3y, quad_and_2__1y,
       quad_and_2__3y, quad_and_2__4y, quad_and_3__1y, quad_and_3__2y, quad_and_3__3y, quad_and_3__4y,
       quad_and_4__1y, quad_and_4__2y, quad_and_4__3y, quad_and_5__1y, quad_and_5__2y, quad_and_5__3y,
       quad_and_5__4y, quad_or_1__3y, quad_or_1__4y, quad_or_2__2y;
  wire [7:7] quad_or_1__2y;

  Hex_Inverter hex_inverter_1 (
    ._1(Instruction[5]), ._1_prime(hex_inverter_1__1_prime), ._2(Instruction[4]),
    ._2_prime(hex_inverter_1__2_prime), ._4(Instruction[2]), ._4_prime(hex_inverter_1__4_prime),
    ._5(Instruction[1]), ._5_prime(hex_inverter_1__5_prime), ._6(Instruction[0]),
    ._6_prime(hex_inverter_1__6_prime));  // open: _3, _3_prime
  Quad_AND_Gate quad_and_1 (
    ._1a(hex_inverter_1__4_prime), ._1b(hex_inverter_1__6_prime), ._1y(quad_and_1__1y), ._2a(Instruction[0]),
    ._2b(hex_inverter_1__5_prime), ._2y(quad_and_1__2y), ._3a(quad_and_1__2y), ._3b(hex_inverter_1__4_prime),
    ._3y(quad_and_1__3y), ._4a(hex_inverter_1__4_prime), ._4b(quad_and_2__3y));  // open: _4y
  Quad_AND_Gate quad_and_2 (
    ._1a(Instruction[3]), ._1b(hex_inverter_1__2_prime), ._1y(quad_and_2__1y), ._2a(hex_inverter_1__1_prime),
    ._2b(quad_and_2__1y), ._2y(Write_Mux_2), ._3a(Instruction[1]), ._3b(hex_inverter_1__6_prime),
    ._3y(quad_and_2__3y), ._4a(quad_and_3__4y), ._4b(hex_inverter_1__6_prime), ._4y(quad_and_2__4y));
  Quad_AND_Gate quad_and_3 (
    ._1a(hex_inverter_1__6_prime), ._1b(hex_inverter_1__5_prime), ._1y(quad_and_3__1y), ._2a(quad_and_3__1y),
    ._2b(hex_inverter_1__4_prime), ._2y(quad_and_3__2y), ._3a(quad_and_3__1y), ._3b(Instruction[2]),
    ._3y(quad_and_3__3y), ._4a(Instruction[2]), ._4b(Instruction[1]), ._4y(quad_and_3__4y));
  Quad_AND_Gate quad_and_4 (
    ._1a(Instruction[0]), ._1b(hex_inverter_1__5_prime), ._1y(quad_and_4__1y), ._2a(quad_and_4__1y),
    ._2b(Instruction[2]), ._2y(quad_and_4__2y), ._3a(Write_Mux_2), ._3b(quad_and_3__2y),
    ._3y(quad_and_4__3y), ._4a(Write_Mux_2), ._4b(quad_and_4__2y), ._4y(out_11));
  Quad_AND_Gate quad_and_5 (
    ._1a(Write_Mux_2), ._1b(quad_and_2__4y), ._1y(quad_and_5__1y), ._2a(Write_Mux_2), ._2b(quad_and_3__3y),
    ._2y(quad_and_5__2y), ._3a(Instruction[1]), ._3b(quad_and_1__1y), ._3y(quad_and_5__3y),
    ._4a(Write_Mux_2), ._4b(quad_and_1__3y), ._4y(quad_and_5__4y));
  Quad_OR_Gate quad_or_1 (
    ._1a(quad_and_5__2y), ._1b(quad_and_5__3y), ._1y(Subtract_nAdd), ._2a(quad_and_5__4y),
    ._2b(quad_and_5__2y), ._2y(quad_or_1__2y[7]), ._3a(quad_and_5__4y), ._3b(quad_and_4__3y),
    ._3y(quad_or_1__3y), ._4a(quad_or_1__3y), ._4b(Subtract_nAdd), ._4y(quad_or_1__4y));
  _8bit_AND_Gate u_8bit_and_1 (.In_2(Data[7:0]), .In_1({8{quad_or_1__2y[7]}}), .Out(Write_Value));
  Quad_OR_Gate quad_or_2 (
    ._1a(quad_and_5__1y), ._1b(out_11), ._1y(shift_nother), ._2a(shift_nother), ._2b(quad_or_1__4y),
    ._2y(quad_or_2__2y));  // open: _3a, _3b, _3y, _4a, _4b, _4y
  Quad_AND_Gate quad_and_6 (
    ._1a(quad_or_2__2y), ._1b(Data[13]), ._1y(Read_Mux_1_1), ._2a(quad_or_2__2y), ._2b(Data[12]),
    ._2y(Read_Mux_1_2), ._3a(quad_or_2__2y), ._3b(Data[11]), ._3y(Read_Mux_1_3));  // open: _4a, _4b, _4y
  Quad_AND_Gate quad_and_7 (
    ._1a(quad_or_1__4y), ._1b(Data[10]), ._1y(Read_Mux_2_1), ._2a(quad_or_1__4y), ._2b(Data[9]),
    ._2y(Read_Mux_2_2), ._3a(quad_or_1__4y), ._3b(Data[8]), ._3y(Read_Mux_2_3));  // open: _4a, _4b, _4y

  assign A_EW = Data[17];
  assign B_EW = Data[16];
  assign C_EW = Data[15];
  assign D_EW = Data[14];
endmodule

module Control_Logical (
  input  [5:0] Instruction,
  input  [17:0] Data
);
endmodule

module Control_Logical_Comparison (
  input  [5:0] Instruction,
  input  [17:0] Data
);
endmodule

module Control_Load_PC (
  input  [5:0] Instruction,
  input  [17:0] Data
);
endmodule

module Control_Misc (
  input  [5:0] Instruction,
  input  [17:0] Data
);
endmodule
