// Logisim project version-CF-DisplayCircuit.circ as structural Verilog: 8 circuits, main circuit main
module main (
  input  CLR
);

  wire CLK_out, hex_inverter_1__1_prime, hex_inverter_1__2_prime, \n4bit_adder_1_σ1 , \n4bit_adder_1_σ2 ,
       n4bit_adder_2_c4, \n4bit_adder_2_σ1 , \n4bit_adder_2_σ2 , \n4bit_adder_2_σ3 , \n4bit_adder_2_σ4 ,
       quad_and_1__1y, quad_and_1__2y, quad_and_1__3y, quad_and_1__4y;
  wire [1:0] n4bit_register_1__1q;
  wire [3:0] n4bit_register_2__1q;

  Hex_Digit_Display hex_digit_display_1 (.value({2'b00, n4bit_register_1__1q}));  // open: dp
  Clock CLK (.out(CLK_out));
  Hex_Digit_Display hex_digit_display_2 (.value(n4bit_register_2__1q));  // open: dp
  _4bit_register u_4bit_register_1 (
    .M(1'b0), .N(1'b0), ._1Q(n4bit_register_1__1q[0]), ._2Q(n4bit_register_1__1q[1]), .CLK(CLK_out),
    .Gnd(1'b0), .Vcc(1'b1), .CLR(CLR), ._1D(\n4bit_adder_1_σ1 ), ._2D(\n4bit_adder_1_σ2 ), ._3D(1'b0),
    ._4D(1'b0), .G2(1'b0), .G1(1'b0));  // open: _3Q, _4Q
  _4bit_register u_4bit_register_2 (
    .M(1'b0), .N(1'b0), ._1Q(n4bit_register_2__1q[0]), ._2Q(n4bit_register_2__1q[1]),
    ._3Q(n4bit_register_2__1q[2]), ._4Q(n4bit_register_2__1q[3]), .CLK(CLK_out), .Gnd(1'b0), .Vcc(1'b1),
    .CLR(CLR), ._1D(\n4bit_adder_2_σ1 ), ._2D(\n4bit_adder_2_σ2 ), ._3D(\n4bit_adder_2_σ3 ),
    ._4D(\n4bit_adder_2_σ4 ), .G2(1'b0), .G1(1'b0));
  _4bit_adder u_4bit_adder_1 (
    .\Σ2 (\n4bit_adder_1_σ2 ), .B2(1'b0), .A2(n4bit_register_1__1q[1]), .\Σ1 (\n4bit_adder_1_σ1 ),
    .A1(n4bit_register_1__1q[0]), .B1(1'b0), .C0(n4bit_adder_2_c4), .Gnd(1'b0), .Vcc(1'b1), .B3(1'b0),
    .A3(1'b0), .A4(1'b0), .B4(1'b0));  // open: Σ3, Σ4, C4
  _4bit_adder u_4bit_adder_2 (
    .\Σ2 (\n4bit_adder_2_σ2 ), .B2(1'b0), .A2(n4bit_register_2__1q[1]), .\Σ1 (\n4bit_adder_2_σ1 ),
    .A1(n4bit_register_2__1q[0]), .B1(1'b1), .C0(1'b0), .Gnd(1'b0), .Vcc(1'b1), .B3(1'b0),
    .A3(n4bit_register_2__1q[2]), .\Σ3 (\n4bit_adder_2_σ3 ), .A4(n4bit_register_2__1q[3]), .B4(1'b0),
    .\Σ4 (\n4bit_adder_2_σ4 ), .C4(n4bit_adder_2_c4));
  Hex_Inverter hex_inverter_1 (
    ._1(n4bit_register_1__1q[1]), ._1_prime(hex_inverter_1__1_prime), ._2(n4bit_register_1__1q[0]),
    ._2_prime(hex_inverter_1__2_prime), .Gnd(1'b0), .Vcc(1'b1));  // open: _3, _3_prime, _4, _4_prime, _5, _5_prime, _6, _6_prime
  Quad_AND_Gate quad_and_1 (
    ._1a(hex_inverter_1__1_prime), ._1b(hex_inverter_1__2_prime), ._1y(quad_and_1__1y), ._2y(quad_and_1__2y),
    ._2a(hex_inverter_1__1_prime), ._2b(n4bit_register_1__1q[0]), .Gnd(1'b0), .Vcc(1'b1),
    ._3a(n4bit_register_1__1q[1]), ._3b(n4bit_register_1__1q[0]), ._3y(quad_and_1__3y), ._4y(quad_and_1__4y),
    ._4a(hex_inverter_1__2_prime), ._4b(n4bit_register_1__1q[1]));
  LED led_1 (.in(quad_and_1__1y));
  LED led_2 (.in(quad_and_1__2y));
  LED led_3 (.in(quad_and_1__4y));
  LED led_4 (.in(quad_and_1__3y));
endmodule

// 4bit Reg
module _4bit_register (
  input  Vcc,
  input  M,
  input  N,
  input  CLR,
  input  _1D,
  input  _2D,
  input  _3D,
  input  _4D,
  input  CLK,
  input  G2,
  input  G1,
  input  Gnd,
  output _1Q,
  output _2Q,
  output _3Q,
  output _4Q
);

  wire and_1_out, and_2_out, and_3_out, and_4_out, and_5_out, and_6_out, and_7_out, and_8_out, and_9_out,
       and_10_out, d_ff_1_q, d_ff_2_q, d_ff_3_q, d_ff_4_q, not_1_out, not_2_out, not_3_out, not_4_out,
       not_5_out, or_1_out, or_2_out, or_3_out, or_4_out;

  not not_1 (not_1_out, M);
  not not_2 (not_2_out, N);
  and and_1 (and_1_out, not_1_out, not_2_out);
  not not_3 (not_3_out, and_10_out);
  and and_2 (and_2_out, d_ff_1_q, not_3_out);
  and and_3 (and_3_out, and_10_out, _1D);
  and and_4 (and_4_out, d_ff_2_q, not_3_out);
  and and_5 (and_5_out, and_10_out, _2D);
  and and_6 (and_6_out, d_ff_3_q, not_3_out);
  and and_7 (and_7_out, and_10_out, _3D);
  and and_8 (and_8_out, d_ff_4_q, not_3_out);
  and and_9 (and_9_out, and_10_out, _4D);
  or or_1 (or_1_out, and_2_out, and_3_out);
  or or_2 (or_2_out, and_4_out, and_5_out);
  or or_3 (or_3_out, and_6_out, and_7_out);
  or or_4 (or_4_out, and_8_out, and_9_out);
  D_Flip_Flop d_ff_1 (.clk(CLK), .D(or_1_out), .Q(d_ff_1_q), .en(1'b1), .reset(CLR));  // open: Qn, preset
  D_Flip_Flop d_ff_2 (.clk(CLK), .D(or_2_out), .Q(d_ff_2_q), .en(1'b1), .reset(CLR));  // open: Qn, preset
  D_Flip_Flop d_ff_3 (.clk(CLK), .D(or_3_out), .Q(d_ff_3_q), .en(1'b1), .reset(CLR));  // open: Qn, preset
  D_Flip_Flop d_ff_4 (.clk(CLK), .D(or_4_out), .Q(d_ff_4_q), .en(1'b1), .reset(CLR));  // open: Qn, preset
  and and_10 (and_10_out, not_4_out, not_5_out);
  not not_4 (not_4_out, G2);
  not not_5 (not_5_out, G1);
  assign _1Q = and_1_out ? d_ff_1_q : 1'bz;  // Controlled_Buffer controlled_buffer_1
  assign _2Q = and_1_out ? d_ff_2_q : 1'bz;  // Controlled_Buffer controlled_buffer_2
  assign _3Q = and_1_out ? d_ff_3_q : 1'bz;  // Controlled_Buffer controlled_buffer_3
  assign _4Q = and_1_out ? d_ff_4_q : 1'bz;  // Controlled_Buffer controlled_buffer_4
endmodule

// 4bit Adder
module _4bit_adder (
  input  Vcc,
  input  B2,
  input  B3,
  input  A2,
  input  A3,
  input  A1,
  input  A4,
  input  B1,
  input  B4,
  input  C0,
  input  Gnd,
  output \Σ2 ,
  output \Σ1 ,
  output \Σ3 ,
  output \Σ4 ,
  output C4
);

  _4bit_adder___Function_block u_4bit_adder_function_block_1 (
    .In_1({A4, A3, A2, A1}), .In_2({B4, B3, B2, B1}), .C_in(C0), .Out({\Σ4 , \Σ3 , \Σ2 , \Σ1 }), .C_out(C4));
endmodule

// Quad AND
module Quad_AND_Gate (
  input  _1a,
  input  Vcc,
  input  _1b,
  input  _3a,
  input  _3b,
  input  _2a,
  input  _2b,
  input  _4a,
  input  Gnd,
  input  _4b,
  output _1y,
  output _2y,
  output _3y,
  output _4y
);

  and and_1 (_1y, _1a, _1b);
  and and_2 (_2y, _2a, _2b);
  and and_3 (_3y, _3a, _3b);
  and and_4 (_4y, _4a, _4b);
endmodule

module Quad_OR_Gate (
  input  _3a,
  input  _1a,
  input  _3b,
  input  _1b,
  input  _4a,
  input  _2a,
  input  _4b,
  input  _2b,
  output _3y,
  output _1y,
  output _4y,
  output _2y
);

  or or_1 (_1y, _1a, _1b);
  or or_2 (_2y, _2a, _2b);
  or or_3 (_3y, _3a, _3b);
  or or_4 (_4y, _4a, _4b);
endmodule

module Quad_XOR_Gate (
  input  _3a,
  input  _1a,
  input  _3b,
  input  _1b,
  input  _4a,
  input  _2a,
  input  _4b,
  input  _2b,
  output _3_y,
  output _1_y,
  output _4_y,
  output _2_y
);

  xor xor_1 (_1_y, _1a, _1b);
  xor xor_2 (_2_y, _2a, _2b);
  xor xor_3 (_3_y, _3a, _3b);
  xor xor_4 (_4_y, _4a, _4b);

  // Notes on the sheet:
  //   XOR Gate Sn74hc86n
endmodule

module Hex_Inverter (
  input  Vcc,
  input  _1,
  input  _4,
  input  _2,
  input  _5,
  input  _6,
  input  _3,
  input  Gnd,
  output _1_prime,
  output _4_prime,
  output _5_prime,
  output _2_prime,
  output _6_prime,
  output _3_prime
);

  not not_1 (_1_prime, _1);
  not not_2 (_2_prime, _2);
  not not_3 (_3_prime, _3);
  not not_4 (_4_prime, _4);
  not not_5 (_5_prime, _5);
  not not_6 (_6_prime, _6);
endmodule

module _4bit_adder___Function_block (
  input  [3:0] In_1,
  input  [3:0] In_2,
  input  C_in,
  output [3:0] Out,
  output C_out
);

  wire quad_and_1__1y, quad_and_1__2y, quad_and_1__3y, quad_and_1__4y, quad_and_2__1y, quad_and_2__2y,
       quad_and_2__3y, quad_and_2__4y, quad_or_1__1y, quad_or_1__2y, quad_or_1__3y, quad_xor_1__1_y,
       quad_xor_1__3_y, quad_xor_2__1_y, quad_xor_2__3_y;

  Quad_XOR_Gate quad_xor_1 (
    ._1a(In_1[0]), ._1b(In_2[0]), ._1_y(quad_xor_1__1_y), ._2a(quad_xor_1__1_y), ._2b(C_in), ._2_y(Out[0]),
    ._3a(In_1[1]), ._3b(In_2[1]), ._3_y(quad_xor_1__3_y), ._4a(quad_xor_1__3_y), ._4b(quad_or_1__1y),
    ._4_y(Out[1]));
  Quad_XOR_Gate quad_xor_2 (
    ._1a(In_1[2]), ._1b(In_2[2]), ._1_y(quad_xor_2__1_y), ._2a(quad_xor_2__1_y), ._2b(quad_or_1__2y),
    ._2_y(Out[2]), ._3a(In_1[3]), ._3b(In_2[3]), ._3_y(quad_xor_2__3_y), ._4a(quad_xor_2__3_y),
    ._4b(quad_or_1__3y), ._4_y(Out[3]));
  Quad_AND_Gate quad_and_1 (
    ._1a(quad_xor_1__1_y), ._1b(C_in), ._1y(quad_and_1__1y), ._2y(quad_and_1__2y), ._2a(In_2[0]),
    ._2b(In_1[0]), ._3a(quad_xor_1__3_y), ._3b(quad_or_1__1y), ._3y(quad_and_1__3y), ._4y(quad_and_1__4y),
    ._4a(In_1[1]), ._4b(In_2[1]));  // open: Gnd, Vcc
  Quad_AND_Gate quad_and_2 (
    ._1a(quad_xor_2__1_y), ._1b(quad_or_1__2y), ._1y(quad_and_2__1y), ._2y(quad_and_2__2y), ._2a(In_2[2]),
    ._2b(In_1[2]), ._3a(quad_xor_2__3_y), ._3b(quad_or_1__3y), ._3y(quad_and_2__3y), ._4y(quad_and_2__4y),
    ._4a(In_2[3]), ._4b(In_1[3]));  // open: Gnd, Vcc
  Quad_OR_Gate quad_or_1 (
    ._1a(quad_and_1__1y), ._1b(quad_and_1__2y), ._1y(quad_or_1__1y), ._2a(quad_and_1__3y),
    ._2b(quad_and_1__4y), ._2y(quad_or_1__2y), ._3a(quad_and_2__1y), ._3b(quad_and_2__2y),
    ._3y(quad_or_1__3y), ._4a(quad_and_2__3y), ._4b(quad_and_2__4y), ._4y(C_out));
endmodule
