// Logisim project version-CH.circ as structural Verilog
module main (
  input  Read_Select,
  input  Read_From_Ram
);

  wire clock_1_out, control_1_p2, control_1_p3, control_1_p4, control_1_p5, control_1_p6, control_1_p7,
       control_1_p8, control_1_p9, control_1_p10, control_1_p11, control_1_p12, control_1_p14, control_1_p15,
       control_1_p16, control_1_p17, control_1_p18, control_1_p19, control_1_p20, control_1_p21,
       control_1_p22, control_1_p23, control_1_p24, control_1_p25, control_1_p26, control_1_p27,
       control_1_p28, control_1_p29, control_1_p30, control_1_p31, control_1_p32, input_1_ninterrupt,
       Input_Button_out, multiplexer_1_out, RESET_BUTTON_out;
  wire [7:0] A_p6, A_p7, B_p6, C_p1, control_1_p13, D_p1, ram_1_out_1, Read_1_Bus_out_9, Read_2_Bus_out_9,
       undriven;
  wire [15:0] pc_1_pc_value;
  wire [23:0] control_1_p1;

  Button RESET_BUTTON (.out(RESET_BUTTON_out));
  PC pc_1 (
    .write_byte(Read_1_Bus_out_9), .Reset_PC(RESET_BUTTON_out), .nLoad_MSB(control_1_p22),
    .nLoad_LSB(control_1_p23), .nInterrupt(input_1_ninterrupt), .Load_Saved_PC(control_1_p24),
    .Clock(clock_1_out), .PC_value(pc_1_pc_value));
  Button Input_Button (.out(Input_Button_out));
  // Control control_1: pin names not known; wires that end beside it: control_1_p1, control_1_p2, control_1_p3, control_1_p4, control_1_p5, control_1_p6, control_1_p7, control_1_p8, control_1_p9, control_1_p10, control_1_p11, control_1_p12, control_1_p13, control_1_p14, control_1_p15, control_1_p16, control_1_p17, control_1_p18, control_1_p19, control_1_p20, control_1_p21, control_1_p22, control_1_p23, control_1_p24, control_1_p25, control_1_p26, control_1_p27, control_1_p28, control_1_p29, control_1_p30, control_1_p31, control_1_p32
  ROM rom_1 (.PC_Address(pc_1_pc_value), .Instruction(control_1_p1));
  Clock clock_1 (.out(clock_1_out));
  Input input_1 (
    .Input(Input_Button_out), .Clear_Reg(control_1_p32), .Clock(clock_1_out), .nInterrupt(input_1_ninterrupt));  // open: Reg
  // registers A: pin names not known; wires that end beside it: control_1_p12, control_1_p4, control_1_p5, clock_1_out, control_1_p12, A_p6, A_p7
  // registers B: pin names not known; wires that end beside it: control_1_p12, control_1_p6, control_1_p7, clock_1_out, A_p6, B_p6
  _8bit_3_input_multiplexer Write_Bus (
    .Input_1(ram_1_out_1), .Input_2(undriven), .Input_3(Read_1_Bus_out_9), .Control_1(control_1_p20),
    .Control_2(control_1_p21), .out_6(A_p6));
  RAM ram_1 (
    .W_TO(control_1_p26), .R_FROM(control_1_p25), .R_SELECT(control_1_p27), .Addr(Read_2_Bus_out_9),
    .Data(Read_1_Bus_out_9), .CLK(clock_1_out), .OUT_1(ram_1_out_1));  // open: OUT_2
  _8bit_5_input_multiplexer Read_1_Bus (
    .Input_1(D_p1), .Input_2(C_p1), .Input_3(A_p7), .Input_4(B_p6), .Input_5(control_1_p13),
    .Control_1(control_1_p17), .Control_2(control_1_p18), .Control_3(control_1_p19), .out_9(Read_1_Bus_out_9));
  _8bit_5_input_multiplexer Read_2_Bus (
    .Input_1(D_p1), .Input_2(C_p1), .Input_3(A_p7), .Input_4(B_p6), .Input_5(control_1_p13),
    .Control_1(control_1_p14), .Control_2(control_1_p15), .Control_3(control_1_p16), .out_9(Read_2_Bus_out_9));
  // registers C: pin names not known; wires that end beside it: C_p1, A_p6, clock_1_out, control_1_p9, control_1_p8, control_1_p12
  // registers D: pin names not known; wires that end beside it: D_p1, A_p6, control_1_p12, clock_1_out, control_1_p11, control_1_p10, control_1_p12
  Multiplexer #(.enable("false")) multiplexer_1 (
    .in0(1'b1), .in1(Read_Select), .out(multiplexer_1_out), .sel(Read_From_Ram));
  _8bit_register u_8bit_register_1 (
    .M(multiplexer_1_out), .N(multiplexer_1_out));  // open: input, clock, CLR, output, G2, G1

  // Notes on the sheet:
  //   Constant
endmodule

module main_v2 (
  output [13:0] OCL_Value
);

  wire alu_v2_1_nequal_zero_2, clock_1_out, control_1_addition_n_logical____not, control_1_and_nor,
       control_1_clear_registers, control_1_ew1, control_1_ew2, control_1_ew3, control_1_ew4,
       control_1_load_saved_pc, control_1_logical_nnot, control_1_nequal_zero_2, control_1_nload_lsb,
       control_1_nload_msb, control_1_ocl_enable_reg, control_1_out_28, control_1_ram_r_from,
       control_1_ram_w_to, control_1_read_mux_1_1, control_1_read_mux_1_2, control_1_read_mux_1_3,
       control_1_read_mux_2_1, control_1_read_mux_2_2, control_1_read_mux_2_3,
       control_1_regular_n_logical_comparison____shift, control_1_shift____logical_control1,
       control_1_shift____logical_control2, control_1_subtract_nadd, control_1_write_mux_1,
       control_1_write_mux_2, Input_2_ninterrupt, INPUT_out, RESET_out;
  wire [7:0] A_read, alu_v2_1_output, B_read, C_read, control_1_const_out, control_1_const_out_2, D_read,
       ram_1_out_1, Read_1___Mux_out_9, Read__2_Mux_out_10, Write___Mux_out_6;
  wire [15:0] pc_1_pc_value;
  wire [23:0] rom_1_instruction;

  Button RESET (.out(RESET_out));
  Button INPUT (.out(INPUT_out));
  Clock clock_1 (.out(clock_1_out));
  Input Input_2 (
    .Input(INPUT_out), .Clear_Reg(control_1_load_saved_pc), .Clock(clock_1_out),
    .nInterrupt(Input_2_ninterrupt));  // open: Reg
  ROM rom_1 (.PC_Address(pc_1_pc_value), .Instruction(rom_1_instruction));
  PC pc_1 (
    .write_byte(Read_1___Mux_out_9), .Reset_PC(RESET_out), .nLoad_MSB(control_1_nload_msb),
    .nLoad_LSB(control_1_nload_lsb), .nInterrupt(Input_2_ninterrupt),
    .Load_Saved_PC(control_1_load_saved_pc), .Clock(clock_1_out), .PC_value(pc_1_pc_value));
  Control control_1 (
    .Instruction_Input(rom_1_instruction), .nequal_zero(alu_v2_1_nequal_zero_2),
    .RAM_R_From(control_1_ram_r_from), .RAM_W_To(control_1_ram_w_to), .EW1(control_1_ew1),
    .EW2(control_1_ew2), .EW3(control_1_ew3), .EW4(control_1_ew4),
    .Clear_registers(control_1_clear_registers), .Const_Out(control_1_const_out),
    .Const_Out_2(control_1_const_out_2), .Read_Mux_1_1(control_1_read_mux_1_1),
    .Read_Mux_1_2(control_1_read_mux_1_2), .Read_Mux_1_3(control_1_read_mux_1_3),
    .Read_Mux_2_1(control_1_read_mux_2_1), .Read_Mux_2_2(control_1_read_mux_2_2),
    .Read_Mux_2_3(control_1_read_mux_2_3), .Write_Mux_1(control_1_write_mux_1),
    .Write_Mux_2(control_1_write_mux_2), .nLoad_MSB(control_1_nload_msb), .nLoad_LSB(control_1_nload_lsb),
    .Load_Saved_PC(control_1_load_saved_pc), .nequal_zero_2(control_1_nequal_zero_2),
    .subtract_nadd(control_1_subtract_nadd), .And_nOr(control_1_and_nor),
    .addition_n_logical____not(control_1_addition_n_logical____not),
    .regular_n_logical_comparison____shift(control_1_regular_n_logical_comparison____shift),
    .out_28(control_1_out_28), .logical_nnot(control_1_logical_nnot),
    .shift____logical_control1(control_1_shift____logical_control1),
    .shift____logical_control2(control_1_shift____logical_control2), .OCL_Enable_Reg(control_1_ocl_enable_reg));
  registers A (.Read(A_read), .Write(Write___Mux_out_6), .Clock(clock_1_out), .EW(control_1_ew1));
  registers B (.Read(B_read), .Write(Write___Mux_out_6), .Clock(clock_1_out), .EW(control_1_ew2));
  RAM ram_1 (
    .W_TO(control_1_ram_w_to), .R_FROM(control_1_ram_r_from), .R_SELECT(1'b1), .Addr(Read_1___Mux_out_9),
    .Data(Read__2_Mux_out_10), .CLK(clock_1_out), .OUT_1(ram_1_out_1));  // open: OUT_2
  _8bit_3_input_multiplexer Write___Mux (
    .Input_1(ram_1_out_1), .Input_2(alu_v2_1_output), .Input_3(Read_1___Mux_out_9),
    .Control_1(control_1_write_mux_1), .Control_2(control_1_write_mux_2), .out_6(Write___Mux_out_6));
  _8bit_5_input_multiplexer Read_1___Mux (
    .Input_1(D_read), .Input_2(C_read), .Input_3(B_read), .Input_4(A_read), .Input_5(control_1_const_out),
    .Control_1(control_1_read_mux_1_1), .Control_2(control_1_read_mux_1_2),
    .Control_3(control_1_read_mux_1_3), .out_9(Read_1___Mux_out_9));
  _8bit_6_input_multiplexer Read__2_Mux (
    .Input_1(D_read), .Input_2(C_read), .Input_3(B_read), .Input_4(A_read), .Input_5(control_1_const_out),
    .Input_6(control_1_const_out_2), .Control_1(control_1_read_mux_2_1), .Control_2(control_1_read_mux_2_2),
    .Control_3(control_1_read_mux_2_3), .out_10(Read__2_Mux_out_10));
  registers D (.Read(D_read), .Write(Write___Mux_out_6), .Clock(clock_1_out), .EW(control_1_ew4));
  registers C (.Read(C_read), .Write(Write___Mux_out_6), .Clock(clock_1_out), .EW(control_1_ew3));
  ALU_v2 alu_v2_1 (
    .Input_1(Read_1___Mux_out_9), .Input_2(Read__2_Mux_out_10), .nEqual_Zero(control_1_nequal_zero_2),
    .Subtract_nAdd(control_1_subtract_nadd), .And___Or(control_1_and_nor), .in_6(control_1_out_28),
    .addition_n_logical____not(control_1_addition_n_logical____not), .logical___not(control_1_logical_nnot),
    .regular_n_logical_comparison____shift(control_1_regular_n_logical_comparison____shift),
    .shift____logical_control1(control_1_shift____logical_control1),
    .shift____logical_control2(control_1_shift____logical_control2), .Output(alu_v2_1_output),
    .nEqual_Zero_2(alu_v2_1_nequal_zero_2));
  Clock_Reg clock_reg_1 (
    .Reset(RESET_out), .Clock(clock_1_out), .OCL_Enable(control_1_ocl_enable_reg), .MSB(Read__2_Mux_out_10),
    .LSB(Read_1___Mux_out_9), .out_6(OCL_Value));
endmodule

// Reg
module registers (
  input  Clock,
  input  [7:0] Write,
  input  EW,
  output [7:0] Read
);

  _8bit_register u_8bit_register_1 (
    .M(1'b0), .N(1'b0), .\input (Write), .clock(Clock), .CLR(1'b0), .\output (Read), .G2(EW), .G1(EW));
endmodule

module ALU (
  input  [7:0] Input_1,
  input  [7:0] Input_2,
  input  nEqual_Zero,
  input  Subtract_nAdd,
  input  Or_nAnd,
  input  in_6,
  input  shift_nother,
  input  addition_nother,
  input  not_nlogical,
  input  regular_nlogical_comparison,
  input  in_11,
  output [7:0] Output,
  output Carry,
  output Equal
);

  wire hex_inverter_1__6_prime, quad_or_1__1y, quad_or_1__2y, quad_or_1__3y, quad_or_1__4y, quad_or_2__1y,
       quad_or_2__2y;
  wire [7:0] adder_2_output, adder_output, And_out, demux_2_output_1, demux_2_output_2, demux_output_1,
       demux_output_2, mux_output, n8bit_2_input_multiplexer_1_output, n8bit_2_input_multiplexer_2_output,
       n8bit_2_output_demuliplexer_1_output_1, n8bit_2_output_demuliplexer_1_output_2,
       n8bit_3_input_multiplexer_1_out_6, n8bit_and_out, n8bit_or_out, or_out, xor_write;

  Hex_Inverter hex_inverter_1 (
    ._6(in_6), ._6_prime(hex_inverter_1__6_prime));  // open: _1, _1_prime, _2, _2_prime, _3, _3_prime, _4, _4_prime, _5, _5_prime
  _8bit_AND_Gate And (.In_2(Input_2), .In_1({8{nEqual_Zero}}), .Out(And_out));
  _8bit_2_output_demuliplexer demux (
    .Output_1(demux_output_1), .Output_2(demux_output_2), .Input(And_out), .Control(Or_nAnd));
  _8bit_2_output_demuliplexer u_8bit_2_output_demuliplexer_1 (
    .Output_1(n8bit_2_output_demuliplexer_1_output_1), .Output_2(n8bit_2_output_demuliplexer_1_output_2),
    .Input(Input_1), .Control(in_6));
  _8bit_XOR \xor  (.Read_1(And_out), .Read_2({8{1'b1}}), .Write(xor_write));
  _8bit_AND_Gate u_8bit_and (.In_2(demux_output_2), .In_1(demux_2_output_2), .Out(n8bit_and_out));
  _8bit_OR_Gate u_8bit_or (.In_2(demux_output_1), .In_1(demux_2_output_1), .Out(n8bit_or_out));
  _8bit_adder adder (.Input1(xor_write), .Input_2(8'h1), .Output(adder_output));  // open: Carry
  _8bit_2_output_demuliplexer demux_2 (
    .Output_1(demux_2_output_1), .Output_2(demux_2_output_2), .Input(Input_1), .Control(Or_nAnd));
  _8bit_2_input_multiplexer mux (
    .Input_1(adder_output), .Input_2(And_out), .Output(mux_output), .Control(Subtract_nAdd));
  _8bit_OR_Gate \or  (.In_2(n8bit_and_out), .In_1(n8bit_or_out), .Out(or_out));
  _8bit_2_input_multiplexer u_8bit_2_input_multiplexer_1 (
    .Input_1({n8bit_2_output_demuliplexer_1_output_2[6:0], 1'b0}),
    .Input_2({1'b0, n8bit_2_output_demuliplexer_1_output_1[7:1]}),
    .Output(n8bit_2_input_multiplexer_1_output), .Control(hex_inverter_1__6_prime));
  _8bit_adder adder_2 (.Input1(Input_1), .Input_2(mux_output), .Output(adder_2_output), .Carry(Carry));
  _8bit_3_input_multiplexer u_8bit_3_input_multiplexer_1 (
    .Input_1(xor_write), .Input_2(or_out), .Input_3(adder_2_output), .Control_1(addition_nother),
    .Control_2(not_nlogical), .out_6(n8bit_3_input_multiplexer_1_out_6));
  _8bit_2_input_multiplexer u_8bit_2_input_multiplexer_2 (
    .Input_1(n8bit_2_input_multiplexer_1_output), .Input_2(n8bit_3_input_multiplexer_1_out_6),
    .Output(n8bit_2_input_multiplexer_2_output), .Control(shift_nother));
  Quad_OR_Gate quad_or_1 (
    ._1a(n8bit_3_input_multiplexer_1_out_6[0]), ._1b(n8bit_3_input_multiplexer_1_out_6[1]),
    ._1y(quad_or_1__1y), ._2a(n8bit_3_input_multiplexer_1_out_6[2]),
    ._2b(n8bit_3_input_multiplexer_1_out_6[3]), ._2y(quad_or_1__2y),
    ._3a(n8bit_3_input_multiplexer_1_out_6[4]), ._3b(n8bit_3_input_multiplexer_1_out_6[5]),
    ._3y(quad_or_1__3y), ._4a(n8bit_3_input_multiplexer_1_out_6[6]),
    ._4b(n8bit_3_input_multiplexer_1_out_6[7]), ._4y(quad_or_1__4y));
  _8bit_3_input_multiplexer u_8bit_3_input_multiplexer_2 (
    .Input_1({{7{1'b0}}, Carry}), .Input_2({{7{1'b0}}, Equal}), .Input_3(n8bit_2_input_multiplexer_2_output),
    .Control_1(regular_nlogical_comparison), .Control_2(in_11), .out_6(Output));
  Quad_OR_Gate quad_or_2 (
    ._1a(quad_or_1__3y), ._1b(quad_or_1__4y), ._1y(quad_or_2__1y), ._2a(quad_or_1__1y), ._2b(quad_or_1__2y),
    ._2y(quad_or_2__2y), ._4a(quad_or_2__1y), ._4b(quad_or_2__2y), ._4y(Equal));  // open: _3a, _3b, _3y
endmodule

// ALU
module ALU_v2 (
  input  [7:0] Input_1,
  input  [7:0] Input_2,
  input  nEqual_Zero,
  input  Subtract_nAdd,
  input  And___Or,
  input  in_6,
  input  addition_n_logical____not,
  input  logical___not,
  input  regular_n_logical_comparison____shift,
  input  shift____logical_control1,
  input  shift____logical_control2,
  output [7:0] Output,
  output nEqual_Zero_2
);

  wire adder_2_carry, adder_carry, quad_or_1__1y, quad_or_1__2y, quad_or_1__3y, quad_or_1__4y, quad_or_2__1y,
       quad_or_2__2y;
  wire [0:0] quad_and_1__4y, quad_or_2__3y;
  wire [7:0] adder_2_output, adder_output, And_out, mux_output, n8bit_2_input_multiplexer_1_output,
       n8bit_2_input_multiplexer_2_output, n8bit_3_input_multiplexer_1_out_6, n8bit_and_out, n8bit_or_out,
       xor_write;

  _8bit_AND_Gate And (.In_2(Input_2), .In_1({8{nEqual_Zero}}), .Out(And_out));
  _8bit_XOR \xor  (.Read_1(And_out), .Read_2({8{1'b1}}), .Write(xor_write));
  _8bit_AND_Gate u_8bit_and (.In_2(Input_1), .In_1(And_out), .Out(n8bit_and_out));
  _8bit_OR_Gate u_8bit_or (.In_2(Input_1), .In_1(And_out), .Out(n8bit_or_out));
  _8bit_adder adder (.Input1(xor_write), .Input_2(8'h1), .Output(adder_output), .Carry(adder_carry));
  _8bit_2_input_multiplexer mux (
    .Input_1(adder_output), .Input_2(And_out), .Output(mux_output), .Control(Subtract_nAdd));
  _8bit_2_input_multiplexer u_8bit_2_input_multiplexer_1 (
    .Input_1(n8bit_and_out), .Input_2(n8bit_or_out), .Output(n8bit_2_input_multiplexer_1_output),
    .Control(And___Or));
  _8bit_2_input_multiplexer u_8bit_2_input_multiplexer_2 (
    .Input_1({Input_1[6:0], 1'b0}), .Input_2({1'b0, Input_1[7:1]}),
    .Output(n8bit_2_input_multiplexer_2_output), .Control(in_6));
  _8bit_adder adder_2 (.Input1(Input_1), .Input_2(mux_output), .Output(adder_2_output), .Carry(adder_2_carry));
  _8bit_3_input_multiplexer u_8bit_3_input_multiplexer_1 (
    .Input_1(xor_write), .Input_2(n8bit_2_input_multiplexer_1_output), .Input_3(adder_2_output),
    .Control_1(addition_n_logical____not), .Control_2(logical___not),
    .out_6(n8bit_3_input_multiplexer_1_out_6));
  Quad_OR_Gate quad_or_1 (
    ._1a(n8bit_3_input_multiplexer_1_out_6[0]), ._1b(n8bit_3_input_multiplexer_1_out_6[1]),
    ._1y(quad_or_1__1y), ._2a(n8bit_3_input_multiplexer_1_out_6[2]),
    ._2b(n8bit_3_input_multiplexer_1_out_6[3]), ._2y(quad_or_1__2y),
    ._3a(n8bit_3_input_multiplexer_1_out_6[4]), ._3b(n8bit_3_input_multiplexer_1_out_6[5]),
    ._3y(quad_or_1__3y), ._4a(n8bit_3_input_multiplexer_1_out_6[6]),
    ._4b(n8bit_3_input_multiplexer_1_out_6[7]), ._4y(quad_or_1__4y));
  _8bit_5_input_multiplexer u_8bit_5_input_multiplexer_1 (
    .Input_1({{7{1'b0}}, quad_or_2__3y[0]}), .Input_2({{7{1'b0}}, nEqual_Zero_2}),
    .Input_3({{7{1'b0}}, quad_and_1__4y[0]}), .Input_4(n8bit_2_input_multiplexer_2_output),
    .Input_5(n8bit_3_input_multiplexer_1_out_6), .Control_1(regular_n_logical_comparison____shift),
    .Control_2(shift____logical_control1), .Control_3(shift____logical_control2), .out_9(Output));
  Quad_AND_Gate quad_and_1 (
    ._4a(quad_or_2__3y[0]), ._4b(nEqual_Zero_2), ._4y(quad_and_1__4y[0]));  // open: _1a, _1b, _1y, _2a, _2b, _2y, _3a, _3b, _3y
  Quad_OR_Gate quad_or_2 (
    ._1a(quad_or_1__3y), ._1b(quad_or_1__4y), ._1y(quad_or_2__1y), ._2a(quad_or_1__1y), ._2b(quad_or_1__2y),
    ._2y(quad_or_2__2y), ._3a(adder_carry), ._3b(adder_2_carry), ._3y(quad_or_2__3y[0]), ._4a(quad_or_2__1y),
    ._4b(quad_or_2__2y), ._4y(nEqual_Zero_2));
endmodule

module Input (
  input  Input,
  input  Clear_Reg,
  input  Clock,
  output [7:0] Reg,
  output nInterrupt
);

  wire clock_1_out, hex_inverter_1__4_prime, hex_inverter_1__5_prime, hex_inverter_1__6_prime,
       n4bit_register_1__1d, n4bit_register_1__2d, quad_and_1__1y, quad_and_1__2y, quad_and_1__4y;

  Clock clock_1 (.out(clock_1_out));
  Quad_AND_Gate quad_and_1 (
    ._1a(Input), ._1b(quad_and_1__4y), ._1y(quad_and_1__1y), ._2a(quad_and_1__1y),
    ._2b(hex_inverter_1__6_prime), ._2y(quad_and_1__2y), ._4a(hex_inverter_1__4_prime),
    ._4b(n4bit_register_1__1d), ._4y(quad_and_1__4y));  // open: _3a, _3b, _3y
  Hex_Inverter hex_inverter_1 (
    ._1(quad_and_1__2y), ._1_prime(nInterrupt), ._4(n4bit_register_1__2d),
    ._4_prime(hex_inverter_1__4_prime), ._5(quad_and_1__1y), ._5_prime(hex_inverter_1__5_prime), ._6(Reg[0]),
    ._6_prime(hex_inverter_1__6_prime));  // open: _2, _2_prime, _3, _3_prime
  _4bit_register u_4bit_register_1 (
    .M(1'b0), .N(1'b0), ._1Q(Input), ._2Q(n4bit_register_1__1d), .CLK(clock_1_out), .CLR(1'b0),
    ._1D(n4bit_register_1__1d), ._2D(n4bit_register_1__2d), .G2(1'b0), .G1(1'b0));  // open: _3Q, _4Q, _3D, _4D
  _4bit_register u_4bit_register_2 (
    .M(1'b0), .N(1'b0), ._1Q(Input), .CLK(clock_1_out), .CLR(Clear_Reg), ._1D(Reg[0]),
    .G2(hex_inverter_1__5_prime), .G1(hex_inverter_1__5_prime));  // open: _2Q, _3Q, _4Q, _2D, _3D, _4D

  assign Reg[7:1] = {7{1'b0}};
endmodule

module Control (
  input  [23:0] Instruction_Input,
  input  nequal_zero,
  output RAM_R_From,
  output RAM_W_To,
  output EW1,
  output EW2,
  output EW3,
  output EW4,
  output Clear_registers,
  output [7:0] Const_Out,
  output [7:0] Const_Out_2,
  output Read_Mux_1_1,
  output Read_Mux_1_2,
  output Read_Mux_1_3,
  output Read_Mux_2_1,
  output Read_Mux_2_2,
  output Read_Mux_2_3,
  output Write_Mux_1,
  output Write_Mux_2,
  output nLoad_MSB,
  output nLoad_LSB,
  output Load_Saved_PC,
  output nequal_zero_2,
  output subtract_nadd,
  output And_nOr,
  output addition_n_logical____not,
  output regular_n_logical_comparison____shift,
  output out_28,
  output logical_nnot,
  output shift____logical_control1,
  output shift____logical_control2,
  output OCL_Enable_Reg
);

  wire control_addition_1_read_mux_1_1, control_addition_1_read_mux_1_2, control_addition_1_read_mux_1_3,
       control_addition_1_read_mux_2_1, control_addition_1_read_mux_2_2, control_addition_1_read_mux_2_3,
       control_addition_1_shift__logical_control1, control_addition_1_shift__logical_control2,
       control_addition_1_subtract_nadd, control_addition_1_write_byte, control_addition_1_write_mux_2,
       control_load_1_mux_1_1, control_load_1_mux_1_2, control_load_1_mux_1_3, control_load_1_write_byte,
       control_logical_1_read_mux_1_1, control_logical_1_read_mux_1_2, control_logical_1_read_mux_1_3,
       control_logical_1_read_mux_2_1, control_logical_1_read_mux_2_2, control_logical_1_read_mux_2_3,
       control_logical_1_write_byte, control_logical_1_write_mux_2,
       control_logical_comparison_1_read_mux_1_1, control_logical_comparison_1_read_mux_1_2,
       control_logical_comparison_1_read_mux_1_3, control_logical_comparison_1_read_mux_2_1,
       control_logical_comparison_1_read_mux_2_2, control_logical_comparison_1_read_mux_2_3,
       control_logical_comparison_1_shift____logical_control1__equals,
       control_logical_comparison_1_shift____logical_control2__1_2,
       control_logical_comparison_1_subtract_nadd, control_logical_comparison_1_write_byte,
       control_logical_comparison_1_write_mux_2, control_misc_1_read_mux_1_1, control_misc_1_read_mux_1_2,
       control_misc_1_read_mux_1_3, control_misc_1_read_mux_2_1, control_misc_1_read_mux_2_2,
       control_misc_1_read_mux_2_3, control_misc_1_write_byte, hex_inverter_1__1_prime,
       hex_inverter_1__2_prime, hex_inverter_1__3_prime, hex_inverter_1__4_prime, hex_inverter_1__5_prime,
       hex_inverter_1__6_prime, quad_and_1__1y, quad_and_1__3y, quad_and_2__2y, quad_and_3__3y,
       quad_and_4__1y, quad_and_4__2y, quad_and_4__3y, quad_and_4__4y, quad_and_5__1y, quad_and_5__2y,
       quad_and_5__3y, quad_and_5__4y, quad_and_6__1y, quad_and_6__2y, quad_and_6__3y, quad_or_1__1y,
       quad_or_1__2y, quad_or_1__4y, quad_or_2__1y, quad_or_2__2y, quad_or_2__3y, quad_or_3__1y,
       quad_or_3__2y, quad_or_3__3y, quad_or_4__1y, quad_or_4__3y, quad_or_4__4y, quad_or_5__1y,
       quad_or_5__2y, quad_or_5__4y, quad_or_6__1y, quad_or_8__1y, quad_or_8__2y, quad_or_8__3y;
  wire [6:0] quad_and_2__1y;
  wire [7:7] control_misc_1_write_byte_2, quad_or_3__4y;

  Hex_Inverter hex_inverter_1 (
    ._1(Instruction_Input[21]), ._1_prime(hex_inverter_1__1_prime), ._2(Instruction_Input[22]),
    ._2_prime(hex_inverter_1__2_prime), ._3(Instruction_Input[23]), ._3_prime(hex_inverter_1__3_prime),
    ._4(Instruction_Input[20]), ._4_prime(hex_inverter_1__4_prime), ._5(Instruction_Input[19]),
    ._5_prime(hex_inverter_1__5_prime), ._6(Instruction_Input[18]), ._6_prime(hex_inverter_1__6_prime));
  Quad_AND_Gate quad_and_1 (
    ._1a(Instruction_Input[19]), ._1b(hex_inverter_1__4_prime), ._1y(quad_and_1__1y), ._2a(quad_and_1__1y),
    ._2b(hex_inverter_1__6_prime), ._2y(quad_and_2__1y[2]), ._3a(hex_inverter_1__5_prime),
    ._3b(Instruction_Input[20]), ._3y(quad_and_1__3y), ._4a(quad_and_1__3y), ._4b(hex_inverter_1__6_prime),
    ._4y(quad_and_2__1y[4]));
  Quad_AND_Gate quad_and_2 (
    ._1a(hex_inverter_1__6_prime), ._1b(quad_and_2__2y), ._1y(quad_and_2__1y[0]),
    ._2a(hex_inverter_1__5_prime), ._2b(hex_inverter_1__4_prime), ._2y(quad_and_2__2y), ._3a(quad_and_2__2y),
    ._3b(Instruction_Input[18]), ._3y(quad_and_2__1y[1]), ._4a(Instruction_Input[18]), ._4b(quad_and_1__1y),
    ._4y(quad_and_2__1y[3]));
  Quad_AND_Gate quad_and_3 (
    ._1a(Instruction_Input[18]), ._1b(quad_and_1__3y), ._1y(quad_and_2__1y[5]),
    ._3a(hex_inverter_1__6_prime), ._3b(Instruction_Input[20]), ._3y(quad_and_3__3y), ._4a(quad_and_3__3y),
    ._4b(Instruction_Input[19]), ._4y(quad_and_2__1y[6]));  // open: _2a, _2b, _2y
  Quad_AND_Gate quad_and_4 (
    ._1a(hex_inverter_1__1_prime), ._1b(quad_and_4__2y), ._1y(quad_and_4__1y), ._2a(hex_inverter_1__2_prime),
    ._2b(hex_inverter_1__3_prime), ._2y(quad_and_4__2y), ._3a(hex_inverter_1__1_prime),
    ._3b(Instruction_Input[22]), ._3y(quad_and_4__3y), ._4a(Instruction_Input[21]), ._4b(quad_and_4__2y),
    ._4y(quad_and_4__4y));
  Quad_AND_Gate quad_and_5 (
    ._1a(hex_inverter_1__3_prime), ._1b(Instruction_Input[22]), ._1y(quad_and_5__1y), ._2a(quad_and_5__1y),
    ._2b(Instruction_Input[21]), ._2y(quad_and_5__2y), ._3a(hex_inverter_1__3_prime), ._3b(quad_and_4__3y),
    ._3y(quad_and_5__3y), ._4a(quad_and_6__1y), ._4b(Instruction_Input[21]), ._4y(quad_and_5__4y));
  Quad_AND_Gate quad_and_6 (
    ._1a(hex_inverter_1__2_prime), ._1b(Instruction_Input[23]), ._1y(quad_and_6__1y), ._2a(quad_and_6__1y),
    ._2b(hex_inverter_1__1_prime), ._2y(quad_and_6__2y), ._3a(quad_and_4__3y), ._3b(Instruction_Input[23]),
    ._3y(quad_and_6__3y));  // open: _4a, _4b, _4y
  Control_Load control_load_1 (
    .Instruction_enable(quad_and_4__1y), .Sub_instruction(quad_and_2__1y),
    .Read_From_1({Instruction_Input[11], Instruction_Input[12], Instruction_Input[13]}),
    .Clear(Clear_registers), .Write_Byte(control_load_1_write_byte), .Mux_1_1(control_load_1_mux_1_1),
    .Mux_1_2(control_load_1_mux_1_2), .Mux_1_3(control_load_1_mux_1_3), .Mux_3_1(Write_Mux_1),
    .Ram_EW_TO(RAM_W_To), .Ram_ER_FROM(RAM_R_From));
  Control_Addition control_addition_1 (
    .Instruction_enable(quad_and_4__4y), .Sub_instruction(quad_and_2__1y),
    .Read_From_1({Instruction_Input[11], Instruction_Input[12], Instruction_Input[13]}),
    .Read_From_2({Instruction_Input[8], Instruction_Input[9], Instruction_Input[10]}),
    .Write_Byte(control_addition_1_write_byte), .Write_Mux_2(control_addition_1_write_mux_2),
    .Read_Mux_1_1(control_addition_1_read_mux_1_1), .Read_Mux_1_2(control_addition_1_read_mux_1_2),
    .Read_Mux_1_3(control_addition_1_read_mux_1_3), .Read_Mux_2_1(control_addition_1_read_mux_2_1),
    .Read_Mux_2_2(control_addition_1_read_mux_2_2), .Read_Mux_2_3(control_addition_1_read_mux_2_3),
    .Subtract_nAdd(control_addition_1_subtract_nadd), .out_14(out_28),
    .shift__logical_control1(control_addition_1_shift__logical_control1),
    .shift__logical_control2(control_addition_1_shift__logical_control2));
  Control_Logical control_logical_1 (
    .Instruction_enable(quad_and_5__3y), .Sub_instruction(quad_and_2__1y),
    .Read_From_1({Instruction_Input[11], Instruction_Input[12], Instruction_Input[13]}),
    .Read_From_2({Instruction_Input[8], Instruction_Input[9], Instruction_Input[10]}),
    .Write_Byte(control_logical_1_write_byte), .And_nOr(And_nOr), .Logical_nnot(logical_nnot),
    .regular_n_logical_comparison____shift(regular_n_logical_comparison____shift),
    .Write_Mux_2(control_logical_1_write_mux_2), .Read_Mux_1_1(control_logical_1_read_mux_1_1),
    .Read_Mux_1_2(control_logical_1_read_mux_1_2), .Read_Mux_1_3(control_logical_1_read_mux_1_3),
    .Read_Mux_2_1(control_logical_1_read_mux_2_1), .Read_Mux_2_2(control_logical_1_read_mux_2_2),
    .Read_Mux_2_3(control_logical_1_read_mux_2_3));
  Control_Logical_Comparison control_logical_comparison_1 (
    .Instruction_enable(quad_and_5__2y), .Sub_instruction(quad_and_2__1y),
    .Read_From_1({Instruction_Input[11], Instruction_Input[12], Instruction_Input[13]}),
    .Read_From_2({Instruction_Input[8], Instruction_Input[9], Instruction_Input[10]}),
    .Write_Byte(control_logical_comparison_1_write_byte),
    .shift____logical_control1__equals(control_logical_comparison_1_shift____logical_control1__equals),
    .shift____logical_control2__1_2(control_logical_comparison_1_shift____logical_control2__1_2),
    .Subtract_nAdd(control_logical_comparison_1_subtract_nadd),
    .addition_n_logical____not(addition_n_logical____not),
    .Write_Mux_2(control_logical_comparison_1_write_mux_2),
    .Read_Mux_1_1(control_logical_comparison_1_read_mux_1_1),
    .Read_Mux_1_2(control_logical_comparison_1_read_mux_1_2),
    .Read_Mux_1_3(control_logical_comparison_1_read_mux_1_3),
    .Read_Mux_2_1(control_logical_comparison_1_read_mux_2_1),
    .Read_Mux_2_2(control_logical_comparison_1_read_mux_2_2),
    .Read_Mux_2_3(control_logical_comparison_1_read_mux_2_3));
  Control_Misc control_misc_1 (
    .Instruction_enable(quad_and_6__2y), .Sub_instruction(quad_and_2__1y),
    .Read_From_1({Instruction_Input[11], Instruction_Input[12], Instruction_Input[13]}),
    .nequal_zero(nequal_zero), .nLoad_MSB(nLoad_MSB), .nLoad_LSB(nLoad_LSB), .Load_Saved_PC(Load_Saved_PC),
    .nequal_zero_2(nequal_zero_2), .Write_Byte(control_misc_1_write_byte),
    .Write_Byte_2(control_misc_1_write_byte_2[7]), .OCL_Register_Enable(OCL_Enable_Reg),
    .Read_Mux_1_1(control_misc_1_read_mux_1_1), .Read_Mux_1_2(control_misc_1_read_mux_1_2),
    .Read_Mux_1_3(control_misc_1_read_mux_1_3), .Read_Mux_2_1(control_misc_1_read_mux_2_1),
    .Read_Mux_2_2(control_misc_1_read_mux_2_2), .Read_Mux_2_3(control_misc_1_read_mux_2_3));
  Quad_OR_Gate quad_or_1 (
    ._1a(control_load_1_mux_1_2), ._1b(control_addition_1_read_mux_1_2), ._1y(quad_or_1__1y),
    ._2a(quad_or_1__1y), ._2b(control_logical_1_read_mux_1_2), ._2y(quad_or_1__2y),
    ._3a(control_misc_1_read_mux_1_2), ._3b(quad_or_1__4y), ._3y(Read_Mux_1_2),
    ._4a(control_logical_comparison_1_read_mux_1_2), ._4b(quad_or_1__2y), ._4y(quad_or_1__4y));
  Quad_OR_Gate quad_or_2 (
    ._1a(control_addition_1_read_mux_2_1), ._1b(control_logical_1_read_mux_2_1), ._1y(quad_or_2__1y),
    ._2a(quad_or_2__1y), ._2b(control_logical_comparison_1_read_mux_2_1), ._2y(quad_or_2__2y),
    ._3a(control_logical_1_read_mux_2_2), ._3b(control_addition_1_read_mux_2_2), ._3y(quad_or_2__3y),
    ._4a(control_misc_1_read_mux_2_1), ._4b(quad_or_2__2y), ._4y(Read_Mux_2_1));
  Quad_OR_Gate quad_or_3 (
    ._1a(control_load_1_write_byte), ._1b(control_addition_1_write_byte), ._1y(quad_or_3__1y),
    ._2a(quad_or_3__1y), ._2b(control_logical_1_write_byte), ._2y(quad_or_3__2y), ._3a(quad_or_3__2y),
    ._3b(control_misc_1_write_byte), ._3y(quad_or_3__3y), ._4a(quad_or_3__3y),
    ._4b(control_logical_comparison_1_write_byte), ._4y(quad_or_3__4y[7]));
  Quad_OR_Gate quad_or_4 (
    ._1a(control_logical_comparison_1_read_mux_2_2), ._1b(control_misc_1_read_mux_2_2), ._1y(quad_or_4__1y),
    ._2a(quad_or_2__3y), ._2b(quad_or_4__1y), ._2y(Read_Mux_2_2), ._3a(control_logical_1_read_mux_2_3),
    ._3b(control_addition_1_read_mux_2_3), ._3y(quad_or_4__3y), ._4a(quad_or_4__3y),
    ._4b(control_logical_comparison_1_read_mux_2_3), ._4y(quad_or_4__4y));
  _8bit_AND_Gate u_8bit_and_1 (.In_2(Instruction_Input[7:0]), .In_1({8{quad_or_3__4y[7]}}), .Out(Const_Out));
  _8bit_AND_Gate u_8bit_and_2 (
    .In_2({Instruction_Input[11], Instruction_Input[12], Instruction_Input[13], Instruction_Input[8], Instruction_Input[9], Instruction_Input[10], 2'b00}),
    .In_1({8{control_misc_1_write_byte_2[7]}}), .Out(Const_Out_2));
  Quad_OR_Gate quad_or_5 (
    ._1a(control_load_1_mux_1_3), ._1b(control_addition_1_read_mux_1_3), ._1y(quad_or_5__1y),
    ._2a(quad_or_5__1y), ._2b(control_logical_1_read_mux_1_3), ._2y(quad_or_5__2y),
    ._3a(control_misc_1_read_mux_1_3), ._3b(quad_or_5__4y), ._3y(Read_Mux_1_3),
    ._4a(control_logical_comparison_1_read_mux_1_3), ._4b(quad_or_5__2y), ._4y(quad_or_5__4y));
  Quad_OR_Gate quad_or_6 (
    ._1a(control_logical_1_write_mux_2), ._1b(control_addition_1_write_mux_2), ._1y(quad_or_6__1y),
    ._2a(quad_or_4__4y), ._2b(control_misc_1_read_mux_2_3), ._2y(Read_Mux_2_3), ._3a(quad_or_6__1y),
    ._3b(control_logical_comparison_1_write_mux_2), ._3y(Write_Mux_2),
    ._4a(control_addition_1_subtract_nadd), ._4b(control_logical_comparison_1_subtract_nadd),
    ._4y(subtract_nadd));
  Quad_OR_Gate quad_or_7 (
    ._1a(control_logical_comparison_1_shift____logical_control1__equals),
    ._1b(control_addition_1_shift__logical_control1), ._1y(shift____logical_control1),
    ._2a(control_addition_1_shift__logical_control2),
    ._2b(control_logical_comparison_1_shift____logical_control2__1_2), ._2y(shift____logical_control2));  // open: _3a, _3b, _3y, _4a, _4b, _4y
  Quad_OR_Gate quad_or_8 (
    ._1a(control_load_1_mux_1_1), ._1b(control_addition_1_read_mux_1_1), ._1y(quad_or_8__1y),
    ._2a(quad_or_8__1y), ._2b(control_logical_1_read_mux_1_1), ._2y(quad_or_8__2y),
    ._3a(control_misc_1_read_mux_1_1), ._3b(control_logical_comparison_1_read_mux_1_1), ._3y(quad_or_8__3y),
    ._4a(quad_or_8__3y), ._4b(quad_or_8__2y), ._4y(Read_Mux_1_1));

  assign EW1 = Instruction_Input[17];
  assign EW2 = Instruction_Input[16];
  assign EW3 = Instruction_Input[15];
  assign EW4 = Instruction_Input[14];
endmodule

module ROM (
  input  [15:0] PC_Address,
  output [23:0] Instruction
);

  ROM_part #(.addrWidth(16), .dataWidth(24)) rom_1 (.addr(PC_Address), .data(Instruction), .sel(1'b1));
endmodule

module RAM (
  input  W_TO,
  input  R_FROM,
  input  R_SELECT,
  input  [7:0] Addr,
  input  [7:0] Data,
  input  CLK,
  output [7:0] OUT_1,
  output [7:0] OUT_2
);

  wire hex_inverter_1__1_prime, hex_inverter_1__2_prime, hex_inverter_1__3_prime, hex_inverter_1__4_prime,
       hex_inverter_1__5_prime, hex_inverter_1__6_prime, hex_inverter_2__1_prime, hex_inverter_2__2_prime,
       hex_inverter_2__3_prime, hex_inverter_2__4_prime, hex_inverter_2__5_prime, hex_inverter_2__6_prime,
       hex_inverter_3__1_prime, hex_inverter_3__2_prime, hex_inverter_3__3_prime, hex_inverter_3__4_prime,
       hex_inverter_3__5_prime, hex_inverter_3__6_prime, hex_inverter_4__1_prime, hex_inverter_4__2_prime,
       hex_inverter_4__3_prime, hex_inverter_4__4_prime, hex_inverter_4__5_prime, hex_inverter_4__6_prime,
       hex_inverter_5__1_prime, hex_inverter_5__2_prime, hex_inverter_5__3_prime, hex_inverter_5__4_prime,
       hex_inverter_5__5_prime, hex_inverter_5__6_prime, hex_inverter_6__1_prime, hex_inverter_6__2_prime,
       hex_inverter_6__3_prime, hex_inverter_6__4_prime, hex_inverter_6__5_prime, hex_inverter_6__6_prime,
       hex_inverter_7__1_prime, hex_inverter_7__2_prime, hex_inverter_7__3_prime, hex_inverter_7__4_prime,
       hex_inverter_7__5_prime, hex_inverter_7__6_prime, hex_inverter_8__1_prime, hex_inverter_8__2_prime,
       hex_inverter_8__3_prime, hex_inverter_8__4_prime, hex_inverter_8__5_prime, hex_inverter_8__6_prime,
       hex_inverter_9__1_prime, hex_inverter_9__2_prime, hex_inverter_9__3_prime, hex_inverter_9__4_prime,
       hex_inverter_9__5_prime, hex_inverter_9__6_prime, hex_inverter_10__1_prime, hex_inverter_10__2_prime,
       hex_inverter_10__3_prime, hex_inverter_10__4_prime, hex_inverter_10__5_prime,
       hex_inverter_10__6_prime, hex_inverter_11__1_prime, hex_inverter_11__2_prime,
       hex_inverter_11__4_prime, hex_inverter_11__5_prime, quad_and_1__1y, quad_and_1__2y, quad_and_1__3y,
       quad_and_1__4y, quad_and_2__1y, quad_and_2__2y, quad_and_2__3y, quad_and_2__4y, quad_and_3__1y,
       quad_and_3__2y, quad_and_3__3y, quad_and_3__4y, quad_and_4__1y, quad_and_4__2y, quad_and_4__3y,
       quad_and_4__4y, quad_and_5__1y, quad_and_5__2y, quad_and_5__3y, quad_and_5__4y, quad_and_6__1y,
       quad_and_6__2y, quad_and_6__3y, quad_and_6__4y, quad_and_7__1y, quad_and_7__2y, quad_and_7__3y,
       quad_and_7__4y, quad_and_8__1y, quad_and_8__2y, quad_and_8__3y, quad_and_8__4y, quad_and_9__1y,
       quad_and_9__2y, quad_and_9__3y, quad_and_9__4y, quad_and_10__1y, quad_and_10__2y, quad_and_10__3y,
       quad_and_10__4y, quad_and_11__1y, quad_and_11__2y, quad_and_11__3y, quad_and_11__4y, quad_and_12__1y,
       quad_and_12__2y, quad_and_12__3y, quad_and_12__4y, quad_and_13__1y, quad_and_13__2y, quad_and_13__3y,
       quad_and_13__4y, quad_and_14__1y, quad_and_14__2y, quad_and_14__3y, quad_and_14__4y, quad_and_15__1y,
       quad_and_15__2y, quad_and_15__3y, quad_and_15__4y, quad_and_16__1y, quad_and_16__2y, quad_and_16__3y,
       quad_and_16__4y, quad_and_17__1y, quad_and_17__3y, triple_2_channel_demux_1_ax,
       triple_2_channel_demux_1_ay, triple_2_channel_demux_1_bx, triple_2_channel_demux_1_by,
       triple_2_channel_demux_1_cx, triple_2_channel_demux_1_cy, triple_2_channel_demux_2_ax,
       triple_2_channel_demux_2_ay, triple_2_channel_demux_2_bx, triple_2_channel_demux_2_by,
       triple_2_channel_demux_2_cx, triple_2_channel_demux_2_cy, triple_2_channel_demux_3_ax,
       triple_2_channel_demux_3_ay, triple_2_channel_demux_3_bx, triple_2_channel_demux_3_by,
       triple_2_channel_demux_3_cx, triple_2_channel_demux_3_cy, triple_2_channel_demux_4_ax,
       triple_2_channel_demux_4_ay, triple_2_channel_demux_4_by, triple_2_channel_demux_4_cx,
       triple_2_channel_demux_4_cy, triple_2_channel_demux_5_ax, triple_2_channel_demux_5_ay,
       triple_2_channel_demux_5_bx, triple_2_channel_demux_5_by, triple_2_channel_demux_5_cx,
       triple_2_channel_demux_5_cy, triple_2_channel_demux_6_ax, triple_2_channel_demux_6_ay,
       triple_2_channel_demux_6_bx, triple_2_channel_demux_6_by, triple_2_channel_demux_6_cx,
       triple_2_channel_demux_6_cy, triple_2_channel_demux_7_ax, triple_2_channel_demux_7_ay,
       triple_2_channel_demux_7_bx, triple_2_channel_demux_7_by, triple_2_channel_demux_7_cx,
       triple_2_channel_demux_7_cy, triple_2_channel_demux_8_ax, triple_2_channel_demux_8_ay,
       triple_2_channel_demux_8_bx, triple_2_channel_demux_8_by, triple_2_channel_demux_8_cx,
       triple_2_channel_demux_8_cy, triple_2_channel_demux_9_ax, triple_2_channel_demux_9_ay,
       triple_2_channel_demux_9_bx, triple_2_channel_demux_9_by, triple_2_channel_demux_9_cx,
       triple_2_channel_demux_9_cy, triple_2_channel_demux_10_ax, triple_2_channel_demux_10_ay,
       triple_2_channel_demux_10_bx, triple_2_channel_demux_10_by, triple_2_channel_demux_10_cx,
       triple_2_channel_demux_10_cy, triple_2_channel_demux_11_bx, triple_2_channel_demux_11_by;
  wire [7:0] n8bit_register_1_output;

  triple_2_channel_demux triple_2_channel_demux_1 (
    .bx(triple_2_channel_demux_1_bx), .by(triple_2_channel_demux_1_by), .cy(triple_2_channel_demux_1_cy),
    .c_in(triple_2_channel_demux_2_bx), .cx(triple_2_channel_demux_1_cx), .enable(1'b1),
    .b_in(triple_2_channel_demux_2_cy), .a_in(triple_2_channel_demux_2_cx), .ax(triple_2_channel_demux_1_ax),
    .ay(triple_2_channel_demux_1_ay), .A(Addr[0]), .B(Addr[0]), .C(Addr[0]));
  triple_2_channel_demux triple_2_channel_demux_2 (
    .bx(triple_2_channel_demux_2_bx), .by(triple_2_channel_demux_2_by), .cy(triple_2_channel_demux_2_cy),
    .c_in(triple_2_channel_demux_4_cx), .cx(triple_2_channel_demux_2_cx), .enable(1'b1),
    .b_in(triple_2_channel_demux_4_cy), .a_in(triple_2_channel_demux_4_cy), .ax(triple_2_channel_demux_2_ax),
    .ay(triple_2_channel_demux_2_ay), .A(Addr[1]), .B(Addr[1]), .C(Addr[1]));
  Quad_AND_Gate quad_and_1 (
    ._1a(R_FROM), ._1b(triple_2_channel_demux_1_ax), ._1y(quad_and_1__1y), ._2a(R_FROM),
    ._2b(triple_2_channel_demux_1_ay), ._2y(quad_and_1__2y), ._3a(W_TO), ._3b(triple_2_channel_demux_1_ax),
    ._3y(quad_and_1__3y), ._4a(W_TO), ._4b(triple_2_channel_demux_1_ay), ._4y(quad_and_1__4y));
  Quad_AND_Gate quad_and_2 (
    ._1a(R_FROM), ._1b(triple_2_channel_demux_1_bx), ._1y(quad_and_2__1y), ._2a(R_FROM),
    ._2b(triple_2_channel_demux_1_by), ._2y(quad_and_2__2y), ._3a(W_TO), ._3b(triple_2_channel_demux_1_bx),
    ._3y(quad_and_2__3y), ._4a(W_TO), ._4b(triple_2_channel_demux_1_by), ._4y(quad_and_2__4y));
  Quad_AND_Gate quad_and_3 (
    ._1a(R_FROM), ._1b(triple_2_channel_demux_1_cx), ._1y(quad_and_3__1y), ._2a(R_FROM),
    ._2b(triple_2_channel_demux_1_cy), ._2y(quad_and_3__2y), ._3a(W_TO), ._3b(triple_2_channel_demux_1_cx),
    ._3y(quad_and_3__3y), ._4a(W_TO), ._4b(triple_2_channel_demux_1_cy), ._4y(quad_and_3__4y));
  Hex_Inverter hex_inverter_1 (
    ._1(quad_and_1__1y), ._1_prime(hex_inverter_1__1_prime), ._2(quad_and_1__2y),
    ._2_prime(hex_inverter_1__2_prime), ._3(quad_and_2__1y), ._3_prime(hex_inverter_1__3_prime),
    ._4(quad_and_1__3y), ._4_prime(hex_inverter_1__4_prime), ._5(quad_and_1__4y),
    ._5_prime(hex_inverter_1__5_prime), ._6(quad_and_2__3y), ._6_prime(hex_inverter_1__6_prime));
  Hex_Inverter hex_inverter_2 (
    ._1(quad_and_2__2y), ._1_prime(hex_inverter_2__1_prime), ._2(quad_and_3__1y),
    ._2_prime(hex_inverter_2__2_prime), ._3(quad_and_3__2y), ._3_prime(hex_inverter_2__3_prime),
    ._4(quad_and_2__4y), ._4_prime(hex_inverter_2__4_prime), ._5(quad_and_3__3y),
    ._5_prime(hex_inverter_2__5_prime), ._6(quad_and_3__4y), ._6_prime(hex_inverter_2__6_prime));
  _8bit_register u_8bit_register_1 (
    .M(hex_inverter_1__1_prime), .N(hex_inverter_1__1_prime), .\input (Data), .clock(CLK),
    .CLR(quad_and_17__1y), .\output (n8bit_register_1_output), .G2(hex_inverter_1__4_prime),
    .G1(hex_inverter_1__4_prime));
  _8bit_register u_8bit_register_2 (
    .M(hex_inverter_1__2_prime), .N(hex_inverter_1__2_prime), .\input (Data), .clock(CLK),
    .CLR(quad_and_17__1y), .\output (n8bit_register_1_output), .G2(hex_inverter_1__5_prime),
    .G1(hex_inverter_1__5_prime));
  _8bit_register u_8bit_register_3 (
    .M(hex_inverter_1__3_prime), .N(hex_inverter_1__3_prime), .\input (Data), .clock(CLK),
    .CLR(quad_and_17__1y), .\output (n8bit_register_1_output), .G2(hex_inverter_1__6_prime),
    .G1(hex_inverter_1__6_prime));
  _8bit_register u_8bit_register_4 (
    .M(hex_inverter_2__1_prime), .N(hex_inverter_2__1_prime), .\input (Data), .clock(CLK),
    .CLR(quad_and_17__1y), .\output (n8bit_register_1_output), .G2(hex_inverter_2__4_prime),
    .G1(hex_inverter_2__4_prime));
  _8bit_register u_8bit_register_5 (
    .M(hex_inverter_2__2_prime), .N(hex_inverter_2__2_prime), .\input (Data), .clock(CLK),
    .CLR(quad_and_17__1y), .\output (n8bit_register_1_output), .G2(hex_inverter_2__5_prime),
    .G1(hex_inverter_2__5_prime));
  _8bit_register u_8bit_register_6 (
    .M(hex_inverter_2__3_prime), .N(hex_inverter_2__3_prime), .\input (Data), .clock(CLK),
    .CLR(quad_and_17__1y), .\output (n8bit_register_1_output), .G2(hex_inverter_2__6_prime),
    .G1(hex_inverter_2__6_prime));
  triple_2_channel_demux triple_2_channel_demux_3 (
    .bx(triple_2_channel_demux_3_bx), .by(triple_2_channel_demux_3_by), .cy(triple_2_channel_demux_3_cy),
    .c_in(triple_2_channel_demux_2_ay), .cx(triple_2_channel_demux_3_cx), .enable(1'b1),
    .b_in(triple_2_channel_demux_2_ax), .a_in(triple_2_channel_demux_4_cy), .ax(triple_2_channel_demux_3_ax),
    .ay(triple_2_channel_demux_3_ay), .A(Addr[0]), .B(Addr[0]), .C(Addr[0]));
  Quad_AND_Gate quad_and_4 (
    ._1a(R_FROM), ._1b(triple_2_channel_demux_3_ax), ._1y(quad_and_4__1y), ._2a(R_FROM),
    ._2b(triple_2_channel_demux_3_ay), ._2y(quad_and_4__2y), ._3a(W_TO), ._3b(triple_2_channel_demux_3_ax),
    ._3y(quad_and_4__3y), ._4a(W_TO), ._4b(triple_2_channel_demux_3_ay), ._4y(quad_and_4__4y));
  Quad_AND_Gate quad_and_5 (
    ._1a(R_FROM), ._1b(triple_2_channel_demux_3_bx), ._1y(quad_and_5__1y), ._2a(R_FROM),
    ._2b(triple_2_channel_demux_3_by), ._2y(quad_and_5__2y), ._3a(W_TO), ._3b(triple_2_channel_demux_3_bx),
    ._3y(quad_and_5__3y), ._4a(W_TO), ._4b(triple_2_channel_demux_3_by), ._4y(quad_and_5__4y));
  Quad_AND_Gate quad_and_6 (
    ._1a(R_FROM), ._1b(triple_2_channel_demux_3_cx), ._1y(quad_and_6__1y), ._2a(R_FROM),
    ._2b(triple_2_channel_demux_3_cy), ._2y(quad_and_6__2y), ._3a(W_TO), ._3b(triple_2_channel_demux_3_cx),
    ._3y(quad_and_6__3y), ._4a(W_TO), ._4b(triple_2_channel_demux_3_cy), ._4y(quad_and_6__4y));
  Hex_Inverter hex_inverter_3 (
    ._1(quad_and_4__1y), ._1_prime(hex_inverter_3__1_prime), ._2(quad_and_4__2y),
    ._2_prime(hex_inverter_3__2_prime), ._3(quad_and_5__1y), ._3_prime(hex_inverter_3__3_prime),
    ._4(quad_and_4__3y), ._4_prime(hex_inverter_3__4_prime), ._5(quad_and_4__4y),
    ._5_prime(hex_inverter_3__5_prime), ._6(quad_and_5__3y), ._6_prime(hex_inverter_3__6_prime));
  Hex_Inverter hex_inverter_4 (
    ._1(quad_and_5__2y), ._1_prime(hex_inverter_4__1_prime), ._2(quad_and_6__1y),
    ._2_prime(hex_inverter_4__2_prime), ._3(quad_and_6__2y), ._3_prime(hex_inverter_4__3_prime),
    ._4(quad_and_5__4y), ._4_prime(hex_inverter_4__4_prime), ._5(quad_and_6__3y),
    ._5_prime(hex_inverter_4__5_prime), ._6(quad_and_6__4y), ._6_prime(hex_inverter_4__6_prime));
  _8bit_register u_8bit_register_7 (
    .M(hex_inverter_3__1_prime), .N(hex_inverter_3__1_prime), .\input (Data), .clock(CLK),
    .CLR(quad_and_17__1y), .\output (n8bit_register_1_output), .G2(hex_inverter_3__4_prime),
    .G1(hex_inverter_3__4_prime));
  _8bit_register u_8bit_register_8 (
    .M(hex_inverter_3__2_prime), .N(hex_inverter_3__2_prime), .\input (Data), .clock(CLK),
    .CLR(quad_and_17__1y), .\output (n8bit_register_1_output), .G2(hex_inverter_3__5_prime),
    .G1(hex_inverter_3__5_prime));
  _8bit_register u_8bit_register_9 (
    .M(hex_inverter_3__3_prime), .N(hex_inverter_3__3_prime), .\input (Data), .clock(CLK),
    .CLR(quad_and_17__1y), .\output (n8bit_register_1_output), .G2(hex_inverter_3__6_prime),
    .G1(hex_inverter_3__6_prime));
  _8bit_register u_8bit_register_10 (
    .M(hex_inverter_4__1_prime), .N(hex_inverter_4__1_prime), .\input (Data), .clock(CLK),
    .CLR(quad_and_17__1y), .\output (n8bit_register_1_output), .G2(hex_inverter_4__4_prime),
    .G1(hex_inverter_4__4_prime));
  _8bit_register u_8bit_register_11 (
    .M(hex_inverter_4__2_prime), .N(hex_inverter_4__2_prime), .\input (Data), .clock(CLK),
    .CLR(quad_and_17__1y), .\output (n8bit_register_1_output), .G2(hex_inverter_4__5_prime),
    .G1(hex_inverter_4__5_prime));
  _8bit_register u_8bit_register_12 (
    .M(hex_inverter_4__3_prime), .N(hex_inverter_4__3_prime), .\input (Data), .clock(CLK),
    .CLR(quad_and_17__1y), .\output (n8bit_register_1_output), .G2(hex_inverter_4__6_prime),
    .G1(hex_inverter_4__6_prime));
  triple_2_channel_demux triple_2_channel_demux_4 (
    .bx(triple_2_channel_demux_2_by), .by(triple_2_channel_demux_4_by), .cy(triple_2_channel_demux_4_cy),
    .c_in(triple_2_channel_demux_9_bx), .cx(triple_2_channel_demux_4_cx), .enable(1'b1),
    .b_in(triple_2_channel_demux_9_by), .a_in(triple_2_channel_demux_9_ax), .ax(triple_2_channel_demux_4_ax),
    .ay(triple_2_channel_demux_4_ay), .A(Addr[2]), .B(Addr[2]), .C(Addr[2]));
  triple_2_channel_demux triple_2_channel_demux_5 (
    .bx(triple_2_channel_demux_5_bx), .by(triple_2_channel_demux_5_by), .cy(triple_2_channel_demux_5_cy),
    .c_in(triple_2_channel_demux_6_bx), .cx(triple_2_channel_demux_5_cx), .enable(1'b1),
    .b_in(triple_2_channel_demux_6_cy), .a_in(triple_2_channel_demux_6_cx), .ax(triple_2_channel_demux_5_ax),
    .ay(triple_2_channel_demux_5_ay), .A(Addr[0]), .B(Addr[0]), .C(Addr[0]));
  Quad_AND_Gate quad_and_7 (
    ._1a(R_FROM), ._1b(triple_2_channel_demux_5_ax), ._1y(quad_and_7__1y), ._2a(R_FROM),
    ._2b(triple_2_channel_demux_5_ay), ._2y(quad_and_7__2y), ._3a(W_TO), ._3b(triple_2_channel_demux_5_ax),
    ._3y(quad_and_7__3y), ._4a(W_TO), ._4b(triple_2_channel_demux_5_ay), ._4y(quad_and_7__4y));
  Quad_AND_Gate quad_and_8 (
    ._1a(R_FROM), ._1b(triple_2_channel_demux_5_bx), ._1y(quad_and_8__1y), ._2a(R_FROM),
    ._2b(triple_2_channel_demux_5_by), ._2y(quad_and_8__2y), ._3a(W_TO), ._3b(triple_2_channel_demux_5_bx),
    ._3y(quad_and_8__3y), ._4a(W_TO), ._4b(triple_2_channel_demux_5_by), ._4y(quad_and_8__4y));
  Quad_AND_Gate quad_and_9 (
    ._1a(R_FROM), ._1b(triple_2_channel_demux_5_cx), ._1y(quad_and_9__1y), ._2a(R_FROM),
    ._2b(triple_2_channel_demux_5_cy), ._2y(quad_and_9__2y), ._3a(W_TO), ._3b(triple_2_channel_demux_5_cx),
    ._3y(quad_and_9__3y), ._4a(W_TO), ._4b(triple_2_channel_demux_5_cy), ._4y(quad_and_9__4y));
  Hex_Inverter hex_inverter_5 (
    ._1(quad_and_7__1y), ._1_prime(hex_inverter_5__1_prime), ._2(quad_and_7__2y),
    ._2_prime(hex_inverter_5__2_prime), ._3(quad_and_8__1y), ._3_prime(hex_inverter_5__3_prime),
    ._4(quad_and_7__3y), ._4_prime(hex_inverter_5__4_prime), ._5(quad_and_7__4y),
    ._5_prime(hex_inverter_5__5_prime), ._6(quad_and_8__3y), ._6_prime(hex_inverter_5__6_prime));
  Hex_Inverter hex_inverter_6 (
    ._1(quad_and_8__2y), ._1_prime(hex_inverter_6__1_prime), ._2(quad_and_9__1y),
    ._2_prime(hex_inverter_6__2_prime), ._3(quad_and_9__2y), ._3_prime(hex_inverter_6__3_prime),
    ._4(quad_and_8__4y), ._4_prime(hex_inverter_6__4_prime), ._5(quad_and_9__3y),
    ._5_prime(hex_inverter_6__5_prime), ._6(quad_and_9__4y), ._6_prime(hex_inverter_6__6_prime));
  _8bit_register u_8bit_register_13 (
    .M(hex_inverter_5__1_prime), .N(hex_inverter_5__1_prime), .\input (Data), .clock(CLK),
    .CLR(quad_and_17__1y), .\output (n8bit_register_1_output), .G2(hex_inverter_5__4_prime),
    .G1(hex_inverter_5__4_prime));
  _8bit_register u_8bit_register_14 (
    .M(hex_inverter_5__2_prime), .N(hex_inverter_5__2_prime), .\input (Data), .clock(CLK),
    .CLR(quad_and_17__1y), .\output (n8bit_register_1_output), .G2(hex_inverter_5__5_prime),
    .G1(hex_inverter_5__5_prime));
  _8bit_register u_8bit_register_15 (
    .M(hex_inverter_5__3_prime), .N(hex_inverter_5__3_prime), .\input (Data), .clock(CLK),
    .CLR(quad_and_17__1y), .\output (n8bit_register_1_output), .G2(hex_inverter_5__6_prime),
    .G1(hex_inverter_5__6_prime));
  _8bit_register u_8bit_register_16 (
    .M(hex_inverter_6__1_prime), .N(hex_inverter_6__1_prime), .\input (Data), .clock(CLK),
    .CLR(quad_and_17__1y), .\output (n8bit_register_1_output), .G2(hex_inverter_6__4_prime),
    .G1(hex_inverter_6__4_prime));
  _8bit_register u_8bit_register_17 (
    .M(hex_inverter_6__2_prime), .N(hex_inverter_6__2_prime), .\input (Data), .clock(CLK),
    .CLR(quad_and_17__3y), .\output (n8bit_register_1_output), .G2(hex_inverter_6__5_prime),
    .G1(hex_inverter_6__5_prime));
  _8bit_register u_8bit_register_18 (
    .M(hex_inverter_6__3_prime), .N(hex_inverter_6__3_prime), .\input (Data), .clock(CLK),
    .CLR(quad_and_17__3y), .\output (n8bit_register_1_output), .G2(hex_inverter_6__6_prime),
    .G1(hex_inverter_6__6_prime));
  triple_2_channel_demux triple_2_channel_demux_6 (
    .bx(triple_2_channel_demux_6_bx), .by(triple_2_channel_demux_6_by), .cy(triple_2_channel_demux_6_cy),
    .c_in(triple_2_channel_demux_4_by), .cx(triple_2_channel_demux_6_cx), .enable(1'b1),
    .b_in(triple_2_channel_demux_4_ax), .a_in(triple_2_channel_demux_4_ay), .ax(triple_2_channel_demux_6_ax),
    .ay(triple_2_channel_demux_6_ay), .A(Addr[1]), .B(Addr[1]), .C(Addr[1]));
  triple_2_channel_demux triple_2_channel_demux_7 (
    .bx(triple_2_channel_demux_7_bx), .by(triple_2_channel_demux_7_by), .cy(triple_2_channel_demux_7_cy),
    .c_in(triple_2_channel_demux_6_by), .cx(triple_2_channel_demux_7_cx), .enable(1'b1),
    .b_in(triple_2_channel_demux_6_ax), .a_in(triple_2_channel_demux_6_ay), .ax(triple_2_channel_demux_7_ax),
    .ay(triple_2_channel_demux_7_ay), .A(Addr[0]), .B(Addr[0]), .C(Addr[0]));
  Quad_AND_Gate quad_and_10 (
    ._1a(R_FROM), ._1b(triple_2_channel_demux_7_ax), ._1y(quad_and_10__1y), ._2a(R_FROM),
    ._2b(triple_2_channel_demux_7_ay), ._2y(quad_and_10__2y), ._3a(W_TO), ._3b(triple_2_channel_demux_7_ax),
    ._3y(quad_and_10__3y), ._4a(W_TO), ._4b(triple_2_channel_demux_7_ay), ._4y(quad_and_10__4y));
  Quad_AND_Gate quad_and_11 (
    ._1a(R_FROM), ._1b(triple_2_channel_demux_7_bx), ._1y(quad_and_11__1y), ._2a(R_FROM),
    ._2b(triple_2_channel_demux_7_by), ._2y(quad_and_11__2y), ._3a(W_TO), ._3b(triple_2_channel_demux_7_bx),
    ._3y(quad_and_11__3y), ._4a(W_TO), ._4b(triple_2_channel_demux_7_by), ._4y(quad_and_11__4y));
  Quad_AND_Gate quad_and_12 (
    ._1a(R_FROM), ._1b(triple_2_channel_demux_7_cx), ._1y(quad_and_12__1y), ._2a(R_FROM),
    ._2b(triple_2_channel_demux_7_cy), ._2y(quad_and_12__2y), ._3a(W_TO), ._3b(triple_2_channel_demux_7_cx),
    ._3y(quad_and_12__3y), ._4a(W_TO), ._4b(triple_2_channel_demux_7_cy), ._4y(quad_and_12__4y));
  Hex_Inverter hex_inverter_7 (
    ._1(quad_and_10__1y), ._1_prime(hex_inverter_7__1_prime), ._2(quad_and_10__2y),
    ._2_prime(hex_inverter_7__2_prime), ._3(quad_and_11__1y), ._3_prime(hex_inverter_7__3_prime),
    ._4(quad_and_10__3y), ._4_prime(hex_inverter_7__4_prime), ._5(quad_and_10__4y),
    ._5_prime(hex_inverter_7__5_prime), ._6(quad_and_11__3y), ._6_prime(hex_inverter_7__6_prime));
  Hex_Inverter hex_inverter_8 (
    ._1(quad_and_11__2y), ._1_prime(hex_inverter_8__1_prime), ._2(quad_and_12__1y),
    ._2_prime(hex_inverter_8__2_prime), ._3(quad_and_12__2y), ._3_prime(hex_inverter_8__3_prime),
    ._4(quad_and_11__4y), ._4_prime(hex_inverter_8__4_prime), ._5(quad_and_12__3y),
    ._5_prime(hex_inverter_8__5_prime), ._6(quad_and_12__4y), ._6_prime(hex_inverter_8__6_prime));
  _8bit_register u_8bit_register_19 (
    .M(hex_inverter_7__1_prime), .N(hex_inverter_7__1_prime), .\input (Data), .clock(CLK),
    .CLR(quad_and_17__3y), .\output (n8bit_register_1_output), .G2(hex_inverter_7__4_prime),
    .G1(hex_inverter_7__4_prime));
  _8bit_register u_8bit_register_20 (
    .M(hex_inverter_7__2_prime), .N(hex_inverter_7__2_prime), .\input (Data), .clock(CLK),
    .CLR(quad_and_17__3y), .\output (n8bit_register_1_output), .G2(hex_inverter_7__5_prime),
    .G1(hex_inverter_7__5_prime));
  _8bit_register u_8bit_register_21 (
    .M(hex_inverter_7__3_prime), .N(hex_inverter_7__3_prime), .\input (Data), .clock(CLK),
    .CLR(quad_and_17__3y), .\output (n8bit_register_1_output), .G2(hex_inverter_7__6_prime),
    .G1(hex_inverter_7__6_prime));
  _8bit_register u_8bit_register_22 (
    .M(hex_inverter_8__1_prime), .N(hex_inverter_8__1_prime), .\input (Data), .clock(CLK),
    .CLR(quad_and_17__3y), .\output (n8bit_register_1_output), .G2(hex_inverter_8__4_prime),
    .G1(hex_inverter_8__4_prime));
  _8bit_register u_8bit_register_23 (
    .M(hex_inverter_8__2_prime), .N(hex_inverter_8__2_prime), .\input (Data), .clock(CLK),
    .CLR(quad_and_17__3y), .\output (n8bit_register_1_output), .G2(hex_inverter_8__5_prime),
    .G1(hex_inverter_8__5_prime));
  _8bit_register u_8bit_register_24 (
    .M(hex_inverter_8__3_prime), .N(hex_inverter_8__3_prime), .\input (Data), .clock(CLK),
    .CLR(quad_and_17__3y), .\output (n8bit_register_1_output), .G2(hex_inverter_8__6_prime),
    .G1(hex_inverter_8__6_prime));
  triple_2_channel_demux triple_2_channel_demux_8 (
    .bx(triple_2_channel_demux_8_bx), .by(triple_2_channel_demux_8_by), .cy(triple_2_channel_demux_8_cy),
    .c_in(triple_2_channel_demux_10_bx), .cx(triple_2_channel_demux_8_cx), .enable(1'b1),
    .b_in(triple_2_channel_demux_10_cy), .a_in(triple_2_channel_demux_10_cx),
    .ax(triple_2_channel_demux_8_ax), .ay(triple_2_channel_demux_8_ay), .A(Addr[0]), .B(Addr[0]), .C(Addr[0]));
  triple_2_channel_demux triple_2_channel_demux_9 (
    .bx(triple_2_channel_demux_9_bx), .by(triple_2_channel_demux_9_by), .cy(triple_2_channel_demux_9_cy),
    .c_in(triple_2_channel_demux_9_ay), .cx(triple_2_channel_demux_9_cx), .enable(1'b1),
    .b_in(triple_2_channel_demux_11_bx), .a_in(triple_2_channel_demux_11_by),
    .ax(triple_2_channel_demux_9_ax), .ay(triple_2_channel_demux_9_ay), .A(Addr[3]), .B(Addr[3]), .C(Addr[2]));
  Quad_AND_Gate quad_and_13 (
    ._1a(R_FROM), ._1b(triple_2_channel_demux_8_ax), ._1y(quad_and_13__1y), ._2a(R_FROM),
    ._2b(triple_2_channel_demux_8_ay), ._2y(quad_and_13__2y), ._3a(W_TO), ._3b(triple_2_channel_demux_8_ax),
    ._3y(quad_and_13__3y), ._4a(W_TO), ._4b(triple_2_channel_demux_8_ay), ._4y(quad_and_13__4y));
  Quad_AND_Gate quad_and_14 (
    ._1a(R_FROM), ._1b(triple_2_channel_demux_8_bx), ._1y(quad_and_14__1y), ._2a(R_FROM),
    ._2b(triple_2_channel_demux_8_by), ._2y(quad_and_14__2y), ._3a(W_TO), ._3b(triple_2_channel_demux_8_bx),
    ._3y(quad_and_14__3y), ._4a(W_TO), ._4b(triple_2_channel_demux_8_by), ._4y(quad_and_14__4y));
  Quad_AND_Gate quad_and_15 (
    ._1a(R_FROM), ._1b(triple_2_channel_demux_8_cx), ._1y(quad_and_15__1y), ._2a(R_FROM),
    ._2b(triple_2_channel_demux_8_cy), ._2y(quad_and_15__2y), ._3a(W_TO), ._3b(triple_2_channel_demux_8_cx),
    ._3y(quad_and_15__3y), ._4a(W_TO), ._4b(triple_2_channel_demux_8_cy), ._4y(quad_and_15__4y));
  Hex_Inverter hex_inverter_9 (
    ._1(quad_and_13__1y), ._1_prime(hex_inverter_9__1_prime), ._2(quad_and_13__2y),
    ._2_prime(hex_inverter_9__2_prime), ._3(quad_and_14__1y), ._3_prime(hex_inverter_9__3_prime),
    ._4(quad_and_13__3y), ._4_prime(hex_inverter_9__4_prime), ._5(quad_and_13__4y),
    ._5_prime(hex_inverter_9__5_prime), ._6(quad_and_14__3y), ._6_prime(hex_inverter_9__6_prime));
  Hex_Inverter hex_inverter_10 (
    ._1(quad_and_14__2y), ._1_prime(hex_inverter_10__1_prime), ._2(quad_and_15__1y),
    ._2_prime(hex_inverter_10__2_prime), ._3(quad_and_15__2y), ._3_prime(hex_inverter_10__3_prime),
    ._4(quad_and_14__4y), ._4_prime(hex_inverter_10__4_prime), ._5(quad_and_15__3y),
    ._5_prime(hex_inverter_10__5_prime), ._6(quad_and_15__4y), ._6_prime(hex_inverter_10__6_prime));
  _8bit_register u_8bit_register_25 (
    .M(hex_inverter_9__1_prime), .N(hex_inverter_9__1_prime), .\input (Data), .clock(CLK),
    .CLR(quad_and_17__3y), .\output (n8bit_register_1_output), .G2(hex_inverter_9__4_prime),
    .G1(hex_inverter_9__4_prime));
  _8bit_register u_8bit_register_26 (
    .M(hex_inverter_9__2_prime), .N(hex_inverter_9__2_prime), .\input (Data), .clock(CLK),
    .CLR(quad_and_17__3y), .\output (n8bit_register_1_output), .G2(hex_inverter_9__5_prime),
    .G1(hex_inverter_9__5_prime));
  _8bit_register u_8bit_register_27 (
    .M(hex_inverter_9__3_prime), .N(hex_inverter_9__3_prime), .\input (Data), .clock(CLK),
    .CLR(quad_and_17__3y), .\output (n8bit_register_1_output), .G2(hex_inverter_9__6_prime),
    .G1(hex_inverter_9__6_prime));
  _8bit_register u_8bit_register_28 (
    .M(hex_inverter_10__1_prime), .N(hex_inverter_10__1_prime), .\input (Data), .clock(CLK),
    .CLR(quad_and_17__3y), .\output (n8bit_register_1_output), .G2(hex_inverter_10__4_prime),
    .G1(hex_inverter_10__4_prime));
  _8bit_register u_8bit_register_29 (
    .M(hex_inverter_10__2_prime), .N(hex_inverter_10__2_prime), .\input (Data), .clock(CLK),
    .CLR(quad_and_17__3y), .\output (n8bit_register_1_output), .G2(hex_inverter_10__5_prime),
    .G1(hex_inverter_10__5_prime));
  _8bit_register u_8bit_register_30 (
    .M(hex_inverter_10__3_prime), .N(hex_inverter_10__3_prime), .\input (Data), .clock(CLK),
    .CLR(quad_and_17__3y), .\output (n8bit_register_1_output), .G2(hex_inverter_10__6_prime),
    .G1(hex_inverter_10__6_prime));
  triple_2_channel_demux triple_2_channel_demux_10 (
    .bx(triple_2_channel_demux_10_bx), .by(triple_2_channel_demux_10_by), .cy(triple_2_channel_demux_10_cy),
    .c_in(triple_2_channel_demux_9_cx), .cx(triple_2_channel_demux_10_cx), .enable(1'b1),
    .b_in(triple_2_channel_demux_9_cy), .a_in(triple_2_channel_demux_10_by),
    .ax(triple_2_channel_demux_10_ax), .ay(triple_2_channel_demux_10_ay), .A(Addr[0]), .B(Addr[1]),
    .C(Addr[1]));
  triple_2_channel_demux triple_2_channel_demux_11 (
    .bx(triple_2_channel_demux_11_bx), .by(triple_2_channel_demux_11_by), .enable(1'b1), .b_in(1'b1),
    .B(Addr[4]));  // open: cy, c_in, cx, a_in, ax, ay, A, C
  Quad_AND_Gate quad_and_16 (
    ._1a(R_FROM), ._1b(triple_2_channel_demux_10_ax), ._1y(quad_and_16__1y), ._2a(R_FROM),
    ._2b(triple_2_channel_demux_10_ay), ._2y(quad_and_16__2y), ._3a(W_TO),
    ._3b(triple_2_channel_demux_10_ax), ._3y(quad_and_16__3y), ._4a(W_TO),
    ._4b(triple_2_channel_demux_10_ay), ._4y(quad_and_16__4y));
  Hex_Inverter hex_inverter_11 (
    ._1(quad_and_16__1y), ._1_prime(hex_inverter_11__1_prime), ._2(quad_and_16__2y),
    ._2_prime(hex_inverter_11__2_prime), ._4(quad_and_16__3y), ._4_prime(hex_inverter_11__4_prime),
    ._5(quad_and_16__4y), ._5_prime(hex_inverter_11__5_prime));  // open: _3, _3_prime, _6, _6_prime
  _8bit_register u_8bit_register_31 (
    .M(hex_inverter_11__1_prime), .N(hex_inverter_11__1_prime), .\input (Data), .clock(CLK),
    .CLR(quad_and_17__3y), .\output (n8bit_register_1_output), .G2(hex_inverter_11__4_prime),
    .G1(hex_inverter_11__4_prime));
  _8bit_register u_8bit_register_32 (
    .M(hex_inverter_11__2_prime), .N(hex_inverter_11__2_prime), .\input (Data), .clock(CLK),
    .CLR(quad_and_17__3y), .\output (n8bit_register_1_output), .G2(hex_inverter_11__5_prime),
    .G1(hex_inverter_11__5_prime));
  Quad_AND_Gate quad_and_17 (
    ._1a(Addr[6]), ._1b(W_TO), ._1y(quad_and_17__1y), ._3a(Addr[7]), ._3b(W_TO), ._3y(quad_and_17__3y));  // open: _2a, _2b, _2y, _4a, _4b, _4y
  _8bit_2_output_demuliplexer u_8bit_2_output_demuliplexer_1 (
    .Output_1(OUT_2), .Output_2(OUT_1), .Input(n8bit_register_1_output), .Control(R_SELECT));
endmodule

module PC (
  input  [7:0] write_byte,
  input  Reset_PC,
  input  nLoad_MSB,
  input  nLoad_LSB,
  input  nInterrupt,
  input  Load_Saved_PC,
  input  Clock,
  output [15:0] PC_value
);

  wire [0:0] adder_carry;
  wire [7:0] LSB_reg_output, msb_add_output, MSB_reg_output, mux_2_output, mux_3_output, mux_4_output,
       mux_output, n8bit_2_input_multiplexer_1_output, n8bit_2_input_multiplexer_2_output, Save_LSB_output,
       Save_MSB_output;

  _8bit_register msb_add (
    .M(1'b0), .N(1'b0), .\input (write_byte), .clock(Clock), .CLR(Reset_PC), .\output (msb_add_output),
    .G2(nLoad_MSB), .G1(nLoad_MSB));
  _8bit_2_input_multiplexer mux (
    .Input_1(n8bit_2_input_multiplexer_1_output), .Input_2(write_byte), .Output(mux_output),
    .Control(nLoad_LSB));
  _8bit_2_input_multiplexer mux_2 (.Input_1(mux_output), .Input_2(8'h3), .Output(mux_2_output), .Control(nInterrupt));
  _8bit_2_input_multiplexer u_8bit_2_input_multiplexer_1 (
    .Input_1(Save_LSB_output), .Input_2(PC_value[7:0]), .Output(n8bit_2_input_multiplexer_1_output),
    .Control(Load_Saved_PC));
  _8bit_register LSB_reg (
    .M(1'b0), .N(1'b0), .\input (mux_2_output), .clock(Clock), .CLR(Reset_PC), .\output (LSB_reg_output),
    .G2(1'b0), .G1(1'b0));
  _8bit_register Save_LSB (
    .M(1'b0), .N(1'b0), .\input (PC_value[7:0]), .clock(Clock), .CLR(1'b0), .\output (Save_LSB_output),
    .G2(nInterrupt), .G1(nInterrupt));
  _8bit_adder adder (.Input1(LSB_reg_output), .Input_2(8'h1), .Output(PC_value[7:0]), .Carry(adder_carry[0]));
  _8bit_2_input_multiplexer mux_3 (
    .Input_1(mux_4_output), .Input_2({8{1'b0}}), .Output(mux_3_output), .Control(nInterrupt));
  _8bit_2_input_multiplexer mux_4 (
    .Input_1(n8bit_2_input_multiplexer_2_output), .Input_2(msb_add_output), .Output(mux_4_output),
    .Control(nLoad_LSB));
  _8bit_register Save_MSB (
    .M(1'b0), .N(1'b0), .\input (PC_value[15:8]), .clock(Clock), .CLR(1'b0), .\output (Save_MSB_output),
    .G2(nInterrupt), .G1(nInterrupt));
  _8bit_register MSB_reg (
    .M(1'b0), .N(1'b0), .\input (mux_3_output), .clock(Clock), .CLR(Reset_PC), .\output (MSB_reg_output),
    .G2(1'b0), .G1(1'b0));
  _8bit_2_input_multiplexer u_8bit_2_input_multiplexer_2 (
    .Input_1(Save_MSB_output), .Input_2(PC_value[15:8]), .Output(n8bit_2_input_multiplexer_2_output),
    .Control(Load_Saved_PC));
  _8bit_adder adder_2 (
    .Input1(MSB_reg_output), .Input_2({{7{1'b0}}, adder_carry[0]}), .Output(PC_value[15:8]));  // open: Carry
endmodule

module _8bit_AND_Gate (
  input  [7:0] In_1,
  input  [7:0] In_2,
  output [7:0] Out
);

  Quad_AND_Gate quad_and_1 (
    ._1a(In_1[0]), ._1b(In_2[0]), ._1y(Out[0]), ._2a(In_1[1]), ._2b(In_2[1]), ._2y(Out[1]), ._3a(In_1[2]),
    ._3b(In_2[2]), ._3y(Out[2]), ._4a(In_1[3]), ._4b(In_2[3]), ._4y(Out[3]));
  Quad_AND_Gate quad_and_2 (
    ._1a(In_1[4]), ._1b(In_2[4]), ._1y(Out[4]), ._2a(In_1[5]), ._2b(In_2[5]), ._2y(Out[5]), ._3a(In_1[6]),
    ._3b(In_2[6]), ._3y(Out[6]), ._4a(In_1[7]), ._4b(In_2[7]), ._4y(Out[7]));
endmodule

module _8bit_OR_Gate (
  input  [7:0] In_1,
  input  [7:0] In_2,
  output [7:0] Out
);

  Quad_OR_Gate quad_or_1 (
    ._1a(In_1[0]), ._1b(In_2[0]), ._1y(Out[0]), ._2a(In_1[1]), ._2b(In_2[1]), ._2y(Out[1]), ._3a(In_1[2]),
    ._3b(In_2[2]), ._3y(Out[2]), ._4a(In_1[3]), ._4b(In_2[3]), ._4y(Out[3]));
  Quad_OR_Gate quad_or_2 (
    ._1a(In_1[4]), ._1b(In_2[4]), ._1y(Out[4]), ._2a(In_1[5]), ._2b(In_2[5]), ._2y(Out[5]), ._3a(In_1[6]),
    ._3b(In_2[6]), ._3y(Out[6]), ._4a(In_1[7]), ._4b(In_2[7]), ._4y(Out[7]));
endmodule

module _8bit_XOR (
  input  [7:0] Read_1,
  input  [7:0] Read_2,
  output [7:0] Write
);

  Quad_XOR_gate quad_xor_gate_1 (
    ._1a(Read_1[2]), ._1b(Read_2[2]), ._1_y(Write[2]), ._2a(Read_2[3]), ._2b(Read_1[3]), ._2_y(Write[3]),
    ._3a(Read_1[0]), ._3b(Read_2[0]), ._3_y(Write[0]), ._4a(Read_2[1]), ._4b(Read_1[1]), ._4_y(Write[1]));
  Quad_XOR_gate quad_xor_gate_2 (
    ._1a(Read_1[6]), ._1b(Read_2[6]), ._1_y(Write[6]), ._2a(Read_1[7]), ._2b(Read_2[7]), ._2_y(Write[7]),
    ._3a(Read_2[4]), ._3b(Read_1[4]), ._3_y(Write[4]), ._4a(Read_2[5]), ._4b(Read_1[5]), ._4_y(Write[5]));
endmodule

module _8bit_2_input_multiplexer (
  input  [7:0] Input_1,
  input  [7:0] Input_2,
  input  Control,
  output [7:0] Output
);

  triple_2_channel_mux triple_2_channel_mux_1 (
    .bx(Input_2[0]), .by(Input_1[0]), .cy(Input_1[1]), .c_out(Output[1]), .cx(Input_2[1]), .enable(1'b1),
    .b_out(Output[0]), .A(Control), .B(Control), .C(Control));  // open: a_out, ax, ay
  triple_2_channel_mux triple_2_channel_mux_2 (
    .bx(Input_2[3]), .by(Input_1[3]), .cy(Input_1[4]), .c_out(Output[4]), .cx(Input_2[4]), .enable(1'b1),
    .b_out(Output[3]), .a_out(Output[2]), .ax(Input_2[2]), .ay(Input_1[2]), .A(Control), .B(Control),
    .C(Control));
  triple_2_channel_mux triple_2_channel_mux_3 (
    .bx(Input_2[6]), .by(Input_1[6]), .cy(Input_1[7]), .c_out(Output[7]), .cx(Input_2[7]), .enable(1'b1),
    .b_out(Output[6]), .a_out(Output[5]), .ax(Input_2[5]), .ay(Input_1[5]), .A(Control), .B(Control),
    .C(Control));
endmodule

module _8bit_2_output_demuliplexer (
  input  [7:0] Input,
  input  Control,
  output [7:0] Output_1,
  output [7:0] Output_2
);

  triple_2_channel_demux triple_2_channel_demux_1 (
    .bx(Output_2[0]), .by(Output_1[0]), .cy(Output_1[1]), .c_in(Input[1]), .cx(Output_2[1]), .enable(1'b1),
    .b_in(Input[0]), .A(Control), .B(Control), .C(Control));  // open: a_in, ax, ay
  triple_2_channel_demux triple_2_channel_demux_2 (
    .bx(Output_2[3]), .by(Output_1[3]), .cy(Output_1[4]), .c_in(Input[4]), .cx(Output_2[4]), .enable(1'b1),
    .b_in(Input[3]), .a_in(Input[2]), .ax(Output_2[2]), .ay(Output_1[2]), .A(Control), .B(Control),
    .C(Control));
  triple_2_channel_demux triple_2_channel_demux_3 (
    .bx(Output_2[6]), .by(Output_1[6]), .cy(Output_1[7]), .c_in(Input[7]), .cx(Output_2[7]), .enable(1'b1),
    .b_in(Input[6]), .a_in(Input[5]), .ax(Output_2[5]), .ay(Output_1[5]), .A(Control), .B(Control),
    .C(Control));
endmodule

module _8bit_5_input_multiplexer (
  input  [7:0] Input_1,
  input  [7:0] Input_2,
  input  [7:0] Input_3,
  input  [7:0] Input_4,
  input  [7:0] Input_5,
  input  Control_1,
  input  Control_2,
  input  Control_3,
  output [7:0] out_9
);

  wire hex_inverter_1__3_prime, hex_inverter_1__4_prime, hex_inverter_1__6_prime, quad_and_1__3y;
  wire [7:0] n8bit_and_1_out, n8bit_and_2_out, n8bit_and_3_out, n8bit_and_4_out, n8bit_and_5_out,
       n8bit_or_1_out, n8bit_or_2_out, n8bit_or_3_out;
  wire [7:7] quad_and_1__1y, quad_and_1__2y, quad_and_1__4y, quad_and_2__1y;

  Hex_Inverter hex_inverter_1 (
    ._3(Control_2), ._3_prime(hex_inverter_1__3_prime), ._4(Control_1), ._4_prime(hex_inverter_1__4_prime),
    ._6(Control_3), ._6_prime(hex_inverter_1__6_prime));  // open: _1, _1_prime, _2, _2_prime, _5, _5_prime
  _8bit_AND_Gate u_8bit_and_1 (.In_2(Input_1), .In_1({8{quad_and_2__1y[7]}}), .Out(n8bit_and_1_out));
  _8bit_AND_Gate u_8bit_and_2 (.In_2(Input_2), .In_1({8{quad_and_1__4y[7]}}), .Out(n8bit_and_2_out));
  _8bit_AND_Gate u_8bit_and_3 (.In_2(Input_3), .In_1({8{quad_and_1__2y[7]}}), .Out(n8bit_and_3_out));
  _8bit_AND_Gate u_8bit_and_4 (.In_2(Input_4), .In_1({8{quad_and_1__1y[7]}}), .Out(n8bit_and_4_out));
  _8bit_AND_Gate u_8bit_and_5 (.In_2(Input_5), .In_1({8{Control_1}}), .Out(n8bit_and_5_out));
  Quad_AND_Gate quad_and_1 (
    ._1a(Control_3), ._1b(Control_2), ._1y(quad_and_1__1y[7]), ._2a(hex_inverter_1__3_prime),
    ._2b(Control_3), ._2y(quad_and_1__2y[7]), ._3a(hex_inverter_1__6_prime), ._3b(hex_inverter_1__3_prime),
    ._3y(quad_and_1__3y), ._4a(hex_inverter_1__6_prime), ._4b(Control_2), ._4y(quad_and_1__4y[7]));
  _8bit_OR_Gate u_8bit_or_1 (.In_2(n8bit_and_2_out), .In_1(n8bit_and_1_out), .Out(n8bit_or_1_out));
  _8bit_OR_Gate u_8bit_or_2 (.In_2(n8bit_and_3_out), .In_1(n8bit_or_1_out), .Out(n8bit_or_2_out));
  _8bit_OR_Gate u_8bit_or_3 (.In_2(n8bit_and_5_out), .In_1(n8bit_and_4_out), .Out(n8bit_or_3_out));
  Quad_AND_Gate quad_and_2 (
    ._1a(hex_inverter_1__4_prime), ._1b(quad_and_1__3y), ._1y(quad_and_2__1y[7]));  // open: _2a, _2b, _2y, _3a, _3b, _3y, _4a, _4b, _4y
  _8bit_OR_Gate u_8bit_or_4 (.In_2(n8bit_or_3_out), .In_1(n8bit_or_2_out), .Out(out_9));
endmodule

module _8bit_6_input_multiplexer (
  input  [7:0] Input_1,
  input  [7:0] Input_2,
  input  [7:0] Input_3,
  input  [7:0] Input_4,
  input  [7:0] Input_5,
  input  [7:0] Input_6,
  input  Control_1,
  input  Control_2,
  input  Control_3,
  output [7:0] out_10
);

  wire hex_inverter_1__3_prime, hex_inverter_1__4_prime, hex_inverter_1__6_prime, quad_and_1__1y,
       quad_and_1__3y;
  wire [7:0] n8bit_and_1_out, n8bit_and_2_out, n8bit_and_3_out, n8bit_and_4_out, n8bit_and_5_out,
       n8bit_and_6_out, n8bit_or_1_out, n8bit_or_2_out, n8bit_or_3_out, n8bit_or_5_out;
  wire [7:7] quad_and_1__2y, quad_and_1__4y, quad_and_2__1y, quad_and_2__2y, quad_and_2__3y, quad_and_2__4y;

  _8bit_AND_Gate u_8bit_and_1 (.In_2(Input_1), .In_1({8{quad_and_2__1y[7]}}), .Out(n8bit_and_1_out));
  _8bit_AND_Gate u_8bit_and_2 (.In_2(Input_2), .In_1({8{quad_and_1__4y[7]}}), .Out(n8bit_and_2_out));
  _8bit_AND_Gate u_8bit_and_3 (.In_2(Input_3), .In_1({8{quad_and_1__2y[7]}}), .Out(n8bit_and_3_out));
  _8bit_AND_Gate u_8bit_and_4 (.In_2(Input_4), .In_1({8{quad_and_2__2y[7]}}), .Out(n8bit_and_4_out));
  _8bit_AND_Gate u_8bit_and_5 (.In_2(Input_5), .In_1({8{quad_and_2__3y[7]}}), .Out(n8bit_and_5_out));
  _8bit_AND_Gate u_8bit_and_6 (.In_2(Input_6), .In_1({8{quad_and_2__4y[7]}}), .Out(n8bit_and_6_out));
  Hex_Inverter hex_inverter_1 (
    ._3(Control_2), ._3_prime(hex_inverter_1__3_prime), ._4(Control_1), ._4_prime(hex_inverter_1__4_prime),
    ._6(Control_3), ._6_prime(hex_inverter_1__6_prime));  // open: _1, _1_prime, _2, _2_prime, _5, _5_prime
  Quad_AND_Gate quad_and_1 (
    ._1a(Control_3), ._1b(Control_2), ._1y(quad_and_1__1y), ._2a(hex_inverter_1__3_prime), ._2b(Control_3),
    ._2y(quad_and_1__2y[7]), ._3a(hex_inverter_1__6_prime), ._3b(hex_inverter_1__3_prime),
    ._3y(quad_and_1__3y), ._4a(hex_inverter_1__6_prime), ._4b(Control_2), ._4y(quad_and_1__4y[7]));
  _8bit_OR_Gate u_8bit_or_1 (.In_2(n8bit_and_2_out), .In_1(n8bit_and_1_out), .Out(n8bit_or_1_out));
  _8bit_OR_Gate u_8bit_or_2 (.In_2(n8bit_and_3_out), .In_1(n8bit_and_4_out), .Out(n8bit_or_2_out));
  _8bit_OR_Gate u_8bit_or_3 (.In_2(n8bit_and_5_out), .In_1(n8bit_and_6_out), .Out(n8bit_or_3_out));
  Quad_AND_Gate quad_and_2 (
    ._1a(hex_inverter_1__4_prime), ._1b(quad_and_1__3y), ._1y(quad_and_2__1y[7]), ._2a(quad_and_1__1y),
    ._2b(hex_inverter_1__4_prime), ._2y(quad_and_2__2y[7]), ._3a(quad_and_1__3y), ._3b(Control_1),
    ._3y(quad_and_2__3y[7]), ._4a(Control_1), ._4b(quad_and_1__1y), ._4y(quad_and_2__4y[7]));
  _8bit_OR_Gate u_8bit_or_4 (.In_2(n8bit_or_1_out), .In_1(n8bit_or_5_out), .Out(out_10));
  _8bit_OR_Gate u_8bit_or_5 (.In_2(n8bit_or_3_out), .In_1(n8bit_or_2_out), .Out(n8bit_or_5_out));
endmodule

module _8bit_3_input_multiplexer (
  input  [7:0] Input_1,
  input  [7:0] Input_2,
  input  [7:0] Input_3,
  input  Control_1,
  input  Control_2,
  output [7:0] out_6
);

  wire hex_inverter_1__1_prime, hex_inverter_1__2_prime;
  wire [7:0] n8bit_and_1_out, n8bit_and_2_out, n8bit_and_3_out, n8bit_or_1_out;
  wire [7:7] quad_and_1__1y, quad_and_1__2y, quad_and_1__3y;

  Hex_Inverter hex_inverter_1 (
    ._1(Control_1), ._1_prime(hex_inverter_1__1_prime), ._2(Control_2), ._2_prime(hex_inverter_1__2_prime));  // open: _3, _3_prime, _4, _4_prime, _5, _5_prime, _6, _6_prime
  _8bit_AND_Gate u_8bit_and_1 (.In_2(Input_1), .In_1({8{quad_and_1__1y[7]}}), .Out(n8bit_and_1_out));
  _8bit_AND_Gate u_8bit_and_2 (.In_2(Input_2), .In_1({8{quad_and_1__2y[7]}}), .Out(n8bit_and_2_out));
  _8bit_AND_Gate u_8bit_and_3 (.In_2(Input_3), .In_1({8{quad_and_1__3y[7]}}), .Out(n8bit_and_3_out));
  Quad_AND_Gate quad_and_1 (
    ._1a(hex_inverter_1__2_prime), ._1b(hex_inverter_1__1_prime), ._1y(quad_and_1__1y[7]),
    ._2a(hex_inverter_1__1_prime), ._2b(Control_2), ._2y(quad_and_1__2y[7]), ._3a(Control_1),
    ._3b(hex_inverter_1__2_prime), ._3y(quad_and_1__3y[7]));  // open: _4a, _4b, _4y
  _8bit_OR_Gate u_8bit_or_1 (.In_2(n8bit_and_2_out), .In_1(n8bit_and_1_out), .Out(n8bit_or_1_out));
  _8bit_OR_Gate u_8bit_or_2 (.In_2(n8bit_and_3_out), .In_1(n8bit_or_1_out), .Out(out_6));
endmodule

module _8bit_adder (
  input  [7:0] Input1,
  input  [7:0] Input_2,
  output [7:0] Output,
  output Carry
);

  wire n4bit_adder_1_c_out;

  _4bit_adder u_4bit_adder_1 (
    .In_1(Input1[3:0]), .In_2(Input_2[3:0]), .C_in(1'b0), .Out(Output[3:0]), .C_out(n4bit_adder_1_c_out));
  _4bit_adder u_4bit_adder_2 (
    .In_1(Input1[7:4]), .In_2(Input_2[7:4]), .C_in(n4bit_adder_1_c_out), .Out(Output[7:4]), .C_out(Carry));
endmodule

module _8bit_register (
  input  M,
  input  CLR,
  input  N,
  input  [7:0] \input ,
  input  clock,
  input  G2,
  input  G1,
  output [7:0] \output 
);

  _4bit_register u_4bit_register_1 (
    .M(M), .N(N), ._1Q(\input [0]), ._2Q(\input [1]), ._3Q(\input [2]), ._4Q(\input [3]), .CLK(clock),
    .CLR(CLR), ._1D(\output [0]), ._2D(\output [1]), ._3D(\output [2]), ._4D(\output [3]), .G2(G2), .G1(G1));
  _4bit_register u_4bit_register_2 (
    .M(M), .N(N), ._1Q(\input [4]), ._2Q(\input [5]), ._3Q(\input [6]), ._4Q(\input [7]), .CLK(clock),
    .CLR(CLR), ._1D(\output [4]), ._2D(\output [5]), ._3D(\output [6]), ._4D(\output [7]), .G2(G2), .G1(G1));
endmodule

module triple_2_channel_mux (
  input  bx,
  input  by,
  input  cy,
  input  ax,
  input  ay,
  input  cx,
  input  A,
  input  enable,
  input  B,
  input  C,
  output b_out,
  output a_out,
  output c_out
);

  Multiplexer multiplexer_1 (.in0(cx), .in1(cy), .out(c_out), .sel(C), .en(enable));
  Multiplexer multiplexer_2 (.in0(bx), .in1(by), .out(b_out), .sel(B), .en(enable));
  Multiplexer multiplexer_3 (.in0(ax), .in1(ay), .out(a_out), .sel(A), .en(enable));

  // Notes on the sheet:
  //   Cd4053B as multiplexer
endmodule

module triple_2_channel_demux (
  input  b_in,
  input  a_in,
  input  c_in,
  input  A,
  input  enable,
  input  B,
  input  C,
  output bx,
  output by,
  output cy,
  output ax,
  output ay,
  output cx
);

  Demultiplexer demultiplexer_1 (.out0(cx), .out1(cy), .in(c_in), .sel(C), .en(enable));
  Demultiplexer demultiplexer_2 (.out0(bx), .out1(by), .in(b_in), .sel(B), .en(enable));
  Demultiplexer demultiplexer_3 (.out0(ax), .out1(ay), .in(a_in), .sel(A), .en(enable));

  // Notes on the sheet:
  //   Cd4053B as demultiplexer
endmodule

// Or
module Quad_OR_Gate (
  input  _3a,
  input  _1a,
  input  _3b,
  input  _1b,
  input  _4a,
  input  _2a,
  input  _4b,
  input  _2b,
  output _3y,
  output _1y,
  output _4y,
  output _2y
);

  or or_1 (_1y, _1a, _1b);
  or or_2 (_2y, _2a, _2b);
  or or_3 (_3y, _3a, _3b);
  or or_4 (_4y, _4a, _4b);
endmodule

// And
module Quad_AND_Gate (
  input  _3a,
  input  _1a,
  input  _3b,
  input  _1b,
  input  _4a,
  input  _2a,
  input  _4b,
  input  _2b,
  output _3y,
  output _1y,
  output _4y,
  output _2y
);

  and and_1 (_1y, _1a, _1b);
  and and_2 (_2y, _2a, _2b);
  and and_3 (_3y, _3a, _3b);
  and and_4 (_4y, _4a, _4b);
endmodule

module _4bit_adder (
  input  [3:0] In_1,
  input  [3:0] In_2,
  input  C_in,
  output [3:0] Out,
  output C_out
);

  wire quad_and_1__1y, quad_and_1__2y, quad_and_1__3y, quad_and_1__4y, quad_and_2__1y, quad_and_2__2y,
       quad_and_2__3y, quad_and_2__4y, quad_or_1__1y, quad_or_1__2y, quad_or_1__3y, quad_xor_gate_1__1_y,
       quad_xor_gate_1__3_y, quad_xor_gate_2__1_y, quad_xor_gate_2__3_y;

  Quad_XOR_gate quad_xor_gate_1 (
    ._1a(In_1[0]), ._1b(In_2[0]), ._1_y(quad_xor_gate_1__1_y), ._2a(quad_xor_gate_1__1_y), ._2b(C_in),
    ._2_y(Out[0]), ._3a(In_1[1]), ._3b(In_2[1]), ._3_y(quad_xor_gate_1__3_y), ._4a(quad_xor_gate_1__3_y),
    ._4b(quad_or_1__1y), ._4_y(Out[1]));
  Quad_XOR_gate quad_xor_gate_2 (
    ._1a(In_1[2]), ._1b(In_2[2]), ._1_y(quad_xor_gate_2__1_y), ._2a(quad_xor_gate_2__1_y),
    ._2b(quad_or_1__2y), ._2_y(Out[2]), ._3a(In_1[3]), ._3b(In_2[3]), ._3_y(quad_xor_gate_2__3_y),
    ._4a(quad_xor_gate_2__3_y), ._4b(quad_or_1__3y), ._4_y(Out[3]));
  Quad_AND_Gate quad_and_1 (
    ._1a(quad_xor_gate_1__1_y), ._1b(C_in), ._1y(quad_and_1__1y), ._2a(In_2[0]), ._2b(In_1[0]),
    ._2y(quad_and_1__2y), ._3a(quad_xor_gate_1__3_y), ._3b(quad_or_1__1y), ._3y(quad_and_1__3y),
    ._4a(In_1[1]), ._4b(In_2[1]), ._4y(quad_and_1__4y));
  Quad_AND_Gate quad_and_2 (
    ._1a(quad_xor_gate_2__1_y), ._1b(quad_or_1__2y), ._1y(quad_and_2__1y), ._2a(In_2[2]), ._2b(In_1[2]),
    ._2y(quad_and_2__2y), ._3a(quad_xor_gate_2__3_y), ._3b(quad_or_1__3y), ._3y(quad_and_2__3y),
    ._4a(In_2[3]), ._4b(In_1[3]), ._4y(quad_and_2__4y));
  Quad_OR_Gate quad_or_1 (
    ._1a(quad_and_1__1y), ._1b(quad_and_1__2y), ._1y(quad_or_1__1y), ._2a(quad_and_1__3y),
    ._2b(quad_and_1__4y), ._2y(quad_or_1__2y), ._3a(quad_and_2__1y), ._3b(quad_and_2__2y),
    ._3y(quad_or_1__3y), ._4a(quad_and_2__3y), ._4b(quad_and_2__4y), ._4y(C_out));
endmodule

module _4bit_register (
  input  M,
  input  N,
  input  CLR,
  input  _1Q,
  input  _2Q,
  input  _3Q,
  input  _4Q,
  input  CLK,
  input  G2,
  input  G1,
  output _1D,
  output _2D,
  output _3D,
  output _4D
);

  wire and_1_out, and_2_out, and_3_out, and_4_out, and_5_out, and_6_out, and_7_out, and_8_out, and_9_out,
       and_10_out, d_ff_1_q, d_ff_2_q, d_ff_3_q, d_ff_4_q, not_1_out, not_2_out, not_3_out, not_4_out,
       not_5_out, or_1_out, or_2_out, or_3_out, or_4_out;

  not not_1 (not_1_out, M);
  not not_2 (not_2_out, N);
  and and_1 (and_1_out, not_1_out, not_2_out);
  not not_3 (not_3_out, and_10_out);
  and and_2 (and_2_out, d_ff_1_q, not_3_out);
  and and_3 (and_3_out, _1Q, and_10_out);
  and and_4 (and_4_out, d_ff_2_q, not_3_out);
  and and_5 (and_5_out, _2Q, and_10_out);
  and and_6 (and_6_out, d_ff_3_q, not_3_out);
  and and_7 (and_7_out, _3Q, and_10_out);
  and and_8 (and_8_out, d_ff_4_q, not_3_out);
  and and_9 (and_9_out, _4Q, and_10_out);
  or or_1 (or_1_out, and_2_out, and_3_out);
  or or_2 (or_2_out, and_4_out, and_5_out);
  or or_3 (or_3_out, and_6_out, and_7_out);
  or or_4 (or_4_out, and_8_out, and_9_out);
  D_Flip_Flop d_ff_1 (.clk(CLK), .D(or_1_out), .Q(d_ff_1_q), .en(1'b1), .reset(CLR));  // open: Qn, preset
  D_Flip_Flop d_ff_2 (.clk(CLK), .D(or_2_out), .Q(d_ff_2_q), .en(1'b1), .reset(CLR));  // open: Qn, preset
  D_Flip_Flop d_ff_3 (.clk(CLK), .D(or_3_out), .Q(d_ff_3_q), .en(1'b1), .reset(CLR));  // open: Qn, preset
  D_Flip_Flop d_ff_4 (.clk(CLK), .D(or_4_out), .Q(d_ff_4_q), .en(1'b1), .reset(CLR));  // open: Qn, preset
  and and_10 (and_10_out, not_4_out, not_5_out);
  not not_4 (not_4_out, G2);
  not not_5 (not_5_out, G1);
  assign _1D = and_1_out ? d_ff_1_q : 1'bz;  // Controlled_Buffer controlled_buffer_1
  assign _2D = and_1_out ? d_ff_2_q : 1'bz;  // Controlled_Buffer controlled_buffer_2
  assign _3D = and_1_out ? d_ff_3_q : 1'bz;  // Controlled_Buffer controlled_buffer_3
  assign _4D = and_1_out ? d_ff_4_q : 1'bz;  // Controlled_Buffer controlled_buffer_4
endmodule

// Not
module Hex_Inverter (
  input  _1,
  input  _4,
  input  _2,
  input  _5,
  input  _6,
  input  _3,
  output _1_prime,
  output _4_prime,
  output _5_prime,
  output _2_prime,
  output _6_prime,
  output _3_prime
);

  not not_1 (_1_prime, _1);
  not not_2 (_2_prime, _2);
  not not_3 (_3_prime, _3);
  not not_4 (_4_prime, _4);
  not not_5 (_5_prime, _5);
  not not_6 (_6_prime, _6);
endmodule

module Quad_XOR_gate (
  input  _3a,
  input  _1a,
  input  _3b,
  input  _1b,
  input  _4a,
  input  _2a,
  input  _4b,
  input  _2b,
  output _3_y,
  output _1_y,
  output _4_y,
  output _2_y
);

  xor xor_1 (_1_y, _1a, _1b);
  xor xor_2 (_2_y, _2a, _2b);
  xor xor_3 (_3_y, _3a, _3b);
  xor xor_4 (_4_y, _4a, _4b);

  // Notes on the sheet:
  //   XOR Gate Sn74hc86n
endmodule

module _8bit_5_input_mux_w__zero_output (
  input  [7:0] Input_1,
  input  [7:0] Input_2,
  input  [7:0] Input_3,
  input  [7:0] Input_4,
  input  [7:0] Input_5,
  input  Control_1,
  input  Control_2,
  input  Control_3,
  output [7:0] out_9
);

  wire hex_inverter_1__3_prime, hex_inverter_1__4_prime, hex_inverter_1__6_prime, quad_and_1__3y,
       quad_and_2__2y;
  wire [7:0] n8bit_and_1_out, n8bit_and_2_out, n8bit_and_3_out, n8bit_and_4_out, n8bit_and_5_out,
       n8bit_or_1_out, n8bit_or_2_out, n8bit_or_3_out, n8bit_or_4_out;
  wire [7:7] hex_inverter_1__5_prime, quad_and_1__1y, quad_and_1__2y, quad_and_1__4y, quad_and_2__1y;

  Hex_Inverter hex_inverter_1 (
    ._3(Control_2), ._3_prime(hex_inverter_1__3_prime), ._4(Control_1), ._4_prime(hex_inverter_1__4_prime),
    ._5(quad_and_2__2y), ._5_prime(hex_inverter_1__5_prime[7]), ._6(Control_3),
    ._6_prime(hex_inverter_1__6_prime));  // open: _1, _1_prime, _2, _2_prime
  _8bit_AND_Gate u_8bit_and_1 (.In_2(Input_1), .In_1({8{quad_and_2__1y[7]}}), .Out(n8bit_and_1_out));
  _8bit_AND_Gate u_8bit_and_2 (.In_2(Input_2), .In_1({8{quad_and_1__4y[7]}}), .Out(n8bit_and_2_out));
  _8bit_AND_Gate u_8bit_and_3 (.In_2(Input_3), .In_1({8{quad_and_1__2y[7]}}), .Out(n8bit_and_3_out));
  _8bit_AND_Gate u_8bit_and_4 (.In_2(Input_4), .In_1({8{quad_and_1__1y[7]}}), .Out(n8bit_and_4_out));
  _8bit_AND_Gate u_8bit_and_5 (.In_2(Input_5), .In_1({8{Control_1}}), .Out(n8bit_and_5_out));
  Quad_AND_Gate quad_and_1 (
    ._1a(Control_3), ._1b(Control_2), ._1y(quad_and_1__1y[7]), ._2a(hex_inverter_1__3_prime),
    ._2b(Control_3), ._2y(quad_and_1__2y[7]), ._3a(hex_inverter_1__6_prime), ._3b(hex_inverter_1__3_prime),
    ._3y(quad_and_1__3y), ._4a(hex_inverter_1__6_prime), ._4b(Control_2), ._4y(quad_and_1__4y[7]));
  _8bit_OR_Gate u_8bit_or_1 (.In_2(n8bit_and_2_out), .In_1(n8bit_and_1_out), .Out(n8bit_or_1_out));
  _8bit_OR_Gate u_8bit_or_2 (.In_2(n8bit_and_3_out), .In_1(n8bit_or_1_out), .Out(n8bit_or_2_out));
  _8bit_OR_Gate u_8bit_or_3 (.In_2(n8bit_and_5_out), .In_1(n8bit_and_4_out), .Out(n8bit_or_3_out));
  Quad_AND_Gate quad_and_2 (
    ._1a(hex_inverter_1__4_prime), ._1b(quad_and_1__3y), ._1y(quad_and_2__1y[7]), ._2a(Control_1),
    ._2b(quad_and_1__2y[7]), ._2y(quad_and_2__2y));  // open: _3a, _3b, _3y, _4a, _4b, _4y
  _8bit_OR_Gate u_8bit_or_4 (.In_2(n8bit_or_3_out), .In_1(n8bit_or_2_out), .Out(n8bit_or_4_out));
  _8bit_AND_Gate u_8bit_and_6 (.In_2(n8bit_or_4_out), .In_1({8{hex_inverter_1__5_prime[7]}}), .Out(out_9));
endmodule

module Control_Load (
  input  Instruction_enable,
  input  [6:0] Sub_instruction,
  input  [2:0] Read_From_1,
  output Clear,
  output Write_Byte,
  output Mux_1_1,
  output Mux_1_2,
  output Mux_1_3,
  output Mux_3_1,
  output Ram_EW_TO,
  output Ram_ER_FROM
);

  wire quad_and_1__1y, quad_or_1__1y, quad_or_1__3y;

  Quad_AND_Gate quad_and_1 (
    ._1a(Instruction_enable), ._1b(Sub_instruction[0]), ._1y(quad_and_1__1y), ._2a(Sub_instruction[1]),
    ._2b(Instruction_enable), ._2y(Ram_ER_FROM), ._3a(Instruction_enable), ._3b(Sub_instruction[3]),
    ._3y(Mux_3_1), ._4a(Sub_instruction[2]), ._4b(Instruction_enable), ._4y(Ram_EW_TO));
  Quad_AND_Gate quad_and_2 (
    ._1a(Instruction_enable), ._1b(Sub_instruction[4]), ._1y(Clear));  // open: _2a, _2b, _2y, _3a, _3b, _3y, _4a, _4b, _4y
  Quad_OR_Gate quad_or_1 (
    ._1a(Mux_3_1), ._1b(quad_and_1__1y), ._1y(quad_or_1__1y), ._3a(Ram_ER_FROM), ._3b(Ram_EW_TO),
    ._3y(quad_or_1__3y), ._4a(quad_or_1__3y), ._4b(Mux_3_1), ._4y(Write_Byte));  // open: _2a, _2b, _2y
  Quad_AND_Gate quad_and_3 (
    ._1a(quad_or_1__1y), ._1b(Read_From_1[0]), ._1y(Mux_1_1), ._2a(quad_or_1__1y), ._2b(Read_From_1[1]),
    ._2y(Mux_1_2), ._4a(quad_or_1__1y), ._4b(Read_From_1[2]), ._4y(Mux_1_3));  // open: _3a, _3b, _3y
endmodule

module Control_Addition (
  input  Instruction_enable,
  input  [6:0] Sub_instruction,
  input  [2:0] Read_From_1,
  input  [2:0] Read_From_2,
  output Write_Byte,
  output Write_Mux_2,
  output Read_Mux_1_1,
  output Read_Mux_1_2,
  output Read_Mux_1_3,
  output Read_Mux_2_1,
  output Read_Mux_2_2,
  output Read_Mux_2_3,
  output Subtract_nAdd,
  output out_14,
  output shift__logical_control1,
  output shift__logical_control2
);

  wire quad_and_1__1y, quad_and_1__2y, quad_and_1__3y, quad_and_1__4y, quad_and_2__1y, quad_and_2__2y,
       quad_or_1__2y;

  Quad_AND_Gate quad_and_1 (
    ._1a(Instruction_enable), ._1b(Sub_instruction[0]), ._1y(quad_and_1__1y), ._2a(Sub_instruction[1]),
    ._2b(Instruction_enable), ._2y(quad_and_1__2y), ._3a(Instruction_enable), ._3b(Sub_instruction[3]),
    ._3y(quad_and_1__3y), ._4a(Sub_instruction[2]), ._4b(Instruction_enable), ._4y(quad_and_1__4y));
  Quad_AND_Gate quad_and_2 (
    ._1a(Instruction_enable), ._1b(Sub_instruction[4]), ._1y(quad_and_2__1y), ._2a(Instruction_enable),
    ._2b(Sub_instruction[5]), ._2y(quad_and_2__2y));  // open: _3a, _3b, _3y, _4a, _4b, _4y
  Quad_AND_Gate quad_and_3 (
    ._1a(quad_or_1__2y), ._1b(Read_From_2[0]), ._1y(Read_Mux_2_1), ._2a(quad_or_1__2y), ._2b(Read_From_2[1]),
    ._2y(Read_Mux_2_2), ._3a(quad_or_1__2y), ._3b(Read_From_2[2]), ._3y(Read_Mux_2_3));  // open: _4a, _4b, _4y
  Quad_OR_Gate quad_or_1 (
    ._1a(quad_and_1__3y), ._1b(quad_and_1__2y), ._1y(Write_Byte), ._2a(quad_and_1__1y), ._2b(quad_and_1__4y),
    ._2y(quad_or_1__2y), ._3a(quad_and_1__3y), ._3b(quad_and_1__4y), ._3y(Subtract_nAdd),
    ._4a(quad_and_2__1y), ._4b(quad_and_2__2y), ._4y(out_14));

  assign Read_Mux_1_1 = Read_From_1[0];
  assign Read_Mux_1_2 = Read_From_1[1];
  assign Read_Mux_1_3 = Read_From_1[2];
  assign shift__logical_control1 = out_14;
  assign shift__logical_control2 = out_14;
  assign Write_Mux_2 = Instruction_enable;
endmodule

module Control_Logical (
  input  Instruction_enable,
  input  [6:0] Sub_instruction,
  input  [2:0] Read_From_1,
  input  [2:0] Read_From_2,
  output Write_Byte,
  output And_nOr,
  output Logical_nnot,
  output regular_n_logical_comparison____shift,
  output Write_Mux_2,
  output Read_Mux_1_1,
  output Read_Mux_1_2,
  output Read_Mux_1_3,
  output Read_Mux_2_1,
  output Read_Mux_2_2,
  output Read_Mux_2_3
);

  wire hex_inverter_1__1_prime, quad_and_1__1y, quad_and_1__2y, quad_and_1__3y, quad_and_2__1y,
       quad_and_2__2y, quad_or_1__1y, quad_or_1__4y;

  Quad_AND_Gate quad_and_1 (
    ._1a(Instruction_enable), ._1b(Sub_instruction[0]), ._1y(quad_and_1__1y), ._2a(Sub_instruction[1]),
    ._2b(Instruction_enable), ._2y(quad_and_1__2y), ._3a(Instruction_enable), ._3b(Sub_instruction[3]),
    ._3y(quad_and_1__3y));  // open: _4a, _4b, _4y
  Quad_AND_Gate quad_and_2 (
    ._1a(Instruction_enable), ._1b(Sub_instruction[4]), ._1y(quad_and_2__1y), ._2a(Instruction_enable),
    ._2b(Sub_instruction[5]), ._2y(quad_and_2__2y));  // open: _3a, _3b, _3y, _4a, _4b, _4y
  Quad_OR_Gate quad_or_1 (
    ._1a(quad_and_1__3y), ._1b(quad_and_1__2y), ._1y(quad_or_1__1y), ._2a(quad_or_1__1y),
    ._2b(quad_and_2__2y), ._2y(Write_Byte), ._3a(quad_and_1__2y), ._3b(quad_and_1__1y), ._3y(And_nOr),
    ._4a(quad_and_2__1y), ._4b(Write_Byte), ._4y(quad_or_1__4y));
  Hex_Inverter hex_inverter_1 (
    ._1(Write_Byte), ._1_prime(hex_inverter_1__1_prime), ._4(quad_or_1__4y), ._4_prime(Logical_nnot));  // open: _2, _2_prime, _3, _3_prime, _5, _5_prime, _6, _6_prime
  Quad_AND_Gate quad_and_3 (
    ._1a(hex_inverter_1__1_prime), ._1b(Read_From_2[0]), ._1y(Read_Mux_2_1), ._2a(hex_inverter_1__1_prime),
    ._2b(Read_From_2[1]), ._2y(Read_Mux_2_2), ._3a(hex_inverter_1__1_prime), ._3b(Read_From_2[2]),
    ._3y(Read_Mux_2_3));  // open: _4a, _4b, _4y

  assign Read_Mux_1_1 = Read_From_1[0];
  assign Read_Mux_1_2 = Read_From_1[1];
  assign Read_Mux_1_3 = Read_From_1[2];
  assign regular_n_logical_comparison____shift = Instruction_enable;
  assign Write_Mux_2 = Instruction_enable;
endmodule

module Control_Logical_Comparison (
  input  Instruction_enable,
  input  [6:0] Sub_instruction,
  input  [2:0] Read_From_1,
  input  [2:0] Read_From_2,
  output Write_Byte,
  output shift____logical_control1__equals,
  output shift____logical_control2__1_2,
  output Subtract_nAdd,
  output addition_n_logical____not,
  output Write_Mux_2,
  output Read_Mux_1_1,
  output Read_Mux_1_2,
  output Read_Mux_1_3,
  output Read_Mux_2_1,
  output Read_Mux_2_2,
  output Read_Mux_2_3
);

  wire quad_and_1__1y, quad_and_1__2y, quad_and_1__3y, quad_and_1__4y, quad_and_2__1y, quad_and_2__2y,
       quad_or_1__1y, quad_or_1__2y, quad_or_2__3y;

  Quad_AND_Gate quad_and_1 (
    ._1a(Instruction_enable), ._1b(Sub_instruction[0]), ._1y(quad_and_1__1y), ._2a(Sub_instruction[1]),
    ._2b(Instruction_enable), ._2y(quad_and_1__2y), ._3a(Instruction_enable), ._3b(Sub_instruction[3]),
    ._3y(quad_and_1__3y), ._4a(Instruction_enable), ._4b(Sub_instruction[2]), ._4y(quad_and_1__4y));
  Quad_AND_Gate quad_and_2 (
    ._1a(Instruction_enable), ._1b(Sub_instruction[4]), ._1y(quad_and_2__1y), ._2a(Instruction_enable),
    ._2b(Sub_instruction[5]), ._2y(quad_and_2__2y));  // open: _3a, _3b, _3y, _4a, _4b, _4y
  Quad_OR_Gate quad_or_1 (
    ._1a(quad_and_2__1y), ._1b(quad_and_1__1y), ._1y(quad_or_1__1y), ._2a(quad_or_1__1y),
    ._2b(quad_and_1__4y), ._2y(quad_or_1__2y));  // open: _3a, _3b, _3y, _4a, _4b, _4y
  Quad_OR_Gate quad_or_2 (
    ._1a(quad_and_2__2y), ._1b(quad_and_2__1y), ._1y(shift____logical_control1__equals),
    ._2a(quad_and_1__1y), ._2b(quad_and_1__2y), ._2y(shift____logical_control2__1_2), ._3a(quad_and_2__2y),
    ._3b(quad_and_1__2y), ._3y(quad_or_2__3y), ._4a(quad_or_2__3y), ._4b(quad_and_1__3y), ._4y(Write_Byte));
  Quad_AND_Gate quad_and_3 (
    ._1a(quad_or_1__2y), ._1b(Read_From_2[0]), ._1y(Read_Mux_2_1), ._2a(quad_or_1__2y), ._2b(Read_From_2[1]),
    ._2y(Read_Mux_2_2), ._3a(quad_or_1__2y), ._3b(Read_From_2[2]), ._3y(Read_Mux_2_3));  // open: _4a, _4b, _4y

  assign addition_n_logical____not = Instruction_enable;
  assign Read_Mux_1_1 = Read_From_1[0];
  assign Read_Mux_1_2 = Read_From_1[1];
  assign Read_Mux_1_3 = Read_From_1[2];
  assign Subtract_nAdd = Instruction_enable;
  assign Write_Mux_2 = Instruction_enable;
endmodule

module Control_Misc (
  input  Instruction_enable,
  input  [6:0] Sub_instruction,
  input  [2:0] Read_From_1,
  input  nequal_zero,
  output nLoad_MSB,
  output nLoad_LSB,
  output Load_Saved_PC,
  output nequal_zero_2,
  output Write_Byte,
  output Write_Byte_2,
  output OCL_Register_Enable,
  output Read_Mux_1_1,
  output Read_Mux_1_2,
  output Read_Mux_1_3,
  output Read_Mux_2_1,
  output Read_Mux_2_2,
  output Read_Mux_2_3
);

  wire hex_inverter_1__2_prime, hex_inverter_1__3_prime, hex_inverter_1__5_prime, quad_and_1__1y,
       quad_and_1__2y, quad_and_1__3y, quad_and_2__4y, quad_or_1__1y, quad_or_1__3y;

  Quad_AND_Gate quad_and_1 (
    ._1a(Instruction_enable), ._1b(Sub_instruction[0]), ._1y(quad_and_1__1y), ._2a(Sub_instruction[1]),
    ._2b(Instruction_enable), ._2y(quad_and_1__2y), ._3a(Instruction_enable), ._3b(Sub_instruction[3]),
    ._3y(quad_and_1__3y), ._4a(Instruction_enable), ._4b(Sub_instruction[2]), ._4y(Load_Saved_PC));
  Quad_AND_Gate quad_and_2 (
    ._2a(Instruction_enable), ._2b(Sub_instruction[5]), ._2y(Read_Mux_2_1), ._3a(hex_inverter_1__5_prime),
    ._3b(hex_inverter_1__2_prime), ._3y(nLoad_LSB), ._4a(quad_and_1__3y), ._4b(hex_inverter_1__3_prime),
    ._4y(quad_and_2__4y));  // open: _1a, _1b, _1y
  Hex_Inverter hex_inverter_1 (
    ._1(Read_Mux_2_1), ._1_prime(OCL_Register_Enable), ._2(quad_and_2__4y),
    ._2_prime(hex_inverter_1__2_prime), ._3(nequal_zero), ._3_prime(hex_inverter_1__3_prime),
    ._4(quad_and_1__1y), ._4_prime(nLoad_MSB), ._5(quad_and_1__2y), ._5_prime(hex_inverter_1__5_prime),
    ._6(quad_and_1__3y), ._6_prime(nequal_zero_2));
  Quad_OR_Gate quad_or_1 (
    ._1a(quad_and_1__3y), ._1b(Read_Mux_2_1), ._1y(quad_or_1__1y), ._3a(quad_and_1__1y),
    ._3b(quad_and_1__2y), ._3y(quad_or_1__3y), ._4a(quad_or_1__3y), ._4b(quad_or_1__1y), ._4y(Write_Byte));  // open: _2a, _2b, _2y
  Quad_AND_Gate quad_and_3 (
    ._1a(quad_and_1__3y), ._1b(Read_From_1[1]), ._1y(Read_Mux_1_2), ._2a(quad_and_1__3y),
    ._2b(Read_From_1[2]), ._2y(Read_Mux_1_3), ._3a(quad_and_1__3y), ._3b(Read_From_1[0]), ._3y(Read_Mux_1_1));  // open: _4a, _4b, _4y

  assign Read_Mux_2_2 = Read_Mux_2_1;
  assign Read_Mux_2_3 = Read_Mux_2_1;
  assign Write_Byte_2 = Read_Mux_2_1;
endmodule
module Display (
  input  Read,
  input  Write,
  input  [7:0] Addr,
  input  [7:0] Data,
  output [7:0] Out
);

  wire clk_out, hex_inverter_1__1_prime, hex_inverter_1__2_prime, hex_inverter_1__3_prime,
       hex_inverter_1__4_prime, hex_inverter_1__5_prime, hex_inverter_1__6_prime, hex_inverter_2__1_prime,
       hex_inverter_2__2_prime, hex_inverter_2__3_prime, hex_inverter_2__4_prime, hex_inverter_2__5_prime,
       hex_inverter_2__6_prime, hex_inverter_3__1_prime, hex_inverter_3__4_prime, hex_inverter_3__5_prime,
       hex_inverter_3__6_prime, quad_and_1__3y, triple_2_channel_demux_1_ax, triple_2_channel_demux_1_ay,
       triple_2_channel_demux_1_bx, triple_2_channel_demux_1_by, triple_2_channel_demux_1_cx,
       triple_2_channel_demux_1_cy, triple_2_channel_demux_2_ax, triple_2_channel_demux_2_ay,
       triple_2_channel_demux_2_bx, triple_2_channel_demux_2_by, triple_2_channel_demux_2_cx,
       triple_2_channel_demux_2_cy, triple_2_channel_demux_3_ax, triple_2_channel_demux_3_ay,
       triple_2_channel_demux_3_bx, triple_2_channel_demux_3_by, triple_2_channel_demux_3_cx,
       triple_2_channel_demux_3_cy, triple_2_channel_demux_4_ax, triple_2_channel_demux_4_ay,
       triple_2_channel_demux_4_bx, triple_2_channel_demux_4_by, triple_2_channel_demux_4_cx,
       triple_2_channel_demux_4_cy, triple_2_channel_demux_5_ax, triple_2_channel_demux_5_ay,
       triple_2_channel_demux_5_bx, triple_2_channel_demux_5_by, triple_2_channel_demux_5_cx,
       triple_2_channel_demux_5_cy;
  wire [7:0] n8bit_register_1_output, n8bit_register_2_output, n8bit_register_3_output,
       n8bit_register_4_output, n8bit_register_5_output, n8bit_register_6_output, n8bit_register_7_output,
       n8bit_register_8_output, n8bit_register_9_output, n8bit_register_10_output, n8bit_register_11_output,
       n8bit_register_12_output, n8bit_register_13_output, n8bit_register_14_output,
       n8bit_register_15_output, n8bit_register_16_output;

  Clock clk (.out(clk_out));
  _8bit_register u_8bit_register_1 (
    .M(1'b0), .N(1'b0), .\input (Data), .clock(clk_out), .CLR(quad_and_1__3y),
    .\output (n8bit_register_1_output), .G2(hex_inverter_1__3_prime), .G1(hex_inverter_1__3_prime));
  _8bit_register u_8bit_register_2 (
    .M(1'b0), .N(1'b0), .\input (Data), .clock(clk_out), .CLR(quad_and_1__3y),
    .\output (n8bit_register_2_output), .G2(hex_inverter_1__2_prime), .G1(hex_inverter_1__2_prime));
  _8bit_register u_8bit_register_3 (
    .M(1'b0), .N(1'b0), .\input (Data), .clock(clk_out), .CLR(quad_and_1__3y),
    .\output (n8bit_register_3_output), .G2(hex_inverter_1__1_prime), .G1(hex_inverter_1__1_prime));
  _8bit_register u_8bit_register_4 (
    .M(1'b0), .N(1'b0), .\input (Data), .clock(clk_out), .CLR(quad_and_1__3y),
    .\output (n8bit_register_4_output), .G2(hex_inverter_1__4_prime), .G1(hex_inverter_1__4_prime));
  Hex_Inverter hex_inverter_1 (
    ._1(triple_2_channel_demux_1_cx), ._1_prime(hex_inverter_1__1_prime), ._2(triple_2_channel_demux_1_by),
    ._2_prime(hex_inverter_1__2_prime), ._3(triple_2_channel_demux_1_bx), ._3_prime(hex_inverter_1__3_prime),
    ._4(triple_2_channel_demux_1_cy), ._4_prime(hex_inverter_1__4_prime), ._5(triple_2_channel_demux_2_bx),
    ._5_prime(hex_inverter_1__5_prime), ._6(triple_2_channel_demux_2_by), ._6_prime(hex_inverter_1__6_prime));
  triple_2_channel_demux triple_2_channel_demux_1 (
    .bx(triple_2_channel_demux_1_bx), .by(triple_2_channel_demux_1_by), .cy(triple_2_channel_demux_1_cy),
    .c_in(triple_2_channel_demux_1_ay), .cx(triple_2_channel_demux_1_cx), .enable(1'b1),
    .b_in(triple_2_channel_demux_1_ax), .a_in(triple_2_channel_demux_5_bx), .ax(triple_2_channel_demux_1_ax),
    .ay(triple_2_channel_demux_1_ay), .A(Addr[1]), .B(Addr[0]), .C(Addr[0]));
  _8bit_register u_8bit_register_5 (
    .M(1'b0), .N(1'b0), .\input (Data), .clock(clk_out), .CLR(quad_and_1__3y),
    .\output (n8bit_register_5_output), .G2(hex_inverter_1__5_prime), .G1(hex_inverter_1__5_prime));
  _8bit_register u_8bit_register_6 (
    .M(1'b0), .N(1'b0), .\input (Data), .clock(clk_out), .CLR(quad_and_1__3y),
    .\output (n8bit_register_6_output), .G2(hex_inverter_1__6_prime), .G1(hex_inverter_1__6_prime));
  _8bit_register u_8bit_register_7 (
    .M(1'b0), .N(1'b0), .\input (Data), .clock(clk_out), .CLR(quad_and_1__3y),
    .\output (n8bit_register_7_output), .G2(hex_inverter_2__3_prime), .G1(hex_inverter_2__3_prime));
  _8bit_register u_8bit_register_8 (
    .M(1'b0), .N(1'b0), .\input (Data), .clock(clk_out), .CLR(quad_and_1__3y),
    .\output (n8bit_register_8_output), .G2(hex_inverter_2__2_prime), .G1(hex_inverter_2__2_prime));
  LED led_1 (.in(n8bit_register_1_output[0]));
  LED led_2 (.in(n8bit_register_1_output[1]));
  LED led_3 (.in(n8bit_register_1_output[2]));
  LED led_4 (.in(n8bit_register_1_output[3]));
  LED led_5 (.in(n8bit_register_1_output[4]));
  LED led_6 (.in(n8bit_register_1_output[5]));
  LED led_7 (.in(n8bit_register_1_output[6]));
  LED led_8 (.in(n8bit_register_1_output[7]));
  LED led_9 (.in(n8bit_register_2_output[0]));
  LED led_10 (.in(n8bit_register_2_output[1]));
  LED led_11 (.in(n8bit_register_2_output[2]));
  LED led_12 (.in(n8bit_register_2_output[3]));
  LED led_13 (.in(n8bit_register_2_output[4]));
  LED led_14 (.in(n8bit_register_2_output[5]));
  LED led_15 (.in(n8bit_register_2_output[6]));
  LED led_16 (.in(n8bit_register_2_output[7]));
  triple_2_channel_demux triple_2_channel_demux_2 (
    .bx(triple_2_channel_demux_2_bx), .by(triple_2_channel_demux_2_by), .cy(triple_2_channel_demux_2_cy),
    .c_in(triple_2_channel_demux_2_ay), .cx(triple_2_channel_demux_2_cx), .enable(1'b1),
    .b_in(triple_2_channel_demux_2_ax), .a_in(triple_2_channel_demux_5_by), .ax(triple_2_channel_demux_2_ax),
    .ay(triple_2_channel_demux_2_ay), .A(Addr[1]), .B(Addr[0]), .C(Addr[0]));
  LED led_17 (.in(n8bit_register_3_output[0]));
  LED led_18 (.in(n8bit_register_3_output[1]));
  LED led_19 (.in(n8bit_register_3_output[2]));
  LED led_20 (.in(n8bit_register_3_output[3]));
  LED led_21 (.in(n8bit_register_3_output[4]));
  LED led_22 (.in(n8bit_register_3_output[5]));
  LED led_23 (.in(n8bit_register_3_output[6]));
  LED led_24 (.in(n8bit_register_3_output[7]));
  Hex_Inverter hex_inverter_2 (
    ._1(triple_2_channel_demux_3_bx), ._1_prime(hex_inverter_2__1_prime), ._2(triple_2_channel_demux_2_cy),
    ._2_prime(hex_inverter_2__2_prime), ._3(triple_2_channel_demux_2_cx), ._3_prime(hex_inverter_2__3_prime),
    ._4(triple_2_channel_demux_3_by), ._4_prime(hex_inverter_2__4_prime), ._5(triple_2_channel_demux_3_cx),
    ._5_prime(hex_inverter_2__5_prime), ._6(triple_2_channel_demux_3_cy), ._6_prime(hex_inverter_2__6_prime));
  _8bit_register u_8bit_register_9 (
    .M(1'b0), .N(1'b0), .\input (Data), .clock(clk_out), .CLR(quad_and_1__3y),
    .\output (n8bit_register_9_output), .G2(hex_inverter_2__1_prime), .G1(hex_inverter_2__1_prime));
  _8bit_register u_8bit_register_10 (
    .M(1'b0), .N(1'b0), .\input (Data), .clock(clk_out), .CLR(quad_and_1__3y),
    .\output (n8bit_register_10_output), .G2(hex_inverter_2__4_prime), .G1(hex_inverter_2__4_prime));
  _8bit_register u_8bit_register_11 (
    .M(1'b0), .N(1'b0), .\input (Data), .clock(clk_out), .CLR(quad_and_1__3y),
    .\output (n8bit_register_11_output), .G2(hex_inverter_2__5_prime), .G1(hex_inverter_2__5_prime));
  _8bit_register u_8bit_register_12 (
    .M(1'b0), .N(1'b0), .\input (Data), .clock(clk_out), .CLR(quad_and_1__3y),
    .\output (n8bit_register_12_output), .G2(hex_inverter_2__6_prime), .G1(hex_inverter_2__6_prime));
  triple_2_channel_demux triple_2_channel_demux_3 (
    .bx(triple_2_channel_demux_3_bx), .by(triple_2_channel_demux_3_by), .cy(triple_2_channel_demux_3_cy),
    .c_in(triple_2_channel_demux_3_ay), .cx(triple_2_channel_demux_3_cx), .enable(1'b1),
    .b_in(triple_2_channel_demux_3_ax), .a_in(triple_2_channel_demux_5_cx), .ax(triple_2_channel_demux_3_ax),
    .ay(triple_2_channel_demux_3_ay), .A(Addr[1]), .B(Addr[0]), .C(Addr[0]));
  LED led_25 (.in(n8bit_register_4_output[0]));
  LED led_26 (.in(n8bit_register_4_output[1]));
  LED led_27 (.in(n8bit_register_4_output[2]));
  LED led_28 (.in(n8bit_register_4_output[3]));
  LED led_29 (.in(n8bit_register_4_output[4]));
  LED led_30 (.in(n8bit_register_4_output[5]));
  LED led_31 (.in(n8bit_register_4_output[6]));
  LED led_32 (.in(n8bit_register_4_output[7]));
  Hex_Inverter hex_inverter_3 (
    ._1(triple_2_channel_demux_4_bx), ._1_prime(hex_inverter_3__1_prime), ._4(triple_2_channel_demux_4_by),
    ._4_prime(hex_inverter_3__4_prime), ._5(triple_2_channel_demux_4_cx), ._5_prime(hex_inverter_3__5_prime),
    ._6(triple_2_channel_demux_4_cy), ._6_prime(hex_inverter_3__6_prime));  // open: _2, _2_prime, _3, _3_prime
  _8bit_register u_8bit_register_13 (
    .M(1'b0), .N(1'b0), .\input (Data), .clock(clk_out), .CLR(quad_and_1__3y),
    .\output (n8bit_register_13_output), .G2(hex_inverter_3__1_prime), .G1(hex_inverter_3__1_prime));
  _8bit_register u_8bit_register_14 (
    .M(1'b0), .N(1'b0), .\input (Data), .clock(clk_out), .CLR(quad_and_1__3y),
    .\output (n8bit_register_14_output), .G2(hex_inverter_3__4_prime), .G1(hex_inverter_3__4_prime));
  _8bit_register u_8bit_register_15 (
    .M(1'b0), .N(1'b0), .\input (Data), .clock(clk_out), .CLR(quad_and_1__3y),
    .\output (n8bit_register_15_output), .G2(hex_inverter_3__5_prime), .G1(hex_inverter_3__5_prime));
  _8bit_register u_8bit_register_16 (
    .M(1'b0), .N(1'b0), .\input (Data), .clock(clk_out), .CLR(quad_and_1__3y),
    .\output (n8bit_register_16_output), .G2(hex_inverter_3__6_prime), .G1(hex_inverter_3__6_prime));
  LED led_33 (.in(n8bit_register_5_output[0]));
  LED led_34 (.in(n8bit_register_5_output[1]));
  LED led_35 (.in(n8bit_register_5_output[2]));
  LED led_36 (.in(n8bit_register_5_output[3]));
  LED led_37 (.in(n8bit_register_5_output[4]));
  LED led_38 (.in(n8bit_register_5_output[5]));
  LED led_39 (.in(n8bit_register_5_output[6]));
  LED led_40 (.in(n8bit_register_5_output[7]));
  triple_2_channel_demux triple_2_channel_demux_4 (
    .bx(triple_2_channel_demux_4_bx), .by(triple_2_channel_demux_4_by), .cy(triple_2_channel_demux_4_cy),
    .c_in(triple_2_channel_demux_4_ay), .cx(triple_2_channel_demux_4_cx), .enable(1'b1),
    .b_in(triple_2_channel_demux_4_ax), .a_in(triple_2_channel_demux_5_cy), .ax(triple_2_channel_demux_4_ax),
    .ay(triple_2_channel_demux_4_ay), .A(Addr[1]), .B(Addr[0]), .C(Addr[0]));
  triple_2_channel_demux triple_2_channel_demux_5 (
    .bx(triple_2_channel_demux_5_bx), .by(triple_2_channel_demux_5_by), .cy(triple_2_channel_demux_5_cy),
    .c_in(triple_2_channel_demux_5_ay), .cx(triple_2_channel_demux_5_cx), .enable(1'b1),
    .b_in(triple_2_channel_demux_5_ax), .a_in(Write), .ax(triple_2_channel_demux_5_ax),
    .ay(triple_2_channel_demux_5_ay), .A(Addr[3]), .B(Addr[2]), .C(Addr[2]));
  Quad_AND_Gate quad_and_1 (
    ._3a(Addr[4]), ._3b(Write), ._3y(quad_and_1__3y));  // open: _1a, _1b, _1y, _2a, _2b, _2y, _4a, _4b, _4y
  LED led_41 (.in(n8bit_register_6_output[0]));
  LED led_42 (.in(n8bit_register_6_output[1]));
  LED led_43 (.in(n8bit_register_6_output[2]));
  LED led_44 (.in(n8bit_register_6_output[3]));
  LED led_45 (.in(n8bit_register_6_output[4]));
  LED led_46 (.in(n8bit_register_6_output[5]));
  LED led_47 (.in(n8bit_register_6_output[6]));
  LED led_48 (.in(n8bit_register_6_output[7]));
  LED led_49 (.in(n8bit_register_7_output[0]));
  LED led_50 (.in(n8bit_register_7_output[1]));
  LED led_51 (.in(n8bit_register_7_output[2]));
  LED led_52 (.in(n8bit_register_7_output[3]));
  LED led_53 (.in(n8bit_register_7_output[4]));
  LED led_54 (.in(n8bit_register_7_output[5]));
  LED led_55 (.in(n8bit_register_7_output[6]));
  LED led_56 (.in(n8bit_register_7_output[7]));
  LED led_57 (.in(n8bit_register_8_output[0]));
  LED led_58 (.in(n8bit_register_8_output[1]));
  LED led_59 (.in(n8bit_register_8_output[2]));
  LED led_60 (.in(n8bit_register_8_output[3]));
  LED led_61 (.in(n8bit_register_8_output[4]));
  LED led_62 (.in(n8bit_register_8_output[5]));
  LED led_63 (.in(n8bit_register_8_output[6]));
  LED led_64 (.in(n8bit_register_8_output[7]));
  LED led_65 (.in(n8bit_register_9_output[0]));
  LED led_66 (.in(n8bit_register_9_output[1]));
  LED led_67 (.in(n8bit_register_9_output[2]));
  LED led_68 (.in(n8bit_register_9_output[3]));
  LED led_69 (.in(n8bit_register_9_output[4]));
  LED led_70 (.in(n8bit_register_9_output[5]));
  LED led_71 (.in(n8bit_register_9_output[6]));
  LED led_72 (.in(n8bit_register_9_output[7]));
  LED led_73 (.in(n8bit_register_10_output[0]));
  LED led_74 (.in(n8bit_register_10_output[1]));
  LED led_75 (.in(n8bit_register_10_output[2]));
  LED led_76 (.in(n8bit_register_10_output[3]));
  LED led_77 (.in(n8bit_register_10_output[4]));
  LED led_78 (.in(n8bit_register_10_output[5]));
  LED led_79 (.in(n8bit_register_10_output[6]));
  LED led_80 (.in(n8bit_register_10_output[7]));
  LED led_81 (.in(n8bit_register_11_output[0]));
  LED led_82 (.in(n8bit_register_11_output[1]));
  LED led_83 (.in(n8bit_register_11_output[2]));
  LED led_84 (.in(n8bit_register_11_output[3]));
  LED led_85 (.in(n8bit_register_11_output[4]));
  LED led_86 (.in(n8bit_register_11_output[5]));
  LED led_87 (.in(n8bit_register_11_output[6]));
  LED led_88 (.in(n8bit_register_11_output[7]));
  LED led_89 (.in(n8bit_register_12_output[0]));
  LED led_90 (.in(n8bit_register_12_output[1]));
  LED led_91 (.in(n8bit_register_12_output[2]));
  LED led_92 (.in(n8bit_register_12_output[3]));
  LED led_93 (.in(n8bit_register_12_output[4]));
  LED led_94 (.in(n8bit_register_12_output[5]));
  LED led_95 (.in(n8bit_register_12_output[6]));
  LED led_96 (.in(n8bit_register_12_output[7]));
  LED led_97 (.in(n8bit_register_13_output[0]));
  LED led_98 (.in(n8bit_register_13_output[1]));
  LED led_99 (.in(n8bit_register_13_output[2]));
  LED led_100 (.in(n8bit_register_13_output[3]));
  LED led_101 (.in(n8bit_register_13_output[4]));
  LED led_102 (.in(n8bit_register_13_output[5]));
  LED led_103 (.in(n8bit_register_13_output[6]));
  LED led_104 (.in(n8bit_register_13_output[7]));
  LED led_105 (.in(n8bit_register_14_output[0]));
  LED led_106 (.in(n8bit_register_14_output[1]));
  LED led_107 (.in(n8bit_register_14_output[2]));
  LED led_108 (.in(n8bit_register_14_output[3]));
  LED led_109 (.in(n8bit_register_14_output[4]));
  LED led_110 (.in(n8bit_register_14_output[5]));
  LED led_111 (.in(n8bit_register_14_output[6]));
  LED led_112 (.in(n8bit_register_14_output[7]));
  LED led_113 (.in(n8bit_register_15_output[0]));
  LED led_114 (.in(n8bit_register_15_output[1]));
  LED led_115 (.in(n8bit_register_15_output[2]));
  LED led_116 (.in(n8bit_register_15_output[3]));
  LED led_117 (.in(n8bit_register_15_output[4]));
  LED led_118 (.in(n8bit_register_15_output[5]));
  LED led_119 (.in(n8bit_register_15_output[6]));
  LED led_120 (.in(n8bit_register_15_output[7]));
  LED led_121 (.in(n8bit_register_16_output[0]));
  LED led_122 (.in(n8bit_register_16_output[1]));
  LED led_123 (.in(n8bit_register_16_output[2]));
  LED led_124 (.in(n8bit_register_16_output[3]));
  LED led_125 (.in(n8bit_register_16_output[4]));
  LED led_126 (.in(n8bit_register_16_output[5]));
  LED led_127 (.in(n8bit_register_16_output[6]));
  LED led_128 (.in(n8bit_register_16_output[7]));
endmodule

module Clock_Reg (
  input  Reset,
  input  Clock,
  input  OCL_Enable,
  input  [7:0] MSB,
  input  [7:0] LSB,
  output [13:0] out_6
);

  wire [7:6] n8bit_register_1_output;

  _8bit_register u_8bit_register_1 (
    .M(1'b0), .N(1'b0), .\input (MSB), .clock(Clock), .CLR(Reset),
    .\output ({n8bit_register_1_output, out_6[13:8]}), .G2(OCL_Enable), .G1(OCL_Enable));
  _8bit_register u_8bit_register_2 (
    .M(1'b0), .N(1'b0), .\input (LSB), .clock(Clock), .CLR(Reset), .\output (out_6[7:0]), .G2(OCL_Enable),
    .G1(OCL_Enable));
endmodule
