// Logisim project version-CH3.circ as structural Verilog
module main_v3 (
  output [15:0] out_1
);

  wire alu_v4_1_nequal_zero_2, clock_1_out, clock_2_system_clock, control_v2_1_clear_registers,
       control_v2_1_load_saved_pc, control_v2_1_n_anything_else, control_v2_1_nenable_interrupts,
       control_v2_1_nequal_zero_2, control_v2_1_nload_pc_lsb, control_v2_1_nload_pc_msb,
       control_v2_1_ocl_enable_reg, control_v2_1_page_reg_write_enable, control_v2_1_ram_w_to,
       control_v2_1_subtract_____add, Interrupt_ninterrupt, pc_1_interrupt_occured, reg_selecter_1__14,
       reg_selecter_1_out_12, reg_selecter_1_out_16, reg_selecter_1_out_18, RESET_out, undriven;
  wire [2:0] control_v2_1_to_read_reg_1, control_v2_1_to_read_reg_2;
  wire [3:0] A_read, A_read_2, B_read, B_read_2, C_read, C_read_2, control_v2_1_alu_control_bits,
       control_v2_1_enable_reg_write, control_v2_1_write_mux_control_bits, counter_1_q, counter_1_q_2,
       D_read, D_read_2, n8bit_16_input_multiplexer_1_out_21, n8bit_16_input_multiplexer_1_out_21_2,
       Page_Register_read, Page_Register_read_2, pc_1_pc_value, pc_1_pc_value_2, pc_1_pc_value_3;
  wire [6:0] keyboard_1_data;
  wire [7:0] alu_v4_1_output, clock_reg_1_lsb_2, clock_reg_1_msb_2, control_v2_1_const_out,
       control_v2_1_const_out_2, display_1_out_6, display_1_out_7, display_1_out_8, display_1_out_9,
       display_1_out_10, display_1_out_11, display_1_out_12, display_1_out_13, display_1_out_14,
       display_1_out_15, display_1_out_16, display_1_out_17, display_1_out_18, display_1_out_19,
       display_1_out_20, display_1_out_21, display_driver_1_out_4, Interrupt_output,
       n8bit_5_input_multiplexer_1_out_9, n8bit_6_input_multiplexer_1_out_10, ram_v2_1_out;
  wire [15:8] counter_1_q_3;
  wire [15:12] pc_1_pc_value_4;
  wire [23:0] rom_1_instruction;

  Hex_Digit_Display hex_digit_display_1 (.value(counter_1_q_3[15:12]));  // open: dp
  Clock_part clock_1 (.out(clock_1_out));
  Hex_Digit_Display hex_digit_display_2 (.value(pc_1_pc_value_4));  // open: dp
  Keyboard keyboard_1 (.clk(clock_2_system_clock), .re(1'b1), .clr(undriven), .data(keyboard_1_data));  // open: avail
  Hex_Digit_Display hex_digit_display_3 (.value(counter_1_q_3[11:8]));  // open: dp
  Hex_Digit_Display hex_digit_display_4 (.value(counter_1_q_2));  // open: dp
  Hex_Digit_Display hex_digit_display_5 (.value(pc_1_pc_value_3));  // open: dp
  Hex_Digit_Display hex_digit_display_6 (.value(pc_1_pc_value_2));  // open: dp
  Button RESET (.out(RESET_out));
  Clock clock_2 (.Clock_Input(clock_1_out), .System_Clock(clock_2_system_clock));  // open: Display_Clock
  Hex_Digit_Display hex_digit_display_7 (.value(counter_1_q));  // open: dp
  Counter #(.width(16), .max('hffff)) counter_1 (
    .load(1'b0), .D({16{1'b1}}), .count(1'b1), .Q({counter_1_q_3, counter_1_q_2, counter_1_q}),
    .clk(clock_1_out));  // open: carry, clr
  Hex_Digit_Display hex_digit_display_8 (.value(pc_1_pc_value));  // open: dp
  PC pc_1 (
    .write_byte(n8bit_6_input_multiplexer_1_out_10), .Reset_PC(RESET_out),
    .nLoad_MSB(control_v2_1_nload_pc_msb), .nLoad_LSB(control_v2_1_nload_pc_lsb),
    .nInterrupt(Interrupt_ninterrupt), .Load_Saved_PC(control_v2_1_load_saved_pc), .Clock(clock_1_out),
    .Enable_nInterrupts(control_v2_1_nenable_interrupts),
    .PC_value({pc_1_pc_value_4, pc_1_pc_value_3, pc_1_pc_value_2, pc_1_pc_value}),
    .Interrupt_Occured(pc_1_interrupt_occured));
  Interrupt Interrupt (
    .clock(clock_1_out), .CLR_Reg(control_v2_1_load_saved_pc), .Interrupt_Occured(pc_1_interrupt_occured),
    .Input(keyboard_1_data), .ninterrupt(Interrupt_ninterrupt), .Output(Interrupt_output));
  Reg_selecter reg_selecter_1 (
    .S0(control_v2_1_enable_reg_write[0]), .S1(control_v2_1_enable_reg_write[1]),
    .S2(control_v2_1_enable_reg_write[2]), .S3(control_v2_1_enable_reg_write[3]),
    .out_12(reg_selecter_1_out_12), .out_16(reg_selecter_1_out_16), .out_18(reg_selecter_1_out_18),
    ._14(reg_selecter_1__14));  // open: _0, out_6, out_7, out_8, out_9, out_10, out_11, out_13, out_14, out_15, out_17
  ROM rom_1 (
    .PC_Address({pc_1_pc_value_4, pc_1_pc_value_3, pc_1_pc_value_2, pc_1_pc_value}),
    .Instruction(rom_1_instruction));
  Hex_Digit_Display hex_digit_display_9 (.value(A_read_2));  // open: dp
  Control_v2 control_v2_1 (
    .Instruction_Input(rom_1_instruction), .nEqual_Zero(alu_v4_1_nequal_zero_2), .CLK(clock_1_out),
    .Page_Reg_Write_Enable(control_v2_1_page_reg_write_enable), .RAM_W_To(control_v2_1_ram_w_to),
    .Enable_reg_write(control_v2_1_enable_reg_write), .Clear_Registers(control_v2_1_clear_registers),
    .nLoad_PC_MSB(control_v2_1_nload_pc_msb), .nLoad_PC_LSB(control_v2_1_nload_pc_lsb),
    .Load_Saved_PC(control_v2_1_load_saved_pc), .nEqual_Zero_2(control_v2_1_nequal_zero_2),
    .subtract_____add(control_v2_1_subtract_____add), .ALU_Control_Bits(control_v2_1_alu_control_bits),
    .n_anything_else(control_v2_1_n_anything_else), .OCL_Enable_Reg(control_v2_1_ocl_enable_reg),
    .nEnable_Interrupts(control_v2_1_nenable_interrupts),
    .Write_Mux_Control_Bits(control_v2_1_write_mux_control_bits), .To_read_reg_1(control_v2_1_to_read_reg_1),
    .To_read_reg_2(control_v2_1_to_read_reg_2), .Const_Out(control_v2_1_const_out),
    .Const_Out_2(control_v2_1_const_out_2));
  Display_Driver display_driver_1 (
    .in_1(n8bit_6_input_multiplexer_1_out_10), .Clock(clock_1_out), .W_To(control_v2_1_ram_w_to),
    .out_4(display_driver_1_out_4));
  Hex_Digit_Display hex_digit_display_10 (.value(A_read));  // open: dp
  Hex_Digit_Display hex_digit_display_11 (.value(B_read));  // open: dp
  Hex_Digit_Display hex_digit_display_12 (.value(B_read_2));  // open: dp
  DotMatrix #(.matrixcols(16), .matrixrows(8)) dotmatrix_1 (
    .col0(display_1_out_6), .col1(display_1_out_7), .col2(display_1_out_8), .col3(display_1_out_9),
    .col4(display_1_out_10), .col5(display_1_out_11), .col6(display_1_out_12), .col7(display_1_out_13),
    .col8(display_1_out_14), .col9(display_1_out_15), .col10(display_1_out_16), .col11(display_1_out_17),
    .col12(display_1_out_18), .col13(display_1_out_19), .col14(display_1_out_20), .col15(display_1_out_21));
  Display display_1 (
    .CLR(control_v2_1_clear_registers), .Write(control_v2_1_ram_w_to), .Addr(display_driver_1_out_4),
    .Data(n8bit_5_input_multiplexer_1_out_9), .clk(clock_1_out), .out_6(display_1_out_6),
    .out_7(display_1_out_7), .out_8(display_1_out_8), .out_9(display_1_out_9), .out_10(display_1_out_10),
    .out_11(display_1_out_11), .out_12(display_1_out_12), .out_13(display_1_out_13),
    .out_14(display_1_out_14), .out_15(display_1_out_15), .out_16(display_1_out_16),
    .out_17(display_1_out_17), .out_18(display_1_out_18), .out_19(display_1_out_19),
    .out_20(display_1_out_20), .out_21(display_1_out_21));
  registers A (
    .Read({A_read_2, A_read}),
    .Write({n8bit_16_input_multiplexer_1_out_21_2, n8bit_16_input_multiplexer_1_out_21}),
    .Clock(clock_1_out), .Clear(control_v2_1_clear_registers), .EW(reg_selecter_1__14));
  registers B (
    .Read({B_read_2, B_read}),
    .Write({n8bit_16_input_multiplexer_1_out_21_2, n8bit_16_input_multiplexer_1_out_21}),
    .Clock(clock_1_out), .Clear(control_v2_1_clear_registers), .EW(reg_selecter_1_out_18));
  RAM_v2 ram_v2_1 (
    .CLR(control_v2_1_clear_registers), .W__nR(control_v2_1_ram_w_to),
    .AddrU({Page_Register_read_2, Page_Register_read}), .AddrL(n8bit_6_input_multiplexer_1_out_10),
    .Data(n8bit_5_input_multiplexer_1_out_9), .Clock(clock_1_out), .Out(ram_v2_1_out));
  Hex_Digit_Display hex_digit_display_13 (.value(n8bit_16_input_multiplexer_1_out_21_2));  // open: dp
  _8bit_16_input_multiplexer u_8bit_16_input_multiplexer_1 (
    .Input_0({8{1'b0}}), .Input_1(ram_v2_1_out), .Input_2(n8bit_5_input_multiplexer_1_out_9),
    .Input_3(alu_v4_1_output), .Input_4({Page_Register_read_2, Page_Register_read}),
    .Input_5(Interrupt_output), .Input_6(clock_reg_1_lsb_2), .Input_7(clock_reg_1_msb_2),
    .out_21({n8bit_16_input_multiplexer_1_out_21_2, n8bit_16_input_multiplexer_1_out_21}),
    .S3(control_v2_1_write_mux_control_bits[3]), .S2(control_v2_1_write_mux_control_bits[2]),
    .S1(control_v2_1_write_mux_control_bits[1]), .S0(control_v2_1_write_mux_control_bits[0]));  // open: Input_8, Input_9, Input_10, Input_11, Input_12, Input_13, Input_14, Input_15
  Hex_Digit_Display hex_digit_display_14 (.value(n8bit_16_input_multiplexer_1_out_21));  // open: dp
  _8bit_5_input_multiplexer u_8bit_5_input_multiplexer_1 (
    .Input_0(control_v2_1_const_out), .Input_1({B_read_2, B_read}), .Input_2({A_read_2, A_read}),
    .Input_3({C_read_2, C_read}), .Input_4({D_read_2, D_read}), .out_9(n8bit_5_input_multiplexer_1_out_9),
    .S2(control_v2_1_to_read_reg_1[2]), .S1(control_v2_1_to_read_reg_1[1]), .S0(control_v2_1_to_read_reg_1[0]));
  _8bit_6_input_multiplexer u_8bit_6_input_multiplexer_1 (
    .Input_0(control_v2_1_const_out), .Input_1({B_read_2, B_read}), .Input_2({A_read_2, A_read}),
    .Input_3({C_read_2, C_read}), .Input_4({D_read_2, D_read}), .Input_7(control_v2_1_const_out_2),
    .out_10(n8bit_6_input_multiplexer_1_out_10), .S2(control_v2_1_to_read_reg_2[2]),
    .S1(control_v2_1_to_read_reg_2[1]), .S0(control_v2_1_to_read_reg_2[0]));
  registers D (
    .Read({D_read_2, D_read}),
    .Write({n8bit_16_input_multiplexer_1_out_21_2, n8bit_16_input_multiplexer_1_out_21}),
    .Clock(clock_1_out), .Clear(control_v2_1_clear_registers), .EW(reg_selecter_1_out_12));
  registers C (
    .Read({C_read_2, C_read}),
    .Write({n8bit_16_input_multiplexer_1_out_21_2, n8bit_16_input_multiplexer_1_out_21}),
    .Clock(clock_1_out), .Clear(control_v2_1_clear_registers), .EW(reg_selecter_1_out_16));
  Hex_Digit_Display hex_digit_display_15 (.value(D_read));  // open: dp
  Hex_Digit_Display hex_digit_display_16 (.value(D_read_2));  // open: dp
  Hex_Digit_Display hex_digit_display_17 (.value(C_read));  // open: dp
  Hex_Digit_Display hex_digit_display_18 (.value(C_read_2));  // open: dp
  ALU_v4 alu_v4_1 (
    .Input_1(n8bit_5_input_multiplexer_1_out_9), .Input_2(n8bit_6_input_multiplexer_1_out_10),
    .nEqual_Zero(control_v2_1_nequal_zero_2), .Subtract_nAdd(control_v2_1_subtract_____add),
    .ALU_Control_Bits(control_v2_1_alu_control_bits), .anything_else(control_v2_1_n_anything_else),
    .Output(alu_v4_1_output), .nEqual_Zero_2(alu_v4_1_nequal_zero_2));
  Clock_Reg clock_reg_1 (
    .OCL_Enable(control_v2_1_ocl_enable_reg), .MSB(n8bit_6_input_multiplexer_1_out_10),
    .LSB(n8bit_5_input_multiplexer_1_out_9), .Clock(clock_1_out), .Clear(control_v2_1_clear_registers),
    .out_6(out_1), .LSB_2(clock_reg_1_lsb_2), .MSB_2(clock_reg_1_msb_2));
  registers Page_Register (
    .Read({Page_Register_read_2, Page_Register_read}), .Write(n8bit_6_input_multiplexer_1_out_10),
    .Clock(clock_1_out), .Clear(control_v2_1_clear_registers), .EW(control_v2_1_page_reg_write_enable));
  Hex_Digit_Display hex_digit_display_19 (.value(Page_Register_read));  // open: dp
  Hex_Digit_Display hex_digit_display_20 (.value(Page_Register_read_2));  // open: dp

  // Notes on the sheet:
  //   Num Of Clock Cycles
  //   PC Value
  //   Reg A
  //   Reg B
  //   Write Bus
  //   Reg D
  //   Reg C
  //   OCL reg
  //   Page reg
endmodule

// Reg
module registers (
  input  Clock,
  input  Clear,
  input  [7:0] Write,
  input  EW,
  output [7:0] Read
);

  _8bit_register u_8bit_register_1 (
    .M(1'b0), .N(1'b0), .\input (Write), .clock(Clock), .CLR(Clear), .\output (Read), .G2(EW), .G1(EW));
endmodule

// ALU
module ALU_v2 (
  input  [7:0] Input_1,
  input  [7:0] Input_2,
  input  nEqual_Zero,
  input  Subtract_nAdd,
  input  And___Or,
  input  in_6,
  input  addition_n_logical____not,
  input  logical___not,
  input  regular_n_logical_comparison____shift,
  input  shift____logical_control1,
  input  shift____logical_control2,
  output [7:0] Output,
  output nEqual_Zero_2
);

  wire adder_2_carry, quad_or_1__1y, quad_or_1__2y, quad_or_1__3y, quad_or_1__4y, quad_or_2__1y,
       quad_or_2__2y, quad_or_2__4y;
  wire [0:0] n8bit_5_input_multiplexer_1_p1, n8bit_5_input_multiplexer_1_p3;
  wire [7:0] adder_2_output, adder_output, And_out, mux_output, n8bit_2_input_multiplexer_1_output,
       n8bit_2_input_multiplexer_2_output, n8bit_3_input_multiplexer_1_p6, n8bit_and_out, n8bit_or_out,
       xor_write;

  _8bit_AND_Gate And (.In_2(Input_2), .In_1({8{nEqual_Zero}}), .Out(And_out));
  _8bit_XOR \xor  (.Read_1(And_out), .Read_2({8{1'b1}}), .Write(xor_write));
  _8bit_AND_Gate u_8bit_and (.In_2(Input_1), .In_1(And_out), .Out(n8bit_and_out));
  _8bit_OR_Gate u_8bit_or (.In_2(Input_1), .In_1(And_out), .Out(n8bit_or_out));
  _8bit_adder adder (.Input1(xor_write), .Input_2(8'h1), .Output(adder_output), .Carry(shift____logical_control1));
  _8bit_2_input_multiplexer mux (
    .Input_1(adder_output), .Input_2(And_out), .Output(mux_output), .Control(Subtract_nAdd));
  _8bit_2_input_multiplexer u_8bit_2_input_multiplexer_1 (
    .Input_1(n8bit_and_out), .Input_2(n8bit_or_out), .Output(n8bit_2_input_multiplexer_1_output),
    .Control(And___Or));
  _8bit_2_input_multiplexer u_8bit_2_input_multiplexer_2 (
    .Input_1({Input_1[7], Input_1[5:0], 1'b0}), .Input_2({{2{Input_1[7]}}, Input_1[6:1]}),
    .Output(n8bit_2_input_multiplexer_2_output), .Control(in_6));
  _8bit_adder adder_2 (.Input1(Input_1), .Input_2(mux_output), .Output(adder_2_output), .Carry(adder_2_carry));
  // _8bit_3_input_multiplexer 8bit_3_input_multiplexer_1: pin names not known; wires that end beside it: xor_write, n8bit_2_input_multiplexer_1_output, adder_2_output, addition_n_logical____not, logical___not, n8bit_3_input_multiplexer_1_p6
  Quad_OR_Gate quad_or_1 (
    ._1a(n8bit_3_input_multiplexer_1_p6[0]), ._1b(n8bit_3_input_multiplexer_1_p6[1]), ._1y(quad_or_1__1y),
    ._2a(n8bit_3_input_multiplexer_1_p6[2]), ._2b(n8bit_3_input_multiplexer_1_p6[3]), ._2y(quad_or_1__2y),
    ._3a(n8bit_3_input_multiplexer_1_p6[4]), ._3b(n8bit_3_input_multiplexer_1_p6[5]), ._3y(quad_or_1__3y),
    ._4a(n8bit_3_input_multiplexer_1_p6[6]), ._4b(n8bit_3_input_multiplexer_1_p6[7]), ._4y(quad_or_1__4y));
  // _8bit_5_input_multiplexer 8bit_5_input_multiplexer_1: pin names not known; wires that end beside it: {{7{1'b0}}, n8bit_5_input_multiplexer_1_p1[0]}, {{7{1'b0}}, nEqual_Zero_2}, {{7{1'b0}}, n8bit_5_input_multiplexer_1_p3[0]}, n8bit_2_input_multiplexer_2_output, n8bit_3_input_multiplexer_1_p6, regular_n_logical_comparison____shift, shift____logical_control1, shift____logical_control2, Output
  Quad_AND_Gate quad_and_1 (
    ._4a(n8bit_5_input_multiplexer_1_p1[0]), ._4b(quad_or_2__4y), ._4y(n8bit_5_input_multiplexer_1_p3[0]));  // open: _1a, _1b, _1y, _2a, _2b, _2y, _3a, _3b, _3y
  Quad_OR_Gate quad_or_2 (
    ._1a(quad_or_1__3y), ._1b(quad_or_1__4y), ._1y(quad_or_2__1y), ._2a(quad_or_1__1y), ._2b(quad_or_1__2y),
    ._2y(quad_or_2__2y), ._3a(shift____logical_control1), ._3b(adder_2_carry),
    ._3y(n8bit_5_input_multiplexer_1_p1[0]), ._4a(quad_or_2__1y), ._4b(quad_or_2__2y), ._4y(quad_or_2__4y));
  Hex_Inverter hex_inverter_1 (
    ._2(quad_or_2__4y), ._2_prime(nEqual_Zero_2));  // open: _1, _1_prime, _3, _3_prime, _4, _4_prime, _5, _5_prime, _6, _6_prime

  // Notes on the sheet:
  //   >=
  //   =
  //   >
endmodule

module ALU_v3 (
  input  [7:0] Input_1,
  input  [7:0] Input_2,
  input  nEqual_Zero,
  input  Subtract_nAdd,
  input  ALU_Control_1,
  input  ALU_Control_1_2,
  input  ALU_Control_1_3,
  input  ALU_Control_1_4,
  input  anything_else,
  output [7:0] Output,
  output nEqual_Zero_2
);

  wire adder_2_carry, adder_carry, hex_inverter_1__5_prime, hex_inverter_1__6_prime, quad_or_1__1y,
       quad_or_1__2y, quad_or_1__3y, quad_or_1__4y, quad_or_2__1y, quad_or_2__2y, quad_or_2__4y;
  wire [0:0] quad_and_1__4y, quad_or_2__3y;
  wire [7:0] adder_2_output, adder_output, And_out, mux_output, n8bit_and_out, n8bit_or_out, xor_write;
  wire [7:7] triple_2_channel_mux_1_a_out, triple_2_channel_mux_1_b_out;

  _8bit_AND_Gate And (.In_2(Input_2), .In_1({8{nEqual_Zero}}), .Out(And_out));
  _8bit_adder adder (.Input1(xor_write), .Input_2(8'h1), .Output(adder_output), .Carry(adder_carry));
  _8bit_XOR \xor  (.Read_1({triple_2_channel_mux_1_b_out[7], And_out[6:0]}), .Read_2({8{1'b1}}), .Write(xor_write));
  _8bit_AND_Gate u_8bit_and (.In_2(Input_1), .In_1(And_out), .Out(n8bit_and_out));
  _8bit_OR_Gate u_8bit_or (.In_2(Input_1), .In_1(And_out), .Out(n8bit_or_out));
  _8bit_2_input_multiplexer mux (
    .Input_1(adder_output), .Input_2(And_out), .Output(mux_output), .Control(Subtract_nAdd));
  Hex_Inverter hex_inverter_1 (
    ._5(And_out[7]), ._5_prime(hex_inverter_1__5_prime), ._6(Input_1[7]), ._6_prime(hex_inverter_1__6_prime));  // open: _1, _1_prime, _2, _2_prime, _3, _3_prime, _4, _4_prime
  _8bit_adder adder_2 (
    .Input1({triple_2_channel_mux_1_a_out[7], Input_1[6:0]}), .Input_2(mux_output), .Output(adder_2_output),
    .Carry(adder_2_carry));
  triple_2_channel_mux triple_2_channel_mux_1 (
    .bx(And_out[7]), .by(hex_inverter_1__5_prime), .b_out(triple_2_channel_mux_1_b_out[7]),
    .a_out(triple_2_channel_mux_1_a_out[7]), .ax(Input_1[7]), .ay(hex_inverter_1__6_prime),
    .A(anything_else), .B(anything_else));  // open: cy, c_out, cx, enable, C
  _8bit_16_input_multiplexer u_8bit_16_input_multiplexer_1 (
    .Input_0(adder_2_output), .Input_1({{7{1'b0}}, quad_or_2__3y[0]}), .Input_2({{7{1'b0}}, nEqual_Zero_2}),
    .Input_3({{7{1'b0}}, quad_and_1__4y[0]}), .Input_4({Input_1[7], Input_1[5:0], 1'b0}),
    .Input_5({{2{Input_1[7]}}, Input_1[6:1]}), .Input_6({Input_1[6:0], 1'b0}),
    .Input_7({1'b0, Input_1[7:1]}), .Input_8(xor_write), .Input_9(n8bit_and_out), .Input_10(n8bit_or_out),
    .Input_11({Input_1[6:0], Input_1[7]}), .Input_12({Input_1[0], Input_1[7:1]}), .out_21(Output),
    .S3(ALU_Control_1_4), .S2(ALU_Control_1_3), .S1(ALU_Control_1_2), .S0(ALU_Control_1));  // open: Input_13, Input_14, Input_15
  Quad_OR_Gate quad_or_1 (
    ._1a(adder_2_output[0]), ._1b(adder_2_output[1]), ._1y(quad_or_1__1y), ._2a(adder_2_output[2]),
    ._2b(adder_2_output[3]), ._2y(quad_or_1__2y), ._3a(adder_2_output[4]), ._3b(adder_2_output[5]),
    ._3y(quad_or_1__3y), ._4a(adder_2_output[6]), ._4b(adder_2_output[7]), ._4y(quad_or_1__4y));
  Quad_AND_Gate quad_and_1 (
    ._4a(quad_or_2__3y[0]), ._4b(quad_or_2__4y), ._4y(quad_and_1__4y[0]));  // open: _1a, _1b, _1y, _2a, _2b, _2y, _3a, _3b, _3y
  Quad_OR_Gate quad_or_2 (
    ._1a(quad_or_1__3y), ._1b(quad_or_1__4y), ._1y(quad_or_2__1y), ._2a(quad_or_1__1y), ._2b(quad_or_1__2y),
    ._2y(quad_or_2__2y), ._3a(adder_carry), ._3b(adder_2_carry), ._3y(quad_or_2__3y[0]), ._4a(quad_or_2__1y),
    ._4b(quad_or_2__2y), ._4y(quad_or_2__4y));
  Hex_Inverter hex_inverter_2 (
    ._2(quad_or_2__4y), ._2_prime(nEqual_Zero_2));  // open: _1, _1_prime, _3, _3_prime, _4, _4_prime, _5, _5_prime, _6, _6_prime

  // Notes on the sheet:
  //   >=
  //   =
  //   >
endmodule

// ALU
module ALU_v4 (
  input  [7:0] Input_1,
  input  [7:0] Input_2,
  input  nEqual_Zero,
  input  Subtract_nAdd,
  input  [3:0] ALU_Control_Bits,
  input  anything_else,
  output [7:0] Output,
  output nEqual_Zero_2
);

  wire adder_2_carry, adder_carry, hex_inverter_1__5_prime, hex_inverter_1__6_prime, quad_or_1__1y,
       quad_or_1__2y, quad_or_1__3y, quad_or_1__4y, quad_or_2__1y, quad_or_2__2y, quad_or_2__4y;
  wire [0:0] quad_and_1__4y, quad_or_2__3y;
  wire [7:0] adder_2_output, adder_output, And_out, mux_output, n8bit_and_out, n8bit_or_out, xor_write;
  wire [7:7] triple_2_channel_mux_1_a_out, triple_2_channel_mux_1_b_out;

  _8bit_AND_Gate And (.In_2(Input_2), .In_1({8{nEqual_Zero}}), .Out(And_out));
  _8bit_XOR \xor  (.Read_1({triple_2_channel_mux_1_b_out[7], And_out[6:0]}), .Read_2({8{1'b1}}), .Write(xor_write));
  _8bit_adder adder (.Input1(xor_write), .Input_2(8'h1), .Output(adder_output), .Carry(adder_carry));
  _8bit_AND_Gate u_8bit_and (.In_2(Input_1), .In_1(And_out), .Out(n8bit_and_out));
  _8bit_OR_Gate u_8bit_or (.In_2(Input_1), .In_1(And_out), .Out(n8bit_or_out));
  _8bit_2_input_multiplexer mux (
    .Input_1(adder_output), .Input_2(And_out), .Output(mux_output), .Control(Subtract_nAdd));
  Hex_Inverter hex_inverter_1 (
    ._5(And_out[7]), ._5_prime(hex_inverter_1__5_prime), ._6(Input_1[7]), ._6_prime(hex_inverter_1__6_prime));  // open: _1, _1_prime, _2, _2_prime, _3, _3_prime, _4, _4_prime
  _8bit_adder adder_2 (
    .Input1({triple_2_channel_mux_1_a_out[7], Input_1[6:0]}), .Input_2(mux_output), .Output(adder_2_output),
    .Carry(adder_2_carry));
  triple_2_channel_mux triple_2_channel_mux_1 (
    .bx(And_out[7]), .by(hex_inverter_1__5_prime), .b_out(triple_2_channel_mux_1_b_out[7]),
    .a_out(triple_2_channel_mux_1_a_out[7]), .ax(Input_1[7]), .ay(hex_inverter_1__6_prime),
    .A(anything_else), .B(anything_else));  // open: cy, c_out, cx, enable, C
  _8bit_16_input_multiplexer u_8bit_16_input_multiplexer_1 (
    .Input_0(adder_2_output), .Input_1({{7{1'b0}}, quad_or_2__3y[0]}), .Input_2({{7{1'b0}}, nEqual_Zero_2}),
    .Input_3({{7{1'b0}}, quad_and_1__4y[0]}), .Input_4({Input_1[7], Input_1[5:0], 1'b0}),
    .Input_5({{2{Input_1[7]}}, Input_1[6:1]}), .Input_6({Input_1[6:0], 1'b0}),
    .Input_7({1'b0, Input_1[7:1]}), .Input_8(xor_write), .Input_9(n8bit_and_out), .Input_10(n8bit_or_out),
    .Input_11({Input_1[6:0], Input_1[7]}), .Input_12({Input_1[0], Input_1[7:1]}), .Input_13(adder_output),
    .out_21(Output), .S3(ALU_Control_Bits[3]), .S2(ALU_Control_Bits[2]), .S1(ALU_Control_Bits[1]),
    .S0(ALU_Control_Bits[0]));  // open: Input_14, Input_15
  Quad_OR_Gate quad_or_1 (
    ._1a(adder_2_output[0]), ._1b(adder_2_output[1]), ._1y(quad_or_1__1y), ._2a(adder_2_output[2]),
    ._2b(adder_2_output[3]), ._2y(quad_or_1__2y), ._3a(adder_2_output[4]), ._3b(adder_2_output[5]),
    ._3y(quad_or_1__3y), ._4a(adder_2_output[6]), ._4b(adder_2_output[7]), ._4y(quad_or_1__4y));
  Quad_AND_Gate quad_and_1 (
    ._4a(quad_or_2__3y[0]), ._4b(quad_or_2__4y), ._4y(quad_and_1__4y[0]));  // open: _1a, _1b, _1y, _2a, _2b, _2y, _3a, _3b, _3y
  Quad_OR_Gate quad_or_2 (
    ._1a(quad_or_1__3y), ._1b(quad_or_1__4y), ._1y(quad_or_2__1y), ._2a(quad_or_1__1y), ._2b(quad_or_1__2y),
    ._2y(quad_or_2__2y), ._3a(adder_carry), ._3b(adder_2_carry), ._3y(quad_or_2__3y[0]), ._4a(quad_or_2__1y),
    ._4b(quad_or_2__2y), ._4y(quad_or_2__4y));
  Hex_Inverter hex_inverter_2 (
    ._2(quad_or_2__4y), ._2_prime(nEqual_Zero_2));  // open: _1, _1_prime, _3, _3_prime, _4, _4_prime, _5, _5_prime, _6, _6_prime

  // Notes on the sheet:
  //   >=
  //   =
  //   >
endmodule

module Input (
  input  Input,
  input  Clear_Reg,
  input  Clock,
  output out_4,
  output nInterrupt
);

  wire hex_inverter_1__4_prime, hex_inverter_1__5_prime, hex_inverter_1__6_prime, n4bit_register_1__1d,
       n4bit_register_1__2d, quad_and_1__1y, quad_and_1__2y, quad_and_1__4y;

  Quad_AND_Gate quad_and_1 (
    ._1a(Input), ._1b(quad_and_1__4y), ._1y(quad_and_1__1y), ._2a(quad_and_1__1y),
    ._2b(hex_inverter_1__6_prime), ._2y(quad_and_1__2y), ._4a(hex_inverter_1__4_prime),
    ._4b(n4bit_register_1__1d), ._4y(quad_and_1__4y));  // open: _3a, _3b, _3y
  Hex_Inverter hex_inverter_1 (
    ._1(quad_and_1__2y), ._1_prime(nInterrupt), ._4(n4bit_register_1__2d),
    ._4_prime(hex_inverter_1__4_prime), ._5(quad_and_1__1y), ._5_prime(hex_inverter_1__5_prime), ._6(out_4),
    ._6_prime(hex_inverter_1__6_prime));  // open: _2, _2_prime, _3, _3_prime
  _4bit_register u_4bit_register_1 (
    .M(1'b0), .N(1'b0), ._1Q(Input), ._2Q(n4bit_register_1__1d), .CLK(Clock), .CLR(1'b0),
    ._1D(n4bit_register_1__1d), ._2D(n4bit_register_1__2d), .G2(1'b0), .G1(1'b0));  // open: _3Q, _4Q, _3D, _4D
  _4bit_register u_4bit_register_2 (
    .M(1'b0), .N(1'b0), ._1Q(Input), .CLK(Clock), .CLR(Clear_Reg), ._1D(out_4), .G2(hex_inverter_1__5_prime),
    .G1(hex_inverter_1__5_prime));  // open: _2Q, _3Q, _4Q, _2D, _3D, _4D
endmodule

module Input_v2 (
  input  Input,
  input  nInterrupt_Occured,
  input  Clear_Reg,
  input  Clock,
  output Reg_bit,
  output nInterrupt
);

  wire hex_inverter_1__1_prime, hex_inverter_1__4_prime, n4bit_register_1__1d, n4bit_register_1__2d,
       quad_and_1__1y, quad_and_1__2y, quad_or_1__1y, triple_2_channel_mux_1_a_out,
       triple_2_channel_mux_1_b_out, triple_2_channel_mux_1_c_out;

  Quad_AND_Gate quad_and_1 (
    ._1a(Input), ._1b(hex_inverter_1__4_prime), ._1y(quad_and_1__1y), ._2a(quad_and_1__1y), ._2b(1'b1),
    ._2y(quad_and_1__2y), ._3a(n4bit_register_1__2d));  // open: _3b, _3y, _4a, _4b, _4y
  Hex_Inverter hex_inverter_1 (
    ._1(nInterrupt_Occured), ._1_prime(hex_inverter_1__1_prime), ._4(n4bit_register_1__1d),
    ._4_prime(hex_inverter_1__4_prime), ._5(n4bit_register_1__2d), ._5_prime(nInterrupt));  // open: _2, _2_prime, _3, _3_prime, _6, _6_prime
  Quad_OR_Gate quad_or_1 (
    ._1a(quad_and_1__2y), ._1b(triple_2_channel_mux_1_b_out), ._1y(quad_or_1__1y));  // open: _2a, _2b, _2y, _3a, _3b, _3y, _4a, _4b, _4y
  triple_2_channel_mux triple_2_channel_mux_1 (
    .bx(n4bit_register_1__2d), .by(1'b0), .cy(1'b0), .c_out(triple_2_channel_mux_1_c_out),
    .cx(triple_2_channel_mux_1_a_out), .enable(1'b1), .b_out(triple_2_channel_mux_1_b_out),
    .a_out(triple_2_channel_mux_1_a_out), .ax(Reg_bit), .ay(n4bit_register_1__2d),
    .A(hex_inverter_1__1_prime), .B(hex_inverter_1__1_prime), .C(Clear_Reg));
  _4bit_register u_4bit_register_1 (
    .M(1'b0), .N(1'b0), ._1Q(Input), ._2Q(quad_or_1__1y), ._3Q(triple_2_channel_mux_1_c_out), .CLK(Clock),
    .CLR(1'b0), ._1D(n4bit_register_1__1d), ._2D(n4bit_register_1__2d), ._3D(Reg_bit), .G2(1'b0), .G1(1'b0));  // open: _4Q, _4D
endmodule

module Control (
  input  [23:0] Instruction_Input,
  input  nequal_zero,
  input  clock,
  input  clear,
  output RAM_W_To,
  output EW1,
  output EW2,
  output EW3,
  output EW4,
  output Clear_registers,
  output [7:0] Const_Out,
  output [7:0] Const_Out_2,
  output Read_Mux_1_2,
  output Read_Mux_1_1,
  output Read_Mux_1_0,
  output Read_Mux_2_2,
  output Read_Mux_2_1,
  output Read_Mux_2_0,
  output Write_Mux_1,
  output Write_Mux_2,
  output Write_Mux_3,
  output Write_Mux_4,
  output nLoad_MSB,
  output nLoad_LSB,
  output Load_Saved_PC,
  output nequal_zero_2,
  output subtract_nadd,
  output ALU_Control_1,
  output ALU_Control_2,
  output ALU_Control_3,
  output ALU_Control_4,
  output n_anything_else,
  output OCL_Enable_Reg,
  output Enable_nInterrupts
);

  wire control_addition_1_alu_control_1, control_addition_1_alu_control_2, control_addition_1_alu_control_3,
       control_addition_1_read_mux_1_1, control_addition_1_read_mux_1_2, control_addition_1_read_mux_1_3,
       control_addition_1_read_mux_2_1, control_addition_1_read_mux_2_2, control_addition_1_read_mux_2_3,
       control_addition_1_subtract_nadd, control_addition_1_write_byte, control_addition_1_write_mux_2,
       control_io_1_write_mux_1, control_io_1_write_mux_2, control_load_1_mux_1_1, control_load_1_mux_1_2,
       control_load_1_mux_1_3, control_load_1_mux_3_1, control_load_1_write_byte,
       control_logical_1_alu_control_1, control_logical_1_alu_control_2, control_logical_1_alu_control_3,
       control_logical_1_read_mux_1_1, control_logical_1_read_mux_1_2, control_logical_1_read_mux_1_3,
       control_logical_1_read_mux_2_1, control_logical_1_read_mux_2_2, control_logical_1_read_mux_2_3,
       control_logical_1_write_byte, control_logical_1_write_mux_2,
       control_logical_comparison_1_alu_control_1, control_logical_comparison_1_alu_control_2,
       control_logical_comparison_1_n_anyhting_else, control_logical_comparison_1_read_mux_1_1,
       control_logical_comparison_1_read_mux_1_2, control_logical_comparison_1_read_mux_1_3,
       control_logical_comparison_1_read_mux_2_1, control_logical_comparison_1_read_mux_2_2,
       control_logical_comparison_1_read_mux_2_3, control_logical_comparison_1_subtract_nadd,
       control_logical_comparison_1_write_byte, control_logical_comparison_1_write_mux_2,
       control_misc_1_n_anything_else, control_misc_1_read_mux_1_1, control_misc_1_read_mux_1_2,
       control_misc_1_read_mux_1_3, control_misc_1_read_mux_2_1, control_misc_1_read_mux_2_2,
       control_misc_1_read_mux_2_3, control_misc_1_subtract_nadd, control_misc_1_write_byte,
       hex_inverter_1__1_prime, hex_inverter_1__2_prime, hex_inverter_1__3_prime, hex_inverter_1__4_prime,
       hex_inverter_1__5_prime, hex_inverter_1__6_prime, quad_and_1__1y, quad_and_1__3y, quad_and_2__2y,
       quad_and_3__3y, quad_and_5__1y, quad_and_5__2y, quad_and_5__3y, quad_and_5__4y, quad_and_6__1y,
       quad_and_6__2y, quad_and_6__3y, quad_and_6__4y, quad_and_7__1y, quad_and_7__2y, quad_and_7__3y,
       quad_or_1__1y, quad_or_1__2y, quad_or_1__4y, quad_or_2__1y, quad_or_2__2y, quad_or_2__3y,
       quad_or_3__1y, quad_or_3__3y, quad_or_4__1y, quad_or_4__2y, quad_or_4__3y, quad_or_5__1y,
       quad_or_5__3y, quad_or_5__4y, quad_or_6__1y, quad_or_6__2y, quad_or_6__4y, quad_or_9__1y,
       quad_or_9__3y, quad_or_9__4y, quad_or_10__1y, quad_or_10__2y, quad_or_10__3y;
  wire [7:0] quad_and_2__1y;
  wire [7:7] control_misc_1_write_byte_2, quad_or_4__4y;

  Hex_Inverter hex_inverter_1 (
    ._1(Instruction_Input[21]), ._1_prime(hex_inverter_1__1_prime), ._2(Instruction_Input[22]),
    ._2_prime(hex_inverter_1__2_prime), ._3(Instruction_Input[23]), ._3_prime(hex_inverter_1__3_prime),
    ._4(Instruction_Input[20]), ._4_prime(hex_inverter_1__4_prime), ._5(Instruction_Input[22]),
    ._5_prime(hex_inverter_1__5_prime), ._6(Instruction_Input[18]), ._6_prime(hex_inverter_1__6_prime));
  Quad_AND_Gate quad_and_1 (
    ._1a(Instruction_Input[22]), ._1b(hex_inverter_1__4_prime), ._1y(quad_and_1__1y), ._2a(quad_and_1__1y),
    ._2b(hex_inverter_1__6_prime), ._2y(quad_and_2__1y[2]), ._3a(hex_inverter_1__5_prime),
    ._3b(Instruction_Input[20]), ._3y(quad_and_1__3y), ._4a(quad_and_1__3y), ._4b(hex_inverter_1__6_prime),
    ._4y(quad_and_2__1y[4]));
  Quad_AND_Gate quad_and_2 (
    ._1a(hex_inverter_1__6_prime), ._1b(quad_and_2__2y), ._1y(quad_and_2__1y[0]),
    ._2a(hex_inverter_1__5_prime), ._2b(hex_inverter_1__4_prime), ._2y(quad_and_2__2y), ._3a(quad_and_2__2y),
    ._3b(Instruction_Input[18]), ._3y(quad_and_2__1y[1]), ._4a(Instruction_Input[18]), ._4b(quad_and_1__1y),
    ._4y(quad_and_2__1y[3]));
  Quad_AND_Gate quad_and_3 (
    ._1a(Instruction_Input[18]), ._1b(quad_and_1__3y), ._1y(quad_and_2__1y[5]), ._2a(Instruction_Input[22]),
    ._2b(Instruction_Input[20]), ._2y(Instruction_Input[22]), ._3a(hex_inverter_1__6_prime),
    ._3b(Instruction_Input[20]), ._3y(quad_and_3__3y), ._4a(quad_and_3__3y), ._4b(Instruction_Input[22]),
    ._4y(quad_and_2__1y[6]));
  Quad_AND_Gate quad_and_4 (
    ._1a(Instruction_Input[22]), ._1b(Instruction_Input[18]), ._1y(quad_and_2__1y[7]));  // open: _2a, _2b, _2y, _3a, _3b, _3y, _4a, _4b, _4y
  Quad_AND_Gate quad_and_5 (
    ._1a(hex_inverter_1__1_prime), ._1b(quad_and_5__2y), ._1y(quad_and_5__1y), ._2a(hex_inverter_1__2_prime),
    ._2b(hex_inverter_1__3_prime), ._2y(quad_and_5__2y), ._3a(hex_inverter_1__1_prime),
    ._3b(Instruction_Input[22]), ._3y(quad_and_5__3y), ._4a(Instruction_Input[21]), ._4b(quad_and_5__2y),
    ._4y(quad_and_5__4y));
  Quad_AND_Gate quad_and_6 (
    ._1a(hex_inverter_1__3_prime), ._1b(Instruction_Input[22]), ._1y(quad_and_6__1y), ._2a(quad_and_6__1y),
    ._2b(Instruction_Input[21]), ._2y(quad_and_6__2y), ._3a(hex_inverter_1__3_prime), ._3b(quad_and_5__3y),
    ._3y(quad_and_6__3y), ._4a(quad_and_7__1y), ._4b(Instruction_Input[21]), ._4y(quad_and_6__4y));
  Quad_AND_Gate quad_and_7 (
    ._1a(hex_inverter_1__2_prime), ._1b(Instruction_Input[23]), ._1y(quad_and_7__1y), ._2a(quad_and_7__1y),
    ._2b(hex_inverter_1__1_prime), ._2y(quad_and_7__2y), ._3a(quad_and_5__3y), ._3b(Instruction_Input[23]),
    ._3y(quad_and_7__3y));  // open: _4a, _4b, _4y
  Control_Load control_load_1 (
    .Instruction_enable(quad_and_5__1y), .Sub_instruction(quad_and_2__1y),
    .Read_From_1({Instruction_Input[11], Instruction_Input[12], Instruction_Input[13]}),
    .Clear(Clear_registers), .Write_Byte(control_load_1_write_byte), .Mux_1_1(control_load_1_mux_1_1),
    .Mux_1_2(control_load_1_mux_1_2), .Mux_1_3(control_load_1_mux_1_3), .Mux_3_1(control_load_1_mux_3_1),
    .Ram_EW_TO(RAM_W_To));
  Control_Addition control_addition_1 (
    .Instruction_enable(quad_and_5__4y), .Sub_instruction(quad_and_2__1y),
    .Read_From_1({Instruction_Input[11], Instruction_Input[12], Instruction_Input[13]}),
    .Read_From_2({Instruction_Input[8], Instruction_Input[9], Instruction_Input[10]}),
    .Write_Byte(control_addition_1_write_byte), .Write_Mux_2(control_addition_1_write_mux_2),
    .Read_Mux_1_1(control_addition_1_read_mux_1_1), .Read_Mux_1_2(control_addition_1_read_mux_1_2),
    .Read_Mux_1_3(control_addition_1_read_mux_1_3), .Read_Mux_2_1(control_addition_1_read_mux_2_1),
    .Read_Mux_2_2(control_addition_1_read_mux_2_2), .Read_Mux_2_3(control_addition_1_read_mux_2_3),
    .Subtract_nAdd(control_addition_1_subtract_nadd), .ALU_Control_1(control_addition_1_alu_control_1),
    .ALU_Control_2(control_addition_1_alu_control_2), .ALU_Control_3(control_addition_1_alu_control_3));
  Control_Logical control_logical_1 (
    .Instruction_enable(quad_and_6__3y), .Sub_instruction(quad_and_2__1y),
    .Read_From_1({Instruction_Input[11], Instruction_Input[12], Instruction_Input[13]}),
    .Read_From_2({Instruction_Input[8], Instruction_Input[9], Instruction_Input[10]}),
    .Write_Byte(control_logical_1_write_byte), .ALU_Control_1(control_logical_1_alu_control_1),
    .ALU_Control_2(control_logical_1_alu_control_2), .ALU_Control_3(control_logical_1_alu_control_3),
    .ALU_Control_4(ALU_Control_4), .Write_Mux_2(control_logical_1_write_mux_2),
    .Read_Mux_1_1(control_logical_1_read_mux_1_1), .Read_Mux_1_2(control_logical_1_read_mux_1_2),
    .Read_Mux_1_3(control_logical_1_read_mux_1_3), .Read_Mux_2_1(control_logical_1_read_mux_2_1),
    .Read_Mux_2_2(control_logical_1_read_mux_2_2), .Read_Mux_2_3(control_logical_1_read_mux_2_3));
  Control_Logical_Comparison control_logical_comparison_1 (
    .Instruction_enable(quad_and_6__2y), .Sub_instruction(quad_and_2__1y),
    .Read_From_1({Instruction_Input[11], Instruction_Input[12], Instruction_Input[13]}),
    .Read_From_2({Instruction_Input[8], Instruction_Input[9], Instruction_Input[10]}),
    .Write_Byte(control_logical_comparison_1_write_byte),
    .ALU_Control_1(control_logical_comparison_1_alu_control_1),
    .ALU_Control_2(control_logical_comparison_1_alu_control_2),
    .Subtract_nAdd(control_logical_comparison_1_subtract_nadd),
    .n_anyhting_else(control_logical_comparison_1_n_anyhting_else),
    .Write_Mux_2(control_logical_comparison_1_write_mux_2),
    .Read_Mux_1_1(control_logical_comparison_1_read_mux_1_1),
    .Read_Mux_1_2(control_logical_comparison_1_read_mux_1_2),
    .Read_Mux_1_3(control_logical_comparison_1_read_mux_1_3),
    .Read_Mux_2_1(control_logical_comparison_1_read_mux_2_1),
    .Read_Mux_2_2(control_logical_comparison_1_read_mux_2_2),
    .Read_Mux_2_3(control_logical_comparison_1_read_mux_2_3));
  Control_Misc control_misc_1 (
    .Instruction_enable(quad_and_7__2y), .Sub_instruction(quad_and_2__1y),
    .Read_From_1({Instruction_Input[11], Instruction_Input[12], Instruction_Input[13]}),
    .nequal_zero(nequal_zero), .clock(clock), .clear(clear), .nLoad_MSB(nLoad_MSB), .nLoad_LSB(nLoad_LSB),
    .Load_Saved_PC(Load_Saved_PC), .nequal_zero_2(nequal_zero_2), .Write_Byte(control_misc_1_write_byte),
    .Write_Byte_2(control_misc_1_write_byte_2[7]), .OCL_Register_Enable(OCL_Enable_Reg),
    .Read_Mux_1_1(control_misc_1_read_mux_1_1), .Read_Mux_1_2(control_misc_1_read_mux_1_2),
    .Read_Mux_1_3(control_misc_1_read_mux_1_3), .Read_Mux_2_1(control_misc_1_read_mux_2_1),
    .Read_Mux_2_2(control_misc_1_read_mux_2_2), .Read_Mux_2_3(control_misc_1_read_mux_2_3),
    .Subtract_nadd(control_misc_1_subtract_nadd), .n_anything_else(control_misc_1_n_anything_else),
    .enable_interrupts(Enable_nInterrupts));
  Control_IO control_io_1 (
    .Instruction_enable(quad_and_6__4y), .Sub_instruction(quad_and_2__1y),
    .Write_Mux_1(control_io_1_write_mux_1), .Write_Mux_2(control_io_1_write_mux_2), .Write_Mux_3(Write_Mux_3));
  Quad_OR_Gate quad_or_1 (
    ._1a(control_load_1_mux_1_2), ._1b(control_addition_1_read_mux_1_2), ._1y(quad_or_1__1y),
    ._2a(quad_or_1__1y), ._2b(control_logical_1_read_mux_1_2), ._2y(quad_or_1__2y),
    ._3a(control_misc_1_read_mux_1_2), ._3b(quad_or_1__4y), ._3y(Read_Mux_1_1),
    ._4a(control_logical_comparison_1_read_mux_1_2), ._4b(quad_or_1__2y), ._4y(quad_or_1__4y));
  Quad_OR_Gate quad_or_2 (
    ._1a(control_addition_1_read_mux_2_1), ._1b(control_logical_1_read_mux_2_1), ._1y(quad_or_2__1y),
    ._2a(quad_or_2__1y), ._2b(control_logical_comparison_1_read_mux_2_1), ._2y(quad_or_2__2y),
    ._3a(control_logical_1_read_mux_2_2), ._3b(control_addition_1_read_mux_2_2), ._3y(quad_or_2__3y),
    ._4a(control_misc_1_read_mux_2_1), ._4b(quad_or_2__2y), ._4y(Read_Mux_2_2));
  Quad_OR_Gate quad_or_3 (
    ._1a(control_addition_1_alu_control_2), ._1b(control_logical_1_alu_control_2), ._1y(quad_or_3__1y),
    ._2a(quad_or_3__1y), ._2b(control_logical_comparison_1_alu_control_2), ._2y(ALU_Control_2),
    ._3a(control_logical_comparison_1_alu_control_1), ._3b(control_logical_1_alu_control_1),
    ._3y(quad_or_3__3y), ._4a(quad_or_3__3y), ._4b(control_addition_1_alu_control_1), ._4y(ALU_Control_1));
  Quad_OR_Gate quad_or_4 (
    ._1a(control_load_1_write_byte), ._1b(control_addition_1_write_byte), ._1y(quad_or_4__1y),
    ._2a(quad_or_4__1y), ._2b(control_logical_1_write_byte), ._2y(quad_or_4__2y), ._3a(quad_or_4__2y),
    ._3b(control_misc_1_write_byte), ._3y(quad_or_4__3y), ._4a(quad_or_4__3y),
    ._4b(control_logical_comparison_1_write_byte), ._4y(quad_or_4__4y[7]));
  Quad_OR_Gate quad_or_5 (
    ._1a(control_logical_comparison_1_read_mux_2_2), ._1b(control_misc_1_read_mux_2_2), ._1y(quad_or_5__1y),
    ._2a(quad_or_2__3y), ._2b(quad_or_5__1y), ._2y(Read_Mux_2_1), ._3a(control_logical_1_read_mux_2_3),
    ._3b(control_addition_1_read_mux_2_3), ._3y(quad_or_5__3y), ._4a(quad_or_5__3y),
    ._4b(control_logical_comparison_1_read_mux_2_3), ._4y(quad_or_5__4y));
  _8bit_AND_Gate u_8bit_and_1 (.In_2(Instruction_Input[7:0]), .In_1({8{quad_or_4__4y[7]}}), .Out(Const_Out));
  _8bit_AND_Gate u_8bit_and_2 (
    .In_2({2'b00, Instruction_Input[13:8]}), .In_1({8{control_misc_1_write_byte_2[7]}}), .Out(Const_Out_2));
  Quad_OR_Gate quad_or_6 (
    ._1a(control_load_1_mux_1_3), ._1b(control_addition_1_read_mux_1_3), ._1y(quad_or_6__1y),
    ._2a(quad_or_6__1y), ._2b(control_logical_1_read_mux_1_3), ._2y(quad_or_6__2y),
    ._3a(control_misc_1_read_mux_1_3), ._3b(quad_or_6__4y), ._3y(Read_Mux_1_0),
    ._4a(control_logical_comparison_1_read_mux_1_3), ._4b(quad_or_6__2y), ._4y(quad_or_6__4y));
  Quad_OR_Gate quad_or_7 (
    ._1a(control_misc_1_n_anything_else), ._1b(control_logical_comparison_1_n_anyhting_else),
    ._1y(n_anything_else), ._3a(control_misc_1_subtract_nadd), ._3b(quad_or_9__4y), ._3y(subtract_nadd));  // open: _2a, _2b, _2y, _4a, _4b, _4y
  Quad_OR_Gate quad_or_8 (
    ._3a(control_addition_1_alu_control_3), ._3b(control_logical_1_alu_control_3), ._3y(ALU_Control_3));  // open: _1a, _1b, _1y, _2a, _2b, _2y, _4a, _4b, _4y
  Hex_Inverter hex_inverter_2 (
    ._1(Instruction_Input[17]), ._1_prime(EW1), ._2(Instruction_Input[16]), ._2_prime(EW2),
    ._3(Instruction_Input[15]), ._3_prime(EW3), ._6(Instruction_Input[14]), ._6_prime(EW4));  // open: _4, _4_prime, _5, _5_prime
  Quad_OR_Gate quad_or_9 (
    ._1a(control_logical_1_write_mux_2), ._1b(control_addition_1_write_mux_2), ._1y(quad_or_9__1y),
    ._2a(quad_or_5__4y), ._2b(control_misc_1_read_mux_2_3), ._2y(Read_Mux_2_0), ._3a(quad_or_9__1y),
    ._3b(control_logical_comparison_1_write_mux_2), ._3y(quad_or_9__3y),
    ._4a(control_addition_1_subtract_nadd), ._4b(control_logical_comparison_1_subtract_nadd),
    ._4y(quad_or_9__4y));
  Quad_OR_Gate quad_or_10 (
    ._1a(control_load_1_mux_1_1), ._1b(control_addition_1_read_mux_1_1), ._1y(quad_or_10__1y),
    ._2a(quad_or_10__1y), ._2b(control_logical_1_read_mux_1_1), ._2y(quad_or_10__2y),
    ._3a(control_misc_1_read_mux_1_1), ._3b(control_logical_comparison_1_read_mux_1_1), ._3y(quad_or_10__3y),
    ._4a(quad_or_10__3y), ._4b(quad_or_10__2y), ._4y(Read_Mux_1_2));
  Quad_OR_Gate quad_or_11 (
    ._1a(control_load_1_mux_3_1), ._1b(control_io_1_write_mux_1), ._1y(Write_Mux_1), ._2a(quad_or_9__3y),
    ._2b(control_io_1_write_mux_2), ._2y(Write_Mux_2));  // open: _3a, _3b, _3y, _4a, _4b, _4y

  assign Instruction_Input[19] = Instruction_Input[22];
  assign Write_Mux_4 = 1'b0;
endmodule

module Control_v2 (
  input  [23:0] Instruction_Input,
  input  nEqual_Zero,
  input  CLK,
  output Page_Reg_Write_Enable,
  output RAM_W_To,
  output [3:0] Enable_reg_write,
  output Clear_Registers,
  output nLoad_PC_MSB,
  output nLoad_PC_LSB,
  output Load_Saved_PC,
  output nEqual_Zero_2,
  output subtract_____add,
  output [3:0] ALU_Control_Bits,
  output n_anything_else,
  output OCL_Enable_Reg,
  output nEnable_Interrupts,
  output [3:0] Write_Mux_Control_Bits,
  output [2:0] To_read_reg_1,
  output [2:0] To_read_reg_2,
  output [7:0] Const_Out,
  output [7:0] Const_Out_2
);

  wire hex_inverter_1__6_prime, hex_inverter_3__1_prime, n4bit_register_1__1d, quad_and_1__4y,
       quad_and_2__1y, quad_and_2__2y, quad_and_2__3y, quad_and_2__4y, quad_or_1__4y;
  wire [3:0] n4_bit_and_1_out_3, n4_bit_and_2_out_3;
  wire [31:0] rom_1_data;

  Hex_Inverter hex_inverter_1 (
    ._6(nEqual_Zero), ._6_prime(hex_inverter_1__6_prime));  // open: _1, _1_prime, _2, _2_prime, _3, _3_prime, _4, _4_prime, _5, _5_prime
  Quad_OR_Gate quad_or_1 (
    ._4a(rom_1_data[15]), ._4b(quad_and_1__4y), ._4y(quad_or_1__4y));  // open: _1a, _1b, _1y, _2a, _2b, _2y, _3a, _3b, _3y
  Quad_AND_Gate quad_and_1 (
    ._4a(hex_inverter_1__6_prime), ._4b(rom_1_data[11]), ._4y(quad_and_1__4y));  // open: _1a, _1b, _1y, _2a, _2b, _2y, _3a, _3b, _3y
  ROM_part #(.addrWidth(6), .dataWidth(32)) rom_1 (
    .addr(Instruction_Input[23:18]),
    .data({rom_1_data[31:30], Write_Mux_Control_Bits, rom_1_data[25:24], n_anything_else, ALU_Control_Bits, subtract_____add, rom_1_data[17], Load_Saved_PC, rom_1_data[15:14], Clear_Registers, rom_1_data[12:11], RAM_W_To, rom_1_data[9:0]}),
    .sel(1'b1));
  _4_bit_AND u_4_bit_and_1 (
    .in_1({4{rom_1_data[30]}}), .in_2({Instruction_Input[13:11], 1'b0}), .out_3(n4_bit_and_1_out_3));
  Quad_AND_Gate quad_and_2 (
    ._1a(Instruction_Input[17]), ._1b(rom_1_data[12]), ._1y(quad_and_2__1y), ._2a(Instruction_Input[14]),
    ._2b(rom_1_data[12]), ._2y(quad_and_2__2y), ._3a(Instruction_Input[16]), ._3b(rom_1_data[12]),
    ._3y(quad_and_2__3y), ._4a(Instruction_Input[15]), ._4b(rom_1_data[12]), ._4y(quad_and_2__4y));
  Hex_Inverter hex_inverter_2 (
    ._1(quad_and_2__1y), ._1_prime(Enable_reg_write[0]), ._3(quad_and_2__2y), ._3_prime(Enable_reg_write[3]),
    ._4(quad_and_2__3y), ._4_prime(Enable_reg_write[1]), ._5(rom_1_data[9]),
    ._5_prime(Page_Reg_Write_Enable), ._6(quad_and_2__4y), ._6_prime(Enable_reg_write[2]));  // open: _2, _2_prime
  _4_bit_AND u_4_bit_and_2 (
    .in_1({4{rom_1_data[31]}}), .in_2({Instruction_Input[10:8], 1'b0}), .out_3(n4_bit_and_2_out_3));
  triple_2_channel_mux triple_2_channel_mux_1 (
    .bx(n4_bit_and_1_out_3[2]), .by(1'b0), .cy(1'b0), .c_out(To_read_reg_1[2]), .cx(n4_bit_and_1_out_3[3]),
    .enable(1'b1), .b_out(To_read_reg_1[1]), .a_out(To_read_reg_1[0]), .ax(n4_bit_and_1_out_3[1]), .ay(1'b0),
    .A(rom_1_data[24]), .B(rom_1_data[24]), .C(rom_1_data[24]));
  triple_2_channel_mux triple_2_channel_mux_2 (
    .bx(n4_bit_and_2_out_3[1]), .by(1'b1), .cy(1'b1), .c_out(To_read_reg_2[2]), .cx(n4_bit_and_2_out_3[3]),
    .enable(1'b1), .b_out(To_read_reg_2[1]), .a_out(To_read_reg_2[0]), .ax(n4_bit_and_2_out_3[2]), .ay(1'b1),
    .A(rom_1_data[24]), .B(rom_1_data[24]), .C(rom_1_data[24]));
  _4bit_register u_4bit_register_1 (
    .M(1'b0), .N(1'b0), ._1Q(To_read_reg_1[2]), .CLK(CLK), .CLR(Clear_Registers), ._1D(n4bit_register_1__1d),
    .G2(hex_inverter_3__1_prime), .G1(hex_inverter_3__1_prime));  // open: _2Q, _3Q, _4Q, _2D, _3D, _4D
  Hex_Inverter hex_inverter_3 (
    ._1(rom_1_data[8]), ._1_prime(hex_inverter_3__1_prime), ._2(rom_1_data[17]), ._2_prime(nEqual_Zero_2),
    ._3(rom_1_data[24]), ._3_prime(OCL_Enable_Reg), ._4(rom_1_data[14]), ._4_prime(nLoad_PC_MSB),
    ._6(quad_or_1__4y), ._6_prime(nLoad_PC_LSB));  // open: _5, _5_prime
  Quad_OR_Gate quad_or_2 (
    ._2a(n4bit_register_1__1d), ._2b(rom_1_data[25]), ._2y(nEnable_Interrupts));  // open: _1a, _1b, _1y, _3a, _3b, _3y, _4a, _4b, _4y

  assign Const_Out = Instruction_Input[7:0];
  assign Const_Out_2 = {2'b00, Instruction_Input[13:8]};

  // Notes on the sheet:
  //   contents of rom_1 (hex, n*v repeats v):
  //   48001000 84001000 c4000400 48001000 1003200 ffffff00 ffffff00 ffffff00 cc001000 cc001000 cc041000
  //   cc041000 4c301000 4c381000 ffffff00 ffffff00 cc481000 cc481000 cc501000 cc501000 cc401000 ffffff00
  //   ffffff00 ffffff00 cc9c1000 cc9c1000 cc8c1000 cc8c1000 cc941000 cc941000 ffffff00 ffffff00 82004000
  //   80008000 10000 40020800 0 c1000000
endmodule

module ROM (
  input  [15:0] PC_Address,
  output [23:0] Instruction
);

  ROM_part #(.addrWidth(16), .dataWidth(24)) rom_1 (.addr(PC_Address), .data(Instruction), .sel(1'b1));

  // Notes on the sheet:
  //   contents of rom_1 (hex, n*v repeats v):
  //   e0008 11000 209100 2c5000 286200
endmodule

module RAM (
  input  CLR_L16bytes,
  input  W_TO,
  input  [7:0] Addr,
  input  [7:0] Data,
  input  CLK,
  output [7:0] OUT_1
);

  wire hex_inverter_1__1_prime, hex_inverter_1__2_prime, hex_inverter_1__3_prime, hex_inverter_1__4_prime,
       hex_inverter_1__5_prime, hex_inverter_1__6_prime, hex_inverter_2__1_prime, hex_inverter_2__2_prime,
       hex_inverter_2__3_prime, hex_inverter_2__4_prime, hex_inverter_2__5_prime, hex_inverter_2__6_prime,
       hex_inverter_3__1_prime, hex_inverter_3__2_prime, hex_inverter_3__3_prime, hex_inverter_3__4_prime,
       hex_inverter_3__5_prime, hex_inverter_3__6_prime, hex_inverter_4__1_prime, hex_inverter_4__2_prime,
       hex_inverter_4__3_prime, hex_inverter_4__4_prime, hex_inverter_4__5_prime, hex_inverter_4__6_prime,
       hex_inverter_5__1_prime, hex_inverter_5__2_prime, hex_inverter_5__3_prime, hex_inverter_5__4_prime,
       hex_inverter_5__5_prime, hex_inverter_5__6_prime, hex_inverter_6__1_prime, hex_inverter_6__2_prime,
       hex_inverter_6__3_prime, hex_inverter_6__4_prime, hex_inverter_6__5_prime, hex_inverter_6__6_prime,
       hex_inverter_7__1_prime, hex_inverter_7__2_prime, hex_inverter_7__3_prime, hex_inverter_7__4_prime,
       hex_inverter_7__5_prime, hex_inverter_7__6_prime, hex_inverter_8__1_prime, hex_inverter_8__2_prime,
       hex_inverter_8__3_prime, hex_inverter_8__4_prime, hex_inverter_8__5_prime, hex_inverter_8__6_prime,
       hex_inverter_9__1_prime, hex_inverter_9__2_prime, hex_inverter_9__3_prime, hex_inverter_9__4_prime,
       hex_inverter_9__5_prime, hex_inverter_9__6_prime, hex_inverter_10__1_prime, hex_inverter_10__2_prime,
       hex_inverter_10__3_prime, hex_inverter_10__4_prime, hex_inverter_10__5_prime,
       hex_inverter_10__6_prime, hex_inverter_11__1_prime, hex_inverter_11__2_prime,
       hex_inverter_11__4_prime, hex_inverter_11__5_prime, quad_and_1__1y, quad_and_1__2y, quad_and_1__3y,
       quad_and_1__4y, quad_and_2__1y, quad_and_2__2y, quad_and_2__3y, quad_and_2__4y, quad_and_3__1y,
       quad_and_3__2y, quad_and_3__3y, quad_and_3__4y, quad_and_4__1y, quad_and_4__2y, quad_and_4__3y,
       quad_and_4__4y, quad_and_5__1y, quad_and_5__2y, quad_and_5__3y, quad_and_5__4y, quad_and_6__1y,
       quad_and_6__2y, quad_and_6__3y, quad_and_6__4y, quad_and_7__1y, quad_and_7__2y, quad_and_7__3y,
       quad_and_7__4y, quad_and_8__1y, quad_and_8__2y, quad_and_8__3y, quad_and_8__4y,
       triple_2_channel_demux_1_ax, triple_2_channel_demux_1_ay, triple_2_channel_demux_1_bx,
       triple_2_channel_demux_1_by, triple_2_channel_demux_1_cx, triple_2_channel_demux_1_cy,
       triple_2_channel_demux_2_ax, triple_2_channel_demux_2_ay, triple_2_channel_demux_2_bx,
       triple_2_channel_demux_2_by, triple_2_channel_demux_2_cx, triple_2_channel_demux_2_cy,
       triple_2_channel_demux_3_ax, triple_2_channel_demux_3_ay, triple_2_channel_demux_3_bx,
       triple_2_channel_demux_3_by, triple_2_channel_demux_3_cx, triple_2_channel_demux_3_cy,
       triple_2_channel_demux_4_ax, triple_2_channel_demux_4_ay, triple_2_channel_demux_4_bx,
       triple_2_channel_demux_4_by, triple_2_channel_demux_4_cx, triple_2_channel_demux_4_cy,
       triple_2_channel_demux_5_bx, triple_2_channel_demux_5_by, triple_2_channel_demux_6_ax,
       triple_2_channel_demux_6_ay, triple_2_channel_demux_6_bx, triple_2_channel_demux_6_by,
       triple_2_channel_demux_6_cx, triple_2_channel_demux_6_cy, triple_2_channel_demux_7_ax,
       triple_2_channel_demux_7_ay, triple_2_channel_demux_7_bx, triple_2_channel_demux_7_by,
       triple_2_channel_demux_7_cx, triple_2_channel_demux_7_cy, triple_2_channel_demux_8_ax,
       triple_2_channel_demux_8_ay, triple_2_channel_demux_8_bx, triple_2_channel_demux_8_by,
       triple_2_channel_demux_8_cx, triple_2_channel_demux_8_cy, triple_2_channel_demux_9_ax,
       triple_2_channel_demux_9_ay, triple_2_channel_demux_9_bx, triple_2_channel_demux_9_by,
       triple_2_channel_demux_9_cx, triple_2_channel_demux_9_cy, triple_2_channel_demux_10_ax,
       triple_2_channel_demux_10_ay, triple_2_channel_demux_10_bx, triple_2_channel_demux_10_by,
       triple_2_channel_demux_10_cx, triple_2_channel_demux_10_cy, triple_2_channel_demux_11_ax,
       triple_2_channel_demux_11_ay, triple_2_channel_demux_11_bx, triple_2_channel_demux_11_by,
       triple_2_channel_demux_11_cx, triple_2_channel_demux_11_cy;

  triple_2_channel_demux triple_2_channel_demux_1 (
    .bx(triple_2_channel_demux_1_bx), .by(triple_2_channel_demux_1_by), .cy(triple_2_channel_demux_1_cy),
    .c_in(triple_2_channel_demux_1_ay), .cx(triple_2_channel_demux_1_cx), .enable(1'b1),
    .b_in(triple_2_channel_demux_1_ax), .a_in(triple_2_channel_demux_2_bx), .ax(triple_2_channel_demux_1_ax),
    .ay(triple_2_channel_demux_1_ay), .A(Addr[1]), .B(Addr[0]), .C(Addr[0]));
  Hex_Inverter hex_inverter_1 (
    ._1(triple_2_channel_demux_3_by), ._1_prime(hex_inverter_1__1_prime), ._2(triple_2_channel_demux_3_bx),
    ._2_prime(hex_inverter_1__2_prime), ._3(triple_2_channel_demux_1_cy), ._3_prime(hex_inverter_1__3_prime),
    ._4(quad_and_1__4y), ._4_prime(hex_inverter_1__4_prime), ._5(quad_and_1__3y),
    ._5_prime(hex_inverter_1__5_prime), ._6(quad_and_2__2y), ._6_prime(hex_inverter_1__6_prime));
  Hex_Inverter hex_inverter_2 (
    ._1(triple_2_channel_demux_1_cx), ._1_prime(hex_inverter_2__1_prime), ._2(triple_2_channel_demux_1_by),
    ._2_prime(hex_inverter_2__2_prime), ._3(triple_2_channel_demux_1_bx), ._3_prime(hex_inverter_2__3_prime),
    ._4(quad_and_2__1y), ._4_prime(hex_inverter_2__4_prime), ._5(quad_and_1__2y),
    ._5_prime(hex_inverter_2__5_prime), ._6(quad_and_1__1y), ._6_prime(hex_inverter_2__6_prime));
  _8bit_register u_8bit_register_1 (
    .M(hex_inverter_1__1_prime), .N(hex_inverter_1__1_prime), .\input (Data), .clock(CLK),
    .CLR(CLR_L16bytes), .\output (OUT_1), .G2(hex_inverter_1__4_prime), .G1(hex_inverter_1__4_prime));
  _8bit_register u_8bit_register_2 (
    .M(hex_inverter_1__2_prime), .N(hex_inverter_1__2_prime), .\input (Data), .clock(CLK),
    .CLR(CLR_L16bytes), .\output (OUT_1), .G2(hex_inverter_1__5_prime), .G1(hex_inverter_1__5_prime));
  _8bit_register u_8bit_register_3 (
    .M(hex_inverter_1__3_prime), .N(hex_inverter_1__3_prime), .\input (Data), .clock(CLK),
    .CLR(CLR_L16bytes), .\output (OUT_1), .G2(hex_inverter_1__6_prime), .G1(hex_inverter_1__6_prime));
  _8bit_register u_8bit_register_4 (
    .M(hex_inverter_2__1_prime), .N(hex_inverter_2__1_prime), .\input (Data), .clock(CLK),
    .CLR(CLR_L16bytes), .\output (OUT_1), .G2(hex_inverter_2__4_prime), .G1(hex_inverter_2__4_prime));
  _8bit_register u_8bit_register_5 (
    .M(hex_inverter_2__2_prime), .N(hex_inverter_2__2_prime), .\input (Data), .clock(CLK),
    .CLR(CLR_L16bytes), .\output (OUT_1), .G2(hex_inverter_2__5_prime), .G1(hex_inverter_2__5_prime));
  _8bit_register u_8bit_register_6 (
    .M(hex_inverter_2__3_prime), .N(hex_inverter_2__3_prime), .\input (Data), .clock(CLK),
    .CLR(CLR_L16bytes), .\output (OUT_1), .G2(hex_inverter_2__6_prime), .G1(hex_inverter_2__6_prime));
  triple_2_channel_demux triple_2_channel_demux_2 (
    .bx(triple_2_channel_demux_2_bx), .by(triple_2_channel_demux_2_by), .cy(triple_2_channel_demux_2_cy),
    .c_in(triple_2_channel_demux_2_ay), .cx(triple_2_channel_demux_2_cx), .enable(1'b1),
    .b_in(triple_2_channel_demux_2_ax), .a_in(triple_2_channel_demux_5_bx), .ax(triple_2_channel_demux_2_ax),
    .ay(triple_2_channel_demux_2_ay), .A(Addr[3]), .B(Addr[2]), .C(Addr[2]));
  Quad_AND_Gate quad_and_1 (
    ._1a(W_TO), ._1b(triple_2_channel_demux_1_bx), ._1y(quad_and_1__1y), ._2a(W_TO),
    ._2b(triple_2_channel_demux_1_by), ._2y(quad_and_1__2y), ._3a(W_TO), ._3b(triple_2_channel_demux_3_bx),
    ._3y(quad_and_1__3y), ._4a(W_TO), ._4b(triple_2_channel_demux_3_by), ._4y(quad_and_1__4y));
  Quad_AND_Gate quad_and_2 (
    ._1a(W_TO), ._1b(triple_2_channel_demux_1_cx), ._1y(quad_and_2__1y), ._2a(W_TO),
    ._2b(triple_2_channel_demux_1_cy), ._2y(quad_and_2__2y), ._3a(W_TO), ._3b(triple_2_channel_demux_3_cx),
    ._3y(quad_and_2__3y), ._4a(W_TO), ._4b(triple_2_channel_demux_3_cy), ._4y(quad_and_2__4y));
  triple_2_channel_demux triple_2_channel_demux_3 (
    .bx(triple_2_channel_demux_3_bx), .by(triple_2_channel_demux_3_by), .cy(triple_2_channel_demux_3_cy),
    .c_in(triple_2_channel_demux_3_ay), .cx(triple_2_channel_demux_3_cx), .enable(1'b1),
    .b_in(triple_2_channel_demux_3_ax), .a_in(triple_2_channel_demux_2_by), .ax(triple_2_channel_demux_3_ax),
    .ay(triple_2_channel_demux_3_ay), .A(Addr[1]), .B(Addr[0]), .C(Addr[0]));
  triple_2_channel_demux triple_2_channel_demux_4 (
    .bx(triple_2_channel_demux_4_bx), .by(triple_2_channel_demux_4_by), .cy(triple_2_channel_demux_4_cy),
    .c_in(triple_2_channel_demux_4_ay), .cx(triple_2_channel_demux_4_cx), .enable(1'b1),
    .b_in(triple_2_channel_demux_4_ax), .a_in(triple_2_channel_demux_2_cx), .ax(triple_2_channel_demux_4_ax),
    .ay(triple_2_channel_demux_4_ay), .A(Addr[1]), .B(Addr[0]), .C(Addr[0]));
  Quad_AND_Gate quad_and_3 (
    ._1a(W_TO), ._1b(triple_2_channel_demux_4_bx), ._1y(quad_and_3__1y), ._2a(W_TO),
    ._2b(triple_2_channel_demux_4_by), ._2y(quad_and_3__2y), ._3a(W_TO), ._3b(triple_2_channel_demux_4_cx),
    ._3y(quad_and_3__3y), ._4a(W_TO), ._4b(triple_2_channel_demux_4_cy), ._4y(quad_and_3__4y));
  Hex_Inverter hex_inverter_3 (
    ._1(triple_2_channel_demux_4_cy), ._1_prime(hex_inverter_3__1_prime), ._2(triple_2_channel_demux_4_cx),
    ._2_prime(hex_inverter_3__2_prime), ._3(triple_2_channel_demux_4_by), ._3_prime(hex_inverter_3__3_prime),
    ._4(quad_and_3__4y), ._4_prime(hex_inverter_3__4_prime), ._5(quad_and_3__3y),
    ._5_prime(hex_inverter_3__5_prime), ._6(quad_and_3__2y), ._6_prime(hex_inverter_3__6_prime));
  Hex_Inverter hex_inverter_4 (
    ._1(triple_2_channel_demux_4_bx), ._1_prime(hex_inverter_4__1_prime), ._2(triple_2_channel_demux_3_cy),
    ._2_prime(hex_inverter_4__2_prime), ._3(triple_2_channel_demux_3_cx), ._3_prime(hex_inverter_4__3_prime),
    ._4(quad_and_3__1y), ._4_prime(hex_inverter_4__4_prime), ._5(quad_and_2__4y),
    ._5_prime(hex_inverter_4__5_prime), ._6(quad_and_2__3y), ._6_prime(hex_inverter_4__6_prime));
  _8bit_register u_8bit_register_7 (
    .M(hex_inverter_3__1_prime), .N(hex_inverter_3__1_prime), .\input (Data), .clock(CLK),
    .CLR(CLR_L16bytes), .\output (OUT_1), .G2(hex_inverter_3__4_prime), .G1(hex_inverter_3__4_prime));
  _8bit_register u_8bit_register_8 (
    .M(hex_inverter_3__2_prime), .N(hex_inverter_3__2_prime), .\input (Data), .clock(CLK),
    .CLR(CLR_L16bytes), .\output (OUT_1), .G2(hex_inverter_3__5_prime), .G1(hex_inverter_3__5_prime));
  _8bit_register u_8bit_register_9 (
    .M(hex_inverter_3__3_prime), .N(hex_inverter_3__3_prime), .\input (Data), .clock(CLK),
    .CLR(CLR_L16bytes), .\output (OUT_1), .G2(hex_inverter_3__6_prime), .G1(hex_inverter_3__6_prime));
  _8bit_register u_8bit_register_10 (
    .M(hex_inverter_4__1_prime), .N(hex_inverter_4__1_prime), .\input (Data), .clock(CLK),
    .CLR(CLR_L16bytes), .\output (OUT_1), .G2(hex_inverter_4__4_prime), .G1(hex_inverter_4__4_prime));
  _8bit_register u_8bit_register_11 (
    .M(hex_inverter_4__2_prime), .N(hex_inverter_4__2_prime), .\input (Data), .clock(CLK),
    .CLR(CLR_L16bytes), .\output (OUT_1), .G2(hex_inverter_4__5_prime), .G1(hex_inverter_4__5_prime));
  _8bit_register u_8bit_register_12 (
    .M(hex_inverter_4__3_prime), .N(hex_inverter_4__3_prime), .\input (Data), .clock(CLK),
    .CLR(CLR_L16bytes), .\output (OUT_1), .G2(hex_inverter_4__6_prime), .G1(hex_inverter_4__6_prime));
  triple_2_channel_demux triple_2_channel_demux_5 (
    .bx(triple_2_channel_demux_5_bx), .by(triple_2_channel_demux_5_by), .enable(1'b1), .b_in(1'b1),
    .B(Addr[4]));  // open: cy, c_in, cx, a_in, ax, ay, A, C
  triple_2_channel_demux triple_2_channel_demux_6 (
    .bx(triple_2_channel_demux_6_bx), .by(triple_2_channel_demux_6_by), .cy(triple_2_channel_demux_6_cy),
    .c_in(triple_2_channel_demux_6_ay), .cx(triple_2_channel_demux_6_cx), .enable(1'b1),
    .b_in(triple_2_channel_demux_6_ax), .a_in(triple_2_channel_demux_2_cy), .ax(triple_2_channel_demux_6_ax),
    .ay(triple_2_channel_demux_6_ay), .A(Addr[1]), .B(Addr[0]), .C(Addr[0]));
  Hex_Inverter hex_inverter_5 (
    ._1(triple_2_channel_demux_7_by), ._1_prime(hex_inverter_5__1_prime), ._2(triple_2_channel_demux_7_bx),
    ._2_prime(hex_inverter_5__2_prime), ._3(triple_2_channel_demux_6_cy), ._3_prime(hex_inverter_5__3_prime),
    ._4(quad_and_4__4y), ._4_prime(hex_inverter_5__4_prime), ._5(quad_and_4__3y),
    ._5_prime(hex_inverter_5__5_prime), ._6(quad_and_5__2y), ._6_prime(hex_inverter_5__6_prime));
  Hex_Inverter hex_inverter_6 (
    ._1(triple_2_channel_demux_6_cx), ._1_prime(hex_inverter_6__1_prime), ._2(triple_2_channel_demux_6_by),
    ._2_prime(hex_inverter_6__2_prime), ._3(triple_2_channel_demux_6_bx), ._3_prime(hex_inverter_6__3_prime),
    ._4(quad_and_5__1y), ._4_prime(hex_inverter_6__4_prime), ._5(quad_and_4__2y),
    ._5_prime(hex_inverter_6__5_prime), ._6(quad_and_4__1y), ._6_prime(hex_inverter_6__6_prime));
  _8bit_register u_8bit_register_13 (
    .M(hex_inverter_5__1_prime), .N(hex_inverter_5__1_prime), .\input (Data), .clock(CLK), .CLR(1'b0),
    .\output (OUT_1), .G2(hex_inverter_5__4_prime), .G1(hex_inverter_5__4_prime));
  _8bit_register u_8bit_register_14 (
    .M(hex_inverter_5__2_prime), .N(hex_inverter_5__2_prime), .\input (Data), .clock(CLK), .CLR(1'b0),
    .\output (OUT_1), .G2(hex_inverter_5__5_prime), .G1(hex_inverter_5__5_prime));
  _8bit_register u_8bit_register_15 (
    .M(hex_inverter_5__3_prime), .N(hex_inverter_5__3_prime), .\input (Data), .clock(CLK),
    .CLR(CLR_L16bytes), .\output (OUT_1), .G2(hex_inverter_5__6_prime), .G1(hex_inverter_5__6_prime));
  _8bit_register u_8bit_register_16 (
    .M(hex_inverter_6__1_prime), .N(hex_inverter_6__1_prime), .\input (Data), .clock(CLK),
    .CLR(CLR_L16bytes), .\output (OUT_1), .G2(hex_inverter_6__4_prime), .G1(hex_inverter_6__4_prime));
  _8bit_register u_8bit_register_17 (
    .M(hex_inverter_6__2_prime), .N(hex_inverter_6__2_prime), .\input (Data), .clock(CLK),
    .CLR(CLR_L16bytes), .\output (OUT_1), .G2(hex_inverter_6__5_prime), .G1(hex_inverter_6__5_prime));
  _8bit_register u_8bit_register_18 (
    .M(hex_inverter_6__3_prime), .N(hex_inverter_6__3_prime), .\input (Data), .clock(CLK),
    .CLR(CLR_L16bytes), .\output (OUT_1), .G2(hex_inverter_6__6_prime), .G1(hex_inverter_6__6_prime));
  Quad_AND_Gate quad_and_4 (
    ._1a(W_TO), ._1b(triple_2_channel_demux_6_bx), ._1y(quad_and_4__1y), ._2a(W_TO),
    ._2b(triple_2_channel_demux_6_by), ._2y(quad_and_4__2y), ._3a(W_TO), ._3b(triple_2_channel_demux_7_bx),
    ._3y(quad_and_4__3y), ._4a(W_TO), ._4b(triple_2_channel_demux_7_by), ._4y(quad_and_4__4y));
  Quad_AND_Gate quad_and_5 (
    ._1a(W_TO), ._1b(triple_2_channel_demux_6_cx), ._1y(quad_and_5__1y), ._2a(W_TO),
    ._2b(triple_2_channel_demux_6_cy), ._2y(quad_and_5__2y), ._3a(W_TO), ._3b(triple_2_channel_demux_7_cx),
    ._3y(quad_and_5__3y), ._4a(W_TO), ._4b(triple_2_channel_demux_7_cy), ._4y(quad_and_5__4y));
  triple_2_channel_demux triple_2_channel_demux_7 (
    .bx(triple_2_channel_demux_7_bx), .by(triple_2_channel_demux_7_by), .cy(triple_2_channel_demux_7_cy),
    .c_in(triple_2_channel_demux_7_ay), .cx(triple_2_channel_demux_7_cx), .enable(1'b1),
    .b_in(triple_2_channel_demux_7_ax), .a_in(triple_2_channel_demux_8_bx), .ax(triple_2_channel_demux_7_ax),
    .ay(triple_2_channel_demux_7_ay), .A(Addr[1]), .B(Addr[0]), .C(Addr[0]));
  triple_2_channel_demux triple_2_channel_demux_8 (
    .bx(triple_2_channel_demux_8_bx), .by(triple_2_channel_demux_8_by), .cy(triple_2_channel_demux_8_cy),
    .c_in(triple_2_channel_demux_8_ay), .cx(triple_2_channel_demux_8_cx), .enable(1'b1),
    .b_in(triple_2_channel_demux_8_ax), .a_in(triple_2_channel_demux_5_by), .ax(triple_2_channel_demux_8_ax),
    .ay(triple_2_channel_demux_8_ay), .A(Addr[3]), .B(Addr[2]), .C(Addr[2]));
  triple_2_channel_demux triple_2_channel_demux_9 (
    .bx(triple_2_channel_demux_9_bx), .by(triple_2_channel_demux_9_by), .cy(triple_2_channel_demux_9_cy),
    .c_in(triple_2_channel_demux_9_ay), .cx(triple_2_channel_demux_9_cx), .enable(1'b1),
    .b_in(triple_2_channel_demux_9_ax), .a_in(triple_2_channel_demux_8_by), .ax(triple_2_channel_demux_9_ax),
    .ay(triple_2_channel_demux_9_ay), .A(Addr[1]), .B(Addr[0]), .C(Addr[0]));
  Quad_AND_Gate quad_and_6 (
    ._1a(W_TO), ._1b(triple_2_channel_demux_9_bx), ._1y(quad_and_6__1y), ._2a(W_TO),
    ._2b(triple_2_channel_demux_9_by), ._2y(quad_and_6__2y), ._3a(W_TO), ._3b(triple_2_channel_demux_9_cx),
    ._3y(quad_and_6__3y), ._4a(W_TO), ._4b(triple_2_channel_demux_9_cy), ._4y(quad_and_6__4y));
  Hex_Inverter hex_inverter_7 (
    ._1(triple_2_channel_demux_9_cy), ._1_prime(hex_inverter_7__1_prime), ._2(triple_2_channel_demux_9_cx),
    ._2_prime(hex_inverter_7__2_prime), ._3(triple_2_channel_demux_9_by), ._3_prime(hex_inverter_7__3_prime),
    ._4(quad_and_6__4y), ._4_prime(hex_inverter_7__4_prime), ._5(quad_and_6__3y),
    ._5_prime(hex_inverter_7__5_prime), ._6(quad_and_6__2y), ._6_prime(hex_inverter_7__6_prime));
  Hex_Inverter hex_inverter_8 (
    ._1(triple_2_channel_demux_9_bx), ._1_prime(hex_inverter_8__1_prime), ._2(triple_2_channel_demux_7_cy),
    ._2_prime(hex_inverter_8__2_prime), ._3(triple_2_channel_demux_7_cx), ._3_prime(hex_inverter_8__3_prime),
    ._4(quad_and_6__1y), ._4_prime(hex_inverter_8__4_prime), ._5(quad_and_5__4y),
    ._5_prime(hex_inverter_8__5_prime), ._6(quad_and_5__3y), ._6_prime(hex_inverter_8__6_prime));
  _8bit_register u_8bit_register_19 (
    .M(hex_inverter_7__1_prime), .N(hex_inverter_7__1_prime), .\input (Data), .clock(CLK), .CLR(1'b0),
    .\output (OUT_1), .G2(hex_inverter_7__4_prime), .G1(hex_inverter_7__4_prime));
  _8bit_register u_8bit_register_20 (
    .M(hex_inverter_7__2_prime), .N(hex_inverter_7__2_prime), .\input (Data), .clock(CLK), .CLR(1'b0),
    .\output (OUT_1), .G2(hex_inverter_7__5_prime), .G1(hex_inverter_7__5_prime));
  _8bit_register u_8bit_register_21 (
    .M(hex_inverter_7__3_prime), .N(hex_inverter_7__3_prime), .\input (Data), .clock(CLK), .CLR(1'b0),
    .\output (OUT_1), .G2(hex_inverter_7__6_prime), .G1(hex_inverter_7__6_prime));
  _8bit_register u_8bit_register_22 (
    .M(hex_inverter_8__1_prime), .N(hex_inverter_8__1_prime), .\input (Data), .clock(CLK), .CLR(1'b0),
    .\output (OUT_1), .G2(hex_inverter_8__4_prime), .G1(hex_inverter_8__4_prime));
  _8bit_register u_8bit_register_23 (
    .M(hex_inverter_8__2_prime), .N(hex_inverter_8__2_prime), .\input (Data), .clock(CLK), .CLR(1'b0),
    .\output (OUT_1), .G2(hex_inverter_8__5_prime), .G1(hex_inverter_8__5_prime));
  _8bit_register u_8bit_register_24 (
    .M(hex_inverter_8__3_prime), .N(hex_inverter_8__3_prime), .\input (Data), .clock(CLK), .CLR(1'b0),
    .\output (OUT_1), .G2(hex_inverter_8__6_prime), .G1(hex_inverter_8__6_prime));
  triple_2_channel_demux triple_2_channel_demux_10 (
    .bx(triple_2_channel_demux_10_bx), .by(triple_2_channel_demux_10_by), .cy(triple_2_channel_demux_10_cy),
    .c_in(triple_2_channel_demux_10_ay), .cx(triple_2_channel_demux_10_cx), .enable(1'b1),
    .b_in(triple_2_channel_demux_10_ax), .a_in(triple_2_channel_demux_8_cx),
    .ax(triple_2_channel_demux_10_ax), .ay(triple_2_channel_demux_10_ay), .A(Addr[1]), .B(Addr[0]),
    .C(Addr[0]));
  Hex_Inverter hex_inverter_9 (
    ._1(triple_2_channel_demux_11_by), ._1_prime(hex_inverter_9__1_prime), ._2(triple_2_channel_demux_11_bx),
    ._2_prime(hex_inverter_9__2_prime), ._3(triple_2_channel_demux_10_cy),
    ._3_prime(hex_inverter_9__3_prime), ._4(quad_and_7__4y), ._4_prime(hex_inverter_9__4_prime),
    ._5(quad_and_7__3y), ._5_prime(hex_inverter_9__5_prime), ._6(quad_and_8__2y),
    ._6_prime(hex_inverter_9__6_prime));
  Hex_Inverter hex_inverter_10 (
    ._1(triple_2_channel_demux_10_cx), ._1_prime(hex_inverter_10__1_prime),
    ._2(triple_2_channel_demux_10_by), ._2_prime(hex_inverter_10__2_prime),
    ._3(triple_2_channel_demux_10_bx), ._3_prime(hex_inverter_10__3_prime), ._4(quad_and_8__1y),
    ._4_prime(hex_inverter_10__4_prime), ._5(quad_and_7__2y), ._5_prime(hex_inverter_10__5_prime),
    ._6(quad_and_7__1y), ._6_prime(hex_inverter_10__6_prime));
  _8bit_register u_8bit_register_25 (
    .M(hex_inverter_9__1_prime), .N(hex_inverter_9__1_prime), .\input (Data), .clock(CLK), .CLR(1'b0),
    .\output (OUT_1), .G2(hex_inverter_9__4_prime), .G1(hex_inverter_9__4_prime));
  _8bit_register u_8bit_register_26 (
    .M(hex_inverter_9__2_prime), .N(hex_inverter_9__2_prime), .\input (Data), .clock(CLK), .CLR(1'b0),
    .\output (OUT_1), .G2(hex_inverter_9__5_prime), .G1(hex_inverter_9__5_prime));
  _8bit_register u_8bit_register_27 (
    .M(hex_inverter_9__3_prime), .N(hex_inverter_9__3_prime), .\input (Data), .clock(CLK), .CLR(1'b0),
    .\output (OUT_1), .G2(hex_inverter_9__6_prime), .G1(hex_inverter_9__6_prime));
  _8bit_register u_8bit_register_28 (
    .M(hex_inverter_10__1_prime), .N(hex_inverter_10__1_prime), .\input (Data), .clock(CLK), .CLR(1'b0),
    .\output (OUT_1), .G2(hex_inverter_10__4_prime), .G1(hex_inverter_10__4_prime));
  _8bit_register u_8bit_register_29 (
    .M(hex_inverter_10__2_prime), .N(hex_inverter_10__2_prime), .\input (Data), .clock(CLK), .CLR(1'b0),
    .\output (OUT_1), .G2(hex_inverter_10__5_prime), .G1(hex_inverter_10__5_prime));
  _8bit_register u_8bit_register_30 (
    .M(hex_inverter_10__3_prime), .N(hex_inverter_10__3_prime), .\input (Data), .clock(CLK), .CLR(1'b0),
    .\output (OUT_1), .G2(hex_inverter_10__6_prime), .G1(hex_inverter_10__6_prime));
  Quad_AND_Gate quad_and_7 (
    ._1a(W_TO), ._1b(triple_2_channel_demux_10_bx), ._1y(quad_and_7__1y), ._2a(W_TO),
    ._2b(triple_2_channel_demux_10_by), ._2y(quad_and_7__2y), ._3a(W_TO), ._3b(triple_2_channel_demux_11_bx),
    ._3y(quad_and_7__3y), ._4a(W_TO), ._4b(triple_2_channel_demux_11_by), ._4y(quad_and_7__4y));
  Quad_AND_Gate quad_and_8 (
    ._1a(W_TO), ._1b(triple_2_channel_demux_10_cx), ._1y(quad_and_8__1y), ._2a(W_TO),
    ._2b(triple_2_channel_demux_10_cy), ._2y(quad_and_8__2y), ._3a(W_TO), ._3b(triple_2_channel_demux_11_cx),
    ._3y(quad_and_8__3y), ._4a(W_TO), ._4b(triple_2_channel_demux_11_cy), ._4y(quad_and_8__4y));
  triple_2_channel_demux triple_2_channel_demux_11 (
    .bx(triple_2_channel_demux_11_bx), .by(triple_2_channel_demux_11_by), .cy(triple_2_channel_demux_11_cy),
    .c_in(triple_2_channel_demux_11_ay), .cx(triple_2_channel_demux_11_cx), .enable(1'b1),
    .b_in(triple_2_channel_demux_11_ax), .a_in(triple_2_channel_demux_8_cy),
    .ax(triple_2_channel_demux_11_ax), .ay(triple_2_channel_demux_11_ay), .A(Addr[1]), .B(Addr[0]),
    .C(Addr[0]));
  Hex_Inverter hex_inverter_11 (
    ._1(triple_2_channel_demux_11_cy), ._1_prime(hex_inverter_11__1_prime),
    ._2(triple_2_channel_demux_11_cx), ._2_prime(hex_inverter_11__2_prime), ._4(quad_and_8__4y),
    ._4_prime(hex_inverter_11__4_prime), ._5(quad_and_8__3y), ._5_prime(hex_inverter_11__5_prime));  // open: _3, _3_prime, _6, _6_prime
  _8bit_register u_8bit_register_31 (
    .M(hex_inverter_11__1_prime), .N(hex_inverter_11__1_prime), .\input (Data), .clock(CLK), .CLR(1'b0),
    .\output (OUT_1), .G2(hex_inverter_11__4_prime), .G1(hex_inverter_11__4_prime));
  _8bit_register u_8bit_register_32 (
    .M(hex_inverter_11__2_prime), .N(hex_inverter_11__2_prime), .\input (Data), .clock(CLK), .CLR(1'b0),
    .\output (OUT_1), .G2(hex_inverter_11__5_prime), .G1(hex_inverter_11__5_prime));

  // Notes on the sheet:
  //   CLR H16bytes
endmodule

// RAM
module RAM_v2 (
  input  CLR,
  input  W__nR,
  input  [7:0] AddrU,
  input  [7:0] AddrL,
  input  [7:0] Data,
  input  Clock,
  output [7:0] Out
);

  wire hex_inverter_1__1_prime, hex_inverter_1__6_prime, quad_or_1__1y, quad_or_1__2y, quad_or_1__3y,
       quad_or_1__4y;
  wire [7:0] ram_1_data;

  Hex_Inverter hex_inverter_1 (
    ._1(W__nR), ._1_prime(hex_inverter_1__1_prime), ._6(quad_or_1__1y), ._6_prime(hex_inverter_1__6_prime));  // open: _2, _2_prime, _3, _3_prime, _4, _4_prime, _5, _5_prime
  Quad_OR_Gate quad_or_1 (
    ._1a(hex_inverter_1__1_prime), ._1b(quad_or_1__2y), ._1y(quad_or_1__1y), ._2a(quad_or_1__3y),
    ._2b(quad_or_1__4y), ._2y(quad_or_1__2y), ._3a(AddrU[7]), ._3b(AddrU[6]), ._3y(quad_or_1__3y),
    ._4a(AddrU[5]), ._4b(AddrU[4]), ._4y(quad_or_1__4y));
  RAM_part #(.addrWidth(12)) ram_1 (
    .addr({AddrU[3:0], AddrL}), .data(ram_1_data), .clk(Clock), .ld(quad_or_1__1y), .clr(CLR));  // open: sel
  assign Out = quad_or_1__1y ? ram_1_data : 8'bz;  // Controlled_Buffer controlled_buffer_1
  assign ram_1_data = hex_inverter_1__6_prime ? Data : 8'bz;  // Controlled_Buffer controlled_buffer_2
endmodule

module PC (
  input  [7:0] write_byte,
  input  Reset_PC,
  input  nLoad_MSB,
  input  nLoad_LSB,
  input  nInterrupt,
  input  Load_Saved_PC,
  input  Clock,
  input  Enable_nInterrupts,
  output [15:0] PC_value,
  output Interrupt_Occured
);

  wire Disable_Interrupts_out_4, quad_or_1__3y;
  wire [0:0] adder_carry;
  wire [7:0] adder_2_output, adder_output, msb_add_output, mux_2_output, mux_3_output, mux_4_output,
       mux_output, n8bit_2_input_multiplexer_1_output, n8bit_2_input_multiplexer_2_output, Save_LSB_output,
       Save_MSB_output;

  triple_2_channel_mux triple_2_channel_mux_1 (
    .bx(nInterrupt), .by(1'b1), .enable(1'b1), .b_out(Interrupt_Occured), .B(quad_or_1__3y));  // open: cy, c_out, cx, a_out, ax, ay, A, C
  Quad_OR_Gate quad_or_1 (
    ._3a(Enable_nInterrupts), ._3b(Disable_Interrupts_out_4), ._3y(quad_or_1__3y));  // open: _1a, _1b, _1y, _2a, _2b, _2y, _4a, _4b, _4y
  _8bit_register msb_add (
    .M(1'b0), .N(1'b0), .\input (write_byte), .clock(Clock), .CLR(Reset_PC), .\output (msb_add_output),
    .G2(nLoad_MSB), .G1(nLoad_MSB));
  _8bit_2_input_multiplexer mux (
    .Input_1(n8bit_2_input_multiplexer_1_output), .Input_2(write_byte), .Output(mux_output),
    .Control(nLoad_LSB));
  _8bit_2_input_multiplexer mux_2 (
    .Input_1(mux_output), .Input_2(8'h7), .Output(mux_2_output), .Control(Interrupt_Occured));
  Disable_Interrupts Disable_Interrupts (
    .nInterrupt(Interrupt_Occured), .Clock(Clock), .LSPC(Load_Saved_PC), .out_4(Disable_Interrupts_out_4));
  _8bit_2_input_multiplexer u_8bit_2_input_multiplexer_1 (
    .Input_1(Save_LSB_output), .Input_2(adder_output), .Output(n8bit_2_input_multiplexer_1_output),
    .Control(Load_Saved_PC));
  _8bit_register LSB_reg (
    .M(1'b0), .N(1'b0), .\input (mux_2_output), .clock(Clock), .CLR(Reset_PC), .\output (PC_value[7:0]),
    .G2(1'b0), .G1(1'b0));
  _8bit_register Save_LSB (
    .M(1'b0), .N(1'b0), .\input (adder_output), .clock(Clock), .CLR(1'b0), .\output (Save_LSB_output),
    .G2(Interrupt_Occured), .G1(Interrupt_Occured));
  _8bit_adder adder (.Input1(PC_value[7:0]), .Input_2(8'h1), .Output(adder_output), .Carry(adder_carry[0]));
  _8bit_2_input_multiplexer mux_3 (
    .Input_1(mux_4_output), .Input_2({8{1'b0}}), .Output(mux_3_output), .Control(Interrupt_Occured));
  _8bit_2_input_multiplexer mux_4 (
    .Input_1(n8bit_2_input_multiplexer_2_output), .Input_2(msb_add_output), .Output(mux_4_output),
    .Control(nLoad_LSB));
  _8bit_register Save_MSB (
    .M(1'b0), .N(1'b0), .\input (adder_2_output), .clock(Clock), .CLR(1'b0), .\output (Save_MSB_output),
    .G2(Interrupt_Occured), .G1(Interrupt_Occured));
  _8bit_register MSB_reg (
    .M(1'b0), .N(1'b0), .\input (mux_3_output), .clock(Clock), .CLR(Reset_PC), .\output (PC_value[15:8]),
    .G2(1'b0), .G1(1'b0));
  _8bit_2_input_multiplexer u_8bit_2_input_multiplexer_2 (
    .Input_1(Save_MSB_output), .Input_2(adder_2_output), .Output(n8bit_2_input_multiplexer_2_output),
    .Control(Load_Saved_PC));
  _8bit_adder adder_2 (
    .Input1(PC_value[15:8]), .Input_2({{7{1'b0}}, adder_carry[0]}), .Output(adder_2_output));  // open: Carry
endmodule

module _8bit_AND_Gate (
  input  [7:0] In_1,
  input  [7:0] In_2,
  output [7:0] Out
);

  Quad_AND_Gate quad_and_1 (
    ._1a(In_1[0]), ._1b(In_2[0]), ._1y(Out[0]), ._2a(In_1[1]), ._2b(In_2[1]), ._2y(Out[1]), ._3a(In_1[2]),
    ._3b(In_2[2]), ._3y(Out[2]), ._4a(In_1[3]), ._4b(In_2[3]), ._4y(Out[3]));
  Quad_AND_Gate quad_and_2 (
    ._1a(In_1[4]), ._1b(In_2[4]), ._1y(Out[4]), ._2a(In_1[5]), ._2b(In_2[5]), ._2y(Out[5]), ._3a(In_1[6]),
    ._3b(In_2[6]), ._3y(Out[6]), ._4a(In_1[7]), ._4b(In_2[7]), ._4y(Out[7]));
endmodule

module _8bit_OR_Gate (
  input  [7:0] In_1,
  input  [7:0] In_2,
  output [7:0] Out
);

  Quad_OR_Gate quad_or_1 (
    ._1a(In_1[0]), ._1b(In_2[0]), ._1y(Out[0]), ._2a(In_1[1]), ._2b(In_2[1]), ._2y(Out[1]), ._3a(In_1[2]),
    ._3b(In_2[2]), ._3y(Out[2]), ._4a(In_1[3]), ._4b(In_2[3]), ._4y(Out[3]));
  Quad_OR_Gate quad_or_2 (
    ._1a(In_1[4]), ._1b(In_2[4]), ._1y(Out[4]), ._2a(In_1[5]), ._2b(In_2[5]), ._2y(Out[5]), ._3a(In_1[6]),
    ._3b(In_2[6]), ._3y(Out[6]), ._4a(In_1[7]), ._4b(In_2[7]), ._4y(Out[7]));
endmodule

module _8bit_XOR (
  input  [7:0] Read_1,
  input  [7:0] Read_2,
  output [7:0] Write
);

  Quad_XOR_gate quad_xor_gate_1 (
    ._1a(Read_1[2]), ._1b(Read_2[2]), ._1_y(Write[2]), ._2a(Read_2[3]), ._2b(Read_1[3]), ._2_y(Write[3]),
    ._3a(Read_1[0]), ._3b(Read_2[0]), ._3_y(Write[0]), ._4a(Read_2[1]), ._4b(Read_1[1]), ._4_y(Write[1]));
  Quad_XOR_gate quad_xor_gate_2 (
    ._1a(Read_1[6]), ._1b(Read_2[6]), ._1_y(Write[6]), ._2a(Read_1[7]), ._2b(Read_2[7]), ._2_y(Write[7]),
    ._3a(Read_2[4]), ._3b(Read_1[4]), ._3_y(Write[4]), ._4a(Read_2[5]), ._4b(Read_1[5]), ._4_y(Write[5]));
endmodule

module _1bit_16_input_multiplexer (
  input  C15,
  input  C14,
  input  C13,
  input  C12,
  input  C11,
  input  C10,
  input  C9,
  input  C8,
  input  C7,
  input  C6,
  input  C5,
  input  C4,
  input  C3,
  input  C2,
  input  C1,
  input  C0,
  input  S3,
  input  S2,
  input  S1,
  input  S0,
  input  En,
  output SIG
);

  wire not_1_out;

  Multiplexer #(.select(4)) multiplexer_1 (
    .in0(C0), .in1(C1), .in2(C2), .in3(C3), .in4(C4), .in5(C5), .in6(C6), .in7(C7), .in8(C8), .in9(C9),
    .in10(C10), .in11(C11), .in12(C12), .in13(C13), .in14(C14), .in15(C15), .out(SIG),
    .sel({S3, S2, S1, S0}), .en(not_1_out));
  not not_1 (not_1_out, En);
endmodule

module _1_bit_16_output_demultiplexer (
  input  SIG,
  input  S3,
  input  S2,
  input  S1,
  input  S0,
  input  En,
  output C15,
  output C14,
  output C13,
  output C12,
  output C11,
  output C10,
  output C9,
  output C8,
  output C7,
  output C6,
  output C5,
  output C4,
  output C3,
  output C2,
  output C1,
  output C0
);

  wire not_1_out;

  Demultiplexer #(.select(4)) demultiplexer_1 (
    .out0(C0), .out1(C1), .out2(C2), .out3(C3), .out4(C4), .out5(C5), .out6(C6), .out7(C7), .out8(C8),
    .out9(C9), .out10(C10), .out11(C11), .out12(C12), .out13(C13), .out14(C14), .out15(C15), .in(SIG),
    .sel({S3, S2, S1, S0}), .en(not_1_out));
  not not_1 (not_1_out, En);
endmodule

module _8bit_2_input_multiplexer (
  input  [7:0] Input_1,
  input  [7:0] Input_2,
  input  Control,
  output [7:0] Output
);

  triple_2_channel_mux triple_2_channel_mux_1 (
    .bx(Input_2[0]), .by(Input_1[0]), .cy(Input_1[1]), .c_out(Output[1]), .cx(Input_2[1]), .enable(1'b1),
    .b_out(Output[0]), .A(Control), .B(Control), .C(Control));  // open: a_out, ax, ay
  triple_2_channel_mux triple_2_channel_mux_2 (
    .bx(Input_2[3]), .by(Input_1[3]), .cy(Input_1[4]), .c_out(Output[4]), .cx(Input_2[4]), .enable(1'b1),
    .b_out(Output[3]), .a_out(Output[2]), .ax(Input_2[2]), .ay(Input_1[2]), .A(Control), .B(Control),
    .C(Control));
  triple_2_channel_mux triple_2_channel_mux_3 (
    .bx(Input_2[6]), .by(Input_1[6]), .cy(Input_1[7]), .c_out(Output[7]), .cx(Input_2[7]), .enable(1'b1),
    .b_out(Output[6]), .a_out(Output[5]), .ax(Input_2[5]), .ay(Input_1[5]), .A(Control), .B(Control),
    .C(Control));
endmodule

module _8bit_2_output_demuliplexer (
  input  [7:0] Input,
  input  Control,
  output [7:0] Output_1,
  output [7:0] Output_2
);

  triple_2_channel_demux triple_2_channel_demux_1 (
    .bx(Output_2[0]), .by(Output_1[0]), .cy(Output_1[1]), .c_in(Input[1]), .cx(Output_2[1]), .enable(1'b1),
    .b_in(Input[0]), .A(Control), .B(Control), .C(Control));  // open: a_in, ax, ay
  triple_2_channel_demux triple_2_channel_demux_2 (
    .bx(Output_2[3]), .by(Output_1[3]), .cy(Output_1[4]), .c_in(Input[4]), .cx(Output_2[4]), .enable(1'b1),
    .b_in(Input[3]), .a_in(Input[2]), .ax(Output_2[2]), .ay(Output_1[2]), .A(Control), .B(Control),
    .C(Control));
  triple_2_channel_demux triple_2_channel_demux_3 (
    .bx(Output_2[6]), .by(Output_1[6]), .cy(Output_1[7]), .c_in(Input[7]), .cx(Output_2[7]), .enable(1'b1),
    .b_in(Input[6]), .a_in(Input[5]), .ax(Output_2[5]), .ay(Output_1[5]), .A(Control), .B(Control),
    .C(Control));
endmodule

module _8bit_3_input_multiplexer (
  input  [7:0] Input_0,
  input  [7:0] in_2,
  input  [7:0] in_3,
  input  S1,
  input  S0,
  output [7:0] out_6
);

  _1bit_16_input_multiplexer u_1bit_16_input_multiplexer_1 (
    .C15(1'b0), .C14(1'b0), .C13(1'b0), .C12(1'b0), .C11(1'b0), .C10(1'b0), .C9(1'b0), .C8(1'b0), .C7(1'b0),
    .C6(1'b0), .C5(1'b0), .C4(1'b0), .C3(1'b0), .C2(in_3[0]), .C1(in_2[0]), .C0(Input_0[0]), .SIG(out_6[0]),
    .S3(1'b0), .S2(1'b0), .S1(S1), .S0(S0), .En(1'b0));
  _1bit_16_input_multiplexer u_1bit_16_input_multiplexer_2 (
    .C15(1'b0), .C14(1'b0), .C13(1'b0), .C12(1'b0), .C11(1'b0), .C10(1'b0), .C9(1'b0), .C8(1'b0), .C7(1'b0),
    .C6(1'b0), .C5(1'b0), .C4(1'b0), .C3(1'b0), .C2(in_3[1]), .C1(in_2[1]), .C0(Input_0[1]), .SIG(out_6[1]),
    .S3(1'b0), .S2(1'b0), .S1(S1), .S0(S0), .En(1'b0));
  _1bit_16_input_multiplexer u_1bit_16_input_multiplexer_3 (
    .C15(1'b0), .C14(1'b0), .C13(1'b0), .C12(1'b0), .C11(1'b0), .C10(1'b0), .C9(1'b0), .C8(1'b0), .C7(1'b0),
    .C6(1'b0), .C5(1'b0), .C4(1'b0), .C3(1'b0), .C2(in_3[2]), .C1(in_2[2]), .C0(Input_0[2]), .SIG(out_6[2]),
    .S3(1'b0), .S2(1'b0), .S1(S1), .S0(S0), .En(1'b0));
  _1bit_16_input_multiplexer u_1bit_16_input_multiplexer_4 (
    .C15(1'b0), .C14(1'b0), .C13(1'b0), .C12(1'b0), .C11(1'b0), .C10(1'b0), .C9(1'b0), .C8(1'b0), .C7(1'b0),
    .C6(1'b0), .C5(1'b0), .C4(1'b0), .C3(1'b0), .C2(in_3[3]), .C1(in_2[3]), .C0(Input_0[3]), .SIG(out_6[3]),
    .S3(1'b0), .S2(1'b0), .S1(S1), .S0(S0), .En(1'b0));
  _1bit_16_input_multiplexer u_1bit_16_input_multiplexer_5 (
    .C15(1'b0), .C14(1'b0), .C13(1'b0), .C12(1'b0), .C11(1'b0), .C10(1'b0), .C9(1'b0), .C8(1'b0), .C7(1'b0),
    .C6(1'b0), .C5(1'b0), .C4(1'b0), .C3(1'b0), .C2(in_3[4]), .C1(in_2[4]), .C0(Input_0[4]), .SIG(out_6[4]),
    .S3(1'b0), .S2(1'b0), .S1(S1), .S0(S0), .En(1'b0));
  _1bit_16_input_multiplexer u_1bit_16_input_multiplexer_6 (
    .C15(1'b0), .C14(1'b0), .C13(1'b0), .C12(1'b0), .C11(1'b0), .C10(1'b0), .C9(1'b0), .C8(1'b0), .C7(1'b0),
    .C6(1'b0), .C5(1'b0), .C4(1'b0), .C3(1'b0), .C2(in_3[5]), .C1(in_2[5]), .C0(Input_0[5]), .SIG(out_6[5]),
    .S3(1'b0), .S2(1'b0), .S1(S1), .S0(S0), .En(1'b0));
  _1bit_16_input_multiplexer u_1bit_16_input_multiplexer_7 (
    .C15(1'b0), .C14(1'b0), .C13(1'b0), .C12(1'b0), .C11(1'b0), .C10(1'b0), .C9(1'b0), .C8(1'b0), .C7(1'b0),
    .C6(1'b0), .C5(1'b0), .C4(1'b0), .C3(1'b0), .C2(in_3[6]), .C1(in_2[6]), .C0(Input_0[6]), .SIG(out_6[6]),
    .S3(1'b0), .S2(1'b0), .S1(S1), .S0(S0), .En(1'b0));
  _1bit_16_input_multiplexer u_1bit_16_input_multiplexer_8 (
    .C15(1'b0), .C14(1'b0), .C13(1'b0), .C12(1'b0), .C11(1'b0), .C10(1'b0), .C9(1'b0), .C8(1'b0), .C7(1'b0),
    .C6(1'b0), .C5(1'b0), .C4(1'b0), .C3(1'b0), .C2(in_3[7]), .C1(in_2[7]), .C0(Input_0[7]), .SIG(out_6[7]),
    .S3(1'b0), .S2(1'b0), .S1(S1), .S0(S0), .En(1'b0));
endmodule

// Read Mux
module _8bit_5_input_multiplexer (
  input  [7:0] Input_0,
  input  [7:0] Input_1,
  input  [7:0] Input_2,
  input  [7:0] Input_3,
  input  [7:0] Input_4,
  input  S2,
  input  S1,
  input  S0,
  output [7:0] out_9
);

  _1bit_16_input_multiplexer u_1bit_16_input_multiplexer_1 (
    .C15(1'b0), .C14(1'b0), .C13(1'b0), .C12(1'b0), .C11(1'b0), .C10(1'b0), .C9(1'b0), .C8(1'b0), .C7(1'b0),
    .C6(1'b0), .C5(1'b0), .C4(Input_4[0]), .C3(Input_3[0]), .C2(Input_2[0]), .C1(Input_1[0]),
    .C0(Input_0[0]), .SIG(out_9[0]), .S3(1'b0), .S2(S2), .S1(S1), .S0(S0), .En(1'b0));
  _1bit_16_input_multiplexer u_1bit_16_input_multiplexer_2 (
    .C15(1'b0), .C14(1'b0), .C13(1'b0), .C12(1'b0), .C11(1'b0), .C10(1'b0), .C9(1'b0), .C8(1'b0), .C7(1'b0),
    .C6(1'b0), .C5(1'b0), .C4(Input_4[1]), .C3(Input_3[1]), .C2(Input_2[1]), .C1(Input_1[1]),
    .C0(Input_0[1]), .SIG(out_9[1]), .S3(1'b0), .S2(S2), .S1(S1), .S0(S0), .En(1'b0));
  _1bit_16_input_multiplexer u_1bit_16_input_multiplexer_3 (
    .C15(1'b0), .C14(1'b0), .C13(1'b0), .C12(1'b0), .C11(1'b0), .C10(1'b0), .C9(1'b0), .C8(1'b0), .C7(1'b0),
    .C6(1'b0), .C5(1'b0), .C4(Input_4[2]), .C3(Input_3[2]), .C2(Input_2[2]), .C1(Input_1[2]),
    .C0(Input_0[2]), .SIG(out_9[2]), .S3(1'b0), .S2(S2), .S1(S1), .S0(S0), .En(1'b0));
  _1bit_16_input_multiplexer u_1bit_16_input_multiplexer_4 (
    .C15(1'b0), .C14(1'b0), .C13(1'b0), .C12(1'b0), .C11(1'b0), .C10(1'b0), .C9(1'b0), .C8(1'b0), .C7(1'b0),
    .C6(1'b0), .C5(1'b0), .C4(Input_4[3]), .C3(Input_3[3]), .C2(Input_2[3]), .C1(Input_1[3]),
    .C0(Input_0[3]), .SIG(out_9[3]), .S3(1'b0), .S2(S2), .S1(S1), .S0(S0), .En(1'b0));
  _1bit_16_input_multiplexer u_1bit_16_input_multiplexer_5 (
    .C15(1'b0), .C14(1'b0), .C13(1'b0), .C12(1'b0), .C11(1'b0), .C10(1'b0), .C9(1'b0), .C8(1'b0), .C7(1'b0),
    .C6(1'b0), .C5(1'b0), .C4(Input_4[4]), .C3(Input_3[4]), .C2(Input_2[4]), .C1(Input_1[4]),
    .C0(Input_0[4]), .SIG(out_9[4]), .S3(1'b0), .S2(S2), .S1(S1), .S0(S0), .En(1'b0));
  _1bit_16_input_multiplexer u_1bit_16_input_multiplexer_6 (
    .C15(1'b0), .C14(1'b0), .C13(1'b0), .C12(1'b0), .C11(1'b0), .C10(1'b0), .C9(1'b0), .C8(1'b0), .C7(1'b0),
    .C6(1'b0), .C5(1'b0), .C4(Input_4[5]), .C3(Input_3[5]), .C2(Input_2[5]), .C1(Input_1[5]),
    .C0(Input_0[5]), .SIG(out_9[5]), .S3(1'b0), .S2(S2), .S1(S1), .S0(S0), .En(1'b0));
  _1bit_16_input_multiplexer u_1bit_16_input_multiplexer_7 (
    .C15(1'b0), .C14(1'b0), .C13(1'b0), .C12(1'b0), .C11(1'b0), .C10(1'b0), .C9(1'b0), .C8(1'b0), .C7(1'b0),
    .C6(1'b0), .C5(1'b0), .C4(Input_4[6]), .C3(Input_3[6]), .C2(Input_2[6]), .C1(Input_1[6]),
    .C0(Input_0[6]), .SIG(out_9[6]), .S3(1'b0), .S2(S2), .S1(S1), .S0(S0), .En(1'b0));
  _1bit_16_input_multiplexer u_1bit_16_input_multiplexer_8 (
    .C15(1'b0), .C14(1'b0), .C13(1'b0), .C12(1'b0), .C11(1'b0), .C10(1'b0), .C9(1'b0), .C8(1'b0), .C7(1'b0),
    .C6(1'b0), .C5(1'b0), .C4(Input_4[7]), .C3(Input_3[7]), .C2(Input_2[7]), .C1(Input_1[7]),
    .C0(Input_0[7]), .SIG(out_9[7]), .S3(1'b0), .S2(S2), .S1(S1), .S0(S0), .En(1'b0));
endmodule

// Read Mux
module _8bit_6_input_multiplexer (
  input  [7:0] Input_0,
  input  [7:0] Input_1,
  input  [7:0] Input_2,
  input  [7:0] Input_3,
  input  [7:0] Input_4,
  input  [7:0] Input_7,
  input  S2,
  input  S1,
  input  S0,
  output [7:0] out_10
);

  _1bit_16_input_multiplexer u_1bit_16_input_multiplexer_1 (
    .C15(1'b0), .C14(1'b0), .C13(1'b0), .C12(1'b0), .C11(1'b0), .C10(1'b0), .C9(1'b0), .C8(1'b0),
    .C7(Input_7[0]), .C6(1'b0), .C5(1'b0), .C4(Input_4[0]), .C3(Input_3[0]), .C2(Input_2[0]),
    .C1(Input_1[0]), .C0(Input_0[0]), .SIG(out_10[0]), .S3(1'b0), .S2(S2), .S1(S1), .S0(S0), .En(1'b0));
  _1bit_16_input_multiplexer u_1bit_16_input_multiplexer_2 (
    .C15(1'b0), .C14(1'b0), .C13(1'b0), .C12(1'b0), .C11(1'b0), .C10(1'b0), .C9(1'b0), .C8(1'b0),
    .C7(Input_7[1]), .C6(1'b0), .C5(1'b0), .C4(Input_4[1]), .C3(Input_3[1]), .C2(Input_2[1]),
    .C1(Input_1[1]), .C0(Input_0[1]), .SIG(out_10[1]), .S3(1'b0), .S2(S2), .S1(S1), .S0(S0), .En(1'b0));
  _1bit_16_input_multiplexer u_1bit_16_input_multiplexer_3 (
    .C15(1'b0), .C14(1'b0), .C13(1'b0), .C12(1'b0), .C11(1'b0), .C10(1'b0), .C9(1'b0), .C8(1'b0),
    .C7(Input_7[2]), .C6(1'b0), .C5(1'b0), .C4(Input_4[2]), .C3(Input_3[2]), .C2(Input_2[2]),
    .C1(Input_1[2]), .C0(Input_0[2]), .SIG(out_10[2]), .S3(1'b0), .S2(S2), .S1(S1), .S0(S0), .En(1'b0));
  _1bit_16_input_multiplexer u_1bit_16_input_multiplexer_4 (
    .C15(1'b0), .C14(1'b0), .C13(1'b0), .C12(1'b0), .C11(1'b0), .C10(1'b0), .C9(1'b0), .C8(1'b0),
    .C7(Input_7[3]), .C6(1'b0), .C5(1'b0), .C4(Input_4[3]), .C3(Input_3[3]), .C2(Input_2[3]),
    .C1(Input_1[3]), .C0(Input_0[3]), .SIG(out_10[3]), .S3(1'b0), .S2(S2), .S1(S1), .S0(S0), .En(1'b0));
  _1bit_16_input_multiplexer u_1bit_16_input_multiplexer_5 (
    .C15(1'b0), .C14(1'b0), .C13(1'b0), .C12(1'b0), .C11(1'b0), .C10(1'b0), .C9(1'b0), .C8(1'b0),
    .C7(Input_7[4]), .C6(1'b0), .C5(1'b0), .C4(Input_4[4]), .C3(Input_3[4]), .C2(Input_2[4]),
    .C1(Input_1[4]), .C0(Input_0[4]), .SIG(out_10[4]), .S3(1'b0), .S2(S2), .S1(S1), .S0(S0), .En(1'b0));
  _1bit_16_input_multiplexer u_1bit_16_input_multiplexer_6 (
    .C15(1'b0), .C14(1'b0), .C13(1'b0), .C12(1'b0), .C11(1'b0), .C10(1'b0), .C9(1'b0), .C8(1'b0),
    .C7(Input_7[5]), .C6(1'b0), .C5(1'b0), .C4(Input_4[5]), .C3(Input_3[5]), .C2(Input_2[5]),
    .C1(Input_1[5]), .C0(Input_0[5]), .SIG(out_10[5]), .S3(1'b0), .S2(S2), .S1(S1), .S0(S0), .En(1'b0));
  _1bit_16_input_multiplexer u_1bit_16_input_multiplexer_7 (
    .C15(1'b0), .C14(1'b0), .C13(1'b0), .C12(1'b0), .C11(1'b0), .C10(1'b0), .C9(1'b0), .C8(1'b0),
    .C7(Input_7[6]), .C6(1'b0), .C5(1'b0), .C4(Input_4[6]), .C3(Input_3[6]), .C2(Input_2[6]),
    .C1(Input_1[6]), .C0(Input_0[6]), .SIG(out_10[6]), .S3(1'b0), .S2(S2), .S1(S1), .S0(S0), .En(1'b0));
  _1bit_16_input_multiplexer u_1bit_16_input_multiplexer_8 (
    .C15(1'b0), .C14(1'b0), .C13(1'b0), .C12(1'b0), .C11(1'b0), .C10(1'b0), .C9(1'b0), .C8(1'b0),
    .C7(Input_7[7]), .C6(1'b0), .C5(1'b0), .C4(Input_4[7]), .C3(Input_3[7]), .C2(Input_2[7]),
    .C1(Input_1[7]), .C0(Input_0[7]), .SIG(out_10[7]), .S3(1'b0), .S2(S2), .S1(S1), .S0(S0), .En(1'b0));
endmodule

// Write Mux
module _8bit_16_input_multiplexer (
  input  [7:0] Input_0,
  input  [7:0] Input_1,
  input  [7:0] Input_2,
  input  [7:0] Input_3,
  input  [7:0] Input_4,
  input  [7:0] Input_5,
  input  [7:0] Input_6,
  input  [7:0] Input_7,
  input  [7:0] Input_8,
  input  [7:0] Input_9,
  input  [7:0] Input_10,
  input  [7:0] Input_11,
  input  [7:0] Input_12,
  input  [7:0] Input_13,
  input  [7:0] Input_14,
  input  [7:0] Input_15,
  input  S3,
  input  S2,
  input  S1,
  input  S0,
  output [7:0] out_21
);

  _1bit_16_input_multiplexer u_1bit_16_input_multiplexer_1 (
    .C15(Input_15[0]), .C14(Input_14[0]), .C13(Input_13[0]), .C12(Input_12[0]), .C11(Input_11[0]),
    .C10(Input_10[0]), .C9(Input_9[0]), .C8(Input_8[0]), .C7(Input_7[0]), .C6(Input_6[0]), .C5(Input_5[0]),
    .C4(Input_4[0]), .C3(Input_3[0]), .C2(Input_2[0]), .C1(Input_1[0]), .C0(Input_0[0]), .SIG(out_21[0]),
    .S3(S3), .S2(S2), .S1(S1), .S0(S0), .En(1'b0));
  _1bit_16_input_multiplexer u_1bit_16_input_multiplexer_2 (
    .C15(Input_15[1]), .C14(Input_14[1]), .C13(Input_13[1]), .C12(Input_12[1]), .C11(Input_11[1]),
    .C10(Input_10[1]), .C9(Input_9[1]), .C8(Input_8[1]), .C7(Input_7[1]), .C6(Input_6[1]), .C5(Input_5[1]),
    .C4(Input_4[1]), .C3(Input_3[1]), .C2(Input_2[1]), .C1(Input_1[1]), .C0(Input_0[1]), .SIG(out_21[1]),
    .S3(S3), .S2(S2), .S1(S1), .S0(S0), .En(1'b0));
  _1bit_16_input_multiplexer u_1bit_16_input_multiplexer_3 (
    .C15(Input_15[2]), .C14(Input_14[2]), .C13(Input_13[2]), .C12(Input_12[2]), .C11(Input_11[2]),
    .C10(Input_10[2]), .C9(Input_9[2]), .C8(Input_8[2]), .C7(Input_7[2]), .C6(Input_6[2]), .C5(Input_5[2]),
    .C4(Input_4[2]), .C3(Input_3[2]), .C2(Input_2[2]), .C1(Input_1[2]), .C0(Input_0[2]), .SIG(out_21[2]),
    .S3(S3), .S2(S2), .S1(S1), .S0(S0), .En(1'b0));
  _1bit_16_input_multiplexer u_1bit_16_input_multiplexer_4 (
    .C15(Input_15[3]), .C14(Input_14[3]), .C13(Input_13[3]), .C12(Input_12[3]), .C11(Input_11[3]),
    .C10(Input_10[3]), .C9(Input_9[3]), .C8(Input_8[3]), .C7(Input_7[3]), .C6(Input_6[3]), .C5(Input_5[3]),
    .C4(Input_4[3]), .C3(Input_3[3]), .C2(Input_2[3]), .C1(Input_1[3]), .C0(Input_0[3]), .SIG(out_21[3]),
    .S3(S3), .S2(S2), .S1(S1), .S0(S0), .En(1'b0));
  _1bit_16_input_multiplexer u_1bit_16_input_multiplexer_5 (
    .C15(Input_15[4]), .C14(Input_14[4]), .C13(Input_13[4]), .C12(Input_12[4]), .C11(Input_11[4]),
    .C10(Input_10[4]), .C9(Input_9[4]), .C8(Input_8[4]), .C7(Input_7[4]), .C6(Input_6[4]), .C5(Input_5[4]),
    .C4(Input_4[4]), .C3(Input_3[4]), .C2(Input_2[4]), .C1(Input_1[4]), .C0(Input_0[4]), .SIG(out_21[4]),
    .S3(S3), .S2(S2), .S1(S1), .S0(S0), .En(1'b0));
  _1bit_16_input_multiplexer u_1bit_16_input_multiplexer_6 (
    .C15(Input_15[5]), .C14(Input_14[5]), .C13(Input_13[5]), .C12(Input_12[5]), .C11(Input_11[5]),
    .C10(Input_10[5]), .C9(Input_9[5]), .C8(Input_8[5]), .C7(Input_7[5]), .C6(Input_6[5]), .C5(Input_5[5]),
    .C4(Input_4[5]), .C3(Input_3[5]), .C2(Input_2[5]), .C1(Input_1[5]), .C0(Input_0[5]), .SIG(out_21[5]),
    .S3(S3), .S2(S2), .S1(S1), .S0(S0), .En(1'b0));
  _1bit_16_input_multiplexer u_1bit_16_input_multiplexer_7 (
    .C15(Input_15[6]), .C14(Input_14[6]), .C13(Input_13[6]), .C12(Input_12[6]), .C11(Input_11[6]),
    .C10(Input_10[6]), .C9(Input_9[6]), .C8(Input_8[6]), .C7(Input_7[6]), .C6(Input_6[6]), .C5(Input_5[6]),
    .C4(Input_4[6]), .C3(Input_3[6]), .C2(Input_2[6]), .C1(Input_1[6]), .C0(Input_0[6]), .SIG(out_21[6]),
    .S3(S3), .S2(S2), .S1(S1), .S0(S0), .En(1'b0));
  _1bit_16_input_multiplexer u_1bit_16_input_multiplexer_8 (
    .C15(Input_15[7]), .C14(Input_14[7]), .C13(Input_13[7]), .C12(Input_12[7]), .C11(Input_11[7]),
    .C10(Input_10[7]), .C9(Input_9[7]), .C8(Input_8[7]), .C7(Input_7[7]), .C6(Input_6[7]), .C5(Input_5[7]),
    .C4(Input_4[7]), .C3(Input_3[7]), .C2(Input_2[7]), .C1(Input_1[7]), .C0(Input_0[7]), .SIG(out_21[7]),
    .S3(S3), .S2(S2), .S1(S1), .S0(S0), .En(1'b0));
endmodule

module _8bit_adder (
  input  [7:0] Input1,
  input  [7:0] Input_2,
  output [7:0] Output,
  output Carry
);

  wire n4bit_adder_1_c_out;

  _4bit_adder u_4bit_adder_1 (
    .In_1(Input1[3:0]), .In_2(Input_2[3:0]), .C_in(1'b0), .Out(Output[3:0]), .C_out(n4bit_adder_1_c_out));
  _4bit_adder u_4bit_adder_2 (
    .In_1(Input1[7:4]), .In_2(Input_2[7:4]), .C_in(n4bit_adder_1_c_out), .Out(Output[7:4]), .C_out(Carry));
endmodule

module _8bit_register (
  input  M,
  input  CLR,
  input  N,
  input  [7:0] \input ,
  input  clock,
  input  G2,
  input  G1,
  output [7:0] \output 
);

  _4bit_register u_4bit_register_1 (
    .M(M), .N(N), ._1Q(\input [0]), ._2Q(\input [1]), ._3Q(\input [2]), ._4Q(\input [3]), .CLK(clock),
    .CLR(CLR), ._1D(\output [0]), ._2D(\output [1]), ._3D(\output [2]), ._4D(\output [3]), .G2(G2), .G1(G1));
  _4bit_register u_4bit_register_2 (
    .M(M), .N(N), ._1Q(\input [4]), ._2Q(\input [5]), ._3Q(\input [6]), ._4Q(\input [7]), .CLK(clock),
    .CLR(CLR), ._1D(\output [4]), ._2D(\output [5]), ._3D(\output [6]), ._4D(\output [7]), .G2(G2), .G1(G1));
endmodule

module triple_2_channel_mux (
  input  bx,
  input  by,
  input  cy,
  input  ax,
  input  ay,
  input  cx,
  input  A,
  input  enable,
  input  B,
  input  C,
  output b_out,
  output a_out,
  output c_out
);

  Multiplexer multiplexer_1 (.in0(cx), .in1(cy), .out(c_out), .sel(C), .en(enable));
  Multiplexer multiplexer_2 (.in0(bx), .in1(by), .out(b_out), .sel(B), .en(enable));
  Multiplexer multiplexer_3 (.in0(ax), .in1(ay), .out(a_out), .sel(A), .en(enable));

  // Notes on the sheet:
  //   Cd4053B as multiplexer
endmodule

module triple_2_channel_demux (
  input  b_in,
  input  a_in,
  input  c_in,
  input  A,
  input  enable,
  input  B,
  input  C,
  output bx,
  output by,
  output cy,
  output ax,
  output ay,
  output cx
);

  Demultiplexer demultiplexer_1 (.out0(cx), .out1(cy), .in(c_in), .sel(C), .en(enable));
  Demultiplexer demultiplexer_2 (.out0(bx), .out1(by), .in(b_in), .sel(B), .en(enable));
  Demultiplexer demultiplexer_3 (.out0(ax), .out1(ay), .in(a_in), .sel(A), .en(enable));

  // Notes on the sheet:
  //   Cd4053B as demultiplexer
endmodule

// Or
module Quad_OR_Gate (
  input  _3a,
  input  _1a,
  input  _3b,
  input  _1b,
  input  _4a,
  input  _2a,
  input  _4b,
  input  _2b,
  output _3y,
  output _1y,
  output _4y,
  output _2y
);

  or or_1 (_1y, _1a, _1b);
  or or_2 (_2y, _2a, _2b);
  or or_3 (_3y, _3a, _3b);
  or or_4 (_4y, _4a, _4b);
endmodule

// And
module Quad_AND_Gate (
  input  _3a,
  input  _1a,
  input  _3b,
  input  _1b,
  input  _4a,
  input  _2a,
  input  _4b,
  input  _2b,
  output _3y,
  output _1y,
  output _4y,
  output _2y
);

  and and_1 (_1y, _1a, _1b);
  and and_2 (_2y, _2a, _2b);
  and and_3 (_3y, _3a, _3b);
  and and_4 (_4y, _4a, _4b);
endmodule

module Quad_XOR_gate (
  input  _3a,
  input  _1a,
  input  _3b,
  input  _1b,
  input  _4a,
  input  _2a,
  input  _4b,
  input  _2b,
  output _3_y,
  output _1_y,
  output _4_y,
  output _2_y
);

  xor xor_1 (_1_y, _1a, _1b);
  xor xor_2 (_2_y, _2a, _2b);
  xor xor_3 (_3_y, _3a, _3b);
  xor xor_4 (_4_y, _4a, _4b);

  // Notes on the sheet:
  //   XOR Gate Sn74hc86n
endmodule

module _4bit_adder (
  input  [3:0] In_1,
  input  [3:0] In_2,
  input  C_in,
  output [3:0] Out,
  output C_out
);

  wire quad_and_1__1y, quad_and_1__2y, quad_and_1__3y, quad_and_1__4y, quad_and_2__1y, quad_and_2__2y,
       quad_and_2__3y, quad_and_2__4y, quad_or_1__1y, quad_or_1__2y, quad_or_1__3y, quad_xor_gate_1__1_y,
       quad_xor_gate_1__3_y, quad_xor_gate_2__1_y, quad_xor_gate_2__3_y;

  Quad_XOR_gate quad_xor_gate_1 (
    ._1a(In_1[0]), ._1b(In_2[0]), ._1_y(quad_xor_gate_1__1_y), ._2a(quad_xor_gate_1__1_y), ._2b(C_in),
    ._2_y(Out[0]), ._3a(In_1[1]), ._3b(In_2[1]), ._3_y(quad_xor_gate_1__3_y), ._4a(quad_xor_gate_1__3_y),
    ._4b(quad_or_1__1y), ._4_y(Out[1]));
  Quad_XOR_gate quad_xor_gate_2 (
    ._1a(In_1[2]), ._1b(In_2[2]), ._1_y(quad_xor_gate_2__1_y), ._2a(quad_xor_gate_2__1_y),
    ._2b(quad_or_1__2y), ._2_y(Out[2]), ._3a(In_1[3]), ._3b(In_2[3]), ._3_y(quad_xor_gate_2__3_y),
    ._4a(quad_xor_gate_2__3_y), ._4b(quad_or_1__3y), ._4_y(Out[3]));
  Quad_AND_Gate quad_and_1 (
    ._1a(quad_xor_gate_1__1_y), ._1b(C_in), ._1y(quad_and_1__1y), ._2a(In_2[0]), ._2b(In_1[0]),
    ._2y(quad_and_1__2y), ._3a(quad_xor_gate_1__3_y), ._3b(quad_or_1__1y), ._3y(quad_and_1__3y),
    ._4a(In_1[1]), ._4b(In_2[1]), ._4y(quad_and_1__4y));
  Quad_AND_Gate quad_and_2 (
    ._1a(quad_xor_gate_2__1_y), ._1b(quad_or_1__2y), ._1y(quad_and_2__1y), ._2a(In_2[2]), ._2b(In_1[2]),
    ._2y(quad_and_2__2y), ._3a(quad_xor_gate_2__3_y), ._3b(quad_or_1__3y), ._3y(quad_and_2__3y),
    ._4a(In_2[3]), ._4b(In_1[3]), ._4y(quad_and_2__4y));
  Quad_OR_Gate quad_or_1 (
    ._1a(quad_and_1__1y), ._1b(quad_and_1__2y), ._1y(quad_or_1__1y), ._2a(quad_and_1__3y),
    ._2b(quad_and_1__4y), ._2y(quad_or_1__2y), ._3a(quad_and_2__1y), ._3b(quad_and_2__2y),
    ._3y(quad_or_1__3y), ._4a(quad_and_2__3y), ._4b(quad_and_2__4y), ._4y(C_out));
endmodule

// reg
module _4bit_register (
  input  M,
  input  N,
  input  CLR,
  input  _1Q,
  input  _2Q,
  input  _3Q,
  input  _4Q,
  input  CLK,
  input  G2,
  input  G1,
  output _1D,
  output _2D,
  output _3D,
  output _4D
);

  wire and_1_out, and_2_out, and_3_out, and_4_out, and_5_out, and_6_out, and_7_out, and_8_out, and_9_out,
       and_10_out, d_ff_1_q, d_ff_2_q, d_ff_3_q, d_ff_4_q, not_1_out, not_2_out, not_3_out, not_4_out,
       not_5_out, or_1_out, or_2_out, or_3_out, or_4_out;

  not not_1 (not_1_out, M);
  not not_2 (not_2_out, N);
  and and_1 (and_1_out, not_1_out, not_2_out);
  not not_3 (not_3_out, and_10_out);
  and and_2 (and_2_out, d_ff_1_q, not_3_out);
  and and_3 (and_3_out, _1Q, and_10_out);
  and and_4 (and_4_out, d_ff_2_q, not_3_out);
  and and_5 (and_5_out, _2Q, and_10_out);
  and and_6 (and_6_out, d_ff_3_q, not_3_out);
  and and_7 (and_7_out, _3Q, and_10_out);
  and and_8 (and_8_out, d_ff_4_q, not_3_out);
  and and_9 (and_9_out, _4Q, and_10_out);
  or or_1 (or_1_out, and_2_out, and_3_out);
  or or_2 (or_2_out, and_4_out, and_5_out);
  or or_3 (or_3_out, and_6_out, and_7_out);
  or or_4 (or_4_out, and_8_out, and_9_out);
  D_Flip_Flop d_ff_1 (.clk(CLK), .D(or_1_out), .Q(d_ff_1_q), .en(1'b1), .reset(CLR));  // open: Qn, preset
  D_Flip_Flop d_ff_2 (.clk(CLK), .D(or_2_out), .Q(d_ff_2_q), .en(1'b1), .reset(CLR));  // open: Qn, preset
  D_Flip_Flop d_ff_3 (.clk(CLK), .D(or_3_out), .Q(d_ff_3_q), .en(1'b1), .reset(CLR));  // open: Qn, preset
  D_Flip_Flop d_ff_4 (.clk(CLK), .D(or_4_out), .Q(d_ff_4_q), .en(1'b1), .reset(CLR));  // open: Qn, preset
  and and_10 (and_10_out, not_4_out, not_5_out);
  not not_4 (not_4_out, G2);
  not not_5 (not_5_out, G1);
  assign _1D = and_1_out ? d_ff_1_q : 1'bz;  // Controlled_Buffer controlled_buffer_1
  assign _2D = and_1_out ? d_ff_2_q : 1'bz;  // Controlled_Buffer controlled_buffer_2
  assign _3D = and_1_out ? d_ff_3_q : 1'bz;  // Controlled_Buffer controlled_buffer_3
  assign _4D = and_1_out ? d_ff_4_q : 1'bz;  // Controlled_Buffer controlled_buffer_4
endmodule

// Not
module Hex_Inverter (
  input  _1,
  input  _4,
  input  _2,
  input  _5,
  input  _6,
  input  _3,
  output _1_prime,
  output _4_prime,
  output _5_prime,
  output _2_prime,
  output _6_prime,
  output _3_prime
);

  not not_1 (_1_prime, _1);
  not not_2 (_2_prime, _2);
  not not_3 (_3_prime, _3);
  not not_4 (_4_prime, _4);
  not not_5 (_5_prime, _5);
  not not_6 (_6_prime, _6);
endmodule
module _8bit_5_input_mux_w__zero_output (
  input  [7:0] Input_1,
  input  [7:0] Input_2,
  input  [7:0] Input_3,
  input  [7:0] Input_4,
  input  [7:0] Input_5,
  input  Control_1,
  input  Control_2,
  input  Control_3,
  output [7:0] out_9
);

  wire hex_inverter_1__3_prime, hex_inverter_1__4_prime, hex_inverter_1__6_prime, quad_and_1__3y,
       quad_and_2__2y;
  wire [7:0] n8bit_and_1_out, n8bit_and_2_out, n8bit_and_3_out, n8bit_and_4_out, n8bit_and_5_out,
       n8bit_or_1_out, n8bit_or_2_out, n8bit_or_3_out, n8bit_or_4_out;
  wire [7:7] hex_inverter_1__5_prime, quad_and_1__1y, quad_and_1__2y, quad_and_1__4y, quad_and_2__1y;

  Hex_Inverter hex_inverter_1 (
    ._3(Control_2), ._3_prime(hex_inverter_1__3_prime), ._4(Control_1), ._4_prime(hex_inverter_1__4_prime),
    ._5(quad_and_2__2y), ._5_prime(hex_inverter_1__5_prime[7]), ._6(Control_3),
    ._6_prime(hex_inverter_1__6_prime));  // open: _1, _1_prime, _2, _2_prime
  _8bit_AND_Gate u_8bit_and_1 (.In_2(Input_1), .In_1({8{quad_and_2__1y[7]}}), .Out(n8bit_and_1_out));
  _8bit_AND_Gate u_8bit_and_2 (.In_2(Input_2), .In_1({8{quad_and_1__4y[7]}}), .Out(n8bit_and_2_out));
  _8bit_AND_Gate u_8bit_and_3 (.In_2(Input_3), .In_1({8{quad_and_1__2y[7]}}), .Out(n8bit_and_3_out));
  _8bit_AND_Gate u_8bit_and_4 (.In_2(Input_4), .In_1({8{quad_and_1__1y[7]}}), .Out(n8bit_and_4_out));
  _8bit_AND_Gate u_8bit_and_5 (.In_2(Input_5), .In_1({8{Control_1}}), .Out(n8bit_and_5_out));
  Quad_AND_Gate quad_and_1 (
    ._1a(Control_3), ._1b(Control_2), ._1y(quad_and_1__1y[7]), ._2a(hex_inverter_1__3_prime),
    ._2b(Control_3), ._2y(quad_and_1__2y[7]), ._3a(hex_inverter_1__6_prime), ._3b(hex_inverter_1__3_prime),
    ._3y(quad_and_1__3y), ._4a(hex_inverter_1__6_prime), ._4b(Control_2), ._4y(quad_and_1__4y[7]));
  _8bit_OR_Gate u_8bit_or_1 (.In_2(n8bit_and_2_out), .In_1(n8bit_and_1_out), .Out(n8bit_or_1_out));
  _8bit_OR_Gate u_8bit_or_2 (.In_2(n8bit_and_3_out), .In_1(n8bit_or_1_out), .Out(n8bit_or_2_out));
  _8bit_OR_Gate u_8bit_or_3 (.In_2(n8bit_and_5_out), .In_1(n8bit_and_4_out), .Out(n8bit_or_3_out));
  Quad_AND_Gate quad_and_2 (
    ._1a(hex_inverter_1__4_prime), ._1b(quad_and_1__3y), ._1y(quad_and_2__1y[7]), ._2a(Control_1),
    ._2b(quad_and_1__2y[7]), ._2y(quad_and_2__2y));  // open: _3a, _3b, _3y, _4a, _4b, _4y
  _8bit_OR_Gate u_8bit_or_4 (.In_2(n8bit_or_3_out), .In_1(n8bit_or_2_out), .Out(n8bit_or_4_out));
  _8bit_AND_Gate u_8bit_and_6 (.In_2(n8bit_or_4_out), .In_1({8{hex_inverter_1__5_prime[7]}}), .Out(out_9));
endmodule

module Control_Load (
  input  Instruction_enable,
  input  [7:0] Sub_instruction,
  input  [2:0] Read_From_1,
  output Clear,
  output Write_Byte,
  output Mux_1_1,
  output Mux_1_2,
  output Mux_1_3,
  output Mux_3_1,
  output Ram_EW_TO
);

  wire quad_and_1__1y, quad_and_1__2y, quad_and_1__3y, quad_or_1__1y, quad_or_1__3y;

  Quad_AND_Gate quad_and_1 (
    ._1a(Instruction_enable), ._1b(Sub_instruction[0]), ._1y(quad_and_1__1y), ._2a(Sub_instruction[1]),
    ._2b(Instruction_enable), ._2y(quad_and_1__2y), ._3a(Instruction_enable), ._3b(Sub_instruction[3]),
    ._3y(quad_and_1__3y), ._4a(Sub_instruction[2]), ._4b(Instruction_enable), ._4y(Ram_EW_TO));
  Quad_AND_Gate quad_and_2 (
    ._1a(Instruction_enable), ._1b(Sub_instruction[4]), ._1y(Clear));  // open: _2a, _2b, _2y, _3a, _3b, _3y, _4a, _4b, _4y
  Quad_OR_Gate quad_or_1 (
    ._1a(Ram_EW_TO), ._1b(quad_and_1__1y), ._1y(quad_or_1__1y), ._2a(quad_and_1__3y), ._2b(quad_and_1__1y),
    ._2y(Mux_3_1), ._3a(quad_and_1__2y), ._3b(Ram_EW_TO), ._3y(quad_or_1__3y), ._4a(quad_or_1__3y),
    ._4b(quad_and_1__3y), ._4y(Write_Byte));
  Quad_AND_Gate quad_and_3 (
    ._1a(quad_or_1__1y), ._1b(Read_From_1[0]), ._1y(Mux_1_1), ._2a(quad_or_1__1y), ._2b(Read_From_1[1]),
    ._2y(Mux_1_2), ._4a(quad_or_1__1y), ._4b(Read_From_1[2]), ._4y(Mux_1_3));  // open: _3a, _3b, _3y
endmodule

module Control_Addition (
  input  Instruction_enable,
  input  [7:0] Sub_instruction,
  input  [2:0] Read_From_1,
  input  [2:0] Read_From_2,
  output Write_Byte,
  output Write_Mux_2,
  output Read_Mux_1_1,
  output Read_Mux_1_2,
  output Read_Mux_1_3,
  output Read_Mux_2_1,
  output Read_Mux_2_2,
  output Read_Mux_2_3,
  output Subtract_nAdd,
  output ALU_Control_1,
  output ALU_Control_2,
  output ALU_Control_3
);

  wire quad_and_1__1y, quad_and_1__2y, quad_and_1__3y, quad_and_1__4y, quad_and_2__1y, quad_and_2__2y,
       quad_and_2__3y, quad_and_2__4y, quad_or_1__2y, quad_or_2__2y, quad_or_2__4y;

  Quad_AND_Gate quad_and_1 (
    ._1a(Instruction_enable), ._1b(Sub_instruction[0]), ._1y(quad_and_1__1y), ._2a(Sub_instruction[1]),
    ._2b(Instruction_enable), ._2y(quad_and_1__2y), ._3a(Instruction_enable), ._3b(Sub_instruction[3]),
    ._3y(quad_and_1__3y), ._4a(Sub_instruction[2]), ._4b(Instruction_enable), ._4y(quad_and_1__4y));
  Quad_AND_Gate quad_and_2 (
    ._1a(Instruction_enable), ._1b(Sub_instruction[4]), ._1y(quad_and_2__1y), ._2a(Instruction_enable),
    ._2b(Sub_instruction[5]), ._2y(quad_and_2__2y), ._3a(Instruction_enable), ._3b(Sub_instruction[7]),
    ._3y(quad_and_2__3y), ._4a(Instruction_enable), ._4b(Sub_instruction[6]), ._4y(quad_and_2__4y));
  Quad_AND_Gate quad_and_3 (
    ._1a(quad_or_2__2y), ._1b(Read_From_2[0]), ._1y(Read_Mux_2_1), ._2a(quad_or_2__2y), ._2b(Read_From_2[1]),
    ._2y(Read_Mux_2_2), ._3a(quad_or_2__2y), ._3b(Read_From_2[2]), ._3y(Read_Mux_2_3));  // open: _4a, _4b, _4y
  Quad_OR_Gate quad_or_1 (
    ._1a(quad_and_2__4y), ._1b(quad_and_2__3y), ._1y(ALU_Control_2), ._2a(ALU_Control_2),
    ._2b(quad_and_2__1y), ._2y(quad_or_1__2y), ._3a(quad_and_2__3y), ._3b(quad_and_2__2y),
    ._3y(ALU_Control_1), ._4a(quad_and_2__2y), ._4b(quad_or_1__2y), ._4y(ALU_Control_3));
  Quad_OR_Gate quad_or_2 (
    ._1a(quad_and_1__3y), ._1b(quad_and_1__2y), ._1y(Write_Byte), ._2a(quad_and_1__1y), ._2b(quad_and_1__4y),
    ._2y(quad_or_2__2y), ._3a(quad_and_1__3y), ._3b(quad_and_1__4y), ._3y(Subtract_nAdd),
    ._4a(quad_and_2__1y), ._4b(quad_and_1__1y), ._4y(quad_or_2__4y));
  Quad_AND_Gate quad_and_4 (
    ._1a(Instruction_enable), ._1b(Read_From_1[0]), ._1y(Read_Mux_1_1), ._2a(Instruction_enable),
    ._2b(Read_From_1[1]), ._2y(Read_Mux_1_2), ._3a(Instruction_enable), ._3b(Read_From_1[2]),
    ._3y(Read_Mux_1_3));  // open: _4a, _4b, _4y

  assign Write_Mux_2 = Instruction_enable;
endmodule

module Control_Logical (
  input  Instruction_enable,
  input  [7:0] Sub_instruction,
  input  [2:0] Read_From_1,
  input  [2:0] Read_From_2,
  output Write_Byte,
  output ALU_Control_1,
  output ALU_Control_2,
  output ALU_Control_3,
  output ALU_Control_4,
  output Write_Mux_2,
  output Read_Mux_1_1,
  output Read_Mux_1_2,
  output Read_Mux_1_3,
  output Read_Mux_2_1,
  output Read_Mux_2_2,
  output Read_Mux_2_3
);

  wire hex_inverter_1__4_prime, quad_and_1__1y, quad_and_1__2y, quad_and_1__3y, quad_and_1__4y,
       quad_and_2__3y, quad_or_1__2y, quad_or_1__3y;

  Quad_AND_Gate quad_and_1 (
    ._1a(Instruction_enable), ._1b(Sub_instruction[0]), ._1y(quad_and_1__1y), ._2a(Sub_instruction[1]),
    ._2b(Instruction_enable), ._2y(quad_and_1__2y), ._3a(Instruction_enable), ._3b(Sub_instruction[3]),
    ._3y(quad_and_1__3y), ._4a(Instruction_enable), ._4b(Sub_instruction[2]), ._4y(quad_and_1__4y));
  Quad_AND_Gate quad_and_2 (
    ._3a(Instruction_enable), ._3b(Sub_instruction[5]), ._3y(quad_and_2__3y), ._4a(Instruction_enable),
    ._4b(Sub_instruction[6]), ._4y(ALU_Control_3));  // open: _1a, _1b, _1y, _2a, _2b, _2y
  Quad_AND_Gate quad_and_3 (
    ._1a(Instruction_enable), ._1b(Read_From_1[0]), ._1y(Read_Mux_1_1), ._2a(Instruction_enable),
    ._2b(Read_From_1[1]), ._2y(Read_Mux_1_2), ._3a(Instruction_enable), ._3b(Read_From_1[2]),
    ._3y(Read_Mux_1_3));  // open: _4a, _4b, _4y
  Hex_Inverter hex_inverter_1 (
    ._4(Write_Byte), ._4_prime(hex_inverter_1__4_prime));  // open: _1, _1_prime, _2, _2_prime, _3, _3_prime, _5, _5_prime, _6, _6_prime
  Quad_OR_Gate quad_or_1 (
    ._1a(quad_and_1__3y), ._1b(quad_and_1__2y), ._1y(Write_Byte), ._2a(quad_and_1__3y), ._2b(quad_and_1__4y),
    ._2y(quad_or_1__2y), ._3a(quad_and_1__2y), ._3b(quad_and_1__1y), ._3y(quad_or_1__3y));  // open: _4a, _4b, _4y
  Quad_OR_Gate quad_or_2 (
    ._1a(quad_or_1__2y), ._1b(quad_and_2__3y), ._1y(ALU_Control_2), ._2a(quad_or_1__3y),
    ._2b(quad_and_2__3y), ._2y(ALU_Control_1));  // open: _3a, _3b, _3y, _4a, _4b, _4y
  Quad_AND_Gate quad_and_4 (
    ._1a(hex_inverter_1__4_prime), ._1b(Read_From_2[0]), ._1y(Read_Mux_2_1), ._2a(hex_inverter_1__4_prime),
    ._2b(Read_From_2[1]), ._2y(Read_Mux_2_2), ._3a(hex_inverter_1__4_prime), ._3b(Read_From_2[2]),
    ._3y(Read_Mux_2_3));  // open: _4a, _4b, _4y

  assign ALU_Control_4 = Instruction_enable;
  assign Write_Mux_2 = Instruction_enable;
endmodule

module Control_Logical_Comparison (
  input  Instruction_enable,
  input  [7:0] Sub_instruction,
  input  [2:0] Read_From_1,
  input  [2:0] Read_From_2,
  output Write_Byte,
  output ALU_Control_1,
  output ALU_Control_2,
  output Subtract_nAdd,
  output n_anyhting_else,
  output Write_Mux_2,
  output Read_Mux_1_1,
  output Read_Mux_1_2,
  output Read_Mux_1_3,
  output Read_Mux_2_1,
  output Read_Mux_2_2,
  output Read_Mux_2_3
);

  wire quad_and_1__1y, quad_and_1__2y, quad_and_1__3y, quad_and_1__4y, quad_and_2__1y, quad_and_2__2y,
       quad_or_1__1y, quad_or_1__2y, quad_or_1__3y, quad_or_2__1y, quad_or_2__2y, quad_or_2__3y;

  Quad_AND_Gate quad_and_1 (
    ._1a(Instruction_enable), ._1b(Sub_instruction[0]), ._1y(quad_and_1__1y), ._2a(Sub_instruction[1]),
    ._2b(Instruction_enable), ._2y(quad_and_1__2y), ._3a(Instruction_enable), ._3b(Sub_instruction[3]),
    ._3y(quad_and_1__3y), ._4a(Instruction_enable), ._4b(Sub_instruction[2]), ._4y(quad_and_1__4y));
  Quad_AND_Gate quad_and_2 (
    ._1a(Instruction_enable), ._1b(Sub_instruction[4]), ._1y(quad_and_2__1y), ._2a(Instruction_enable),
    ._2b(Sub_instruction[5]), ._2y(quad_and_2__2y));  // open: _3a, _3b, _3y, _4a, _4b, _4y
  Quad_OR_Gate quad_or_1 (
    ._1a(quad_and_2__1y), ._1b(quad_and_1__1y), ._1y(quad_or_1__1y), ._2a(quad_or_1__1y),
    ._2b(quad_and_1__4y), ._2y(quad_or_1__2y), ._3a(quad_and_1__4y), ._3b(quad_and_1__3y),
    ._3y(quad_or_1__3y), ._4a(quad_or_1__3y), ._4b(quad_or_2__2y), ._4y(ALU_Control_1));
  Quad_AND_Gate quad_and_3 (
    ._1a(Instruction_enable), ._1b(Read_From_1[0]), ._1y(Read_Mux_1_1), ._2a(Instruction_enable),
    ._2b(Read_From_1[1]), ._2y(Read_Mux_1_2), ._3a(Instruction_enable), ._3b(Read_From_1[2]),
    ._3y(Read_Mux_1_3));  // open: _4a, _4b, _4y
  Quad_OR_Gate quad_or_2 (
    ._1a(quad_and_2__2y), ._1b(quad_and_2__1y), ._1y(quad_or_2__1y), ._2a(quad_and_1__1y),
    ._2b(quad_and_1__2y), ._2y(quad_or_2__2y), ._3a(quad_and_2__2y), ._3b(quad_and_1__2y),
    ._3y(quad_or_2__3y), ._4a(quad_or_2__3y), ._4b(quad_and_1__3y), ._4y(Write_Byte));
  Quad_OR_Gate quad_or_3 (
    ._1a(quad_or_2__1y), ._1b(quad_or_2__2y), ._1y(ALU_Control_2));  // open: _2a, _2b, _2y, _3a, _3b, _3y, _4a, _4b, _4y
  Quad_AND_Gate quad_and_4 (
    ._1a(quad_or_1__2y), ._1b(Read_From_2[0]), ._1y(Read_Mux_2_1), ._2a(quad_or_1__2y), ._2b(Read_From_2[1]),
    ._2y(Read_Mux_2_2), ._3a(quad_or_1__2y), ._3b(Read_From_2[2]), ._3y(Read_Mux_2_3));  // open: _4a, _4b, _4y

  assign n_anyhting_else = ALU_Control_1;
  assign Subtract_nAdd = Instruction_enable;
  assign Write_Mux_2 = Instruction_enable;
endmodule

module Control_Misc (
  input  Instruction_enable,
  input  [7:0] Sub_instruction,
  input  [2:0] Read_From_1,
  input  nequal_zero,
  input  clock,
  input  clear,
  output nLoad_MSB,
  output nLoad_LSB,
  output Load_Saved_PC,
  output nequal_zero_2,
  output Write_Byte,
  output Write_Byte_2,
  output OCL_Register_Enable,
  output Read_Mux_1_1,
  output Read_Mux_1_2,
  output Read_Mux_1_3,
  output Read_Mux_2_1,
  output Read_Mux_2_2,
  output Read_Mux_2_3,
  output Subtract_nadd,
  output n_anything_else,
  output enable_interrupts
);

  wire hex_inverter_1__2_prime, hex_inverter_1__3_prime, hex_inverter_1__5_prime, hex_inverter_2__5_prime,
       quad_and_1__1y, quad_and_1__2y, quad_and_2__4y, quad_and_4__1y, quad_and_4__2y, quad_or_1__2y,
       quad_or_2__1y, quad_or_2__3y;

  Quad_AND_Gate quad_and_1 (
    ._1a(Instruction_enable), ._1b(Sub_instruction[0]), ._1y(quad_and_1__1y), ._2a(Sub_instruction[1]),
    ._2b(Instruction_enable), ._2y(quad_and_1__2y), ._3a(Instruction_enable), ._3b(Sub_instruction[3]),
    ._3y(n_anything_else), ._4a(Instruction_enable), ._4b(Sub_instruction[2]), ._4y(Load_Saved_PC));
  Quad_AND_Gate quad_and_2 (
    ._2a(Instruction_enable), ._2b(Sub_instruction[5]), ._2y(Read_Mux_2_1), ._3a(hex_inverter_1__5_prime),
    ._3b(hex_inverter_1__2_prime), ._3y(nLoad_LSB), ._4a(n_anything_else), ._4b(hex_inverter_1__3_prime),
    ._4y(quad_and_2__4y));  // open: _1a, _1b, _1y
  Quad_OR_Gate quad_or_1 (
    ._2a(quad_and_1__1y), ._2b(Read_From_1[2]), ._2y(quad_or_1__2y));  // open: _1a, _1b, _1y, _3a, _3b, _3y, _4a, _4b, _4y
  Hex_Inverter hex_inverter_1 (
    ._1(Read_Mux_2_1), ._1_prime(OCL_Register_Enable), ._2(quad_and_2__4y),
    ._2_prime(hex_inverter_1__2_prime), ._3(nequal_zero), ._3_prime(hex_inverter_1__3_prime),
    ._4(quad_and_1__1y), ._4_prime(nLoad_MSB), ._5(quad_and_1__2y), ._5_prime(hex_inverter_1__5_prime),
    ._6(n_anything_else), ._6_prime(nequal_zero_2));
  Quad_OR_Gate quad_or_2 (
    ._1a(n_anything_else), ._1b(Read_Mux_2_1), ._1y(quad_or_2__1y), ._3a(quad_and_1__1y),
    ._3b(quad_and_1__2y), ._3y(quad_or_2__3y), ._4a(quad_or_2__3y), ._4b(quad_or_2__1y), ._4y(Write_Byte));  // open: _2a, _2b, _2y
  Quad_AND_Gate quad_and_3 (
    ._1a(n_anything_else), ._1b(Read_From_1[1]), ._1y(Read_Mux_1_2), ._2a(n_anything_else),
    ._2b(Read_From_1[2]), ._2y(Read_Mux_1_3), ._3a(n_anything_else), ._3b(Read_From_1[0]), ._3y(Read_Mux_1_1));  // open: _4a, _4b, _4y
  Hex_Inverter hex_inverter_2 (
    ._5(Sub_instruction[7]), ._5_prime(hex_inverter_2__5_prime));  // open: _1, _1_prime, _2, _2_prime, _3, _3_prime, _4, _4_prime, _6, _6_prime
  _4bit_register u_4bit_register_1 (
    .M(1'b0), .N(1'b0), ._1Q(quad_or_1__2y), .CLK(clock), .CLR(clear), ._1D(enable_interrupts),
    .G2(quad_and_4__2y), .G1(quad_and_4__2y));  // open: _2Q, _3Q, _4Q, _2D, _3D, _4D
  Quad_AND_Gate quad_and_4 (
    ._1a(hex_inverter_2__5_prime), ._1b(nLoad_LSB), ._1y(quad_and_4__1y), ._2a(quad_and_4__1y),
    ._2b(nLoad_MSB), ._2y(quad_and_4__2y));  // open: _3a, _3b, _3y, _4a, _4b, _4y

  assign Read_Mux_2_2 = Read_Mux_2_1;
  assign Read_Mux_2_3 = Read_Mux_2_1;
  assign Subtract_nadd = n_anything_else;
  assign Write_Byte_2 = Read_Mux_2_1;
endmodule

module Control_IO (
  input  Instruction_enable,
  input  [7:0] Sub_instruction,
  output Write_Mux_1,
  output Write_Mux_2,
  output Write_Mux_3
);

  wire quad_and_1__1y, quad_and_1__2y, quad_and_1__3y, quad_and_1__4y, quad_and_2__2y, quad_and_2__4y,
       quad_or_1__2y;

  Quad_AND_Gate quad_and_1 (
    ._1a(Instruction_enable), ._1b(Sub_instruction[0]), ._1y(quad_and_1__1y), ._2a(Sub_instruction[1]),
    ._2b(Instruction_enable), ._2y(quad_and_1__2y), ._3a(Instruction_enable), ._3b(Sub_instruction[3]),
    ._3y(quad_and_1__3y), ._4a(Instruction_enable), ._4b(Sub_instruction[2]), ._4y(quad_and_1__4y));
  Quad_AND_Gate quad_and_2 (
    ._1a(Instruction_enable), ._1b(Sub_instruction[4]), ._2a(Instruction_enable), ._2b(Sub_instruction[5]),
    ._2y(quad_and_2__2y), ._3a(Instruction_enable), ._3b(Sub_instruction[6]), ._4a(Instruction_enable),
    ._4b(Sub_instruction[7]), ._4y(quad_and_2__4y));  // open: _1y, _3y
  Quad_OR_Gate quad_or_1 (
    ._1a(quad_and_1__3y), ._1b(quad_and_1__2y), ._1y(Write_Mux_1), ._2a(Write_Mux_1), ._2b(quad_and_1__4y),
    ._2y(quad_or_1__2y), ._3a(quad_and_1__3y), ._3b(quad_and_1__4y), ._3y(Write_Mux_2), ._4a(quad_and_1__1y),
    ._4b(quad_or_1__2y), ._4y(Write_Mux_3));
endmodule

// OCL
module Clock_Reg (
  input  OCL_Enable,
  input  [7:0] MSB,
  input  [7:0] LSB,
  input  Clock,
  input  Clear,
  output [15:0] out_6,
  output [7:0] LSB_2,
  output [7:0] MSB_2
);

  _8bit_register u_8bit_register_1 (
    .M(1'b0), .N(1'b0), .\input ({2'b00, MSB[5:0]}), .clock(Clock), .CLR(Clear), .\output (MSB_2),
    .G2(OCL_Enable), .G1(OCL_Enable));
  _8bit_register u_8bit_register_2 (
    .M(1'b0), .N(1'b0), .\input (LSB), .clock(Clock), .CLR(Clear), .\output (LSB_2), .G2(OCL_Enable),
    .G1(OCL_Enable));

  assign out_6 = {MSB_2, LSB_2};
endmodule

module Display (
  input  CLR,
  input  Write,
  input  [7:0] Addr,
  input  [7:0] Data,
  input  clk,
  output [7:0] out_6,
  output [7:0] out_7,
  output [7:0] out_8,
  output [7:0] out_9,
  output [7:0] out_10,
  output [7:0] out_11,
  output [7:0] out_12,
  output [7:0] out_13,
  output [7:0] out_14,
  output [7:0] out_15,
  output [7:0] out_16,
  output [7:0] out_17,
  output [7:0] out_18,
  output [7:0] out_19,
  output [7:0] out_20,
  output [7:0] out_21
);

  wire hex_inverter_1__1_prime, hex_inverter_1__4_prime, hex_inverter_1__5_prime, hex_inverter_1__6_prime,
       hex_inverter_2__1_prime, hex_inverter_2__2_prime, hex_inverter_2__3_prime, hex_inverter_2__4_prime,
       hex_inverter_2__5_prime, hex_inverter_2__6_prime, hex_inverter_3__1_prime, hex_inverter_3__2_prime,
       hex_inverter_3__3_prime, hex_inverter_3__4_prime, hex_inverter_3__5_prime, hex_inverter_3__6_prime,
       hex_inverter_4__1_prime, hex_inverter_4__4_prime, hex_inverter_4__5_prime, hex_inverter_4__6_prime,
       quad_and_1__1y, quad_and_1__2y, quad_and_1__3y, quad_and_1__4y, triple_2_channel_demux_1_ax,
       triple_2_channel_demux_1_ay, triple_2_channel_demux_1_bx, triple_2_channel_demux_1_by,
       triple_2_channel_demux_1_cx, triple_2_channel_demux_1_cy, triple_2_channel_demux_2_ax,
       triple_2_channel_demux_2_ay, triple_2_channel_demux_2_bx, triple_2_channel_demux_2_by,
       triple_2_channel_demux_2_cx, triple_2_channel_demux_2_cy, triple_2_channel_demux_3_ax,
       triple_2_channel_demux_3_ay, triple_2_channel_demux_3_bx, triple_2_channel_demux_3_by,
       triple_2_channel_demux_3_cx, triple_2_channel_demux_3_cy, triple_2_channel_demux_4_ax,
       triple_2_channel_demux_4_ay, triple_2_channel_demux_4_bx, triple_2_channel_demux_4_by,
       triple_2_channel_demux_4_cx, triple_2_channel_demux_4_cy, triple_2_channel_demux_5_ax,
       triple_2_channel_demux_5_ay, triple_2_channel_demux_5_bx, triple_2_channel_demux_5_by,
       triple_2_channel_demux_5_cx, triple_2_channel_demux_5_cy;

  Quad_AND_Gate quad_and_1 (
    ._1a(Write), ._1b(quad_and_1__2y), ._1y(quad_and_1__1y), ._2a(quad_and_1__3y), ._2b(quad_and_1__4y),
    ._2y(quad_and_1__2y), ._3a(hex_inverter_1__1_prime), ._3b(hex_inverter_1__4_prime), ._3y(quad_and_1__3y),
    ._4a(hex_inverter_1__5_prime), ._4b(hex_inverter_1__6_prime), ._4y(quad_and_1__4y));
  DotMatrix #(.matrixcols(16), .matrixrows(8), .dotshape("circle")) dotmatrix_1 (
    .col0(out_6), .col1(out_7), .col2(out_8), .col3(out_9), .col4(out_10), .col5(out_11), .col6(out_12),
    .col7(out_13), .col8(out_14), .col9(out_15), .col10(out_16), .col11(out_17), .col12(out_18),
    .col13(out_19), .col14(out_20), .col15(out_21));
  Hex_Inverter hex_inverter_1 (
    ._1(Addr[4]), ._1_prime(hex_inverter_1__1_prime), ._4(Addr[5]), ._4_prime(hex_inverter_1__4_prime),
    ._5(Addr[6]), ._5_prime(hex_inverter_1__5_prime), ._6(Addr[7]), ._6_prime(hex_inverter_1__6_prime));  // open: _2, _2_prime, _3, _3_prime
  _8bit_register u_8bit_register_1 (
    .M(1'b0), .N(1'b0), .\input (Data), .clock(clk), .CLR(CLR), .\output (out_6),
    .G2(hex_inverter_2__3_prime), .G1(hex_inverter_2__3_prime));
  _8bit_register u_8bit_register_2 (
    .M(1'b0), .N(1'b0), .\input (Data), .clock(clk), .CLR(CLR), .\output (out_7),
    .G2(hex_inverter_2__2_prime), .G1(hex_inverter_2__2_prime));
  _8bit_register u_8bit_register_3 (
    .M(1'b0), .N(1'b0), .\input (Data), .clock(clk), .CLR(CLR), .\output (out_8),
    .G2(hex_inverter_2__1_prime), .G1(hex_inverter_2__1_prime));
  _8bit_register u_8bit_register_4 (
    .M(1'b0), .N(1'b0), .\input (Data), .clock(clk), .CLR(CLR), .\output (out_9),
    .G2(hex_inverter_2__4_prime), .G1(hex_inverter_2__4_prime));
  triple_2_channel_demux triple_2_channel_demux_1 (
    .bx(triple_2_channel_demux_1_bx), .by(triple_2_channel_demux_1_by), .cy(triple_2_channel_demux_1_cy),
    .c_in(triple_2_channel_demux_1_ay), .cx(triple_2_channel_demux_1_cx), .enable(1'b1),
    .b_in(triple_2_channel_demux_1_ax), .a_in(triple_2_channel_demux_5_bx), .ax(triple_2_channel_demux_1_ax),
    .ay(triple_2_channel_demux_1_ay), .A(Addr[1]), .B(Addr[0]), .C(Addr[0]));
  Hex_Inverter hex_inverter_2 (
    ._1(triple_2_channel_demux_1_cx), ._1_prime(hex_inverter_2__1_prime), ._2(triple_2_channel_demux_1_by),
    ._2_prime(hex_inverter_2__2_prime), ._3(triple_2_channel_demux_1_bx), ._3_prime(hex_inverter_2__3_prime),
    ._4(triple_2_channel_demux_1_cy), ._4_prime(hex_inverter_2__4_prime), ._5(triple_2_channel_demux_2_bx),
    ._5_prime(hex_inverter_2__5_prime), ._6(triple_2_channel_demux_2_by), ._6_prime(hex_inverter_2__6_prime));
  _8bit_register u_8bit_register_5 (
    .M(1'b0), .N(1'b0), .\input (Data), .clock(clk), .CLR(CLR), .\output (out_10),
    .G2(hex_inverter_2__5_prime), .G1(hex_inverter_2__5_prime));
  _8bit_register u_8bit_register_6 (
    .M(1'b0), .N(1'b0), .\input (Data), .clock(clk), .CLR(CLR), .\output (out_11),
    .G2(hex_inverter_2__6_prime), .G1(hex_inverter_2__6_prime));
  _8bit_register u_8bit_register_7 (
    .M(1'b0), .N(1'b0), .\input (Data), .clock(clk), .CLR(CLR), .\output (out_12),
    .G2(hex_inverter_3__3_prime), .G1(hex_inverter_3__3_prime));
  _8bit_register u_8bit_register_8 (
    .M(1'b0), .N(1'b0), .\input (Data), .clock(clk), .CLR(CLR), .\output (out_13),
    .G2(hex_inverter_3__2_prime), .G1(hex_inverter_3__2_prime));
  triple_2_channel_demux triple_2_channel_demux_2 (
    .bx(triple_2_channel_demux_2_bx), .by(triple_2_channel_demux_2_by), .cy(triple_2_channel_demux_2_cy),
    .c_in(triple_2_channel_demux_2_ay), .cx(triple_2_channel_demux_2_cx), .enable(1'b1),
    .b_in(triple_2_channel_demux_2_ax), .a_in(triple_2_channel_demux_5_by), .ax(triple_2_channel_demux_2_ax),
    .ay(triple_2_channel_demux_2_ay), .A(Addr[1]), .B(Addr[0]), .C(Addr[0]));
  Hex_Inverter hex_inverter_3 (
    ._1(triple_2_channel_demux_3_bx), ._1_prime(hex_inverter_3__1_prime), ._2(triple_2_channel_demux_2_cy),
    ._2_prime(hex_inverter_3__2_prime), ._3(triple_2_channel_demux_2_cx), ._3_prime(hex_inverter_3__3_prime),
    ._4(triple_2_channel_demux_3_by), ._4_prime(hex_inverter_3__4_prime), ._5(triple_2_channel_demux_3_cx),
    ._5_prime(hex_inverter_3__5_prime), ._6(triple_2_channel_demux_3_cy), ._6_prime(hex_inverter_3__6_prime));
  _8bit_register u_8bit_register_9 (
    .M(1'b0), .N(1'b0), .\input (Data), .clock(clk), .CLR(CLR), .\output (out_14),
    .G2(hex_inverter_3__1_prime), .G1(hex_inverter_3__1_prime));
  _8bit_register u_8bit_register_10 (
    .M(1'b0), .N(1'b0), .\input (Data), .clock(clk), .CLR(CLR), .\output (out_15),
    .G2(hex_inverter_3__4_prime), .G1(hex_inverter_3__4_prime));
  _8bit_register u_8bit_register_11 (
    .M(1'b0), .N(1'b0), .\input (Data), .clock(clk), .CLR(CLR), .\output (out_16),
    .G2(hex_inverter_3__5_prime), .G1(hex_inverter_3__5_prime));
  _8bit_register u_8bit_register_12 (
    .M(1'b0), .N(1'b0), .\input (Data), .clock(clk), .CLR(CLR), .\output (out_17),
    .G2(hex_inverter_3__6_prime), .G1(hex_inverter_3__6_prime));
  triple_2_channel_demux triple_2_channel_demux_3 (
    .bx(triple_2_channel_demux_3_bx), .by(triple_2_channel_demux_3_by), .cy(triple_2_channel_demux_3_cy),
    .c_in(triple_2_channel_demux_3_ay), .cx(triple_2_channel_demux_3_cx), .enable(1'b1),
    .b_in(triple_2_channel_demux_3_ax), .a_in(triple_2_channel_demux_5_cx), .ax(triple_2_channel_demux_3_ax),
    .ay(triple_2_channel_demux_3_ay), .A(Addr[1]), .B(Addr[0]), .C(Addr[0]));
  Hex_Inverter hex_inverter_4 (
    ._1(triple_2_channel_demux_4_bx), ._1_prime(hex_inverter_4__1_prime), ._4(triple_2_channel_demux_4_by),
    ._4_prime(hex_inverter_4__4_prime), ._5(triple_2_channel_demux_4_cx), ._5_prime(hex_inverter_4__5_prime),
    ._6(triple_2_channel_demux_4_cy), ._6_prime(hex_inverter_4__6_prime));  // open: _2, _2_prime, _3, _3_prime
  _8bit_register u_8bit_register_13 (
    .M(1'b0), .N(1'b0), .\input (Data), .clock(clk), .CLR(CLR), .\output (out_18),
    .G2(hex_inverter_4__1_prime), .G1(hex_inverter_4__1_prime));
  _8bit_register u_8bit_register_14 (
    .M(1'b0), .N(1'b0), .\input (Data), .clock(clk), .CLR(CLR), .\output (out_19),
    .G2(hex_inverter_4__4_prime), .G1(hex_inverter_4__4_prime));
  _8bit_register u_8bit_register_15 (
    .M(1'b0), .N(1'b0), .\input (Data), .clock(clk), .CLR(CLR), .\output (out_20),
    .G2(hex_inverter_4__5_prime), .G1(hex_inverter_4__5_prime));
  _8bit_register u_8bit_register_16 (
    .M(1'b0), .N(1'b0), .\input (Data), .clock(clk), .CLR(CLR), .\output (out_21),
    .G2(hex_inverter_4__6_prime), .G1(hex_inverter_4__6_prime));
  triple_2_channel_demux triple_2_channel_demux_4 (
    .bx(triple_2_channel_demux_4_bx), .by(triple_2_channel_demux_4_by), .cy(triple_2_channel_demux_4_cy),
    .c_in(triple_2_channel_demux_4_ay), .cx(triple_2_channel_demux_4_cx), .enable(1'b1),
    .b_in(triple_2_channel_demux_4_ax), .a_in(triple_2_channel_demux_5_cy), .ax(triple_2_channel_demux_4_ax),
    .ay(triple_2_channel_demux_4_ay), .A(Addr[1]), .B(Addr[0]), .C(Addr[0]));
  triple_2_channel_demux triple_2_channel_demux_5 (
    .bx(triple_2_channel_demux_5_bx), .by(triple_2_channel_demux_5_by), .cy(triple_2_channel_demux_5_cy),
    .c_in(triple_2_channel_demux_5_ay), .cx(triple_2_channel_demux_5_cx), .enable(1'b1),
    .b_in(triple_2_channel_demux_5_ax), .a_in(quad_and_1__1y), .ax(triple_2_channel_demux_5_ax),
    .ay(triple_2_channel_demux_5_ay), .A(Addr[3]), .B(Addr[2]), .C(Addr[2]));
endmodule

module Display_and_RAM_test (
  input  in_1,
  input  in_2,
  input  [7:0] in_3,
  input  [7:0] in_4,
  input  in_5,
  output [7:0] out_6
);

  wire [7:0] display_1_out_6, display_1_out_7, display_1_out_8, display_1_out_9, display_1_out_10,
       display_1_out_11, display_1_out_12, display_1_out_13, display_1_out_14, display_1_out_15,
       display_1_out_16, display_1_out_17, display_1_out_18, display_1_out_19, display_1_out_20,
       display_1_out_21;

  RAM ram_1 (.CLR_L16bytes(in_1), .W_TO(in_2), .Addr(in_3), .Data(in_4), .CLK(in_5), .OUT_1(out_6));
  DotMatrix #(.matrixcols(16), .matrixrows(8)) dotmatrix_1 (
    .col0(display_1_out_6), .col1(display_1_out_7), .col2(display_1_out_8), .col3(display_1_out_9),
    .col4(display_1_out_10), .col5(display_1_out_11), .col6(display_1_out_12), .col7(display_1_out_13),
    .col8(display_1_out_14), .col9(display_1_out_15), .col10(display_1_out_16), .col11(display_1_out_17),
    .col12(display_1_out_18), .col13(display_1_out_19), .col14(display_1_out_20), .col15(display_1_out_21));
  Display display_1 (
    .CLR(in_1), .Write(in_2), .Addr(in_3), .Data(in_4), .clk(in_5), .out_6(display_1_out_6),
    .out_7(display_1_out_7), .out_8(display_1_out_8), .out_9(display_1_out_9), .out_10(display_1_out_10),
    .out_11(display_1_out_11), .out_12(display_1_out_12), .out_13(display_1_out_13),
    .out_14(display_1_out_14), .out_15(display_1_out_15), .out_16(display_1_out_16),
    .out_17(display_1_out_17), .out_18(display_1_out_18), .out_19(display_1_out_19),
    .out_20(display_1_out_20), .out_21(display_1_out_21));
endmodule

module Clock (
  input  Clock_Input,
  output System_Clock,
  output Display_Clock
);

  wire [7:0] n8bit_adder_1_output, n8bit_register_1_output;

  Hex_Inverter hex_inverter_1 (
    ._1(Clock_Input), ._1_prime(Display_Clock));  // open: _2, _2_prime, _3, _3_prime, _4, _4_prime, _5, _5_prime, _6, _6_prime
  _8bit_adder u_8bit_adder_1 (
    .Input1({n8bit_register_1_output[7:2], System_Clock, n8bit_register_1_output[0]}),
    .Input_2({{7{1'b0}}, Clock_Input}), .Output(n8bit_adder_1_output));  // open: Carry
  _8bit_register u_8bit_register_1 (
    .M(1'b0), .N(1'b0), .\input (n8bit_adder_1_output), .clock(Display_Clock), .CLR(1'b0),
    .\output ({n8bit_register_1_output[7:2], System_Clock, n8bit_register_1_output[0]}), .G2(1'b0), .G1(1'b0));
endmodule

module Display_Driver (
  input  [7:0] in_1,
  input  Clock,
  input  W_To,
  output [7:0] out_4
);

  wire hex_inverter_1__4_prime;
  wire [3:0] n4bit_adder_1_out, n4bit_register_1__1d;

  _4bit_adder u_4bit_adder_1 (
    .In_1(n4bit_register_1__1d), .In_2({3'b000, Clock}), .C_in(1'b0), .Out(n4bit_adder_1_out));  // open: C_out
  Hex_Inverter hex_inverter_1 (
    ._4(Clock), ._4_prime(hex_inverter_1__4_prime));  // open: _1, _1_prime, _2, _2_prime, _3, _3_prime, _5, _5_prime, _6, _6_prime
  _4bit_register u_4bit_register_1 (
    .M(1'b0), .N(1'b0), ._1Q(n4bit_adder_1_out[0]), ._2Q(n4bit_adder_1_out[1]), ._3Q(n4bit_adder_1_out[2]),
    ._4Q(n4bit_adder_1_out[3]), .CLK(hex_inverter_1__4_prime), .CLR(1'b0), ._1D(n4bit_register_1__1d[0]),
    ._2D(n4bit_register_1__1d[1]), ._3D(n4bit_register_1__1d[2]), ._4D(n4bit_register_1__1d[3]), .G2(1'b0),
    .G1(1'b0));
  _8bit_2_input_multiplexer u_8bit_2_input_multiplexer_1 (
    .Input_1(in_1), .Input_2({4'b0000, n4bit_register_1__1d}), .Output(out_4), .Control(W_To));
endmodule

module GPIO_Pins (
  input  in_1
);

  _8bit_register u_8bit_register_1 (.M(in_1), .N(in_1));  // open: input, clock, CLR, output, G2, G1
endmodule

module Addr_filter (
  input  [7:0] in_1,
  input  Write_In,
  output Write_Out
);

  wire hex_inverter_1__1_prime, hex_inverter_1__4_prime, hex_inverter_1__5_prime, hex_inverter_1__6_prime,
       quad_and_1__2y, quad_and_1__3y, quad_and_1__4y;

  Quad_AND_Gate quad_and_1 (
    ._1a(Write_In), ._1b(quad_and_1__2y), ._1y(Write_Out), ._2a(quad_and_1__3y), ._2b(quad_and_1__4y),
    ._2y(quad_and_1__2y), ._3a(hex_inverter_1__1_prime), ._3b(hex_inverter_1__6_prime), ._3y(quad_and_1__3y),
    ._4a(hex_inverter_1__5_prime), ._4b(hex_inverter_1__4_prime), ._4y(quad_and_1__4y));
  Hex_Inverter hex_inverter_1 (
    ._1(in_1[7]), ._1_prime(hex_inverter_1__1_prime), ._4(in_1[6]), ._4_prime(hex_inverter_1__4_prime),
    ._5(in_1[5]), ._5_prime(hex_inverter_1__5_prime), ._6(in_1[4]), ._6_prime(hex_inverter_1__6_prime));  // open: _2, _2_prime, _3, _3_prime

  // Notes on the sheet:
  //   If any of the upper 4 bits are set, sets output write line 0
  //   Used to stop addrs > 15 from writing to the display
endmodule

module Interrupt (
  input  clock,
  input  CLR_Reg,
  input  Interrupt_Occured,
  input  [6:0] Input,
  output ninterrupt,
  output [7:0] Output
);

  wire decoder_1_out1, decoder_1_out2, decoder_1_out3, decoder_1_out4, decoder_1_out5, decoder_1_out6,
       decoder_1_out7, input_v2_1_ninterrupt, input_v2_2_ninterrupt, input_v2_3_ninterrupt,
       input_v2_4_ninterrupt, input_v2_5_ninterrupt, input_v2_6_ninterrupt, input_v2_7_ninterrupt,
       quad_and_1__1y, quad_and_1__3y, quad_and_2__1y, quad_and_2__3y, quad_and_2__4y;

  Decoder #(.select(3)) decoder_1 (
    .out1(decoder_1_out1), .out2(decoder_1_out2), .out3(decoder_1_out3), .out4(decoder_1_out4),
    .out5(decoder_1_out5), .out6(decoder_1_out6), .out7(decoder_1_out7), .sel(Input[2:0]));  // open: out0, en
  Input_v2 input_v2_1 (
    .Input(decoder_1_out1), .nInterrupt_Occured(Interrupt_Occured), .Clear_Reg(CLR_Reg), .Clock(clock),
    .Reg_bit(Output[0]), .nInterrupt(input_v2_1_ninterrupt));
  Input_v2 input_v2_2 (
    .Input(decoder_1_out2), .nInterrupt_Occured(Interrupt_Occured), .Clear_Reg(CLR_Reg), .Clock(clock),
    .Reg_bit(Output[1]), .nInterrupt(input_v2_2_ninterrupt));
  Input_v2 input_v2_3 (
    .Input(decoder_1_out3), .nInterrupt_Occured(Interrupt_Occured), .Clear_Reg(CLR_Reg), .Clock(clock),
    .Reg_bit(Output[2]), .nInterrupt(input_v2_3_ninterrupt));
  Input_v2 input_v2_4 (
    .Input(decoder_1_out4), .nInterrupt_Occured(Interrupt_Occured), .Clear_Reg(CLR_Reg), .Clock(clock),
    .Reg_bit(Output[3]), .nInterrupt(input_v2_4_ninterrupt));
  Input_v2 input_v2_5 (
    .Input(decoder_1_out5), .nInterrupt_Occured(Interrupt_Occured), .Clear_Reg(CLR_Reg), .Clock(clock),
    .Reg_bit(Output[4]), .nInterrupt(input_v2_5_ninterrupt));
  Input_v2 input_v2_6 (
    .Input(decoder_1_out6), .nInterrupt_Occured(Interrupt_Occured), .Clear_Reg(CLR_Reg), .Clock(clock),
    .Reg_bit(Output[5]), .nInterrupt(input_v2_6_ninterrupt));
  Input_v2 input_v2_7 (
    .Input(decoder_1_out7), .nInterrupt_Occured(Interrupt_Occured), .Clear_Reg(CLR_Reg), .Clock(clock),
    .Reg_bit(Output[6]), .nInterrupt(input_v2_7_ninterrupt));
  Quad_AND_Gate quad_and_1 (
    ._1a(input_v2_5_ninterrupt), ._1b(input_v2_6_ninterrupt), ._1y(quad_and_1__1y),
    ._3a(input_v2_7_ninterrupt), ._3b(quad_and_1__1y), ._3y(quad_and_1__3y));  // open: _2a, _2b, _2y, _4a, _4b, _4y
  Quad_AND_Gate quad_and_2 (
    ._1a(input_v2_1_ninterrupt), ._1b(input_v2_2_ninterrupt), ._1y(quad_and_2__1y), ._2a(quad_and_1__3y),
    ._2b(quad_and_2__4y), ._2y(ninterrupt), ._3a(input_v2_3_ninterrupt), ._3b(input_v2_4_ninterrupt),
    ._3y(quad_and_2__3y), ._4a(quad_and_2__3y), ._4b(quad_and_2__1y), ._4y(quad_and_2__4y));

  assign Output[7] = 1'b0;
endmodule

module Disable_Interrupts (
  input  nInterrupt,
  input  Clock,
  input  LSPC,
  output out_4
);

  wire hex_inverter_1__3_prime, hex_inverter_1__6_prime, n4bit_register_1__1d, quad_and_1__1y,
       quad_and_1__2y, triple_2_channel_mux_1_b_out;

  Hex_Inverter hex_inverter_1 (
    ._3(nInterrupt), ._3_prime(hex_inverter_1__3_prime), ._6(LSPC), ._6_prime(hex_inverter_1__6_prime));  // open: _1, _1_prime, _2, _2_prime, _4, _4_prime, _5, _5_prime
  _4bit_register u_4bit_register_1 (
    .M(1'b0), .N(1'b0), ._1Q(nInterrupt), ._2Q(quad_and_1__2y), .CLK(Clock), .CLR(1'b0),
    ._1D(n4bit_register_1__1d), ._2D(out_4), .G2(1'b0), .G1(1'b0));  // open: _3Q, _4Q, _3D, _4D
  triple_2_channel_mux triple_2_channel_mux_1 (
    .bx(out_4), .by(quad_and_1__1y), .b_out(triple_2_channel_mux_1_b_out), .B(quad_and_1__1y));  // open: cy, c_out, cx, enable, a_out, ax, ay, A, C
  Quad_AND_Gate quad_and_1 (
    ._1a(hex_inverter_1__3_prime), ._1b(n4bit_register_1__1d), ._1y(quad_and_1__1y),
    ._2a(triple_2_channel_mux_1_b_out), ._2b(hex_inverter_1__6_prime), ._2y(quad_and_1__2y));  // open: _3a, _3b, _3y, _4a, _4b, _4y
endmodule

module Page_Register (
  input  [7:0] Addr
);
endmodule

module _4_bit_OR (
  input  [3:0] in_1,
  input  [3:0] in_2,
  output [3:0] out_3
);

  Quad_OR_Gate quad_or_1 (
    ._1a(in_1[0]), ._1b(in_2[0]), ._1y(out_3[0]), ._2a(in_1[1]), ._2b(in_2[1]), ._2y(out_3[1]),
    ._3a(in_1[2]), ._3b(in_2[2]), ._3y(out_3[2]), ._4a(in_1[3]), ._4b(in_2[3]), ._4y(out_3[3]));
endmodule

module _4_bit_AND (
  input  [3:0] in_1,
  input  [3:0] in_2,
  output [3:0] out_3
);

  Quad_AND_Gate quad_and_1 (
    ._1a(in_1[0]), ._1b(in_2[0]), ._1y(out_3[0]), ._2a(in_1[1]), ._2b(in_2[1]), ._2y(out_3[1]),
    ._3a(in_1[2]), ._3b(in_2[2]), ._3y(out_3[2]), ._4a(in_1[3]), ._4b(in_2[3]), ._4y(out_3[3]));
endmodule

module Reg_selecter (
  input  S0,
  input  S1,
  input  S2,
  input  S3,
  output _0,
  output out_6,
  output out_7,
  output out_8,
  output out_9,
  output out_10,
  output out_11,
  output out_12,
  output out_13,
  output out_14,
  output out_15,
  output out_16,
  output out_17,
  output out_18,
  output _14
);

  wire n1_bit_16_output_demultiplexer_1_c0, n1_bit_16_output_demultiplexer_1_c1,
       n1_bit_16_output_demultiplexer_1_c2, n1_bit_16_output_demultiplexer_1_c3,
       n1_bit_16_output_demultiplexer_1_c4, n1_bit_16_output_demultiplexer_1_c5,
       n1_bit_16_output_demultiplexer_1_c7, n1_bit_16_output_demultiplexer_1_c8,
       n1_bit_16_output_demultiplexer_1_c9, n1_bit_16_output_demultiplexer_1_c10,
       n1_bit_16_output_demultiplexer_1_c11, n1_bit_16_output_demultiplexer_1_c12,
       n1_bit_16_output_demultiplexer_1_c13, n1_bit_16_output_demultiplexer_1_c14;

  _1_bit_16_output_demultiplexer u_1_bit_16_output_demultiplexer_1 (
    .C14(n1_bit_16_output_demultiplexer_1_c14), .C13(n1_bit_16_output_demultiplexer_1_c13),
    .C12(n1_bit_16_output_demultiplexer_1_c12), .C11(n1_bit_16_output_demultiplexer_1_c11),
    .C10(n1_bit_16_output_demultiplexer_1_c10), .C9(n1_bit_16_output_demultiplexer_1_c9),
    .C8(n1_bit_16_output_demultiplexer_1_c8), .C7(n1_bit_16_output_demultiplexer_1_c7),
    .C6(n1_bit_16_output_demultiplexer_1_c10), .C5(n1_bit_16_output_demultiplexer_1_c5),
    .C4(n1_bit_16_output_demultiplexer_1_c4), .C3(n1_bit_16_output_demultiplexer_1_c3),
    .C2(n1_bit_16_output_demultiplexer_1_c2), .C1(n1_bit_16_output_demultiplexer_1_c1),
    .C0(n1_bit_16_output_demultiplexer_1_c0), .SIG(1'b1), .S3(S3), .S2(S2), .S1(S1), .S0(S0), .En(1'b0));  // open: C15
  Hex_Inverter hex_inverter_1 (
    ._1(n1_bit_16_output_demultiplexer_1_c0), ._1_prime(_0), ._2(n1_bit_16_output_demultiplexer_1_c1),
    ._2_prime(out_6), ._3(n1_bit_16_output_demultiplexer_1_c2), ._3_prime(out_7),
    ._4(n1_bit_16_output_demultiplexer_1_c3), ._4_prime(out_8), ._5(n1_bit_16_output_demultiplexer_1_c4),
    ._5_prime(out_9), ._6(n1_bit_16_output_demultiplexer_1_c5), ._6_prime(out_10));
  Hex_Inverter hex_inverter_2 (
    ._1(n1_bit_16_output_demultiplexer_1_c10), ._1_prime(out_11), ._2(n1_bit_16_output_demultiplexer_1_c7),
    ._2_prime(out_12), ._3(n1_bit_16_output_demultiplexer_1_c8), ._3_prime(out_13),
    ._4(n1_bit_16_output_demultiplexer_1_c9), ._4_prime(out_14), ._5(n1_bit_16_output_demultiplexer_1_c10),
    ._5_prime(out_15), ._6(n1_bit_16_output_demultiplexer_1_c11), ._6_prime(out_16));
  Hex_Inverter hex_inverter_3 (
    ._1(n1_bit_16_output_demultiplexer_1_c12), ._1_prime(out_17), ._2(n1_bit_16_output_demultiplexer_1_c13),
    ._2_prime(out_18), ._4(n1_bit_16_output_demultiplexer_1_c14), ._4_prime(_14));  // open: _3, _3_prime, _5, _5_prime, _6, _6_prime
endmodule
