// Logisim project version 2.circ as structural Verilog
module main (
);

  wire clock_1_out;
  wire [7:0] B_output, C_output, D_output, demultiplexer_1_out0, demultiplexer_1_out1, demultiplexer_2_out0,
       demultiplexer_2_out1, demultiplexer_3_out0, demultiplexer_3_out1, demultiplexer_4_out0,
       demultiplexer_4_out1, n8bit_or_1_out, n8bit_or_2_out, n8bit_or_3_out, registers_1_output;

  _8bit_OR_Gate u_8bit_or_1 (.In_2(demultiplexer_1_out0), .In_1(demultiplexer_2_out0), .Out(n8bit_or_1_out));
  _8bit_OR_Gate u_8bit_or_2 (.In_2(n8bit_or_1_out), .In_1(demultiplexer_3_out0), .Out(n8bit_or_2_out));
  _8bit_OR_Gate u_8bit_or_3 (.In_2(n8bit_or_2_out), .In_1(demultiplexer_4_out0), .Out(n8bit_or_3_out));
  Demultiplexer #(.width(8), .enable("false")) demultiplexer_1 (
    .out0(demultiplexer_1_out0), .out1(demultiplexer_1_out1), .in(registers_1_output), .sel(1'b0));
  Demultiplexer #(.width(8), .enable("false")) demultiplexer_2 (
    .out0(demultiplexer_2_out0), .out1(demultiplexer_2_out1), .in(B_output), .sel(1'b0));
  Demultiplexer #(.width(8), .enable("false")) demultiplexer_3 (
    .out0(demultiplexer_3_out0), .out1(demultiplexer_3_out1), .in(C_output), .sel(1'b0));
  Demultiplexer #(.width(8), .enable("false")) demultiplexer_4 (
    .out0(demultiplexer_4_out0), .out1(demultiplexer_4_out1), .in(D_output), .sel(1'b0));
  Clock clock_1 (.out(clock_1_out));
  registers registers_1 (.Clock(clock_1_out), .ER(1'b1), .EW(1'b1), .Input({8{1'b1}}), .Output(registers_1_output));
  registers B (.Clock(clock_1_out), .Input({8{1'b1}}), .Output(B_output));  // open: ER, EW
  registers C (.Clock(clock_1_out), .Input({8{1'b1}}), .Output(C_output));  // open: ER, EW
  registers D (.Clock(clock_1_out), .Input({8{1'b1}}), .Output(D_output));  // open: ER, EW
endmodule

module registers (
  input  [7:0] Input,
  input  Clock,
  input  ER,
  input  EW,
  output [7:0] Output
);

  wire [3:0] multiplexer_1_out, multiplexer_2_out, register_1_q, register_2_q;

  Multiplexer #(.width(4), .enable("false")) multiplexer_1 (
    .in0(register_1_q), .in1(Input[3:0]), .out(multiplexer_1_out), .sel(ER));
  Multiplexer #(.width(4), .enable("false")) multiplexer_2 (
    .in0(register_2_q), .in1(Input[7:4]), .out(multiplexer_2_out), .sel(ER));
  Register #(.width(4)) register_1 (.D(multiplexer_1_out), .Q(register_1_q), .clk(Clock));  // open: en, clr
  Register #(.width(4)) register_2 (.D(multiplexer_2_out), .Q(register_2_q), .clk(Clock));  // open: en, clr
  assign Output = {8{EW}} & {register_2_q, register_1_q};  // AND_Gate and_1, 8 bits wide
endmodule

module ALU (
);

  _8bit_AND_Gate u_8bit_and_1 ();  // open: In_2, In_1, Out
endmodule

module ALU2 (
);

  _8bit_AND_Gate u_8bit_and_1 ();  // open: In_2, In_1, Out
endmodule

module Input (
  input  Input,
  input  Clock
);

  wire [3:0] multiplexer_1_out, register_1_q, undriven_2;
  wire [3:1] undriven;

  Multiplexer #(.width(4), .enable("false")) multiplexer_1 (
    .in0(undriven_2), .in1({undriven, Input}), .out(multiplexer_1_out));  // open: sel
  Register #(.width(4)) register_1 (.D(multiplexer_1_out), .Q(register_1_q));  // open: en, clk, clr
endmodule

module _8bit_AND_Gate (
  input  [7:0] In_1,
  input  [7:0] In_2,
  output [7:0] Out
);

  Quad_AND_Gate quad_and_1 (
    ._1a(In_1[0]), ._1b(In_2[0]), ._1y(Out[0]), ._2a(In_1[1]), ._2b(In_2[1]), ._2y(Out[1]), ._3a(In_1[2]),
    ._3b(In_2[2]), ._3y(Out[2]), ._4a(In_1[3]), ._4b(In_2[3]), ._4y(Out[3]));
  Quad_AND_Gate quad_and_2 (
    ._1a(In_1[4]), ._1b(In_2[4]), ._1y(Out[4]), ._2a(In_1[5]), ._2b(In_2[5]), ._2y(Out[5]), ._3a(In_1[6]),
    ._3b(In_2[6]), ._3y(Out[6]), ._4a(In_1[7]), ._4b(In_2[7]), ._4y(Out[7]));
endmodule

module _8bit_OR_Gate (
  input  [7:0] In_1,
  input  [7:0] In_2,
  output [7:0] Out
);

  Quad_OR_Gate quad_or_1 (
    ._1a(In_1[0]), ._1b(In_2[0]), ._1y(Out[0]), ._2a(In_1[1]), ._2b(In_2[1]), ._2y(Out[1]), ._3a(In_1[2]),
    ._3b(In_2[2]), ._3y(Out[2]), ._4a(In_1[3]), ._4b(In_2[3]), ._4y(Out[3]));
  Quad_OR_Gate quad_or_2 (
    ._1a(In_1[4]), ._1b(In_2[4]), ._1y(Out[4]), ._2a(In_1[5]), ._2b(In_2[5]), ._2y(Out[5]), ._3a(In_1[6]),
    ._3b(In_2[6]), ._3y(Out[6]), ._4a(In_1[7]), ._4b(In_2[7]), ._4y(Out[7]));
endmodule

module _8bit_XOR (
  input  [7:0] Read_1,
  input  [7:0] Read_2,
  output [7:0] Write
);

  Quad_XOR_gate quad_xor_gate_1 (
    ._1a(Read_1[2]), ._1b(Read_2[2]), ._1_y(Write[2]), ._2a(Read_2[3]), ._2b(Read_1[3]), ._2_y(Write[3]),
    ._3a(Read_1[0]), ._3b(Read_2[0]), ._3_y(Write[0]), ._3a_2(Read_2[1]), ._3b_2(Read_1[1]), ._3_y_2(Write[1]));
  Quad_XOR_gate quad_xor_gate_2 (
    ._1a(Read_1[6]), ._1b(Read_2[6]), ._1_y(Write[6]), ._2a(Read_1[7]), ._2b(Read_2[7]), ._2_y(Write[7]),
    ._3a(Read_2[4]), ._3b(Read_1[4]), ._3_y(Write[4]), ._3a_2(Read_2[5]), ._3b_2(Read_1[5]), ._3_y_2(Write[5]));
endmodule

module _8bit_2_input_multiplexer (
  input  [7:0] Input_1,
  input  [7:0] Input_2,
  input  Control,
  output [7:0] Output
);

  triple_2_channel_mux triple_2_channel_mux_1 (
    .bx(Input_2[0]), .by(Input_1[0]), .cy(Input_1[1]), .c_out(Output[1]), .cx(Input_2[1]), .enable(1'b1),
    .b_out(Output[0]), .A(Control), .B(Control), .C(Control));  // open: a_out, ax, ay
  triple_2_channel_mux triple_2_channel_mux_2 (
    .bx(Input_2[3]), .by(Input_1[3]), .cy(Input_1[4]), .c_out(Output[4]), .cx(Input_2[4]), .enable(1'b1),
    .b_out(Output[3]), .a_out(Output[2]), .ax(Input_2[2]), .ay(Input_1[2]), .A(Control), .B(Control),
    .C(Control));
  triple_2_channel_mux triple_2_channel_mux_3 (
    .bx(Input_2[6]), .by(Input_1[6]), .cy(Input_1[7]), .c_out(Output[7]), .cx(Input_2[7]), .enable(1'b1),
    .b_out(Output[6]), .a_out(Output[5]), .ax(Input_2[5]), .ay(Input_1[5]), .A(Control), .B(Control),
    .C(Control));
endmodule

module _8bit_adder (
  input  [7:0] in_1,
  input  [7:0] in_2,
  output [7:0] out_3
);

  wire n4bit_adder_1_c_out;

  _4bit_adder u_4bit_adder_1 (
    .In_1(in_1[3:0]), .In_2(in_2[3:0]), .C_in(1'b0), .Out(out_3[3:0]), .C_out(n4bit_adder_1_c_out));
  _4bit_adder u_4bit_adder_2 (
    .In_1(in_1[7:4]), .In_2(in_2[7:4]), .C_in(n4bit_adder_1_c_out), .Out(out_3[7:4]));  // open: C_out
endmodule

module triple_2_channel_mux (
  input  bx,
  input  by,
  input  cy,
  input  ax,
  input  ay,
  input  cx,
  input  A,
  input  enable,
  input  B,
  input  C,
  output b_out,
  output a_out,
  output c_out
);

  Multiplexer multiplexer_1 (.in0(cx), .in1(cy), .out(c_out), .sel(C), .en(enable));
  Multiplexer multiplexer_2 (.in0(bx), .in1(by), .out(b_out), .sel(B), .en(enable));
  Multiplexer multiplexer_3 (.in0(ax), .in1(ay), .out(a_out), .sel(A), .en(enable));

  // Notes on the sheet:
  //   Cd4053B as multiplexer
endmodule

module triple_2_channel_demux (
  input  b_in,
  input  a_in,
  input  c_in,
  input  A,
  input  enable,
  input  B,
  input  C,
  output bx,
  output by,
  output cy,
  output ax,
  output ay,
  output cx
);

  Demultiplexer demultiplexer_1 (.out0(cx), .out1(cy), .in(c_in), .sel(C), .en(enable));
  Demultiplexer demultiplexer_2 (.out0(bx), .out1(by), .in(b_in), .sel(B), .en(enable));
  Demultiplexer demultiplexer_3 (.out0(ax), .out1(ay), .in(a_in), .sel(A), .en(enable));

  // Notes on the sheet:
  //   Cd4053B as demultiplexer
endmodule

module Quad_OR_Gate (
  input  _3a,
  input  _1a,
  input  _3b,
  input  _1b,
  input  _4a,
  input  _2a,
  input  _4b,
  input  _2b,
  output _3y,
  output _1y,
  output _4y,
  output _2y
);

  or or_1 (_1y, _1a, _1b);
  or or_2 (_2y, _2a, _2b);
  or or_3 (_3y, _3a, _3b);
  or or_4 (_4y, _4a, _4b);
endmodule

module Quad_AND_Gate (
  input  _3a,
  input  _1a,
  input  _3b,
  input  _1b,
  input  _4a,
  input  _2a,
  input  _4b,
  input  _2b,
  output _3y,
  output _1y,
  output _4y,
  output _2y
);

  and and_1 (_1y, _1a, _1b);
  and and_2 (_2y, _2a, _2b);
  and and_3 (_3y, _3a, _3b);
  and and_4 (_4y, _4a, _4b);
endmodule

module Hex_Inverter (
  input  _1,
  input  _4,
  input  _2,
  input  _5,
  input  _6,
  input  _3,
  output _1_prime,
  output _4_prime,
  output _5_prime,
  output _2_prime,
  output _6_prime,
  output _3_prime
);

  not not_1 (_1_prime, _1);
  not not_2 (_2_prime, _2);
  not not_3 (_3_prime, _3);
  not not_4 (_4_prime, _4);
  not not_5 (_5_prime, _5);
  not not_6 (_6_prime, _6);
endmodule

module Quad_XOR_gate (
  input  _3a,
  input  _1a,
  input  _3b,
  input  _1b,
  input  _3a_2,
  input  _2a,
  input  _3b_2,
  input  _2b,
  output _3_y,
  output _1_y,
  output _3_y_2,
  output _2_y
);

  xor xor_1 (_1_y, _1a, _1b);
  xor xor_2 (_2_y, _2a, _2b);
  xor xor_3 (_3_y, _3a, _3b);
  xor xor_4 (_3_y_2, _3a_2, _3b_2);

  // Notes on the sheet:
  //   XOR Gate Sn74hc86n
endmodule

module _4bit_adder (
  input  [3:0] In_1,
  input  [3:0] In_2,
  input  C_in,
  output [3:0] Out,
  output C_out
);

  wire quad_and_1__1y, quad_and_1__2y, quad_and_1__3y, quad_and_1__4y, quad_and_2__1y, quad_and_2__2y,
       quad_and_2__3y, quad_and_2__4y, quad_or_1__1y, quad_or_1__2y, quad_or_1__3y, quad_xor_gate_1__1_y,
       quad_xor_gate_1__3_y, quad_xor_gate_2__1_y, quad_xor_gate_2__3_y;

  Quad_XOR_gate quad_xor_gate_1 (
    ._1a(In_1[0]), ._1b(In_2[0]), ._1_y(quad_xor_gate_1__1_y), ._2a(quad_xor_gate_1__1_y), ._2b(C_in),
    ._2_y(Out[0]), ._3a(In_1[1]), ._3b(In_2[1]), ._3_y(quad_xor_gate_1__3_y), ._3a_2(quad_xor_gate_1__3_y),
    ._3b_2(quad_or_1__1y), ._3_y_2(Out[1]));
  Quad_XOR_gate quad_xor_gate_2 (
    ._1a(In_1[2]), ._1b(In_2[2]), ._1_y(quad_xor_gate_2__1_y), ._2a(quad_xor_gate_2__1_y),
    ._2b(quad_or_1__2y), ._2_y(Out[2]), ._3a(In_1[3]), ._3b(In_2[3]), ._3_y(quad_xor_gate_2__3_y),
    ._3a_2(quad_xor_gate_2__3_y), ._3b_2(quad_or_1__3y), ._3_y_2(Out[3]));
  Quad_AND_Gate quad_and_1 (
    ._1a(quad_xor_gate_1__1_y), ._1b(C_in), ._1y(quad_and_1__1y), ._2a(In_2[0]), ._2b(In_1[0]),
    ._2y(quad_and_1__2y), ._3a(quad_xor_gate_1__3_y), ._3b(quad_or_1__1y), ._3y(quad_and_1__3y),
    ._4a(In_1[1]), ._4b(In_2[1]), ._4y(quad_and_1__4y));
  Quad_AND_Gate quad_and_2 (
    ._1a(quad_xor_gate_2__1_y), ._1b(quad_or_1__2y), ._1y(quad_and_2__1y), ._2a(In_2[2]),
    ._2b(quad_or_1__2y), ._2y(quad_and_2__2y), ._3a(quad_xor_gate_2__3_y), ._3b(quad_or_1__3y),
    ._3y(quad_and_2__3y), ._4a(In_2[3]), ._4b(In_1[3]), ._4y(quad_and_2__4y));
  Quad_OR_Gate quad_or_1 (
    ._1a(quad_and_1__1y), ._1b(quad_and_1__2y), ._1y(quad_or_1__1y), ._2a(quad_and_1__3y),
    ._2b(quad_and_1__4y), ._2y(quad_or_1__2y), ._3a(quad_and_2__1y), ._3b(quad_and_2__2y),
    ._3y(quad_or_1__3y), ._4a(quad_and_2__3y), ._4b(quad_and_2__4y), ._4y(C_out));
endmodule
